// Logisim project alu_module.circ as structural Verilog: 2 circuits, main circuit alu
module alu (
  input  decoded_alu_output_mux,
  input  [7:0] rs,
  input  [7:0] rt,
  input  [1:0] decoded_alu_arithmetic_mux,
  input  reset,
  input  [2:0] core_state,
  input  enable,
  input  clk,
  output [7:0] alu_out
);

  wire decoder_1_out5, not_1_out;
  wire [2:0] comparator_1_lt;
  wire [7:0] adder_1_out, dlv_1_cout, multiplexer_1_out, multiplexer_2_out, multiplier_1_out,
       subtractor_1_out;

  Decoder #(.select(3)) decoder_1 (
    .out5(decoder_1_out5), .sel(core_state));  // open: out0, out1, out2, out3, out4, out6, out7, en
  Adder adder_1 (.a(rs), .b(rt), .out(adder_1_out));  // open: cin, cout
  Subtractor subtractor_1 (.a(rs), .b(rt), .out(subtractor_1_out));  // open: bin, bout
  Multiplier multiplier_1 (.a(rs), .b(rt), .out(multiplier_1_out));  // open: cin, cout
  dlv dlv_1 (.divisor(rs), .dividend(rt), .cout(dlv_1_cout));  // open: err
  Comparator comparator_1 (
    .a(subtractor_1_out), .b({8{1'b0}}), .gt(comparator_1_lt[2]), .eq(comparator_1_lt[1]),
    .lt(comparator_1_lt[0]));
  not not_1 (not_1_out, decoded_alu_output_mux);
  Multiplexer #(.enable("true"), .select(2), .width(8)) multiplexer_1 (
    .in0(adder_1_out), .in1(subtractor_1_out), .in2(multiplier_1_out), .in3(dlv_1_cout),
    .out(multiplexer_1_out), .sel(decoded_alu_arithmetic_mux), .en(decoder_1_out5));
  Multiplexer #(.width(8)) multiplexer_2 (
    .in0({{5{1'b0}}, comparator_1_lt}), .in1(multiplexer_1_out), .out(multiplexer_2_out), .sel(not_1_out));
  Register alu_out_reg (.D(multiplexer_2_out), .en(enable), .clk(clk), .Q(alu_out), .clr(reset));

  // Notes on the sheet:
  //   alu_out: pull=down
endmodule

module dlv (
  input  [7:0] divisor,
  input  [7:0] dividend,
  output [7:0] cout,
  output err
);

  wire [31:0] fpdivider_1_out, inttofp_1_p2, inttofp_2_p2;

  // IntToFP inttofp_1: pin names not known; wires that end beside it: divisor, inttofp_1_p2
  FPDivider fpdivider_1 (.a(inttofp_1_p2), .b(inttofp_2_p2), .out(fpdivider_1_out));
  // IntToFP inttofp_2: pin names not known; wires that end beside it: dividend, inttofp_2_p2, err
  // FPToInt fptoint_1: pin names not known; wires that end beside it: fpdivider_1_out, err, cout

  // Notes on the sheet:
  //   err: pull=down
endmodule
