// Logisim project controller_test.circ as structural Verilog: 1 circuit, main circuit controller
module controller (
  input  reset,
  input  clk,
  input  [3:0] consumer_read_valid,
  input  mem_read_ready,
  input  [7:0] consumer_read_address_0,
  input  [7:0] consumer_read_address_1,
  input  [7:0] consumer_read_address_2,
  input  [7:0] consumer_read_address_3,
  input  mem_write_ready,
  input  [3:0] consumer_write_valid,
  input  [15:0] consumer_write_data_0,
  input  [15:0] consumer_write_data_1,
  input  [15:0] consumer_write_data_2,
  input  [15:0] consumer_write_data_3,
  input  [7:0] consumer_write_address_0,
  input  [7:0] consumer_write_address_1,
  input  [7:0] consumer_write_address_2,
  input  [7:0] consumer_write_address_3,
  output mem_read_valid,
  output [7:0] mem_read_address,
  output mem_write_valid,
  output [15:0] mem_write_data,
  output [7:0] mem_write_address,
  output [3:0] consumer_read_ready,
  output [3:0] consumer_write_ready
);

  wire and_1_out, and_2_out, and_3_out, and_4_out, and_5_out, and_6_out, and_7_out, and_8_out, and_18_out,
       bitfinder_1_found, bitfinder_2_found, channel_serving_consumer_reg_0_q,
       channel_serving_consumer_reg_1_q, channel_serving_consumer_reg_2_q, channel_serving_consumer_reg_3_q,
       consumer_rw_and_channel_serving_consumer_success, decoder_2_out0, decoder_2_out1, decoder_2_out2,
       decoder_2_out3, decoder_3_out0, decoder_3_out1, decoder_3_out2, decoder_3_out3, decoder_4_out0,
       decoder_4_out1, decoder_4_out2, decoder_4_out3, decoder_5_out0, decoder_5_out1, decoder_5_out2,
       decoder_5_out3, decoder_6_out0, decoder_6_out1, decoder_6_out2, decoder_6_out3, IDLE_STATE,
       multiplexer_5_out, multiplexer_6_out, multiplexer_7_out, multiplexer_11_out, multiplexer_13_out,
       not_1_out, not_2_out, not_3_out, not_4_out, not_5_out, not_6_out, not_7_out, not_8_out, not_9_out,
       not_10_out, not_11_out, not_12_out, not_13_out, not_14_out, or_1_out, or_2_out, or_3_out, or_6_out,
       or_7_out, or_9_out, or_10_out, READ_RELAYING_STATE, READ_RELAYING_STATE_UPDATE, READ_WAITING_STATE,
       READ_WAITING_STATE_UPDATE, WRITE_RELAYING_STATE, WRITE_RELAYING_STATE_UPDATE, WRITE_WAITING_STATE,
       WRITE_WAITING_STATE_UPDATE;
  wire [1:0] bitfinder_1_index, bitfinder_2_index, consumer_rw_and_channel_serving_consumer_bit,
       current_consumer;
  wire [2:0] controller_state_reg_q, multiplexer_1_out, multiplexer_2_out, multiplexer_3_out,
       multiplexer_4_out;
  wire [3:0] and_9_out, and_13_out;
  wire [7:0] multiplexer_10_out, multiplexer_12_out;
  wire [15:0] multiplexer_9_out;

  Multiplexer #(.width(3)) multiplexer_1 (
    .in0(3'b000), .in1(3'b101), .out(multiplexer_1_out), .sel(WRITE_WAITING_STATE_UPDATE));
  not not_1 (not_1_out, reset);
  Decoder #(.select(3)) decoder_1 (
    .out0(IDLE_STATE), .out2(READ_WAITING_STATE), .out3(WRITE_WAITING_STATE), .out4(READ_RELAYING_STATE),
    .out5(WRITE_RELAYING_STATE), .sel(controller_state_reg_q), .en(not_1_out));  // open: out1, out6, out7
  Decoder #(.select(2)) decoder_2 (
    .out0(decoder_2_out0), .out1(decoder_2_out1), .out2(decoder_2_out2), .out3(decoder_2_out3),
    .sel(current_consumer), .en(READ_RELAYING_STATE));
  Decoder #(.select(2)) decoder_3 (
    .out0(decoder_3_out0), .out1(decoder_3_out1), .out2(decoder_3_out2), .out3(decoder_3_out3),
    .sel(current_consumer), .en(WRITE_RELAYING_STATE));
  Multiplexer #(.width(3)) multiplexer_2 (
    .in0(multiplexer_1_out), .in1(3'b100), .out(multiplexer_2_out), .sel(READ_WAITING_STATE_UPDATE));
  or or_1 (or_1_out, reset, consumer_rw_and_channel_serving_consumer_success, READ_WAITING_STATE_UPDATE, WRITE_WAITING_STATE_UPDATE, or_3_out);
  or or_2 (or_2_out, WRITE_WAITING_STATE_UPDATE, WRITE_RELAYING_STATE_UPDATE);
  Multiplexer #(.width(3)) multiplexer_3 (
    .in0(multiplexer_2_out), .in1(3'b010), .out(multiplexer_3_out),
    .sel(consumer_rw_and_channel_serving_consumer_success));
  Multiplexer #(.width(3)) multiplexer_4 (.in0(multiplexer_3_out), .in1(3'b000), .out(multiplexer_4_out), .sel(reset));
  not not_2 (not_2_out, consumer_read_valid[0]);
  not not_3 (not_3_out, consumer_read_valid[1]);
  not not_4 (not_4_out, consumer_read_valid[2]);
  not not_5 (not_5_out, consumer_read_valid[3]);
  not not_6 (not_6_out, consumer_write_valid[0]);
  not not_7 (not_7_out, consumer_write_valid[1]);
  not not_8 (not_8_out, consumer_write_valid[2]);
  not not_9 (not_9_out, consumer_write_valid[3]);
  Decoder #(.select(2)) decoder_4 (
    .out0(decoder_4_out0), .out1(decoder_4_out1), .out2(decoder_4_out2), .out3(decoder_4_out3),
    .sel(current_consumer), .en(or_2_out));
  or or_3 (or_3_out, WRITE_RELAYING_STATE_UPDATE, READ_RELAYING_STATE_UPDATE);
  Register #(.width(3)) controller_state_reg (
    .D(multiplexer_4_out), .en(or_1_out), .clk(clk), .Q(controller_state_reg_q));  // open: clr
  and and_1 (and_1_out, decoder_2_out0, not_2_out);
  and and_2 (and_2_out, decoder_2_out1, not_3_out);
  and and_3 (and_3_out, decoder_2_out2, not_4_out);
  and and_4 (and_4_out, decoder_2_out3, not_5_out);
  and and_5 (and_5_out, decoder_3_out0, not_6_out);
  and and_6 (and_6_out, decoder_3_out1, not_7_out);
  and and_7 (and_7_out, decoder_3_out2, not_8_out);
  and and_8 (and_8_out, decoder_3_out3, not_9_out);
  Multiplexer multiplexer_5 (.in0(1'b0), .in1(1'b1), .out(multiplexer_5_out), .sel(WRITE_WAITING_STATE_UPDATE));
  or or_4 (READ_RELAYING_STATE_UPDATE, and_1_out, and_2_out, and_3_out, and_4_out);
  or or_5 (WRITE_RELAYING_STATE_UPDATE, and_5_out, and_6_out, and_7_out, and_8_out);
  Register #(.width(1)) consumer_write_ready_reg_0 (
    .D(multiplexer_5_out), .en(decoder_4_out0), .clk(clk), .Q(consumer_write_ready[0]), .clr(reset));
  Register #(.width(1)) consumer_write_ready_reg_1 (
    .D(multiplexer_5_out), .en(decoder_4_out1), .clk(clk), .Q(consumer_write_ready[1]), .clr(reset));
  Register #(.width(1)) consumer_write_ready_reg_2 (
    .D(multiplexer_5_out), .en(decoder_4_out2), .clk(clk), .Q(consumer_write_ready[2]), .clr(reset));
  Register #(.width(1)) consumer_write_ready_reg_3 (
    .D(multiplexer_5_out), .en(decoder_4_out3), .clk(clk), .Q(consumer_write_ready[3]), .clr(reset));
  or or_6 (or_6_out, consumer_rw_and_channel_serving_consumer_success, WRITE_RELAYING_STATE_UPDATE, READ_RELAYING_STATE_UPDATE);
  Decoder #(.select(2)) decoder_5 (
    .out0(decoder_5_out0), .out1(decoder_5_out1), .out2(decoder_5_out2), .out3(decoder_5_out3),
    .sel(consumer_rw_and_channel_serving_consumer_bit), .en(or_6_out));
  or or_7 (or_7_out, READ_WAITING_STATE_UPDATE, READ_RELAYING_STATE_UPDATE);
  Decoder #(.select(2)) decoder_6 (
    .out0(decoder_6_out0), .out1(decoder_6_out1), .out2(decoder_6_out2), .out3(decoder_6_out3),
    .sel(current_consumer), .en(or_7_out));
  Multiplexer multiplexer_6 (
    .in0(1'b0), .in1(1'b1), .out(multiplexer_6_out), .sel(consumer_rw_and_channel_serving_consumer_success));
  Register #(.width(1)) channel_serving_consumer_reg_0 (
    .D(multiplexer_6_out), .en(decoder_5_out0), .clk(clk), .Q(channel_serving_consumer_reg_0_q), .clr(reset));
  Register #(.width(1)) channel_serving_consumer_reg_1 (
    .D(multiplexer_6_out), .en(decoder_5_out1), .clk(clk), .Q(channel_serving_consumer_reg_1_q), .clr(reset));
  Register #(.width(1)) channel_serving_consumer_reg_2 (
    .D(multiplexer_6_out), .en(decoder_5_out2), .clk(clk), .Q(channel_serving_consumer_reg_2_q), .clr(reset));
  Register #(.width(1)) channel_serving_consumer_reg_3 (
    .D(multiplexer_6_out), .en(decoder_5_out3), .clk(clk), .Q(channel_serving_consumer_reg_3_q), .clr(reset));
  Multiplexer multiplexer_7 (.in0(1'b0), .in1(1'b1), .out(multiplexer_7_out), .sel(READ_WAITING_STATE_UPDATE));
  not not_10 (not_10_out, channel_serving_consumer_reg_0_q);
  not not_11 (not_11_out, channel_serving_consumer_reg_1_q);
  not not_12 (not_12_out, channel_serving_consumer_reg_2_q);
  not not_13 (not_13_out, channel_serving_consumer_reg_3_q);
  Register #(.width(1)) consumer_read_ready_reg_0 (
    .D(multiplexer_7_out), .en(decoder_6_out0), .clk(clk), .Q(consumer_read_ready[0]), .clr(reset));
  Register #(.width(1)) consumer_read_ready_reg_1 (
    .D(multiplexer_7_out), .en(decoder_6_out1), .clk(clk), .Q(consumer_read_ready[1]), .clr(reset));
  Register #(.width(1)) consumer_read_ready_reg_2 (
    .D(multiplexer_7_out), .en(decoder_6_out2), .clk(clk), .Q(consumer_read_ready[2]), .clr(reset));
  Register #(.width(1)) consumer_read_ready_reg_3 (
    .D(multiplexer_7_out), .en(decoder_6_out3), .clk(clk), .Q(consumer_read_ready[3]), .clr(reset));
  and and_9 (and_9_out[0], consumer_read_valid[0], not_10_out, IDLE_STATE);
  and and_10 (and_9_out[1], consumer_read_valid[1], not_11_out, IDLE_STATE);
  and and_11 (and_9_out[2], consumer_read_valid[2], not_12_out, IDLE_STATE);
  and and_12 (and_9_out[3], consumer_read_valid[3], not_13_out, IDLE_STATE);
  and and_13 (and_13_out[0], not_10_out, IDLE_STATE, consumer_write_valid[0]);
  and and_14 (and_13_out[1], not_11_out, IDLE_STATE, consumer_write_valid[1]);
  and and_15 (and_13_out[2], not_12_out, IDLE_STATE, consumer_write_valid[2]);
  and and_16 (and_13_out[3], not_13_out, IDLE_STATE, consumer_write_valid[3]);
  BitFinder #(.width(4)) bitfinder_1 (.in(and_9_out), .index(bitfinder_1_index), .found(bitfinder_1_found));
  or or_8 (consumer_rw_and_channel_serving_consumer_success, bitfinder_1_found, bitfinder_2_found);
  BitFinder #(.width(4)) bitfinder_2 (.in(and_13_out), .index(bitfinder_2_index), .found(bitfinder_2_found));
  Multiplexer #(.width(2)) multiplexer_8 (
    .in0(bitfinder_1_index), .in1(bitfinder_2_index), .out(consumer_rw_and_channel_serving_consumer_bit),
    .sel(bitfinder_2_found));
  and and_17 (READ_WAITING_STATE_UPDATE, mem_read_ready, READ_WAITING_STATE);
  not not_14 (not_14_out, bitfinder_1_found);
  and and_18 (and_18_out, not_14_out, bitfinder_2_found);
  Multiplexer #(.select(2), .width(16)) multiplexer_9 (
    .in0(consumer_write_data_0), .in1(consumer_write_data_1), .in2(consumer_write_data_2),
    .in3(consumer_write_data_3), .out(multiplexer_9_out), .sel(bitfinder_2_index));
  Multiplexer #(.select(2), .width(8)) multiplexer_10 (
    .in0(consumer_write_address_0), .in1(consumer_write_address_1), .in2(consumer_write_address_2),
    .in3(consumer_write_address_3), .out(multiplexer_10_out), .sel(bitfinder_2_index));
  Register #(.width(2)) current_consumer_reg (
    .D(consumer_rw_and_channel_serving_consumer_bit), .en(consumer_rw_and_channel_serving_consumer_success),
    .clk(clk), .Q(current_consumer), .clr(reset));
  Multiplexer multiplexer_11 (.in0(1'b0), .in1(or_9_out), .out(multiplexer_11_out), .sel(bitfinder_1_found));
  or or_9 (or_9_out, READ_WAITING_STATE_UPDATE, bitfinder_1_found);
  Multiplexer #(.select(2), .width(8)) multiplexer_12 (
    .in0(consumer_read_address_0), .in1(consumer_read_address_1), .in2(consumer_read_address_2),
    .in3(consumer_read_address_3), .out(multiplexer_12_out), .sel(bitfinder_1_index));
  Register #(.width(16)) mem_write_data_reg (
    .D(multiplexer_9_out), .en(and_18_out), .clk(clk), .Q(mem_write_data), .clr(reset));
  Register mem_write_address_reg (
    .D(multiplexer_10_out), .en(and_18_out), .clk(clk), .Q(mem_write_address), .clr(reset));
  Register #(.width(1)) mem_read_valid_reg (
    .D(multiplexer_11_out), .en(or_9_out), .clk(clk), .Q(mem_read_valid), .clr(reset));
  Multiplexer multiplexer_13 (.in0(1'b0), .in1(or_10_out), .out(multiplexer_13_out), .sel(and_18_out));
  or or_10 (or_10_out, WRITE_WAITING_STATE_UPDATE, and_18_out);
  Register mem_read_address_reg (
    .D(multiplexer_12_out), .en(consumer_rw_and_channel_serving_consumer_success), .clk(clk),
    .Q(mem_read_address), .clr(reset));
  Register #(.width(1)) mem_write_valid_reg (
    .D(multiplexer_13_out), .en(or_10_out), .clk(clk), .Q(mem_write_valid), .clr(reset));
  and and_19 (WRITE_WAITING_STATE_UPDATE, WRITE_WAITING_STATE, mem_write_ready);
endmodule
