// Logisim project core_module.circ as structural Verilog: 1 circuit, main circuit core
module core (
  input  [2:0] thread_count,
  input  start,
  input  [15:0] program_mem_read_data,
  input  program_mem_read_ready,
  input  clk,
  input  reset,
  input  [7:0] block_id,
  input  [3:0] data_mem_read_ready,
  input  [3:0] data_mem_write_ready_0,
  input  [7:0] data_mem_read_data_0,
  input  [7:0] data_mem_read_data_1,
  input  [7:0] data_mem_read_data_2,
  input  [7:0] data_mem_read_data_3,
  output done,
  output [7:0] program_mem_read_address,
  output program_mem_read_valid,
  output [3:0] data_mem_read_valid,
  output [3:0] data_mem_write_valid,
  output [7:0] data_mem_write_data_0,
  output [7:0] data_mem_write_data_1,
  output [7:0] data_mem_write_data_2,
  output [7:0] data_mem_write_data_3,
  output [7:0] data_mem_write_address_0,
  output [7:0] data_mem_write_address_1,
  output [7:0] data_mem_write_address_2,
  output [7:0] data_mem_write_address_3,
  output [7:0] data_mem_read_address_0,
  output [7:0] data_mem_read_address_1,
  output [7:0] data_mem_read_address_2,
  output [7:0] data_mem_read_address_3
);

  wire d_alu_o_m, d_mem_r_e, d_mem_w_e, d_nzp_w_e, d_pc_mux, d_reg_w_e, decoded_ret, decoder_1_out1,
       decoder_1_out2, decoder_1_out3, decoder_1_out4, decoder_1_out5, decoder_1_out6, decoder_1_out7,
       enable_0, enable_1, enable_2, enable_3, fetcher_1_p9, fetcher_1_p10, register_w_1_p15,
       register_w_1_p16, register_w_2_p15, register_w_2_p16, register_w_3_p15, register_w_3_p16,
       register_w_4_p15, register_w_4_p16;
  wire [1:0] d_alu_arit_mux, d_reg_i_mux, lsu_state_0, lsu_state_1, lsu_state_2, lsu_state_3;
  wire [2:0] CORE_STATE, d_nzp;
  wire [3:0] d_rd_addr, d_rs_addr, d_rt_addr;
  wire [7:0] alu_out_0, alu_out_1, alu_out_2, alu_out_3, current_pc, d_imme, lsu_out_0, lsu_out_1, lsu_out_2,
       lsu_out_3, next_pc_0, next_pc_1, next_pc_2, next_pc_3;

  // fetcher fetcher_1: pin names not known; wires that end beside it: current_pc, program_mem_read_ready, CORE_STATE, clk, reset, program_mem_read_data, program_mem_read_address, program_mem_read_valid, fetcher_1_p9, fetcher_1_p10, fetcher_1_p10, CORE_STATE, clk, reset
  // decoder_w decoder_w_1: pin names not known; wires that end beside it: d_imme, d_rd_addr, d_nzp, d_rs_addr, d_rt_addr, d_pc_mux, d_alu_o_m, d_nzp_w_e, d_mem_w_e, d_reg_w_e, d_reg_i_mux, d_mem_r_e, d_alu_arit_mux, decoded_ret
  // scheduler scheduler_1: pin names not known; wires that end beside it: next_pc_0, next_pc_1, next_pc_2, next_pc_3, reset, clk, decoded_ret, start, fetcher_1_p9, {lsu_state_3, lsu_state_2, lsu_state_1, lsu_state_0}, current_pc, CORE_STATE, done
  // register_w register_w_1: pin names not known; wires that end beside it: {8{1'b0}}, d_rs_addr, block_id, enable_0, reset, clk, d_rt_addr, d_rd_addr, d_reg_w_e, d_reg_i_mux, alu_out_0, lsu_out_0, d_imme, CORE_STATE, register_w_1_p15, register_w_1_p16
  // register_w register_w_2: pin names not known; wires that end beside it: 8'h1, d_rs_addr, block_id, enable_1, reset, clk, d_rt_addr, d_rd_addr, d_reg_w_e, d_reg_i_mux, alu_out_1, lsu_out_1, d_imme, CORE_STATE, register_w_2_p15, register_w_2_p16
  // register_w register_w_3: pin names not known; wires that end beside it: 8'h2, d_rs_addr, block_id, enable_2, reset, clk, d_rt_addr, d_rd_addr, d_reg_w_e, d_reg_i_mux, alu_out_2, lsu_out_2, d_imme, CORE_STATE, register_w_3_p15, register_w_3_p16
  // register_w register_w_4: pin names not known; wires that end beside it: 8'h3, d_rs_addr, block_id, enable_3, reset, clk, d_rt_addr, d_rd_addr, d_reg_w_e, d_reg_i_mux, alu_out_3, lsu_out_3, d_imme, CORE_STATE, register_w_4_p15, register_w_4_p16
  Decoder #(.select(3)) decoder_1 (
    .out1(decoder_1_out1), .out2(decoder_1_out2), .out3(decoder_1_out3), .out4(decoder_1_out4),
    .out5(decoder_1_out5), .out6(decoder_1_out6), .out7(decoder_1_out7), .sel(thread_count));  // open: out0, en
  or or_1 (enable_3, decoder_1_out4, decoder_1_out5, decoder_1_out6, decoder_1_out7);
  or or_2 (enable_0, decoder_1_out1, decoder_1_out2, decoder_1_out3, enable_3);
  or or_3 (enable_1, decoder_1_out2, decoder_1_out3, enable_3);
  or or_4 (enable_2, decoder_1_out3, enable_3);
  // alu alu_1: pin names not known; wires that end beside it: d_alu_o_m, register_w_1_p15, register_w_1_p16, d_alu_arit_mux, reset, CORE_STATE, enable_0, clk, alu_out_0, data_mem_write_ready_0[0], data_mem_read_ready[0], reset, clk
  // alu alu_2: pin names not known; wires that end beside it: d_alu_o_m, register_w_2_p15, register_w_2_p16, d_alu_arit_mux, reset, CORE_STATE, enable_1, clk, alu_out_1, data_mem_write_ready_0[1], data_mem_read_ready[1], reset, clk
  // alu alu_3: pin names not known; wires that end beside it: d_alu_o_m, register_w_3_p15, register_w_3_p16, d_alu_arit_mux, reset, CORE_STATE, enable_2, clk, alu_out_2, data_mem_write_ready_0[2], data_mem_read_ready[2], reset, clk
  // alu alu_4: pin names not known; wires that end beside it: d_alu_o_m, register_w_4_p15, register_w_4_p16, d_alu_arit_mux, reset, CORE_STATE, enable_3, clk, alu_out_3, data_mem_write_ready_0[3], data_mem_read_ready[3], reset, clk
  // lsu lsu_1: pin names not known; wires that end beside it: register_w_1_p16, register_w_1_p15, data_mem_read_data_0, enable_0, d_mem_r_e, d_mem_w_e, CORE_STATE, data_mem_write_data_0, data_mem_write_address_0, data_mem_write_valid[0], data_mem_read_address_0, data_mem_read_valid[0], lsu_out_0, lsu_state_0
  // lsu lsu_2: pin names not known; wires that end beside it: register_w_2_p16, register_w_2_p15, data_mem_read_data_1, enable_1, d_mem_r_e, d_mem_w_e, CORE_STATE, d_pc_mux, current_pc, d_imme, reset, clk, data_mem_write_data_1, data_mem_write_address_1, data_mem_write_valid[1], data_mem_read_address_1, data_mem_read_valid[1], lsu_out_1, lsu_state_1
  // lsu lsu_3: pin names not known; wires that end beside it: register_w_3_p16, register_w_3_p15, data_mem_read_data_2, enable_2, d_mem_r_e, d_mem_w_e, CORE_STATE, enable_1, d_pc_mux, current_pc, d_imme, reset, clk, data_mem_write_data_2, data_mem_write_address_2, data_mem_write_valid[2], data_mem_read_address_2, data_mem_read_valid[2], lsu_out_2, lsu_state_2
  // Probe on lsu_state_0
  // lsu lsu_4: pin names not known; wires that end beside it: register_w_4_p16, register_w_4_p15, data_mem_read_data_3, enable_3, d_mem_r_e, d_mem_w_e, CORE_STATE, current_pc, d_imme, reset, clk, data_mem_write_data_3, data_mem_write_address_3, data_mem_write_valid[3], data_mem_read_address_3, data_mem_read_valid[3], lsu_out_3, lsu_state_3
  // Probe on lsu_out_0
  // pc pc_1: pin names not known; wires that end beside it: alu_out_0, d_nzp_w_e, CORE_STATE, d_nzp, enable_0, next_pc_0
  // pc pc_2: pin names not known; wires that end beside it: alu_out_1, d_nzp_w_e, CORE_STATE, d_nzp, next_pc_1
  // pc pc_3: pin names not known; wires that end beside it: alu_out_2, d_nzp_w_e, CORE_STATE, d_nzp, enable_2, d_pc_mux, next_pc_2
  // pc pc_4: pin names not known; wires that end beside it: alu_out_3, d_nzp_w_e, CORE_STATE, d_nzp, enable_3, d_pc_mux, current_pc, d_imme, reset, clk, next_pc_3

  // Other names for the same wires on the sheet: data_mem_read_ready_0 = data_mem_read_ready[0];
  //   data_mem_read_ready_1 = data_mem_read_ready[1]; data_mem_read_ready_2 = data_mem_read_ready[2];
  //   data_mem_read_ready_3 = data_mem_read_ready[3]; data_mem_read_valid_0 = data_mem_read_valid[0];
  //   data_mem_read_valid_1 = data_mem_read_valid[1]; data_mem_read_valid_2 = data_mem_read_valid[2];
  //   data_mem_read_valid_3 = data_mem_read_valid[3]; data_mem_write_ready_0_t = data_mem_write_ready_0[0];
  //   data_mem_write_ready_1 = data_mem_write_ready_0[1]; data_mem_write_ready_2 = data_mem_write_ready_0[2];
  //   data_mem_write_ready_3 = data_mem_write_ready_0[3]; data_mem_write_valid_0 = data_mem_write_valid[0];
  //   data_mem_write_valid_1 = data_mem_write_valid[1]; data_mem_write_valid_2 = data_mem_write_valid[2];
  //   data_mem_write_valid_3 = data_mem_write_valid[3]
endmodule
