// Logisim project decoder_module.circ as structural Verilog: 1 circuit, main circuit decoder_w
module decoder_w (
  input  [15:0] instruction,
  input  [2:0] core_state,
  input  clk,
  input  reset,
  output [7:0] decoded_immediate,
  output [3:0] decoded_rd_address,
  output [2:0] decoded_nzp,
  output [3:0] decoded_rs_address,
  output [3:0] decoded_rt_address,
  output decoded_pc_mux,
  output decoded_alu_output_mux,
  output decoded_nzp_write_enable,
  output decoded_mem_write_enable,
  output decoded_reg_write_enable,
  output [1:0] decoded_reg_input_mux,
  output decoded_mem_read_enable,
  output [1:0] decoded_alu_arithmetic_mux,
  output decoded_ret
);

  wire decoder_1_out2, decoder_2_out1, decoder_2_out2, decoder_2_out3, decoder_2_out4, decoder_2_out5,
       decoder_2_out6, decoder_2_out8, decoder_2_out15, or_1_out, or_2_out, or_3_out, or_4_out;
  wire [1:0] decoder_2_out7, multiplexer_1_out, multiplexer_2_out, multiplexer_3_out, multiplexer_4_out,
       multiplexer_5_out;

  Multiplexer #(.width(2)) multiplexer_1 (.in0(2'b00), .in1(2'b11), .out(multiplexer_1_out), .sel(decoder_2_out6));
  Decoder #(.select(3)) decoder_1 (
    .out2(decoder_1_out2), .sel(core_state));  // open: out0, out1, out3, out4, out5, out6, out7, en
  Multiplexer #(.width(2)) multiplexer_2 (
    .in0(multiplexer_1_out), .in1(2'b10), .out(multiplexer_2_out), .sel(decoder_2_out5));
  Multiplexer #(.width(2)) multiplexer_3 (
    .in0(multiplexer_2_out), .in1(2'b01), .out(multiplexer_3_out), .sel(decoder_2_out4));
  Decoder #(.select(4)) decoder_2 (
    .out1(decoder_2_out1), .out2(decoder_2_out2), .out3(decoder_2_out3), .out4(decoder_2_out4),
    .out5(decoder_2_out5), .out6(decoder_2_out6), .out7(decoder_2_out7[0]), .out8(decoder_2_out8),
    .out9(decoder_2_out7[1]), .out15(decoder_2_out15), .sel(instruction[15:12]), .en(decoder_1_out2));  // open: out0, out10, out11, out12, out13, out14
  or or_1 (or_1_out, decoder_2_out3, decoder_2_out4, decoder_2_out5, decoder_2_out6);
  Multiplexer #(.width(2)) multiplexer_4 (
    .in0(multiplexer_3_out), .in1(2'b00), .out(multiplexer_4_out), .sel(decoder_2_out3));
  or or_2 (or_2_out, decoder_2_out7[0], decoder_2_out7[1], or_1_out);
  or or_3 (or_3_out, decoder_2_out7[0], decoder_2_out7[1]);
  or or_4 (or_4_out, decoder_1_out2, decoder_2_out7[0]);
  Register #(.width(1)) decoded_pc_mux_reg (
    .D(decoder_2_out1), .en(decoder_1_out2), .clk(clk), .Q(decoded_pc_mux), .clr(reset));
  Register #(.width(1)) decoded_alu_output_mux_reg (
    .D(decoder_2_out2), .en(decoder_1_out2), .clk(clk), .Q(decoded_alu_output_mux), .clr(reset));
  Register #(.width(1)) decoded_nzp_write_enable_reg (
    .D(decoder_2_out2), .en(decoder_1_out2), .clk(clk), .Q(decoded_nzp_write_enable), .clr(reset));
  Register #(.width(1)) decoded_mem_write_enable_reg (
    .D(decoder_2_out8), .en(decoder_1_out2), .clk(clk), .Q(decoded_mem_write_enable), .clr(reset));
  Register #(.width(1)) decoded_reg_write_enable_reg (
    .D(or_2_out), .en(decoder_1_out2), .clk(clk), .Q(decoded_reg_write_enable), .clr(reset));
  Register #(.width(2)) decoded_reg_input_mux_reg (
    .D(multiplexer_5_out), .en(decoder_1_out2), .clk(clk), .Q(decoded_reg_input_mux), .clr(reset));
  Multiplexer #(.width(2)) multiplexer_5 (.in0(2'b00), .in1(decoder_2_out7), .out(multiplexer_5_out), .sel(or_3_out));
  Register #(.width(1)) decoded_mem_read_enable_reg (
    .D(decoder_2_out7[0]), .en(or_4_out), .clk(clk), .Q(decoded_mem_read_enable), .clr(reset));
  Register #(.width(2)) decoded_alu_arithmetic_mux_reg (
    .D(multiplexer_4_out), .en(decoder_1_out2), .clk(clk), .Q(decoded_alu_arithmetic_mux), .clr(reset));
  Register #(.width(1)) decoded_ret_reg (
    .D(decoder_2_out15), .en(decoder_1_out2), .clk(clk), .Q(decoded_ret), .clr(reset));

  assign decoded_immediate = instruction[7:0];
  assign decoded_nzp = instruction[11:9];
  assign decoded_rd_address = instruction[11:8];
  assign decoded_rs_address = instruction[7:4];
  assign decoded_rt_address = instruction[3:0];
endmodule
