// Logisim project dispatch_module.circ as structural Verilog: 1 circuit, main circuit dispatch
module dispatch (
  input  start,
  input  clk,
  input  reset,
  input  [7:0] thread_count,
  input  [1:0] core_done,
  output [1:0] core_reset,
  output done,
  output [1:0] core_start,
  output [7:0] core_block_id_0,
  output [2:0] core_thread_count_0,
  output [7:0] core_block_id_1,
  output [2:0] core_thread_count_1
);

  wire and_1_out, and_2_out, and_3_out, and_6_out, and_11_out, and_12_out, and_13_out, and_14_out,
       block_no_sleep_0, block_no_sleep_1, comparator_1_eq, comparator_1_gt, comparator_3_eq,
       comparator_3_gt, comparator_4_lt, core_done_signal, CORE_RESET_BIT0, CORE_RESET_BIT1, not_1_out,
       not_2_out, not_3_out, or_1_out, or_2_out, or_3_out, or_4_out, or_5_out, or_6_out, or_7_out, or_9_out,
       or_10_out, start_execution_reg_q;
  wire [1:0] and_4_out, and_7_out, bitadder_1_out, multiplexer_1_out, multiplexer_2_out, multiplexer_3_out,
       multiplexer_4_out;
  wire [2:0] bit_extender_2_out, bit_extender_3_out;
  wire [7:0] adder_1_out, adder_2_out, adder_3_out, adder_4_out, bit_extender_1_out, blocks_dispatched_reg_q,
       blocks_done_reg_q, multiplexer_5_out, multiplexer_6_out, multiplexer_7_out, multiplier_1_out,
       multiplier_2_out, subtractor_1_out, subtractor_2_out, subtractor_3_out, subtractor_4_out, total_blocks;

  and and_1 (and_1_out, not_1_out, start);
  not not_1 (not_1_out, start_execution_reg_q);
  Register #(.width(1)) start_execution_reg (
    .D(not_1_out), .en(and_1_out), .clk(clk), .Q(start_execution_reg_q), .clr(reset));
  or or_1 (or_1_out, and_1_out, reset);
  and and_2 (and_2_out, CORE_RESET_BIT0, block_no_sleep_0);
  and and_3 (and_3_out, CORE_RESET_BIT1, block_no_sleep_1);
  or or_2 (or_2_out, and_7_out[1], and_3_out);
  and and_4 (and_4_out[0], CORE_RESET_BIT0, 1'b0);
  and and_5 (and_4_out[1], 1'b0, CORE_RESET_BIT1);
  Multiplexer #(.width(2)) multiplexer_1 (.in0(2'b00), .in1(2'b11), .out(multiplexer_1_out), .sel(or_1_out));
  Multiplexer #(.width(2)) multiplexer_2 (
    .in0(multiplexer_1_out), .in1(and_7_out), .out(multiplexer_2_out), .sel(core_done_signal));
  not not_2 (not_2_out, and_7_out[0]);
  or or_3 (or_3_out, not_2_out, and_2_out);
  or or_4 (or_4_out, and_7_out[0], and_2_out);
  not not_3 (not_3_out, and_7_out[1]);
  or or_5 (or_5_out, not_3_out, and_3_out);
  Multiplexer #(.width(2)) multiplexer_3 (
    .in0(multiplexer_2_out), .in1(and_4_out), .out(multiplexer_3_out), .sel(or_6_out));
  Register #(.width(1)) core_start_reg_bit0 (.D(or_3_out), .en(or_4_out), .clk(clk), .Q(core_start[0]), .clr(reset));
  Register #(.width(1)) core_start_reg_bit1 (.D(or_5_out), .en(or_2_out), .clk(clk), .Q(core_start[1]), .clr(reset));
  or or_6 (or_6_out, CORE_RESET_BIT0, CORE_RESET_BIT1);
  and and_6 (and_6_out, start, core_done_signal);
  Register #(.width(2)) core_reset_reg (.D(multiplexer_4_out), .en(or_7_out), .clk(clk), .Q(core_reset));  // open: clr
  Multiplexer #(.width(2)) multiplexer_4 (.in0(multiplexer_3_out), .in1(2'b11), .out(multiplexer_4_out), .sel(reset));
  or or_7 (or_7_out, or_6_out, or_1_out, and_6_out);
  and and_7 (and_7_out[0], core_start[0], core_done[0]);
  and and_8 (and_7_out[1], core_start[1], core_done[1]);
  BitAdder #(.width(2)) bitadder_1 (.in0(and_7_out), .out(bitadder_1_out));
  or or_8 (core_done_signal, and_7_out[0], and_7_out[1]);
  Adder adder_1 (.a(blocks_dispatched_reg_q), .b({8{1'b0}}), .out(adder_1_out), .cin(and_11_out));  // open: cout
  and and_9 (CORE_RESET_BIT0, start, core_reset[0]);
  assign bit_extender_1_out = {{6{1'b0}}, bitadder_1_out};  // Bit_Extender bit_extender_1
  and and_10 (CORE_RESET_BIT1, core_reset[1], start);
  Multiplexer #(.width(8)) multiplexer_5 (
    .in0({8{1'b0}}), .in1(bit_extender_1_out), .out(multiplexer_5_out), .sel(core_done_signal));
  Adder adder_2 (.a(adder_1_out), .b({8{1'b0}}), .out(adder_2_out), .cin(and_12_out));  // open: cout
  and and_11 (and_11_out, CORE_RESET_BIT0, comparator_4_lt);
  and and_12 (and_12_out, comparator_4_lt, CORE_RESET_BIT1);
  Adder adder_3 (.a(blocks_done_reg_q), .b(multiplexer_5_out), .out(adder_3_out));  // open: cin, cout
  Adder adder_4 (.a(thread_count), .b(8'h3), .out(adder_4_out));  // open: cin, cout
  Register blocks_done_reg (.D(adder_3_out), .en(core_done_signal), .clk(clk), .Q(blocks_done_reg_q), .clr(reset));
  Shifter #(.shift("lr")) shifter_1 (.in(adder_4_out), .\dist (3'b010), .out(total_blocks));
  Register blocks_dispatched_reg (
    .D(adder_2_out), .en(comparator_4_lt), .clk(clk), .Q(blocks_dispatched_reg_q), .clr(reset));
  Multiplier multiplier_1 (.a(blocks_dispatched_reg_q), .b(8'h4), .out(multiplier_1_out));  // open: cin, cout
  Register core_block_id_reg_1 (.D(adder_1_out), .en(and_12_out), .clk(clk), .Q(core_block_id_1), .clr(reset));
  Multiplier multiplier_2 (.a(8'h4), .b(adder_1_out), .out(multiplier_2_out));  // open: cin, cout
  Register core_block_id_reg_0 (
    .D(blocks_dispatched_reg_q), .en(and_11_out), .clk(clk), .Q(core_block_id_0), .clr(reset));
  or or_9 (or_9_out, and_11_out, reset);
  Subtractor subtractor_1 (.a(total_blocks), .b(8'h1), .out(subtractor_1_out));  // open: bin, bout
  Subtractor subtractor_2 (.a(thread_count), .b(multiplier_2_out), .out(subtractor_2_out));  // open: bin, bout
  Subtractor subtractor_3 (.a(total_blocks), .b(8'h1), .out(subtractor_3_out));  // open: bin, bout
  Subtractor subtractor_4 (.a(thread_count), .b(multiplier_1_out), .out(subtractor_4_out));  // open: bin, bout
  Comparator comparator_1 (
    .a(adder_1_out), .b(subtractor_1_out), .gt(comparator_1_gt), .eq(comparator_1_eq));  // open: lt
  or or_10 (or_10_out, and_12_out, reset);
  Comparator comparator_2 (.a(total_blocks), .b(blocks_done_reg_q), .eq(done));  // open: gt, lt
  not not_4 (block_no_sleep_0, comparator_3_gt);
  Comparator comparator_3 (
    .a(blocks_dispatched_reg_q), .b(subtractor_3_out), .gt(comparator_3_gt), .eq(comparator_3_eq));  // open: lt
  not not_5 (block_no_sleep_1, comparator_1_gt);
  Comparator comparator_4 (.a(blocks_dispatched_reg_q), .b(total_blocks), .lt(comparator_4_lt));  // open: gt, eq
  Multiplexer #(.width(8)) multiplexer_6 (
    .in0(8'h4), .in1(subtractor_4_out), .out(multiplexer_6_out), .sel(comparator_3_eq));
  and and_13 (and_13_out, block_no_sleep_0, or_9_out);
  Multiplexer #(.width(8)) multiplexer_7 (
    .in0(8'h4), .in1(subtractor_2_out), .out(multiplexer_7_out), .sel(comparator_1_eq));
  and and_14 (and_14_out, block_no_sleep_1, or_10_out);
  Register #(.width(3)) core_thread_count_reg_0 (
    .D(bit_extender_2_out), .en(and_13_out), .clk(clk), .Q(core_thread_count_0), .clr(reset));
  Bit_Extender #(.out_width(3), .\type ("zero")) bit_extender_2 (.in(multiplexer_6_out), .out(bit_extender_2_out));
  Register #(.width(3)) core_thread_count_reg_1 (
    .D(bit_extender_3_out), .en(and_14_out), .clk(clk), .Q(core_thread_count_1), .clr(reset));
  Bit_Extender #(.out_width(3), .\type ("zero")) bit_extender_3 (.in(multiplexer_7_out), .out(bit_extender_3_out));
endmodule
