// Logisim project dispatch_test.circ as structural Verilog: 3 circuits, main circuit main
module main (
  input  [7:0] thread_count,
  output [7:0] out_2
);

  wire [7:0] adder_1_out;

  Adder adder_1 (.a(thread_count), .b(8'h3), .out(adder_1_out));  // open: cin, cout
  Shifter #(.shift("lr")) shifter_1 (.in(adder_1_out), .\dist (3'b010), .out(out_2));
endmodule

module dispatch (
  input  start,
  input  clk,
  input  reset,
  input  [7:0] thread_count
);

  wire and_1_out, comparator_1_eq, comparator_2_lt, not_1_out, or_1_out, or_2_out, or_3_out, or_4_out,
       or_5_out, or_6_out, start_execution_reg_q;
  wire [1:0] and_2_out, core_done_reg_q, core_reset_reg_q, core_start_reg_q, multiplexer_1_out,
       multiplexer_3_out, multiplexer_4_out, multiplexer_6_out, not_2_out;
  wire [2:0] multiplexer_5_out;
  wire [7:0] adder_1_out, adder_2_out, blocks_dispatched_reg_q, blocks_done_reg_q, multiplexer_2_out,
       shifter_1_out;

  Multiplexer #(.width(2)) multiplexer_1 (.in1(and_2_out), .out(multiplexer_1_out), .sel(or_1_out));  // open: in0
  Register #(.width(2)) core_start_reg (
    .D(multiplexer_1_out), .en(or_1_out), .clk(clk), .Q(core_start_reg_q), .clr(reset));
  Register #(.width(2)) core_done_reg (.clk(clk), .Q(core_done_reg_q), .clr(reset));  // open: D, en
  not not_1 (not_1_out, start_execution_reg_q);
  and and_1 (and_1_out, not_1_out, start);
  Register #(.width(1)) start_execution_reg (
    .D(and_1_out), .en(and_1_out), .clk(clk), .Q(start_execution_reg_q), .clr(reset));
  and and_2 (and_2_out[0], core_start_reg_q[0], core_done_reg_q[0]);
  and and_3 (and_2_out[1], core_start_reg_q[1], core_done_reg_q[1]);
  or or_1 (or_1_out, and_2_out[0], and_2_out[1]);
  or or_2 (or_2_out, and_1_out, reset);
  Multiplexer #(.width(8)) multiplexer_2 (.in0({8{1'b0}}), .in1(8'h1), .out(multiplexer_2_out), .sel(or_1_out));
  Multiplexer #(.width(2)) multiplexer_3 (.in0(2'b00), .in1(2'b11), .out(multiplexer_3_out), .sel(or_2_out));
  Register core_block_id_0 (.clr(reset));  // open: D, en, clk, Q
  Register core_block_id_1 (.clr(reset));  // open: D, en, clk, Q
  Adder adder_1 (.a(thread_count), .b(8'h3), .out(adder_1_out));  // open: cin, cout
  Adder adder_2 (.a(blocks_done_reg_q), .b(multiplexer_2_out), .out(adder_2_out));  // open: cin, cout
  Shifter #(.shift("lr")) shifter_1 (.in(adder_1_out), .\dist (3'b010), .out(shifter_1_out));
  Register blocks_done_reg (.D(adder_2_out), .Q(blocks_done_reg_q), .clr(reset));  // open: en, clk
  Multiplexer #(.width(2)) multiplexer_4 (
    .in0(multiplexer_3_out), .in1(and_2_out), .out(multiplexer_4_out), .sel(or_1_out));
  not not_2 (not_2_out[0], core_reset_reg_q[0]);
  not not_3 (not_2_out[1], core_reset_reg_q[1]);
  or or_3 (or_3_out, or_2_out, or_1_out);
  Multiplexer #(.width(3)) multiplexer_5 (.in0(3'b000), .in1(3'b100), .out(multiplexer_5_out), .sel(reset));
  buf or_4 (or_4_out, reset);  // OR_Gate
  Comparator comparator_1 (.a(shifter_1_out), .b(blocks_done_reg_q), .eq(comparator_1_eq));  // open: gt, lt
  Multiplexer #(.width(2)) multiplexer_6 (
    .in0(multiplexer_4_out), .in1(not_2_out), .out(multiplexer_6_out), .sel(or_6_out));
  Register #(.width(3)) core_thread_count_reg_0 (.D(multiplexer_5_out), .en(or_4_out), .clk(clk));  // open: Q, clr
  Register #(.width(3)) core_thread_count_reg_1 (.D(multiplexer_5_out), .en(or_4_out), .clk(clk));  // open: Q, clr
  or or_5 (or_5_out, or_6_out, or_3_out);
  Register #(.width(1)) done_reg (.D(comparator_1_eq), .en(comparator_1_eq), .clr(reset));  // open: clk, Q
  Register #(.width(2)) core_reset_reg (
    .D(multiplexer_6_out), .en(or_5_out), .clk(clk), .Q(core_reset_reg_q));  // open: clr
  Register blocks_dispatched_reg (.Q(blocks_dispatched_reg_q));  // open: D, en, clk, clr
  or or_6 (or_6_out, core_reset_reg_q[0], core_reset_reg_q[1]);
  Comparator comparator_2 (.a(blocks_dispatched_reg_q), .b(shifter_1_out), .lt(comparator_2_lt));  // open: gt, eq
endmodule

module dispatch_new (
  input  start,
  input  clk,
  input  reset,
  input  [7:0] thread_count,
  input  [1:0] core_done
);

  wire and_1_out, comparator_1_eq, comparator_2_gt, not_1_out, or_1_out, or_2_out, or_3_out, or_4_out,
       or_5_out, or_6_out, start_execution_reg_q;
  wire [1:0] and_3_out, core_reset_reg_q, core_start_reg_q, multiplexer_1_out, multiplexer_2_out,
       multiplexer_3_out, multiplexer_4_out, multiplexer_5_out, not_2_out, not_4_out;
  wire [2:0] multiplexer_7_out;
  wire [7:0] adder_1_out, adder_2_out, adder_3_out, blocks_dispatched_reg_q, blocks_done_reg_q,
       core_block_id_0_q, core_block_id_1_q, multiplexer_6_out, shifter_1_out;

  and and_1 (and_1_out, not_1_out, start);
  not not_1 (not_1_out, start_execution_reg_q);
  Register #(.width(1)) start_execution_reg (
    .D(and_1_out), .en(and_1_out), .clk(reset), .Q(start_execution_reg_q));  // open: clr
  or or_1 (or_1_out, and_1_out, reset);
  Multiplexer #(.width(2)) multiplexer_1 (.in0(2'b00), .in1(2'b11), .out(multiplexer_1_out), .sel(or_1_out));
  not not_2 (not_2_out[0], core_reset_reg_q[0]);
  not not_3 (not_2_out[1], core_reset_reg_q[1]);
  Multiplexer #(.width(2)) multiplexer_2 (
    .in0(multiplexer_1_out), .in1(and_3_out), .out(multiplexer_2_out), .sel(or_5_out));
  not not_4 (not_4_out[0], and_3_out[1]);
  not not_5 (not_4_out[1], and_3_out[0]);
  Multiplexer #(.width(2)) multiplexer_3 (.in0(2'b00), .in1(2'b11), .out(multiplexer_3_out), .sel(comparator_2_gt));
  Multiplexer #(.width(2)) multiplexer_4 (
    .in0(multiplexer_2_out), .in1(not_2_out), .out(multiplexer_4_out), .sel(or_4_out));
  Multiplexer #(.width(2)) multiplexer_5 (
    .in0(multiplexer_3_out), .in1(not_4_out), .out(multiplexer_5_out), .sel(or_5_out));
  Register #(.width(2)) core_reset_reg (
    .D(multiplexer_4_out), .en(or_2_out), .clk(clk), .Q(core_reset_reg_q), .clr(reset));
  or or_2 (or_2_out, or_4_out, or_1_out, or_5_out);
  Register #(.width(2)) core_start_reg (
    .D(multiplexer_5_out), .en(or_3_out), .clk(clk), .Q(core_start_reg_q), .clr(reset));
  or or_3 (or_3_out, or_5_out, comparator_2_gt);
  Adder adder_1 (.a(thread_count), .b(8'h3), .out(adder_1_out));  // open: cin, cout
  or or_4 (or_4_out, core_reset_reg_q[0], core_reset_reg_q[1]);
  and and_2 (and_3_out[1], core_start_reg_q[0], core_done[0]);
  and and_3 (and_3_out[0], core_start_reg_q[1], core_done[1]);
  or or_5 (or_5_out, and_3_out[1], and_3_out[0]);
  Shifter #(.shift("lr")) shifter_1 (.in(adder_1_out), .\dist (3'b010), .out(shifter_1_out));
  Multiplexer #(.width(8)) multiplexer_6 (.in0({8{1'b0}}), .in1(8'h1), .out(multiplexer_6_out), .sel(and_3_out[1]));
  Register blocks_done_reg (.D(adder_2_out), .clk(clk), .Q(blocks_done_reg_q), .clr(reset));  // open: en
  Adder adder_2 (.a(blocks_done_reg_q), .b(multiplexer_6_out), .out(adder_2_out), .cin(and_3_out[0]));  // open: cout
  Register blocks_dispatched_reg (
    .D(adder_3_out), .en(comparator_2_gt), .clk(clk), .Q(blocks_dispatched_reg_q), .clr(reset));
  Adder adder_3 (.a(blocks_dispatched_reg_q), .b(8'h1), .out(adder_3_out));  // open: cin, cout
  Comparator comparator_1 (.a(shifter_1_out), .b(blocks_done_reg_q), .eq(comparator_1_eq));  // open: gt, lt
  Comparator comparator_2 (.a(shifter_1_out), .b(blocks_dispatched_reg_q), .gt(comparator_2_gt));  // open: eq, lt
  Register #(.width(1)) done_reg (.D(comparator_1_eq), .en(comparator_1_eq), .clk(clk), .clr(reset));  // open: Q
  Register core_block_id_0 (.clk(clk), .Q(core_block_id_0_q), .clr(reset));  // open: D, en
  Register core_block_id_1 (.clk(clk), .Q(core_block_id_1_q), .clr(reset));  // open: D, en
  Comparator comparator_3 (.a(core_block_id_0_q), .b(core_block_id_1_q));  // open: gt, eq, lt
  Multiplexer #(.width(3)) multiplexer_7 (.in0(3'b000), .in1(3'b100), .out(multiplexer_7_out), .sel(reset));
  buf or_6 (or_6_out, reset);  // OR_Gate
  Register #(.width(3)) core_thread_count_reg_0 (.D(multiplexer_7_out), .en(or_6_out), .clk(clk));  // open: Q, clr
  Register #(.width(3)) core_thread_count_reg_1 (.D(multiplexer_7_out), .en(or_6_out), .clk(clk));  // open: Q, clr
endmodule
