// Logisim project div_module.circ as structural Verilog: 1 circuit, main circuit div
module dlv (
  input  [7:0] divisor,
  input  [7:0] dividend,
  output [7:0] cout,
  output err
);

  wire [31:0] fpdivider_1_out, inttofp_1_p2, inttofp_2_p2;

  // IntToFP inttofp_1: pin names not known; wires that end beside it: divisor, inttofp_1_p2
  FPDivider fpdivider_1 (.a(inttofp_1_p2), .b(inttofp_2_p2), .out(fpdivider_1_out));
  // IntToFP inttofp_2: pin names not known; wires that end beside it: dividend, inttofp_2_p2, err
  // FPToInt fptoint_1: pin names not known; wires that end beside it: fpdivider_1_out, err, cout

  // Notes on the sheet:
  //   err: pull=down
endmodule
