// Logisim project fetcher_module.circ as structural Verilog: 1 circuit, main circuit fetcher
module fetcher (
  input  [7:0] current_pc,
  input  mem_read_ready,
  input  [2:0] core_state,
  input  clk,
  input  reset,
  input  [15:0] mem_read_data,
  output [7:0] mem_read_address,
  output mem_read_valid,
  output [2:0] fetcher_state,
  output [15:0] instruction
);

  wire and_1_out, and_2_out, and_3_out, decoder_1_out0, decoder_1_out1, decoder_1_out2, decoder_2_out1,
       decoder_2_out2, or_1_out, or_2_out;
  wire [2:0] adder_1_out, bit_extender_1_out, multiplexer_1_out;

  Decoder #(.select(3)) decoder_1 (
    .out0(decoder_1_out0), .out1(decoder_1_out1), .out2(decoder_1_out2), .sel(fetcher_state));  // open: out3, out4, out5, out6, out7, en
  and and_1 (and_1_out, decoder_1_out1, mem_read_ready);
  Decoder #(.select(3)) decoder_2 (
    .out1(decoder_2_out1), .out2(decoder_2_out2), .sel(core_state));  // open: out0, out3, out4, out5, out6, out7, en
  and and_2 (and_2_out, decoder_1_out0, decoder_2_out1);
  or or_1 (or_1_out, and_2_out, and_1_out);
  and and_3 (and_3_out, decoder_1_out2, decoder_2_out2);
  Adder #(.width(3)) adder_1 (.a(fetcher_state), .b(bit_extender_1_out), .out(adder_1_out));  // open: cin, cout
  assign bit_extender_1_out = {{2{1'b0}}, or_1_out};  // Bit_Extender bit_extender_1
  or or_2 (or_2_out, or_1_out, and_3_out);
  Multiplexer #(.width(3)) multiplexer_1 (.in0(adder_1_out), .in1(3'b000), .out(multiplexer_1_out), .sel(and_3_out));
  Register mem_read_address_reg (.D(current_pc), .en(or_1_out), .clk(clk), .Q(mem_read_address), .clr(reset));
  Register #(.width(1)) mem_read_valid_reg (.D(and_2_out), .en(or_1_out), .clk(clk), .Q(mem_read_valid), .clr(reset));
  Register #(.width(3)) fetcher_state_reg (
    .D(multiplexer_1_out), .en(or_2_out), .clk(clk), .Q(fetcher_state), .clr(reset));
  Register #(.width(16)) instruction_reg (.D(mem_read_data), .en(and_1_out), .clk(clk), .Q(instruction), .clr(reset));
endmodule
