// Logisim project gpu.circ as structural Verilog: 20 circuits, main circuit gpu_power_by_wujehy
module gpu_power_by_wujehy (
  input  in_1,
  input  [7:0] in_2,
  input  in_3,
  output done,
  output out_5
);

  wire bitfinder_2_found, bitfinder_3_found, clk, core_done_0, core_done_1, core_reset_0, core_reset_1,
       core_start_0, core_start_1, decoder_1_out0, decoder_1_out1, decoder_1_out2, decoder_1_out3,
       decoder_2_out0, decoder_2_out1, decoder_2_out2, decoder_2_out3, not_1_out, not_2_out, pmr_ready_0,
       pmr_ready_1, pmr_v0, pmr_v1, ram_re, ram_we, read_busy, register_9_q;
  wire [1:0] bitfinder_1_index, bitfinder_3_index, ram_wc_bit;
  wire [2:0] core_thread_count_0, core_thread_count_1;
  wire [3:0] lsu_cr_v0, lsu_cr_v1, lsu_cw_v0, lsu_cw_v1, lsu_read_ready_0, lsu_read_ready_1,
       lsu_write_ready_0, lsu_write_ready_1, mem_read_channels, mem_write_channels, register_4_q,
       register_7_q;
  wire [7:0] core_block_id_0, core_block_id_1, lsu_read_address_0, lsu_read_address_1, lsu_read_address_2,
       lsu_read_address_3, lsu_read_address_4, lsu_read_address_5, lsu_read_address_6, lsu_read_address_7,
       lsu_read_data_0, lsu_read_data_1, lsu_read_data_2, lsu_read_data_3, lsu_read_data_4, lsu_read_data_5,
       lsu_read_data_6, lsu_read_data_7, lsu_write_address_0, lsu_write_address_1, lsu_write_address_2,
       lsu_write_address_3, lsu_write_address_4, lsu_write_address_5, lsu_write_address_6,
       lsu_write_address_7, lsu_write_data_0, lsu_write_data_1, lsu_write_data_2, lsu_write_data_3,
       lsu_write_data_4, lsu_write_data_5, lsu_write_data_6, lsu_write_data_7, multiplexer_4_out, pmr_addr_0,
       pmr_addr_1, ram_io, ram_ra, ram_ra_0, ram_ra_1, ram_ra_2, ram_ra_3, ram_rd_0, ram_rd_1, ram_rd_2,
       ram_rd_3, ram_wa, ram_wa_0, ram_wa_1, ram_wa_2, ram_wa_3, ram_wd, ram_wd_0, ram_wd_1, ram_wd_2,
       ram_wd_3, rom_addr;
  wire [15:0] pmr_data_0, pmr_data_1, rom_data;

  // Probe on mem_read_channels
  // Probe on ram_io
  ROM #(.dataWidth(16)) rom_1 (.addr(rom_addr), .data(rom_data));
  BitFinder #(.width(4)) bitfinder_1 (.in(mem_read_channels), .index(bitfinder_1_index), .found(ram_re));
  Demultiplexer #(.enable("true"), .select(2), .width(8)) demultiplexer_1 (
    .out0(ram_rd_0), .out1(ram_rd_1), .out2(ram_rd_2), .out3(ram_rd_3), .in(ram_io), .sel(bitfinder_1_index),
    .en(ram_re));
  // Probe on mem_write_channels
  not not_1 (not_1_out, read_busy);
  not not_2 (not_2_out, ram_re);
  and and_1 (ram_we, not_2_out, not_1_out, bitfinder_2_found);
  Multiplexer #(.enable("true"), .select(2), .width(8)) multiplexer_1 (
    .in0(ram_ra_0), .in1(ram_ra_1), .in2(ram_ra_2), .in3(ram_ra_3), .out(ram_ra), .sel(bitfinder_1_index),
    .en(ram_re));
  Decoder #(.select(2)) decoder_1 (
    .out0(decoder_1_out0), .out1(decoder_1_out1), .out2(decoder_1_out2), .out3(decoder_1_out3),
    .sel(ram_wc_bit), .en(ram_we));
  BitFinder #(.width(4)) bitfinder_2 (.in(mem_write_channels), .index(ram_wc_bit), .found(bitfinder_2_found));
  Multiplexer #(.enable("true"), .select(2), .width(8)) multiplexer_2 (
    .in0(ram_wd_0), .in1(ram_wd_1), .in2(ram_wd_2), .in3(ram_wd_3), .out(ram_wd), .sel(ram_wc_bit),
    .en(ram_we));
  Multiplexer #(.enable("true"), .select(2), .width(8)) multiplexer_3 (
    .in0(ram_wa_0), .in1(ram_wa_1), .in2(ram_wa_2), .in3(ram_wa_3), .out(ram_wa), .sel(ram_wc_bit),
    .en(ram_we));
  // Probe on ram_ra
  BitFinder #(.width(4)) bitfinder_3 (.in(mem_read_channels), .index(bitfinder_3_index), .found(bitfinder_3_found));
  Register #(.width(1)) register_1 (.D(decoder_1_out1), .en(1'b1), .clk(clk), .Q(register_4_q[1]));  // open: clr
  Register #(.width(1)) register_2 (.D(decoder_1_out2), .en(1'b1), .clk(clk), .Q(register_4_q[2]));  // open: clr
  Register #(.width(1)) register_3 (.D(decoder_1_out3), .en(1'b1), .clk(clk), .Q(register_4_q[3]));  // open: clr
  // Probe on ram_wd
  Decoder #(.select(2)) decoder_2 (
    .out0(decoder_2_out0), .out1(decoder_2_out1), .out2(decoder_2_out2), .out3(decoder_2_out3),
    .sel(bitfinder_3_index), .en(bitfinder_3_found));
  Register #(.width(1)) register_4 (.D(decoder_1_out0), .en(1'b1), .clk(clk), .Q(register_4_q[0]));  // open: clr
  Register #(.width(1)) register_5 (.D(decoder_2_out2), .en(1'b1), .clk(clk), .Q(register_7_q[2]));  // open: clr
  Register #(.width(1)) register_6 (.D(decoder_2_out3), .en(1'b1), .clk(clk), .Q(register_7_q[3]));  // open: clr
  Clock clock_1 (.out(clk));
  Register #(.width(1)) register_7 (.D(decoder_2_out0), .en(1'b1), .clk(clk), .Q(register_7_q[0]));  // open: clr
  Register #(.width(1)) register_8 (.D(decoder_2_out1), .en(1'b1), .clk(clk), .Q(register_7_q[1]));  // open: clr
  Multiplexer #(.width(8)) multiplexer_4 (.in0(ram_ra), .in1(ram_wa), .out(multiplexer_4_out), .sel(ram_we));
  RAM #(.asyncread("true"), .\type ("nonvolatile")) ram_1 (
    .addr(multiplexer_4_out), .we(ram_we), .oe(ram_re), .clk(clk), .din(ram_wd), .dout(ram_io));
  or or_1 (read_busy, register_7_q[0], register_7_q[1], register_7_q[2], register_7_q[3]);
  Register #(.width(1)) register_9 (.D(out_5), .en(1'b1), .clk(clk), .Q(register_9_q));  // open: clr
  // Probe on {lsu_cw_v1, lsu_cw_v0}
  // Probe on {lsu_cr_v1, lsu_cr_v0}
  controller_1c2u ProgramMemoryController (
    .clk(clk), .reset(in_1), .consumer_read_address_0(pmr_addr_0), .consumer_read_address_1(pmr_addr_1),
    .consumer_read_valid({pmr_v1, pmr_v0}), .mem_read_data_0(rom_data), .mem_read_ready(register_9_q),
    .mem_read_address_0(rom_addr), .consumer_read_ready({pmr_ready_1, pmr_ready_0}),
    .consumer_read_data_0(pmr_data_0), .consumer_read_data_1(pmr_data_1), .mem_read_valid(out_5));  // open: consumer_write_address_0, consumer_write_address_1, mem_write_ready, consumer_write_data_0, consumer_write_data_1, consumer_write_valid, consumer_write_ready, mem_write_data_0, mem_write_address_0, mem_write_valid
  controller_4c8u controller_4c8u_1 (
    .clk(clk), .reset(in_1), .mem_read_data_0(ram_rd_0), .mem_read_data_1(ram_rd_1),
    .mem_read_data_2(ram_rd_2), .mem_read_data_3(ram_rd_3), .mem_read_ready(register_7_q),
    .consumer_write_address_0(lsu_write_address_0), .consumer_write_address_1(lsu_write_address_1),
    .consumer_write_address_2(lsu_write_address_2), .consumer_write_address_3(lsu_write_address_3),
    .consumer_write_address_4(lsu_write_address_4), .consumer_write_address_5(lsu_write_address_5),
    .consumer_write_address_6(lsu_write_address_6), .consumer_write_address_7(lsu_write_address_7),
    .mem_write_ready(register_4_q), .consumer_write_data_0(lsu_write_data_0),
    .consumer_write_data_1(lsu_write_data_1), .consumer_write_data_2(lsu_write_data_2),
    .consumer_write_data_3(lsu_write_data_3), .consumer_write_data_4(lsu_write_data_4),
    .consumer_write_data_5(lsu_write_data_5), .consumer_write_data_6(lsu_write_data_6),
    .consumer_write_data_7(lsu_write_data_7), .consumer_read_address_0(lsu_read_address_0),
    .consumer_read_address_1(lsu_read_address_1), .consumer_read_address_2(lsu_read_address_2),
    .consumer_read_address_3(lsu_read_address_3), .consumer_read_address_4(lsu_read_address_4),
    .consumer_read_address_5(lsu_read_address_5), .consumer_read_address_6(lsu_read_address_6),
    .consumer_read_address_7(lsu_read_address_7), .consumer_read_valid({lsu_cr_v1, lsu_cr_v0}),
    .consumer_write_valid({lsu_cw_v1, lsu_cw_v0}), .consumer_read_data_0(lsu_read_data_0),
    .consumer_read_data_1(lsu_read_data_1), .consumer_read_data_2(lsu_read_data_2),
    .consumer_read_data_3(lsu_read_data_3), .consumer_read_data_4(lsu_read_data_4),
    .consumer_read_data_5(lsu_read_data_5), .consumer_read_data_6(lsu_read_data_6),
    .consumer_read_data_7(lsu_read_data_7), .mem_write_data_0(ram_wd_0), .mem_write_data_1(ram_wd_1),
    .mem_write_data_2(ram_wd_2), .mem_write_data_3(ram_wd_3), .mem_read_address_2(ram_ra_2),
    .mem_read_address_3(ram_ra_3), .mem_write_address_0(ram_wa_0), .mem_write_address_1(ram_wa_1),
    .mem_write_address_2(ram_wa_2), .mem_write_address_3(ram_wa_3), .mem_read_address_0(ram_ra_0),
    .mem_read_address_1(ram_ra_1), .consumer_write_ready({lsu_write_ready_1, lsu_write_ready_0}),
    .consumer_read_ready({lsu_read_ready_1, lsu_read_ready_0}), .mem_read_valid(mem_read_channels),
    .mem_write_valid(mem_write_channels));
  // dispatch dispatch_1: pin names not known; wires that end beside it: in_3, clk, in_1, in_2, {core_done_1, core_done_0}, {core_reset_1, core_reset_0}, done, {core_start_1, core_start_0}, core_block_id_0, core_thread_count_0, core_block_id_1, core_thread_count_1
  core core0 (
    .thread_count(core_thread_count_0), .clk(clk), .reset(core_reset_0), .block_id(core_block_id_0),
    .program_mem_read_ready(pmr_ready_0), .data_mem_read_ready(lsu_read_ready_0),
    .data_mem_write_ready_0(lsu_write_ready_0), .data_mem_read_data_0(lsu_read_data_0),
    .data_mem_read_data_1(lsu_read_data_1), .data_mem_read_data_2(lsu_read_data_2),
    .data_mem_read_data_3(lsu_read_data_3), .program_mem_read_data(pmr_data_0), .start(core_start_0),
    .done(core_done_0), .program_mem_read_address(pmr_addr_0), .program_mem_read_valid(pmr_v0),
    .data_mem_write_data_0(lsu_write_data_0), .data_mem_write_data_1(lsu_write_data_1),
    .data_mem_write_data_2(lsu_write_data_2), .data_mem_write_data_3(lsu_write_data_3),
    .data_mem_write_address_0(lsu_write_address_0), .data_mem_write_address_1(lsu_write_address_1),
    .data_mem_write_address_2(lsu_write_address_2), .data_mem_write_address_3(lsu_write_address_3),
    .data_mem_read_address_0(lsu_read_address_0), .data_mem_read_address_1(lsu_read_address_1),
    .data_mem_read_address_2(lsu_read_address_2), .data_mem_read_address_3(lsu_read_address_3),
    .data_mem_write_valid(lsu_cw_v0), .data_mem_read_valid(lsu_cr_v0));
  core core1 (
    .thread_count(core_thread_count_1), .clk(clk), .reset(core_reset_1), .block_id(core_block_id_1),
    .program_mem_read_ready(pmr_ready_1), .data_mem_read_ready(lsu_read_ready_1),
    .data_mem_write_ready_0(lsu_write_ready_1), .data_mem_read_data_0(lsu_read_data_4),
    .data_mem_read_data_1(lsu_read_data_5), .data_mem_read_data_2(lsu_read_data_6),
    .data_mem_read_data_3(lsu_read_data_7), .program_mem_read_data(pmr_data_1), .start(core_start_1),
    .done(core_done_1), .program_mem_read_address(pmr_addr_1), .program_mem_read_valid(pmr_v1),
    .data_mem_write_data_0(lsu_write_data_4), .data_mem_write_data_1(lsu_write_data_5),
    .data_mem_write_data_2(lsu_write_data_6), .data_mem_write_data_3(lsu_write_data_7),
    .data_mem_write_address_0(lsu_write_address_4), .data_mem_write_address_1(lsu_write_address_5),
    .data_mem_write_address_2(lsu_write_address_6), .data_mem_write_address_3(lsu_write_address_7),
    .data_mem_read_address_0(lsu_read_address_4), .data_mem_read_address_1(lsu_read_address_5),
    .data_mem_read_address_2(lsu_read_address_6), .data_mem_read_address_3(lsu_read_address_7),
    .data_mem_write_valid(lsu_cw_v1), .data_mem_read_valid(lsu_cr_v1));

  // Other names for the same wires on the sheet: reset = in_1; start = in_3; thread_count[7:0] = in_2

  // Notes on the sheet:
  //   contents of rom_1 (hex, n*v repeats v):
  //   50de 300f 9100 9208 9310 3410 7440 3520 7550 3645 3730 8076 f000
endmodule

module alu (
  input  decoded_alu_output_mux,
  input  [7:0] rs,
  input  [7:0] rt,
  input  [1:0] decoded_alu_arithmetic_mux,
  input  reset,
  input  [2:0] core_state,
  input  enable,
  input  clk,
  output [7:0] alu_out
);

  wire decoder_1_out5, not_1_out;
  wire [2:0] comparator_1_lt;
  wire [7:0] adder_1_out, dlv_1_cout, multiplexer_1_out, multiplexer_2_out, multiplier_1_out,
       subtractor_1_out;

  Decoder #(.select(3)) decoder_1 (
    .out5(decoder_1_out5), .sel(core_state));  // open: out0, out1, out2, out3, out4, out6, out7, en
  Adder adder_1 (.a(rs), .b(rt), .out(adder_1_out));  // open: cin, cout
  Subtractor subtractor_1 (.a(rs), .b(rt), .out(subtractor_1_out));  // open: bin, bout
  Multiplier multiplier_1 (.a(rs), .b(rt), .out(multiplier_1_out));  // open: cin, cout
  dlv dlv_1 (.divisor(rs), .dividend(rt), .cout(dlv_1_cout));  // open: err
  Comparator comparator_1 (
    .a(subtractor_1_out), .b({8{1'b0}}), .gt(comparator_1_lt[2]), .eq(comparator_1_lt[1]),
    .lt(comparator_1_lt[0]));
  not not_1 (not_1_out, decoded_alu_output_mux);
  Multiplexer #(.enable("true"), .select(2), .width(8)) multiplexer_1 (
    .in0(adder_1_out), .in1(subtractor_1_out), .in2(multiplier_1_out), .in3(dlv_1_cout),
    .out(multiplexer_1_out), .sel(decoded_alu_arithmetic_mux), .en(decoder_1_out5));
  Multiplexer #(.width(8)) multiplexer_2 (
    .in0({{5{1'b0}}, comparator_1_lt}), .in1(multiplexer_1_out), .out(multiplexer_2_out), .sel(not_1_out));
  Register alu_out_reg (.D(multiplexer_2_out), .en(enable), .clk(clk), .Q(alu_out), .clr(reset));

  // Notes on the sheet:
  //   alu_out: pull=down
endmodule

module dlv (
  input  [7:0] divisor,
  input  [7:0] dividend,
  output [7:0] cout,
  output err
);

  wire [31:0] fpdivider_1_out, inttofp_1_p2, inttofp_2_p2;

  // IntToFP inttofp_1: pin names not known; wires that end beside it: divisor, inttofp_1_p2
  FPDivider fpdivider_1 (.a(inttofp_1_p2), .b(inttofp_2_p2), .out(fpdivider_1_out));
  // IntToFP inttofp_2: pin names not known; wires that end beside it: dividend, inttofp_2_p2, err
  // FPToInt fptoint_1: pin names not known; wires that end beside it: fpdivider_1_out, err, cout

  // Notes on the sheet:
  //   err: pull=down
endmodule

module core (
  input  [2:0] thread_count,
  input  start,
  input  [15:0] program_mem_read_data,
  input  program_mem_read_ready,
  input  clk,
  input  reset,
  input  [7:0] block_id,
  input  [3:0] data_mem_read_ready,
  input  [3:0] data_mem_write_ready_0,
  input  [7:0] data_mem_read_data_0,
  input  [7:0] data_mem_read_data_1,
  input  [7:0] data_mem_read_data_2,
  input  [7:0] data_mem_read_data_3,
  output done,
  output [7:0] program_mem_read_address,
  output program_mem_read_valid,
  output [3:0] data_mem_read_valid,
  output [3:0] data_mem_write_valid,
  output [7:0] data_mem_write_data_0,
  output [7:0] data_mem_write_data_1,
  output [7:0] data_mem_write_data_2,
  output [7:0] data_mem_write_data_3,
  output [7:0] data_mem_write_address_0,
  output [7:0] data_mem_write_address_1,
  output [7:0] data_mem_write_address_2,
  output [7:0] data_mem_write_address_3,
  output [7:0] data_mem_read_address_0,
  output [7:0] data_mem_read_address_1,
  output [7:0] data_mem_read_address_2,
  output [7:0] data_mem_read_address_3
);

  wire d_alu_o_m, d_mem_r_e, d_mem_w_e, d_nzp_w_e, d_pc_mux, d_reg_w_e, decoded_ret, decoder_1_out1,
       decoder_1_out2, decoder_1_out3, decoder_1_out4, decoder_1_out5, decoder_1_out6, decoder_1_out7,
       enable_0, enable_1, enable_2, enable_3;
  wire [1:0] d_alu_arit_mux, d_reg_i_mux, fetcher_1_fetcher_state, lsu_state_0, lsu_state_1, lsu_state_2,
       lsu_state_3;
  wire [2:0] CORE_STATE, d_nzp;
  wire [3:0] d_rd_addr, d_rs_addr, d_rt_addr;
  wire [7:0] alu_out_0, alu_out_1, alu_out_2, alu_out_3, current_pc, d_imme, lsu_out_0, lsu_out_1, lsu_out_2,
       lsu_out_3, next_pc_0, next_pc_1, next_pc_2, next_pc_3, register_w_1_rs, register_w_1_rt,
       register_w_2_rs, register_w_2_rt, register_w_3_rs, register_w_3_rt, register_w_4_rs, register_w_4_rt;
  wire [15:0] fetcher_1_instruction;

  fetcher fetcher_1 (
    .mem_read_ready(program_mem_read_ready), .core_state(CORE_STATE), .clk(clk), .reset(reset),
    .current_pc(current_pc), .mem_read_data(program_mem_read_data), .instruction(fetcher_1_instruction),
    .fetcher_state(fetcher_1_fetcher_state), .mem_read_address(program_mem_read_address),
    .mem_read_valid(program_mem_read_valid));
  decoder_w decoder_w_1 (
    .core_state(CORE_STATE), .instruction(fetcher_1_instruction), .clk(clk), .reset(reset),
    .decoded_nzp(d_nzp), .decoded_immediate(d_imme), .decoded_rd_address(d_rd_addr),
    .decoded_rs_address(d_rs_addr), .decoded_rt_address(d_rt_addr), .decoded_pc_mux(d_pc_mux),
    .decoded_alu_output_mux(d_alu_o_m), .decoded_nzp_write_enable(d_nzp_w_e),
    .decoded_mem_write_enable(d_mem_w_e), .decoded_reg_write_enable(d_reg_w_e),
    .decoded_mem_read_enable(d_mem_r_e), .decoded_alu_arithmetic_mux(d_alu_arit_mux),
    .decoded_ret(decoded_ret), .decoded_reg_input_mux(d_reg_i_mux));
  scheduler scheduler_1 (
    .next_pc_1(next_pc_0), .next_pc_2(next_pc_1), .next_pc_3(next_pc_2), .next_pc_4(next_pc_3),
    .reset(reset), .clk(clk), .decoded_ret(decoded_ret), .start(start),
    .fetcher_state(fetcher_1_fetcher_state),
    .lsu_state({lsu_state_3, lsu_state_2, lsu_state_1, lsu_state_0}), .current_pc_1(current_pc),
    .core_state(CORE_STATE), .done(done));  // open: current_pc_2, current_pc_3, current_pc_4
  register_w register_w_1 (
    .decoded_rs_address(d_rs_addr), .decoded_rt_address(d_rt_addr), .decoded_reg_input_mux(d_reg_i_mux),
    .alu_out(alu_out_0), .lsu_out(lsu_out_0), .decoded_immediate(d_imme), .enable(enable_0), .reset(reset),
    .clk(clk), .THREAD_ID({8{1'b0}}), .decoded_rd_address(d_rd_addr), .block_id(block_id),
    .decoded_reg_write_enable(d_reg_w_e), .core_state(CORE_STATE), .rs(register_w_1_rs), .rt(register_w_1_rt));
  register_w register_w_2 (
    .decoded_rs_address(d_rs_addr), .decoded_rt_address(d_rt_addr), .decoded_reg_input_mux(d_reg_i_mux),
    .alu_out(alu_out_1), .lsu_out(lsu_out_1), .decoded_immediate(d_imme), .enable(enable_1), .reset(reset),
    .clk(clk), .THREAD_ID(8'h1), .decoded_rd_address(d_rd_addr), .block_id(block_id),
    .decoded_reg_write_enable(d_reg_w_e), .core_state(CORE_STATE), .rs(register_w_2_rs), .rt(register_w_2_rt));
  register_w register_w_3 (
    .decoded_rs_address(d_rs_addr), .decoded_rt_address(d_rt_addr), .decoded_reg_input_mux(d_reg_i_mux),
    .alu_out(alu_out_2), .lsu_out(lsu_out_2), .decoded_immediate(d_imme), .enable(enable_2), .reset(reset),
    .clk(clk), .THREAD_ID(8'h2), .decoded_rd_address(d_rd_addr), .block_id(block_id),
    .decoded_reg_write_enable(d_reg_w_e), .core_state(CORE_STATE), .rs(register_w_3_rs), .rt(register_w_3_rt));
  register_w register_w_4 (
    .decoded_rs_address(d_rs_addr), .decoded_rt_address(d_rt_addr), .decoded_reg_input_mux(d_reg_i_mux),
    .alu_out(alu_out_3), .lsu_out(lsu_out_3), .decoded_immediate(d_imme), .enable(enable_3), .reset(reset),
    .clk(clk), .THREAD_ID(8'h3), .decoded_rd_address(d_rd_addr), .block_id(block_id),
    .decoded_reg_write_enable(d_reg_w_e), .core_state(CORE_STATE), .rs(register_w_4_rs), .rt(register_w_4_rt));
  Decoder #(.select(3)) decoder_1 (
    .out1(decoder_1_out1), .out2(decoder_1_out2), .out3(decoder_1_out3), .out4(decoder_1_out4),
    .out5(decoder_1_out5), .out6(decoder_1_out6), .out7(decoder_1_out7), .sel(thread_count));  // open: out0, en
  or or_1 (enable_3, decoder_1_out4, decoder_1_out5, decoder_1_out6, decoder_1_out7);
  or or_2 (enable_0, decoder_1_out1, decoder_1_out2, decoder_1_out3, enable_3);
  or or_3 (enable_1, decoder_1_out2, decoder_1_out3, enable_3);
  or or_4 (enable_2, decoder_1_out3, enable_3);
  alu alu_1 (
    .enable(enable_0), .core_state(CORE_STATE), .decoded_alu_output_mux(d_alu_o_m), .rs(register_w_1_rs),
    .rt(register_w_1_rt), .decoded_alu_arithmetic_mux(d_alu_arit_mux), .clk(clk), .reset(reset),
    .alu_out(alu_out_0));
  alu alu_2 (
    .enable(enable_1), .core_state(CORE_STATE), .decoded_alu_output_mux(d_alu_o_m), .rs(register_w_2_rs),
    .rt(register_w_2_rt), .decoded_alu_arithmetic_mux(d_alu_arit_mux), .clk(clk), .reset(reset),
    .alu_out(alu_out_1));
  alu alu_3 (
    .enable(enable_2), .core_state(CORE_STATE), .decoded_alu_output_mux(d_alu_o_m), .rs(register_w_3_rs),
    .rt(register_w_3_rt), .decoded_alu_arithmetic_mux(d_alu_arit_mux), .clk(clk), .reset(reset),
    .alu_out(alu_out_2));
  alu alu_4 (
    .enable(enable_3), .core_state(CORE_STATE), .decoded_alu_output_mux(d_alu_o_m), .rs(register_w_4_rs),
    .rt(register_w_4_rt), .decoded_alu_arithmetic_mux(d_alu_arit_mux), .clk(clk), .reset(reset),
    .alu_out(alu_out_3));
  lsu lsu_1 (
    .mem_read_data(data_mem_read_data_0), .mem_write_ready(data_mem_write_ready_0[0]),
    .mem_read_ready(data_mem_read_ready[0]), .reset(reset), .clk(clk), .decoded_mem_read_enable(d_mem_r_e),
    .decoded_mem_write_enable(d_mem_w_e), .core_state(CORE_STATE), .enable(enable_0), .rs(register_w_1_rs),
    .rt(register_w_1_rt), .mem_read_address(data_mem_read_address_0), .lsu_out(lsu_out_0),
    .lus_state(lsu_state_0), .mem_write_data(data_mem_write_data_0),
    .mem_write_address(data_mem_write_address_0), .mem_write_valid(data_mem_write_valid[0]),
    .mem_read_valid(data_mem_read_valid[0]));
  lsu lsu_2 (
    .mem_read_data(data_mem_read_data_1), .mem_write_ready(data_mem_write_ready_0[1]),
    .mem_read_ready(data_mem_read_ready[1]), .reset(reset), .clk(clk), .decoded_mem_read_enable(d_mem_r_e),
    .decoded_mem_write_enable(d_mem_w_e), .core_state(CORE_STATE), .enable(enable_1), .rs(register_w_2_rs),
    .rt(register_w_2_rt), .mem_read_address(data_mem_read_address_1), .lsu_out(lsu_out_1),
    .lus_state(lsu_state_1), .mem_write_data(data_mem_write_data_1),
    .mem_write_address(data_mem_write_address_1), .mem_write_valid(data_mem_write_valid[1]),
    .mem_read_valid(data_mem_read_valid[1]));
  lsu lsu_3 (
    .mem_read_data(data_mem_read_data_2), .mem_write_ready(data_mem_write_ready_0[2]),
    .mem_read_ready(data_mem_read_ready[2]), .reset(reset), .clk(clk), .decoded_mem_read_enable(d_mem_r_e),
    .decoded_mem_write_enable(d_mem_w_e), .core_state(CORE_STATE), .enable(enable_2), .rs(register_w_3_rs),
    .rt(register_w_3_rt), .mem_read_address(data_mem_read_address_2), .lsu_out(lsu_out_2),
    .lus_state(lsu_state_2), .mem_write_data(data_mem_write_data_2),
    .mem_write_address(data_mem_write_address_2), .mem_write_valid(data_mem_write_valid[2]),
    .mem_read_valid(data_mem_read_valid[2]));
  // Probe on lsu_state_0
  lsu lsu_4 (
    .mem_read_data(data_mem_read_data_3), .mem_write_ready(data_mem_write_ready_0[3]),
    .mem_read_ready(data_mem_read_ready[3]), .reset(reset), .clk(clk), .decoded_mem_read_enable(d_mem_r_e),
    .decoded_mem_write_enable(d_mem_w_e), .core_state(CORE_STATE), .enable(enable_3), .rs(register_w_4_rs),
    .rt(register_w_4_rt), .mem_read_address(data_mem_read_address_3), .lsu_out(lsu_out_3),
    .lus_state(lsu_state_3), .mem_write_data(data_mem_write_data_3),
    .mem_write_address(data_mem_write_address_3), .mem_write_valid(data_mem_write_valid[3]),
    .mem_read_valid(data_mem_read_valid[3]));
  // Probe on lsu_out_0
  pc pc_1 (
    .enable(enable_0), .alu_out(alu_out_0), .decoded_nzp_write_enable(d_nzp_w_e), .core_state(CORE_STATE),
    .decoded_immediate(d_imme), .reset(reset), .clk(clk), .current_pc(current_pc), .decoded_nzp(d_nzp),
    .decoded_pc_mux(d_pc_mux), .next_pc(next_pc_0));
  pc pc_2 (
    .enable(enable_1), .alu_out(alu_out_1), .decoded_nzp_write_enable(d_nzp_w_e), .core_state(CORE_STATE),
    .decoded_immediate(d_imme), .reset(reset), .clk(clk), .current_pc(current_pc), .decoded_nzp(d_nzp),
    .decoded_pc_mux(d_pc_mux), .next_pc(next_pc_1));
  pc pc_3 (
    .enable(enable_2), .alu_out(alu_out_2), .decoded_nzp_write_enable(d_nzp_w_e), .core_state(CORE_STATE),
    .decoded_immediate(d_imme), .reset(reset), .clk(clk), .current_pc(current_pc), .decoded_nzp(d_nzp),
    .decoded_pc_mux(d_pc_mux), .next_pc(next_pc_2));
  pc pc_4 (
    .enable(enable_3), .alu_out(alu_out_3), .decoded_nzp_write_enable(d_nzp_w_e), .core_state(CORE_STATE),
    .decoded_immediate(d_imme), .reset(reset), .clk(clk), .current_pc(current_pc), .decoded_nzp(d_nzp),
    .decoded_pc_mux(d_pc_mux), .next_pc(next_pc_3));

  // Other names for the same wires on the sheet: data_mem_read_ready_0 = data_mem_read_ready[0];
  //   data_mem_read_ready_1 = data_mem_read_ready[1]; data_mem_read_ready_2 = data_mem_read_ready[2];
  //   data_mem_read_ready_3 = data_mem_read_ready[3]; data_mem_read_valid_0 = data_mem_read_valid[0];
  //   data_mem_read_valid_1 = data_mem_read_valid[1]; data_mem_read_valid_2 = data_mem_read_valid[2];
  //   data_mem_read_valid_3 = data_mem_read_valid[3]; data_mem_write_ready_0_t = data_mem_write_ready_0[0];
  //   data_mem_write_ready_1 = data_mem_write_ready_0[1]; data_mem_write_ready_2 = data_mem_write_ready_0[2];
  //   data_mem_write_ready_3 = data_mem_write_ready_0[3]; data_mem_write_valid_0 = data_mem_write_valid[0];
  //   data_mem_write_valid_1 = data_mem_write_valid[1]; data_mem_write_valid_2 = data_mem_write_valid[2];
  //   data_mem_write_valid_3 = data_mem_write_valid[3]
endmodule

module dcr (
  input  [7:0] device_control_data,
  input  device_control_write_enable,
  input  clk,
  input  reset,
  output [7:0] thread_count
);

  wire [7:0] device_conrol_register_reg_q;

  Register device_conrol_register_reg (
    .D(device_control_data), .en(device_control_write_enable), .clk(clk), .Q(device_conrol_register_reg_q),
    .clr(reset));
  Register thread_count_reg (
    .D(device_conrol_register_reg_q), .en(device_control_write_enable), .clk(clk), .Q(thread_count),
    .clr(reset));
endmodule

module pc (
  input  [7:0] alu_out,
  input  decoded_nzp_write_enable,
  input  [2:0] core_state,
  input  [2:0] decoded_nzp,
  input  enable,
  input  decoded_pc_mux,
  input  [7:0] current_pc,
  input  [7:0] decoded_immediate,
  input  reset,
  input  clk,
  output [7:0] next_pc
);

  wire and_1_out, and_2_out, and_3_out, and_4_out, and_5_out, decoder_1_out5, decoder_1_out6, or_1_out,
       or_2_out;
  wire [2:0] bit_extender_1_out, nzp_reg_q;
  wire [7:0] adder_1_out, multiplexer_1_out;

  Decoder #(.select(3)) decoder_1 (
    .out5(decoder_1_out5), .out6(decoder_1_out6), .sel(core_state), .en(enable));  // open: out0, out1, out2, out3, out4, out7
  Adder adder_1 (.a(8'h1), .b(current_pc), .out(adder_1_out));  // open: cin, cout
  Bit_Extender #(.out_width(3), .\type ("zero")) bit_extender_1 (.in(alu_out), .out(bit_extender_1_out));
  Multiplexer #(.enable("true"), .width(8)) multiplexer_1 (
    .in0(adder_1_out), .in1(decoded_immediate), .out(multiplexer_1_out), .sel(and_5_out), .en(decoder_1_out5));
  Register #(.width(3)) nzp_reg (.D(bit_extender_1_out), .en(and_1_out), .clk(clk), .Q(nzp_reg_q), .clr(reset));
  and and_1 (and_1_out, decoded_nzp_write_enable, decoder_1_out6);
  Register next_pc_reg (.D(multiplexer_1_out), .en(decoder_1_out5), .clk(clk), .Q(next_pc), .clr(reset));
  and and_2 (and_2_out, nzp_reg_q[0], decoded_nzp[0]);
  and and_3 (and_3_out, nzp_reg_q[1], decoded_nzp[1]);
  and and_4 (and_4_out, nzp_reg_q[2], decoded_nzp[2]);
  or or_1 (or_1_out, and_2_out, and_3_out);
  or or_2 (or_2_out, or_1_out, and_4_out);
  and and_5 (and_5_out, or_2_out, decoded_pc_mux);
endmodule

module lsu (
  input  [7:0] rt,
  input  [7:0] rs,
  input  [7:0] mem_read_data,
  input  enable,
  input  decoded_mem_read_enable,
  input  decoded_mem_write_enable,
  input  [2:0] core_state,
  input  mem_write_ready,
  input  mem_read_ready,
  input  reset,
  input  clk,
  output [7:0] mem_write_data,
  output [7:0] mem_write_address,
  output mem_write_valid,
  output [7:0] mem_read_address,
  output mem_read_valid,
  output [7:0] lsu_out,
  output [1:0] lus_state
);

  wire and_1_out, and_2_out, and_3_out, and_4_out, and_5_out, decoder_1_out1, decoder_1_out2, decoder_2_out3,
       decoder_2_out6, or_1_out, or_2_out, or_3_out, or_4_out;
  wire [1:0] bit_extender_1_out, multiplexer_1_out, multiplexer_2_out, multiplexer_3_out;

  or or_1 (or_1_out, mem_write_ready, mem_read_ready);
  Decoder #(.select(2)) decoder_1 (
    .out1(decoder_1_out1), .out2(decoder_1_out2), .sel(lus_state));  // open: out0, out3, en
  Decoder #(.select(3)) decoder_2 (
    .out3(decoder_2_out3), .out6(decoder_2_out6), .sel(core_state));  // open: out0, out1, out2, out4, out5, out7, en
  and and_1 (and_1_out, decoded_mem_write_enable, decoder_1_out1);
  and and_2 (and_2_out, decoder_1_out1, decoded_mem_read_enable);
  and and_3 (and_3_out, decoder_1_out2, decoded_mem_read_enable, mem_read_ready);
  or or_2 (or_2_out, decoded_mem_read_enable, decoded_mem_write_enable);
  assign bit_extender_1_out = {{1{1'b0}}, decoder_2_out3};  // Bit_Extender bit_extender_1
  Multiplexer #(.width(2)) multiplexer_1 (.in0(2'b11), .in1(2'b00), .out(multiplexer_1_out), .sel(decoder_2_out6));
  and and_4 (and_4_out, mem_write_ready, decoder_1_out2);
  or or_3 (or_3_out, and_2_out, and_3_out);
  and and_5 (and_5_out, enable, or_2_out);
  Multiplexer #(.width(2)) multiplexer_2 (.in0(2'b10), .in1(2'b11), .out(multiplexer_2_out), .sel(or_1_out));
  Register #(.width(1)) mem_write_valid_reg (.D(and_1_out), .en(or_4_out), .clk(clk), .Q(mem_write_valid), .clr(reset));
  or or_4 (or_4_out, and_1_out, and_4_out);
  Register #(.width(1)) mem_read_valid_reg (.D(and_2_out), .en(or_3_out), .clk(clk), .Q(mem_read_valid), .clr(reset));
  Multiplexer #(.enable("true"), .select(2), .width(2)) multiplexer_3 (
    .in0(bit_extender_1_out), .in1(2'b10), .in2(multiplexer_2_out), .in3(multiplexer_1_out),
    .out(multiplexer_3_out), .sel(lus_state), .en(and_5_out));
  Register #(.width(2)) lsu_state_reg (.D(multiplexer_3_out), .en(and_5_out), .clk(clk), .Q(lus_state), .clr(reset));
  Register mem_write_data_reg (.D(rt), .en(and_1_out), .clk(clk), .Q(mem_write_data), .clr(reset));
  Register mem_write_address_reg (.D(rs), .en(and_1_out), .clk(clk), .Q(mem_write_address), .clr(reset));
  Register mem_read_address_reg (.D(rs), .en(and_2_out), .clk(clk), .Q(mem_read_address), .clr(reset));
  Register lsu_out_reg (.D(mem_read_data), .en(and_3_out), .clk(clk), .Q(lsu_out), .clr(reset));

  // Other names for the same wires on the sheet: lsu_state[1:0] = lus_state
endmodule

module dispatch (
  input  start,
  input  clk,
  input  reset,
  input  [7:0] thread_count,
  input  [1:0] core_done,
  output [1:0] core_reset,
  output done,
  output [1:0] core_start,
  output [7:0] core_block_id_0,
  output [2:0] core_thread_count_0,
  output [7:0] core_block_id_1,
  output [2:0] core_thread_count_1
);

  wire and_1_out, and_2_out, and_3_out, and_6_out, and_11_out, and_12_out, block_no_sleep_0,
       block_no_sleep_1, comparator_1_eq, comparator_1_gt, comparator_3_eq, comparator_3_gt, comparator_4_lt,
       core_done_signal, CORE_RESET_BIT0, CORE_RESET_BIT1, not_1_out, not_2_out, not_3_out, or_1_out,
       or_2_out, or_3_out, or_4_out, or_5_out, or_6_out, or_7_out, or_9_out, or_10_out, start_execution_reg_q;
  wire [1:0] and_4_out, and_7_out, bitadder_1_out, multiplexer_1_out, multiplexer_2_out, multiplexer_3_out,
       multiplexer_4_out;
  wire [2:0] bit_extender_2_out, bit_extender_3_out;
  wire [7:0] adder_1_out, adder_2_out, adder_3_out, adder_4_out, bit_extender_1_out, blocks_dispatched_reg_q,
       blocks_done_reg_q, multiplexer_5_out, multiplexer_6_out, multiplexer_7_out, multiplier_1_out,
       multiplier_2_out, subtractor_1_out, subtractor_2_out, subtractor_3_out, subtractor_4_out, total_blocks;

  and and_1 (and_1_out, not_1_out, start);
  not not_1 (not_1_out, start_execution_reg_q);
  Register #(.width(1)) start_execution_reg (
    .D(not_1_out), .en(and_1_out), .clk(clk), .Q(start_execution_reg_q), .clr(reset));
  or or_1 (or_1_out, and_1_out, reset);
  and and_2 (and_2_out, CORE_RESET_BIT0, block_no_sleep_0);
  and and_3 (and_3_out, CORE_RESET_BIT1, block_no_sleep_1);
  or or_2 (or_2_out, and_7_out[1], and_3_out);
  and and_4 (and_4_out[0], CORE_RESET_BIT0, 1'b0);
  and and_5 (and_4_out[1], 1'b0, CORE_RESET_BIT1);
  Multiplexer #(.width(2)) multiplexer_1 (.in0(2'b00), .in1(2'b11), .out(multiplexer_1_out), .sel(or_1_out));
  Multiplexer #(.width(2)) multiplexer_2 (
    .in0(multiplexer_1_out), .in1(and_7_out), .out(multiplexer_2_out), .sel(core_done_signal));
  not not_2 (not_2_out, and_7_out[0]);
  or or_3 (or_3_out, not_2_out, and_2_out);
  or or_4 (or_4_out, and_7_out[0], and_2_out);
  not not_3 (not_3_out, and_7_out[1]);
  or or_5 (or_5_out, not_3_out, and_3_out);
  Multiplexer #(.width(2)) multiplexer_3 (
    .in0(multiplexer_2_out), .in1(and_4_out), .out(multiplexer_3_out), .sel(or_6_out));
  Register #(.width(1)) core_start_reg_bit0 (.D(or_3_out), .en(or_4_out), .clk(clk), .Q(core_start[0]), .clr(reset));
  Register #(.width(1)) core_start_reg_bit1 (.D(or_5_out), .en(or_2_out), .clk(clk), .Q(core_start[1]), .clr(reset));
  or or_6 (or_6_out, CORE_RESET_BIT0, CORE_RESET_BIT1);
  and and_6 (and_6_out, start, core_done_signal);
  Register #(.width(2)) core_reset_reg (.D(multiplexer_4_out), .en(or_7_out), .clk(clk), .Q(core_reset));  // open: clr
  Multiplexer #(.width(2)) multiplexer_4 (.in0(multiplexer_3_out), .in1(2'b11), .out(multiplexer_4_out), .sel(reset));
  or or_7 (or_7_out, or_6_out, or_1_out, and_6_out);
  and and_7 (and_7_out[0], core_start[0], core_done[0]);
  and and_8 (and_7_out[1], core_start[1], core_done[1]);
  BitAdder #(.width(2)) bitadder_1 (.in0(and_7_out), .out(bitadder_1_out));
  or or_8 (core_done_signal, and_7_out[0], and_7_out[1]);
  Adder adder_1 (.a(blocks_dispatched_reg_q), .b({8{1'b0}}), .out(adder_1_out), .cin(and_11_out));  // open: cout
  and and_9 (CORE_RESET_BIT0, start, core_reset[0]);
  assign bit_extender_1_out = {{6{1'b0}}, bitadder_1_out};  // Bit_Extender bit_extender_1
  and and_10 (CORE_RESET_BIT1, core_reset[1], start);
  Multiplexer #(.width(8)) multiplexer_5 (
    .in0({8{1'b0}}), .in1(bit_extender_1_out), .out(multiplexer_5_out), .sel(core_done_signal));
  Adder adder_2 (.a(adder_1_out), .b({8{1'b0}}), .out(adder_2_out), .cin(and_12_out));  // open: cout
  and and_11 (and_11_out, CORE_RESET_BIT0, block_no_sleep_0, comparator_4_lt);
  and and_12 (and_12_out, comparator_4_lt, CORE_RESET_BIT1, block_no_sleep_1);
  Adder adder_3 (.a(blocks_done_reg_q), .b(multiplexer_5_out), .out(adder_3_out));  // open: cin, cout
  Adder adder_4 (.a(thread_count), .b(8'h3), .out(adder_4_out));  // open: cin, cout
  Register blocks_done_reg (.D(adder_3_out), .en(core_done_signal), .clk(clk), .Q(blocks_done_reg_q), .clr(reset));
  Shifter #(.shift("lr")) shifter_1 (.in(adder_4_out), .\dist (3'b010), .out(total_blocks));
  Register blocks_dispatched_reg (
    .D(adder_2_out), .en(comparator_4_lt), .clk(clk), .Q(blocks_dispatched_reg_q), .clr(reset));
  Multiplier multiplier_1 (.a(blocks_dispatched_reg_q), .b(8'h4), .out(multiplier_1_out));  // open: cin, cout
  Register core_block_id_reg_1 (.D(adder_1_out), .en(and_12_out), .clk(clk), .Q(core_block_id_1), .clr(reset));
  Multiplier multiplier_2 (.a(8'h4), .b(adder_1_out), .out(multiplier_2_out));  // open: cin, cout
  Register core_block_id_reg_0 (
    .D(blocks_dispatched_reg_q), .en(and_11_out), .clk(clk), .Q(core_block_id_0), .clr(reset));
  or or_9 (or_9_out, and_11_out, reset);
  Subtractor subtractor_1 (.a(total_blocks), .b(8'h1), .out(subtractor_1_out));  // open: bin, bout
  Subtractor subtractor_2 (.a(thread_count), .b(multiplier_2_out), .out(subtractor_2_out));  // open: bin, bout
  Subtractor subtractor_3 (.a(total_blocks), .b(8'h1), .out(subtractor_3_out));  // open: bin, bout
  Subtractor subtractor_4 (.a(thread_count), .b(multiplier_1_out), .out(subtractor_4_out));  // open: bin, bout
  Comparator comparator_1 (
    .a(adder_1_out), .b(subtractor_1_out), .gt(comparator_1_gt), .eq(comparator_1_eq));  // open: lt
  or or_10 (or_10_out, and_12_out, reset);
  Comparator comparator_2 (.a(total_blocks), .b(blocks_done_reg_q), .eq(done));  // open: gt, lt
  not not_4 (block_no_sleep_0, comparator_3_gt);
  Comparator comparator_3 (
    .a(blocks_dispatched_reg_q), .b(subtractor_3_out), .gt(comparator_3_gt), .eq(comparator_3_eq));  // open: lt
  not not_5 (block_no_sleep_1, comparator_1_gt);
  Comparator comparator_4 (.a(blocks_dispatched_reg_q), .b(total_blocks), .lt(comparator_4_lt));  // open: gt, eq
  Multiplexer #(.width(8)) multiplexer_6 (
    .in0(8'h4), .in1(subtractor_4_out), .out(multiplexer_6_out), .sel(comparator_3_eq));
  Multiplexer #(.width(8)) multiplexer_7 (
    .in0(8'h4), .in1(subtractor_2_out), .out(multiplexer_7_out), .sel(comparator_1_eq));
  Bit_Extender #(.out_width(3), .\type ("zero")) bit_extender_2 (.in(multiplexer_6_out), .out(bit_extender_2_out));
  Register #(.width(3)) core_thread_count_reg_0 (
    .D(bit_extender_2_out), .en(or_9_out), .clk(clk), .Q(core_thread_count_0), .clr(reset));
  Register #(.width(3)) core_thread_count_reg_1 (
    .D(bit_extender_3_out), .en(or_10_out), .clk(clk), .Q(core_thread_count_1), .clr(reset));
  Bit_Extender #(.out_width(3), .\type ("zero")) bit_extender_3 (.in(multiplexer_7_out), .out(bit_extender_3_out));
endmodule

module fetcher (
  input  [7:0] current_pc,
  input  mem_read_ready,
  input  [2:0] core_state,
  input  clk,
  input  reset,
  input  [15:0] mem_read_data,
  output [7:0] mem_read_address,
  output mem_read_valid,
  output [1:0] fetcher_state,
  output [15:0] instruction
);

  wire and_1_out, and_2_out, and_3_out, decoder_1_out0, decoder_1_out1, decoder_1_out2, decoder_2_out1,
       decoder_2_out2, or_1_out, or_2_out;
  wire [1:0] adder_1_out, bit_extender_1_out, multiplexer_1_out;

  Decoder #(.select(2)) decoder_1 (
    .out0(decoder_1_out0), .out1(decoder_1_out1), .out2(decoder_1_out2), .sel(fetcher_state));  // open: out3, en
  and and_1 (and_1_out, decoder_1_out1, mem_read_ready);
  Decoder #(.select(3)) decoder_2 (
    .out1(decoder_2_out1), .out2(decoder_2_out2), .sel(core_state));  // open: out0, out3, out4, out5, out6, out7, en
  and and_2 (and_2_out, decoder_1_out0, decoder_2_out1);
  or or_1 (or_1_out, and_2_out, and_1_out);
  and and_3 (and_3_out, decoder_1_out2, decoder_2_out2);
  Adder #(.width(2)) adder_1 (.a(fetcher_state), .b(bit_extender_1_out), .out(adder_1_out));  // open: cin, cout
  assign bit_extender_1_out = {{1{1'b0}}, or_1_out};  // Bit_Extender bit_extender_1
  or or_2 (or_2_out, or_1_out, and_3_out);
  Multiplexer #(.width(2)) multiplexer_1 (.in0(adder_1_out), .in1(2'b00), .out(multiplexer_1_out), .sel(and_3_out));
  Register mem_read_address_reg (.D(current_pc), .en(and_2_out), .clk(clk), .Q(mem_read_address), .clr(reset));
  Register #(.width(1)) mem_read_valid_reg (.D(and_2_out), .en(or_1_out), .clk(clk), .Q(mem_read_valid), .clr(reset));
  Register #(.width(2)) fetcher_state_reg (
    .D(multiplexer_1_out), .en(or_2_out), .clk(clk), .Q(fetcher_state), .clr(reset));
  Register #(.width(16)) instruction_reg (.D(mem_read_data), .en(and_1_out), .clk(clk), .Q(instruction), .clr(reset));
endmodule

module scheduler (
  input  [7:0] next_pc_1,
  input  [7:0] next_pc_2,
  input  [7:0] next_pc_3,
  input  [7:0] next_pc_4,
  input  reset,
  input  clk,
  input  decoded_ret,
  input  start,
  input  [1:0] fetcher_state,
  input  [7:0] lsu_state,
  output [7:0] current_pc_1,
  output [7:0] current_pc_2,
  output [7:0] current_pc_3,
  output [7:0] current_pc_4,
  output [2:0] core_state,
  output done
);

  wire and_1_out, and_2_out, comparator_1_eq, decoder_1_out2, multiplexer_1_out, nor_1_out, not_1_out,
       not_2_out, or_1_out, or_2_out, xor_1_out, xor_2_out, xor_3_out, xor_4_out;
  wire [2:0] adder_1_out, bit_extender_1_out, multiplexer_2_out;

  xor xor_1 (xor_1_out, lsu_state[0], lsu_state[1]);
  xor xor_2 (xor_2_out, lsu_state[2], lsu_state[3]);
  xor xor_3 (xor_3_out, lsu_state[4], lsu_state[5]);
  xor xor_4 (xor_4_out, lsu_state[6], lsu_state[7]);
  or or_1 (or_1_out, xor_1_out, xor_2_out);
  or or_2 (or_2_out, xor_3_out, xor_4_out);
  Decoder #(.select(2)) decoder_1 (.out2(decoder_1_out2), .sel(fetcher_state));  // open: out0, out1, out3, en
  nor nor_1 (nor_1_out, or_1_out, or_2_out);
  assign bit_extender_1_out = {{2{1'b0}}, multiplexer_1_out};  // Bit_Extender bit_extender_1
  Multiplexer #(.select(3)) multiplexer_1 (
    .in0(start), .in1(decoder_1_out2), .in2(1'b1), .in3(1'b1), .in4(nor_1_out), .in5(1'b1), .in6(and_2_out),
    .in7(1'b0), .out(multiplexer_1_out), .sel(core_state));
  Adder #(.width(3)) adder_1 (.a(core_state), .b(bit_extender_1_out), .out(adder_1_out));  // open: cin, cout
  and and_1 (and_1_out, comparator_1_eq, not_1_out);
  Comparator #(.width(3)) comparator_1 (.a(core_state), .b(3'b110), .eq(comparator_1_eq));  // open: gt, lt
  Multiplexer #(.width(3)) multiplexer_2 (.in0(adder_1_out), .in1(3'b001), .out(multiplexer_2_out), .sel(and_1_out));
  not not_1 (not_1_out, and_2_out);
  and and_2 (and_2_out, comparator_1_eq, decoded_ret);
  Register current_pc_reg_1 (.D(next_pc_1), .en(and_1_out), .clk(clk), .Q(current_pc_1), .clr(reset));
  Register current_pc_reg_2 (.D(next_pc_2), .en(and_1_out), .clk(clk), .Q(current_pc_2), .clr(reset));
  Register current_pc_reg_3 (.D(next_pc_3), .en(and_1_out), .clk(clk), .Q(current_pc_3), .clr(reset));
  Register current_pc_reg_4 (.D(next_pc_4), .en(and_1_out), .clk(clk), .Q(current_pc_4), .clr(reset));
  Register #(.width(3)) core_state_reg (.D(multiplexer_2_out), .en(not_2_out), .clk(clk), .Q(core_state), .clr(reset));
  not not_2 (not_2_out, reset);
  Register #(.width(1)) register_1 (.D(and_2_out), .en(and_2_out), .clk(clk), .Q(done), .clr(reset));
endmodule

module controller_4c8u (
  input  [7:0] consumer_write_valid,
  input  [7:0] consumer_read_valid,
  input  reset,
  input  clk,
  input  [3:0] mem_read_ready,
  input  [3:0] mem_write_ready,
  input  [7:0] consumer_write_address_0,
  input  [7:0] consumer_write_address_1,
  input  [7:0] consumer_write_address_2,
  input  [7:0] consumer_write_address_3,
  input  [7:0] consumer_write_address_4,
  input  [7:0] consumer_write_address_5,
  input  [7:0] consumer_write_address_6,
  input  [7:0] consumer_write_address_7,
  input  [7:0] consumer_write_data_0,
  input  [7:0] consumer_write_data_1,
  input  [7:0] consumer_write_data_2,
  input  [7:0] consumer_write_data_3,
  input  [7:0] consumer_write_data_4,
  input  [7:0] consumer_write_data_5,
  input  [7:0] consumer_write_data_6,
  input  [7:0] consumer_write_data_7,
  input  [7:0] consumer_read_address_0,
  input  [7:0] consumer_read_address_1,
  input  [7:0] consumer_read_address_2,
  input  [7:0] consumer_read_address_3,
  input  [7:0] consumer_read_address_4,
  input  [7:0] consumer_read_address_5,
  input  [7:0] consumer_read_address_6,
  input  [7:0] consumer_read_address_7,
  input  [7:0] mem_read_data_0,
  input  [7:0] mem_read_data_1,
  input  [7:0] mem_read_data_2,
  input  [7:0] mem_read_data_3,
  output [3:0] mem_write_valid,
  output [3:0] mem_read_valid,
  output [7:0] mem_read_address_0,
  output [7:0] mem_read_address_1,
  output [7:0] mem_read_address_2,
  output [7:0] mem_read_address_3,
  output [7:0] mem_write_address_0,
  output [7:0] mem_write_address_1,
  output [7:0] mem_write_address_2,
  output [7:0] mem_write_address_3,
  output [7:0] mem_write_data_0,
  output [7:0] mem_write_data_1,
  output [7:0] mem_write_data_2,
  output [7:0] mem_write_data_3,
  output [7:0] consumer_write_ready,
  output [7:0] consumer_read_data_0,
  output [7:0] consumer_read_data_1,
  output [7:0] consumer_read_data_2,
  output [7:0] consumer_read_data_3,
  output [7:0] consumer_read_data_4,
  output [7:0] consumer_read_data_5,
  output [7:0] consumer_read_data_6,
  output [7:0] consumer_read_data_7,
  output [7:0] consumer_read_ready
);

  wire and_19_out, and_21_out, and_23_out, and_25_out, and_27_out, and_29_out, and_31_out, and_33_out,
       and_34_out, and_35_out, and_36_out, and_37_out, and_38_out, and_39_out, and_40_out, and_50_out,
       and_52_out, and_54_out, and_56_out, and_58_out, and_60_out, and_62_out, and_64_out, and_66_out,
       and_67_out, and_69_out, and_70_out, and_72_out, and_73_out, and_75_out, and_76_out, and_78_out,
       and_79_out, and_81_out, and_82_out, and_84_out, and_85_out, and_87_out, and_88_out, and_89_out,
       and_90_out, and_91_out, and_92_out, and_93_out, and_94_out, and_96_out, and_98_out, and_100_out,
       and_102_out, and_104_out, and_106_out, and_108_out, bitselector_1_out, bitselector_2_out,
       bitselector_3_out, bitselector_4_out, bitselector_5_out, bitselector_6_out, bitselector_7_out,
       bitselector_8_out, bitselector_9_out, bitselector_10_out, bitselector_11_out, bitselector_12_out,
       channel_sc_reg_0, channel_sc_reg_1, channel_sc_reg_2, channel_sc_reg_3, channel_sc_reg_4,
       channel_sc_reg_5, channel_sc_reg_6, channel_sc_reg_7, channel_serving_consumer_reg_7_q,
       decoder_3_out0, decoder_3_out1, decoder_3_out2, decoder_3_out3, decoder_3_out4, decoder_3_out5,
       decoder_3_out6, decoder_3_out7, decoder_4_out0, decoder_4_out1, decoder_4_out2, decoder_4_out3,
       decoder_4_out4, decoder_4_out5, decoder_4_out6, decoder_4_out7, decoder_5_out0, decoder_5_out1,
       decoder_5_out2, decoder_5_out3, decoder_5_out4, decoder_5_out5, decoder_5_out6, decoder_5_out7,
       decoder_6_out0, decoder_6_out1, decoder_6_out2, decoder_6_out3, decoder_6_out4, decoder_6_out5,
       decoder_6_out6, decoder_6_out7, Find_READ_IDLE_TYPE_0, Find_READ_IDLE_TYPE_1, Find_READ_IDLE_TYPE_2,
       Find_READ_IDLE_TYPE_3, IDLE_STATE_0, IDLE_STATE_1, IDLE_STATE_2, IDLE_STATE_3, IDLE_TYPE_READ_0,
       IDLE_TYPE_READ_1, IDLE_TYPE_READ_2, IDLE_TYPE_READ_3, IDLE_TYPE_WRITE_0, IDLE_TYPE_WRITE_1,
       IDLE_TYPE_WRITE_2, IDLE_TYPE_WRITE_3, multiplexer_3_out, multiplexer_6_out, multiplexer_9_out,
       multiplexer_10_out, multiplexer_16_out, multiplexer_19_out, multiplexer_24_out, multiplexer_25_out,
       multiplexer_31_out, multiplexer_32_out, multiplexer_33_out, multiplexer_34_out, multiplexer_35_out,
       multiplexer_36_out, multiplexer_37_out, multiplexer_38_out, not_1_out, not_2_out, not_3_out,
       not_4_out, not_5_out, not_6_out, not_7_out, not_8_out, not_9_out, not_10_out, not_11_out, not_12_out,
       not_13_out, not_14_out, not_15_out, not_16_out, not_17_out, not_18_out, not_19_out, not_20_out,
       not_21_out, not_22_out, not_23_out, not_24_out, not_25_out, not_26_out, not_27_out, not_28_out,
       not_29_out, not_30_out, not_31_out, not_32_out, not_33_out, not_34_out, not_35_out, not_36_out,
       not_37_out, not_38_out, not_39_out, not_40_out, not_41_out, not_42_out, not_43_out, not_44_out,
       not_45_out, not_46_out, not_47_out, not_48_out, not_49_out, not_50_out, not_51_out, not_52_out,
       not_53_out, not_54_out, not_55_out, not_56_out, not_57_out, not_58_out, not_59_out, not_60_out,
       not_61_out, not_62_out, not_63_out, not_64_out, not_65_out, not_66_out, not_67_out, not_68_out,
       not_69_out, not_70_out, not_71_out, not_72_out, not_73_out, not_74_out, not_75_out, not_76_out,
       not_77_out, not_78_out, not_79_out, not_80_out, not_81_out, not_82_out, not_83_out, not_84_out,
       not_85_out, not_86_out, not_87_out, not_88_out, not_89_out, not_90_out, not_91_out, not_92_out,
       or_1_out, or_2_out, or_3_out, or_4_out, or_5_out, or_6_out, or_7_out, or_8_out, or_9_out, or_10_out,
       or_11_out, or_12_out, or_13_out, or_14_out, or_15_out, or_16_out, or_17_out, or_18_out, or_19_out,
       or_20_out, or_21_out, or_22_out, or_23_out, or_24_out, or_25_out, or_26_out, or_27_out, or_28_out,
       or_29_out, or_30_out, or_31_out, or_32_out, or_33_out, or_34_out, or_35_out, or_36_out, or_37_out,
       or_38_out, or_39_out, or_40_out, or_41_out, or_42_out, or_43_out, or_44_out, or_45_out, or_46_out,
       or_47_out, or_48_out, or_49_out, or_50_out, or_51_out, or_52_out, or_53_out, or_54_out, or_55_out,
       or_56_out, or_57_out, or_58_out, or_59_out, or_60_out, read_data_router_1_e_0, read_data_router_1_e_1,
       read_data_router_1_e_2, read_data_router_1_e_3, read_data_router_1_e_4, read_data_router_1_e_5,
       read_data_router_1_e_6, read_data_router_1_e_7, READ_RELAYING_STATE_0, READ_RELAYING_STATE_1,
       READ_RELAYING_STATE_2, READ_RELAYING_STATE_3, READ_RELAYING_STATE_UPDATE_0,
       READ_RELAYING_STATE_UPDATE_1, READ_RELAYING_STATE_UPDATE_2, READ_RELAYING_STATE_UPDATE_3,
       READ_WAITING_STATE_0, READ_WAITING_STATE_1, READ_WAITING_STATE_2, READ_WAITING_STATE_3,
       READ_WAITING_STATE_UPDATE_0, READ_WAITING_STATE_UPDATE_1, READ_WAITING_STATE_UPDATE_2,
       READ_WAITING_STATE_UPDATE_3, register_26_q, register_27_q, register_28_q, register_29_q,
       register_30_q, register_31_q, register_32_q, RESET_t, wr_waiting_merger_cc_enable_1_o0,
       wr_waiting_merger_cc_enable_1_o1, wr_waiting_merger_cc_enable_1_o2, wr_waiting_merger_cc_enable_1_o3,
       wr_waiting_merger_cc_enable_1_o4, wr_waiting_merger_cc_enable_1_o5, wr_waiting_merger_cc_enable_1_o6,
       wr_waiting_merger_cc_enable_1_o7, wr_waiting_merger_cc_enable_1_on0,
       wr_waiting_merger_cc_enable_1_on1, wr_waiting_merger_cc_enable_1_on2,
       wr_waiting_merger_cc_enable_1_on3, wr_waiting_merger_cc_enable_1_on4,
       wr_waiting_merger_cc_enable_1_on5, wr_waiting_merger_cc_enable_1_on6,
       wr_waiting_merger_cc_enable_1_on7, wr_waiting_merger_cc_enable_2_o0, wr_waiting_merger_cc_enable_2_o1,
       wr_waiting_merger_cc_enable_2_o2, wr_waiting_merger_cc_enable_2_o3, wr_waiting_merger_cc_enable_2_o4,
       wr_waiting_merger_cc_enable_2_o5, wr_waiting_merger_cc_enable_2_o6, wr_waiting_merger_cc_enable_2_o7,
       wr_waiting_merger_cc_enable_2_on0, wr_waiting_merger_cc_enable_2_on1,
       wr_waiting_merger_cc_enable_2_on2, wr_waiting_merger_cc_enable_2_on3,
       wr_waiting_merger_cc_enable_2_on4, wr_waiting_merger_cc_enable_2_on5,
       wr_waiting_merger_cc_enable_2_on6, wr_waiting_merger_cc_enable_2_on7, WRITE_RELAYING_STATE_0,
       WRITE_RELAYING_STATE_1, WRITE_RELAYING_STATE_2, WRITE_RELAYING_STATE_3, WRITE_RELAYING_STATE_UPDATE_0,
       WRITE_RELAYING_STATE_UPDATE_1, WRITE_RELAYING_STATE_UPDATE_2, WRITE_RELAYING_STATE_UPDATE_3,
       WRITE_WAITING_STATE_0, WRITE_WAITING_STATE_1, WRITE_WAITING_STATE_2, WRITE_WAITING_STATE_3,
       WRITE_WAITING_STATE_UPDATE_0, WRITE_WAITING_STATE_UPDATE_1, WRITE_WAITING_STATE_UPDATE_2,
       WRITE_WAITING_STATE_UPDATE_3;
  wire [2:0] controller_state_reg_0_q, controller_state_reg_1_q, current_consumer_0, current_consumer_1,
       current_consumer_2, current_consumer_3, Find_READ_IDLE_TYPE_BIT_0, Find_READ_IDLE_TYPE_BIT_1,
       Find_READ_IDLE_TYPE_BIT_2, Find_READ_IDLE_TYPE_BIT_3, multiplexer_11_out, multiplexer_12_out,
       multiplexer_13_out, multiplexer_14_out, multiplexer_15_out, multiplexer_26_out, multiplexer_27_out,
       multiplexer_28_out, multiplexer_29_out, multiplexer_30_out, multiplexer_39_out, multiplexer_40_out,
       multiplexer_41_out, multiplexer_42_out, multiplexer_43_out, multiplexer_44_out, multiplexer_45_out,
       multiplexer_46_out, multiplexer_47_out, multiplexer_48_out, register_33_q, register_49_q;
  wire [7:0] and_32_out, and_63_out, and_86_out, and_109_out, multiplexer_1_out, multiplexer_2_out,
       multiplexer_4_out, multiplexer_5_out, multiplexer_7_out, multiplexer_8_out, multiplexer_17_out,
       multiplexer_18_out, multiplexer_20_out, multiplexer_21_out, multiplexer_22_out, multiplexer_23_out,
       read_data_router_1_o_0, read_data_router_1_o_1, read_data_router_1_o_2, read_data_router_1_o_3,
       read_data_router_1_o_4, read_data_router_1_o_5, read_data_router_1_o_6, read_data_router_1_o_7;

  and and_1 (RESET_t, reset, clk);
  and and_2 (READ_WAITING_STATE_UPDATE_3, READ_WAITING_STATE_3, mem_read_ready[3]);
  and and_3 (READ_WAITING_STATE_UPDATE_2, READ_WAITING_STATE_2, mem_read_ready[2]);
  and and_4 (READ_WAITING_STATE_UPDATE_1, READ_WAITING_STATE_1, mem_read_ready[1]);
  and and_5 (WRITE_WAITING_STATE_UPDATE_3, WRITE_WAITING_STATE_3, mem_write_ready[3]);
  and and_6 (WRITE_WAITING_STATE_UPDATE_2, WRITE_WAITING_STATE_2, mem_write_ready[2]);
  and and_7 (WRITE_WAITING_STATE_UPDATE_1, WRITE_WAITING_STATE_1, mem_write_ready[1]);
  or or_1 (or_1_out, READ_WAITING_STATE_UPDATE_0, IDLE_TYPE_READ_0);
  Multiplexer #(.select(3), .width(8)) multiplexer_1 (
    .in0(consumer_write_data_0), .in1(consumer_write_data_1), .in2(consumer_write_data_2),
    .in3(consumer_write_data_3), .in4(consumer_write_data_4), .in5(consumer_write_data_5),
    .in6(consumer_write_data_6), .in7(consumer_write_data_7), .out(multiplexer_1_out),
    .sel(Find_READ_IDLE_TYPE_BIT_0));
  or or_2 (or_2_out, READ_WAITING_STATE_UPDATE_2, IDLE_TYPE_READ_2);
  Multiplexer #(.select(3), .width(8)) multiplexer_2 (
    .in0(consumer_write_data_0), .in1(consumer_write_data_1), .in2(consumer_write_data_2),
    .in3(consumer_write_data_3), .in4(consumer_write_data_4), .in5(consumer_write_data_5),
    .in6(consumer_write_data_6), .in7(consumer_write_data_7), .out(multiplexer_2_out),
    .sel(Find_READ_IDLE_TYPE_BIT_2));
  and and_8 (READ_WAITING_STATE_UPDATE_0, READ_WAITING_STATE_0, mem_read_ready[0]);
  and and_9 (WRITE_WAITING_STATE_UPDATE_0, WRITE_WAITING_STATE_0, mem_write_ready[0]);
  Register #(.width(1)) mem_read_valid_reg_0 (
    .D(multiplexer_3_out), .en(or_1_out), .clk(clk), .Q(mem_read_valid[0]), .clr(RESET_t));
  Multiplexer multiplexer_3 (.in0(1'b1), .in1(1'b0), .out(multiplexer_3_out), .sel(READ_WAITING_STATE_UPDATE_0));
  Multiplexer #(.enable("true"), .select(3), .width(8)) multiplexer_4 (
    .in0(consumer_read_address_0), .in1(consumer_read_address_1), .in2(consumer_read_address_2),
    .in3(consumer_read_address_3), .in4(consumer_read_address_4), .in5(consumer_read_address_5),
    .in6(consumer_read_address_6), .in7(consumer_read_address_7), .out(multiplexer_4_out),
    .sel(Find_READ_IDLE_TYPE_BIT_0), .en(IDLE_TYPE_READ_0));
  or or_3 (or_3_out, IDLE_TYPE_WRITE_0, WRITE_RELAYING_STATE_0);
  Register mem_write_data_reg_0 (
    .D(multiplexer_1_out), .en(IDLE_TYPE_WRITE_0), .clk(clk), .Q(mem_write_data_0), .clr(RESET_t));
  Register mem_write_address_reg_0 (
    .D(multiplexer_5_out), .en(IDLE_TYPE_WRITE_0), .clk(clk), .Q(mem_write_address_0), .clr(RESET_t));
  Multiplexer #(.select(3), .width(8)) multiplexer_5 (
    .in0(consumer_write_address_0), .in1(consumer_write_address_1), .in2(consumer_write_address_2),
    .in3(consumer_write_address_3), .in4(consumer_write_address_4), .in5(consumer_write_address_5),
    .in6(consumer_write_address_6), .in7(consumer_write_address_7), .out(multiplexer_5_out),
    .sel(Find_READ_IDLE_TYPE_BIT_0));
  Register #(.width(1)) register_1 (
    .D(multiplexer_6_out), .en(or_2_out), .clk(clk), .Q(mem_read_valid[2]), .clr(RESET_t));
  Multiplexer multiplexer_6 (.in0(1'b1), .in1(1'b0), .out(multiplexer_6_out), .sel(READ_WAITING_STATE_UPDATE_2));
  Multiplexer #(.enable("true"), .select(3), .width(8)) multiplexer_7 (
    .in0(consumer_read_address_0), .in1(consumer_read_address_1), .in2(consumer_read_address_2),
    .in3(consumer_read_address_3), .in4(consumer_read_address_4), .in5(consumer_read_address_5),
    .in6(consumer_read_address_6), .in7(consumer_read_address_7), .out(multiplexer_7_out),
    .sel(Find_READ_IDLE_TYPE_BIT_2), .en(IDLE_TYPE_READ_2));
  or or_4 (or_4_out, IDLE_TYPE_WRITE_2, WRITE_RELAYING_STATE_2);
  Register register_2 (.D(multiplexer_2_out), .en(IDLE_TYPE_WRITE_2), .clk(clk), .Q(mem_write_data_2), .clr(RESET_t));
  Register register_3 (
    .D(multiplexer_8_out), .en(IDLE_TYPE_WRITE_2), .clk(clk), .Q(mem_write_address_2), .clr(RESET_t));
  Multiplexer #(.select(3), .width(8)) multiplexer_8 (
    .in0(consumer_write_address_0), .in1(consumer_write_address_1), .in2(consumer_write_address_2),
    .in3(consumer_write_address_3), .in4(consumer_write_address_4), .in5(consumer_write_address_5),
    .in6(consumer_write_address_6), .in7(consumer_write_address_7), .out(multiplexer_8_out),
    .sel(Find_READ_IDLE_TYPE_BIT_2));
  Register #(.width(1)) mem_write_valid_reg_0 (
    .D(multiplexer_9_out), .en(or_3_out), .clk(clk), .Q(mem_write_valid[0]), .clr(RESET_t));
  Multiplexer multiplexer_9 (.in0(1'b1), .in1(1'b0), .out(multiplexer_9_out), .sel(WRITE_RELAYING_STATE_0));
  Register #(.width(1)) register_4 (
    .D(multiplexer_10_out), .en(or_4_out), .clk(clk), .Q(mem_write_valid[2]), .clr(RESET_t));
  Multiplexer multiplexer_10 (.in0(1'b1), .in1(1'b0), .out(multiplexer_10_out), .sel(WRITE_RELAYING_STATE_2));
  Register mem_read_address_reg_0 (
    .D(multiplexer_4_out), .en(IDLE_TYPE_READ_0), .clk(clk), .Q(mem_read_address_0), .clr(RESET_t));
  Register register_5 (.D(multiplexer_7_out), .en(IDLE_TYPE_READ_2), .clk(clk), .Q(mem_read_address_2), .clr(RESET_t));
  READ_DATA_ROUTER read_data_router_1 (
    .en_0(READ_WAITING_STATE_UPDATE_0), .en_1(READ_WAITING_STATE_UPDATE_1),
    .en_2(READ_WAITING_STATE_UPDATE_2), .en_3(READ_WAITING_STATE_UPDATE_3), .cn_0(current_consumer_0),
    .cn_1(current_consumer_1), .cn_2(current_consumer_2), .cn_3(current_consumer_3), .c0(mem_read_data_0),
    .c1(mem_read_data_1), .c2(mem_read_data_2), .c3(mem_read_data_3), .e_0(read_data_router_1_e_0),
    .e_1(read_data_router_1_e_1), .e_2(read_data_router_1_e_2), .e_3(read_data_router_1_e_3),
    .e_4(read_data_router_1_e_4), .e_5(read_data_router_1_e_5), .e_6(read_data_router_1_e_6),
    .e_7(read_data_router_1_e_7), .o_0(read_data_router_1_o_0), .o_1(read_data_router_1_o_1),
    .o_2(read_data_router_1_o_2), .o_3(read_data_router_1_o_3), .o_4(read_data_router_1_o_4),
    .o_5(read_data_router_1_o_5), .o_6(read_data_router_1_o_6), .o_7(read_data_router_1_o_7));
  not not_1 (not_1_out, bitselector_1_out);
  BitSelector bitselector_1 (.in(consumer_read_valid), .out(bitselector_1_out), .sel(current_consumer_0));
  not not_2 (not_2_out, bitselector_2_out);
  BitSelector bitselector_2 (.in(consumer_read_valid), .out(bitselector_2_out), .sel(current_consumer_1));
  not not_3 (not_3_out, bitselector_3_out);
  BitSelector bitselector_3 (.in(consumer_read_valid), .out(bitselector_3_out), .sel(current_consumer_3));
  not not_4 (not_4_out, bitselector_4_out);
  BitSelector bitselector_4 (.in(consumer_read_valid), .out(bitselector_4_out), .sel(current_consumer_3));
  and and_10 (READ_RELAYING_STATE_UPDATE_0, READ_RELAYING_STATE_0, not_1_out);
  and and_11 (READ_RELAYING_STATE_UPDATE_1, READ_RELAYING_STATE_1, not_2_out);
  and and_12 (READ_RELAYING_STATE_UPDATE_2, READ_RELAYING_STATE_2, not_3_out);
  and and_13 (READ_RELAYING_STATE_UPDATE_3, READ_RELAYING_STATE_3, not_4_out);
  Register consumer_read_data_reg_0 (
    .D(read_data_router_1_o_0), .en(read_data_router_1_e_0), .clk(clk), .Q(consumer_read_data_0),
    .clr(RESET_t));
  Register register_6 (
    .D(read_data_router_1_o_1), .en(read_data_router_1_e_1), .clk(clk), .Q(consumer_read_data_1),
    .clr(RESET_t));
  Register register_7 (
    .D(read_data_router_1_o_2), .en(read_data_router_1_e_2), .clk(clk), .Q(consumer_read_data_2),
    .clr(RESET_t));
  Register register_8 (
    .D(read_data_router_1_o_3), .en(read_data_router_1_e_3), .clk(clk), .Q(consumer_read_data_3),
    .clr(RESET_t));
  Register register_9 (
    .D(read_data_router_1_o_4), .en(read_data_router_1_e_4), .clk(clk), .Q(consumer_read_data_4),
    .clr(RESET_t));
  Register register_10 (
    .D(read_data_router_1_o_5), .en(read_data_router_1_e_5), .clk(clk), .Q(consumer_read_data_5),
    .clr(RESET_t));
  Register register_11 (
    .D(read_data_router_1_o_6), .en(read_data_router_1_e_6), .clk(clk), .Q(consumer_read_data_6),
    .clr(RESET_t));
  Register register_12 (
    .D(read_data_router_1_o_7), .en(read_data_router_1_e_7), .clk(clk), .Q(consumer_read_data_7),
    .clr(RESET_t));
  Multiplexer #(.width(3)) multiplexer_11 (
    .in0(3'b000), .in1(3'b101), .out(multiplexer_11_out), .sel(WRITE_WAITING_STATE_UPDATE_0));
  Multiplexer #(.width(3)) multiplexer_12 (
    .in0(multiplexer_11_out), .in1(3'b100), .out(multiplexer_12_out), .sel(READ_WAITING_STATE_UPDATE_0));
  Multiplexer #(.width(3)) multiplexer_13 (
    .in0(multiplexer_12_out), .in1(3'b011), .out(multiplexer_13_out), .sel(IDLE_TYPE_WRITE_0));
  or or_5 (or_5_out, READ_WAITING_STATE_UPDATE_0, READ_RELAYING_STATE_UPDATE_0, WRITE_RELAYING_STATE_UPDATE_0);
  Multiplexer #(.width(3)) multiplexer_14 (
    .in0(multiplexer_13_out), .in1(3'b010), .out(multiplexer_14_out), .sel(IDLE_TYPE_READ_0));
  Multiplexer #(.width(3)) multiplexer_15 (
    .in0(multiplexer_14_out), .in1(3'b000), .out(multiplexer_15_out), .sel(RESET_t));
  or or_6 (or_6_out, RESET_t, or_5_out, WRITE_WAITING_STATE_UPDATE_0, IDLE_TYPE_WRITE_0, IDLE_TYPE_READ_0);
  not not_5 (not_5_out, bitselector_5_out);
  BitSelector bitselector_5 (.in(consumer_write_valid), .out(bitselector_5_out), .sel(current_consumer_0));
  not not_6 (not_6_out, bitselector_6_out);
  BitSelector bitselector_6 (.in(consumer_write_valid), .out(bitselector_6_out), .sel(current_consumer_1));
  not not_7 (not_7_out, bitselector_7_out);
  BitSelector bitselector_7 (.in(consumer_write_valid), .out(bitselector_7_out), .sel(current_consumer_3));
  not not_8 (not_8_out, bitselector_8_out);
  BitSelector bitselector_8 (.in(consumer_write_valid), .out(bitselector_8_out), .sel(current_consumer_3));
  or or_7 (or_7_out, READ_WAITING_STATE_UPDATE_1, IDLE_TYPE_READ_1);
  or or_8 (or_8_out, READ_WAITING_STATE_UPDATE_3, IDLE_TYPE_READ_3);
  Register #(.width(3)) controller_state_reg_0 (
    .D(multiplexer_15_out), .en(or_6_out), .clk(clk), .Q(controller_state_reg_0_q), .clr(RESET_t));
  and and_14 (WRITE_RELAYING_STATE_UPDATE_0, WRITE_RELAYING_STATE_0, not_5_out);
  and and_15 (WRITE_RELAYING_STATE_UPDATE_1, WRITE_RELAYING_STATE_1, not_6_out);
  and and_16 (WRITE_RELAYING_STATE_UPDATE_2, WRITE_RELAYING_STATE_2, not_7_out);
  and and_17 (WRITE_RELAYING_STATE_UPDATE_3, WRITE_RELAYING_STATE_3, not_8_out);
  Register #(.width(3)) register_13 (
    .D(Find_READ_IDLE_TYPE_BIT_0), .en(Find_READ_IDLE_TYPE_0), .clk(clk), .Q(current_consumer_0),
    .clr(RESET_t));
  Register #(.width(3)) register_14 (
    .D(Find_READ_IDLE_TYPE_BIT_1), .en(Find_READ_IDLE_TYPE_1), .clk(clk), .Q(current_consumer_1),
    .clr(RESET_t));
  Register #(.width(3)) register_15 (
    .D(Find_READ_IDLE_TYPE_BIT_2), .en(Find_READ_IDLE_TYPE_2), .clk(clk), .Q(current_consumer_2),
    .clr(RESET_t));
  Register #(.width(3)) register_16 (
    .D(Find_READ_IDLE_TYPE_BIT_3), .en(Find_READ_IDLE_TYPE_3), .clk(clk), .Q(current_consumer_3),
    .clr(RESET_t));
  Register #(.width(1)) mem_read_valid_reg_1 (
    .D(multiplexer_16_out), .en(or_7_out), .clk(clk), .Q(mem_read_valid[1]), .clr(RESET_t));
  Multiplexer multiplexer_16 (.in0(1'b1), .in1(1'b0), .out(multiplexer_16_out), .sel(READ_WAITING_STATE_UPDATE_1));
  Multiplexer #(.select(3), .width(8)) multiplexer_17 (
    .in0(consumer_write_data_0), .in1(consumer_write_data_1), .in2(consumer_write_data_2),
    .in3(consumer_write_data_3), .in4(consumer_write_data_4), .in5(consumer_write_data_5),
    .in6(consumer_write_data_6), .in7(consumer_write_data_7), .out(multiplexer_17_out),
    .sel(Find_READ_IDLE_TYPE_BIT_1));
  Multiplexer #(.select(3), .width(8)) multiplexer_18 (
    .in0(consumer_write_address_0), .in1(consumer_write_address_1), .in2(consumer_write_address_2),
    .in3(consumer_write_address_3), .in4(consumer_write_address_4), .in5(consumer_write_address_5),
    .in6(consumer_write_address_6), .in7(consumer_write_address_7), .out(multiplexer_18_out),
    .sel(Find_READ_IDLE_TYPE_BIT_1));
  Register #(.width(1)) register_17 (
    .D(multiplexer_19_out), .en(or_8_out), .clk(clk), .Q(mem_read_valid[3]), .clr(RESET_t));
  Multiplexer multiplexer_19 (.in0(1'b1), .in1(1'b0), .out(multiplexer_19_out), .sel(READ_WAITING_STATE_UPDATE_3));
  Multiplexer #(.select(3), .width(8)) multiplexer_20 (
    .in0(consumer_write_data_0), .in1(consumer_write_data_1), .in2(consumer_write_data_2),
    .in3(consumer_write_data_3), .in4(consumer_write_data_4), .in5(consumer_write_data_5),
    .in6(consumer_write_data_6), .in7(consumer_write_data_7), .out(multiplexer_20_out),
    .sel(Find_READ_IDLE_TYPE_BIT_3));
  Multiplexer #(.select(3), .width(8)) multiplexer_21 (
    .in0(consumer_write_address_0), .in1(consumer_write_address_1), .in2(consumer_write_address_2),
    .in3(consumer_write_address_3), .in4(consumer_write_address_4), .in5(consumer_write_address_5),
    .in6(consumer_write_address_6), .in7(consumer_write_address_7), .out(multiplexer_21_out),
    .sel(Find_READ_IDLE_TYPE_BIT_3));
  not not_9 (not_9_out, RESET_t);
  Multiplexer #(.enable("true"), .select(3), .width(8)) multiplexer_22 (
    .in0(consumer_read_address_0), .in1(consumer_read_address_1), .in2(consumer_read_address_2),
    .in3(consumer_read_address_3), .in4(consumer_read_address_4), .in5(consumer_read_address_5),
    .in6(consumer_read_address_6), .in7(consumer_read_address_7), .out(multiplexer_22_out),
    .sel(Find_READ_IDLE_TYPE_BIT_1), .en(IDLE_TYPE_READ_1));
  or or_9 (or_9_out, IDLE_TYPE_WRITE_1, WRITE_RELAYING_STATE_1);
  Register register_18 (.D(multiplexer_17_out), .en(IDLE_TYPE_WRITE_1), .clk(clk), .Q(mem_write_data_1), .clr(RESET_t));
  Register register_19 (
    .D(multiplexer_18_out), .en(IDLE_TYPE_WRITE_1), .clk(clk), .Q(mem_write_address_1), .clr(RESET_t));
  Multiplexer #(.enable("true"), .select(3), .width(8)) multiplexer_23 (
    .in0(consumer_read_address_0), .in1(consumer_read_address_1), .in2(consumer_read_address_2),
    .in3(consumer_read_address_3), .in4(consumer_read_address_4), .in5(consumer_read_address_5),
    .in6(consumer_read_address_6), .in7(consumer_read_address_7), .out(multiplexer_23_out),
    .sel(Find_READ_IDLE_TYPE_BIT_3), .en(IDLE_TYPE_READ_3));
  or or_10 (or_10_out, IDLE_TYPE_WRITE_3, WRITE_RELAYING_STATE_3);
  Register register_20 (.D(multiplexer_20_out), .en(IDLE_TYPE_WRITE_3), .clk(clk), .Q(mem_write_data_3), .clr(RESET_t));
  Register register_21 (
    .D(multiplexer_21_out), .en(IDLE_TYPE_WRITE_3), .clk(clk), .Q(mem_write_address_3), .clr(RESET_t));
  Decoder #(.select(3)) decoder_1 (
    .out0(IDLE_STATE_0), .out2(READ_WAITING_STATE_0), .out3(WRITE_WAITING_STATE_0),
    .out4(READ_RELAYING_STATE_0), .out5(WRITE_RELAYING_STATE_0), .sel(controller_state_reg_0_q),
    .en(not_9_out));  // open: out1, out6, out7
  Register #(.width(1)) register_22 (
    .D(multiplexer_24_out), .en(or_9_out), .clk(clk), .Q(mem_write_valid[1]), .clr(RESET_t));
  Multiplexer multiplexer_24 (.in0(1'b1), .in1(1'b0), .out(multiplexer_24_out), .sel(WRITE_RELAYING_STATE_1));
  Register #(.width(1)) register_23 (
    .D(multiplexer_25_out), .en(or_10_out), .clk(clk), .Q(mem_write_valid[3]), .clr(RESET_t));
  Multiplexer multiplexer_25 (.in0(1'b1), .in1(1'b0), .out(multiplexer_25_out), .sel(WRITE_RELAYING_STATE_3));
  Register register_24 (
    .D(multiplexer_22_out), .en(IDLE_TYPE_READ_1), .clk(clk), .Q(mem_read_address_1), .clr(RESET_t));
  Register register_25 (
    .D(multiplexer_23_out), .en(IDLE_TYPE_READ_3), .clk(clk), .Q(mem_read_address_3), .clr(RESET_t));
  Multiplexer #(.width(3)) multiplexer_26 (
    .in0(3'b000), .in1(3'b101), .out(multiplexer_26_out), .sel(WRITE_WAITING_STATE_UPDATE_1));
  Multiplexer #(.width(3)) multiplexer_27 (
    .in0(multiplexer_26_out), .in1(3'b100), .out(multiplexer_27_out), .sel(READ_WAITING_STATE_UPDATE_1));
  Multiplexer #(.width(3)) multiplexer_28 (
    .in0(multiplexer_27_out), .in1(3'b011), .out(multiplexer_28_out), .sel(IDLE_TYPE_WRITE_1));
  or or_11 (or_11_out, READ_WAITING_STATE_UPDATE_1, READ_RELAYING_STATE_UPDATE_1, WRITE_RELAYING_STATE_UPDATE_1);
  Multiplexer #(.width(3)) multiplexer_29 (
    .in0(multiplexer_28_out), .in1(3'b010), .out(multiplexer_29_out), .sel(IDLE_TYPE_READ_1));
  or or_12 (or_12_out, RESET_t, or_11_out, WRITE_WAITING_STATE_UPDATE_1, IDLE_TYPE_WRITE_1, IDLE_TYPE_READ_1);
  or or_13 (or_13_out, READ_RELAYING_STATE_UPDATE_0, WRITE_RELAYING_STATE_UPDATE_0);
  Register #(.width(3)) controller_state_reg_1 (
    .D(multiplexer_30_out), .en(or_12_out), .clk(clk), .Q(controller_state_reg_1_q), .clr(RESET_t));
  Multiplexer #(.width(3)) multiplexer_30 (
    .in0(multiplexer_29_out), .in1(3'b000), .out(multiplexer_30_out), .sel(RESET_t));
  Multiplexer multiplexer_31 (.in0(1'b0), .in1(1'b1), .out(multiplexer_31_out), .sel(or_32_out));
  or or_14 (or_14_out, channel_sc_reg_7, or_32_out);
  Multiplexer multiplexer_32 (.in0(1'b0), .in1(1'b1), .out(multiplexer_32_out), .sel(or_33_out));
  or or_15 (or_15_out, channel_sc_reg_6, or_33_out);
  Multiplexer multiplexer_33 (.in0(1'b0), .in1(1'b1), .out(multiplexer_33_out), .sel(or_34_out));
  or or_16 (or_16_out, channel_sc_reg_5, or_34_out);
  Multiplexer multiplexer_34 (.in0(1'b0), .in1(1'b1), .out(multiplexer_34_out), .sel(or_35_out));
  or or_17 (or_17_out, channel_sc_reg_4, or_35_out);
  Multiplexer multiplexer_35 (.in0(1'b0), .in1(1'b1), .out(multiplexer_35_out), .sel(or_36_out));
  or or_18 (or_18_out, channel_sc_reg_3, or_36_out);
  Multiplexer multiplexer_36 (.in0(1'b0), .in1(1'b1), .out(multiplexer_36_out), .sel(or_37_out));
  or or_19 (or_19_out, channel_sc_reg_2, or_37_out);
  Multiplexer multiplexer_37 (.in0(1'b0), .in1(1'b1), .out(multiplexer_37_out), .sel(or_38_out));
  or or_20 (or_20_out, channel_sc_reg_1, or_38_out);
  Multiplexer multiplexer_38 (.in0(1'b0), .in1(1'b1), .out(multiplexer_38_out), .sel(or_39_out));
  or or_21 (or_21_out, channel_sc_reg_0, or_39_out);
  Register #(.width(1)) channel_serving_consumer_reg_7 (
    .D(multiplexer_31_out), .en(or_14_out), .clk(clk), .Q(channel_serving_consumer_reg_7_q), .clr(RESET_t));
  Register #(.width(1)) register_26 (
    .D(multiplexer_32_out), .en(or_15_out), .clk(clk), .Q(register_26_q), .clr(RESET_t));
  Register #(.width(1)) register_27 (
    .D(multiplexer_33_out), .en(or_16_out), .clk(clk), .Q(register_27_q), .clr(RESET_t));
  Register #(.width(1)) register_28 (
    .D(multiplexer_34_out), .en(or_17_out), .clk(clk), .Q(register_28_q), .clr(RESET_t));
  Register #(.width(1)) register_29 (
    .D(multiplexer_35_out), .en(or_18_out), .clk(clk), .Q(register_29_q), .clr(RESET_t));
  Register #(.width(1)) register_30 (
    .D(multiplexer_36_out), .en(or_19_out), .clk(clk), .Q(register_30_q), .clr(RESET_t));
  Register #(.width(1)) register_31 (
    .D(multiplexer_37_out), .en(or_20_out), .clk(clk), .Q(register_31_q), .clr(RESET_t));
  Register #(.width(1)) register_32 (
    .D(multiplexer_38_out), .en(or_21_out), .clk(clk), .Q(register_32_q), .clr(RESET_t));
  not not_10 (not_10_out, RESET_t);
  Decoder #(.select(3)) decoder_2 (
    .out0(IDLE_STATE_1), .out2(READ_WAITING_STATE_1), .out3(WRITE_WAITING_STATE_1),
    .out4(READ_RELAYING_STATE_1), .out5(WRITE_RELAYING_STATE_1), .sel(controller_state_reg_1_q),
    .en(not_10_out));  // open: out1, out6, out7
  not not_11 (not_11_out, channel_serving_consumer_reg_7_q);
  not not_12 (not_12_out, register_26_q);
  not not_13 (not_13_out, register_27_q);
  not not_14 (not_14_out, register_28_q);
  not not_15 (not_15_out, register_29_q);
  not not_16 (not_16_out, register_30_q);
  not not_17 (not_17_out, register_31_q);
  not not_18 (not_18_out, register_32_q);
  Decoder #(.select(3)) decoder_3 (
    .out0(decoder_3_out0), .out1(decoder_3_out1), .out2(decoder_3_out2), .out3(decoder_3_out3),
    .out4(decoder_3_out4), .out5(decoder_3_out5), .out6(decoder_3_out6), .out7(decoder_3_out7),
    .sel(current_consumer_0), .en(or_13_out));
  or or_22 (or_22_out, READ_RELAYING_STATE_UPDATE_1, WRITE_RELAYING_STATE_UPDATE_1);
  Decoder #(.select(3)) decoder_4 (
    .out0(decoder_4_out0), .out1(decoder_4_out1), .out2(decoder_4_out2), .out3(decoder_4_out3),
    .out4(decoder_4_out4), .out5(decoder_4_out5), .out6(decoder_4_out6), .out7(decoder_4_out7),
    .sel(current_consumer_1), .en(or_22_out));
  or or_23 (or_23_out, consumer_write_valid[7], consumer_read_valid[7]);
  or or_24 (or_24_out, consumer_write_valid[6], consumer_read_valid[6]);
  or or_25 (or_25_out, consumer_write_valid[5], consumer_read_valid[5]);
  or or_26 (or_26_out, consumer_write_valid[4], consumer_read_valid[4]);
  or or_27 (or_27_out, consumer_write_valid[3], consumer_read_valid[3]);
  or or_28 (or_28_out, consumer_write_valid[2], consumer_read_valid[2]);
  or or_29 (or_29_out, consumer_write_valid[1], consumer_read_valid[1]);
  or or_30 (or_30_out, consumer_write_valid[0], consumer_read_valid[0]);
  or or_31 (or_31_out, READ_RELAYING_STATE_UPDATE_2, WRITE_RELAYING_STATE_UPDATE_2);
  Decoder #(.select(3)) decoder_5 (
    .out0(decoder_5_out0), .out1(decoder_5_out1), .out2(decoder_5_out2), .out3(decoder_5_out3),
    .out4(decoder_5_out4), .out5(decoder_5_out5), .out6(decoder_5_out6), .out7(decoder_5_out7),
    .sel(current_consumer_2), .en(or_31_out));
  Multiplexer #(.width(3)) multiplexer_39 (
    .in0(3'b000), .in1(3'b101), .out(multiplexer_39_out), .sel(WRITE_WAITING_STATE_UPDATE_2));
  or or_32 (or_32_out, and_32_out[7], and_63_out[7], and_86_out[7], and_109_out[7]);
  or or_33 (or_33_out, and_32_out[6], and_63_out[6], and_86_out[6], and_109_out[6]);
  or or_34 (or_34_out, and_32_out[5], and_63_out[5], and_86_out[5], and_109_out[5]);
  or or_35 (or_35_out, and_32_out[4], and_63_out[4], and_86_out[4], and_109_out[4]);
  or or_36 (or_36_out, and_32_out[3], and_63_out[3], and_86_out[3], and_109_out[3]);
  or or_37 (or_37_out, and_32_out[2], and_63_out[2], and_86_out[2], and_109_out[2]);
  or or_38 (or_38_out, and_32_out[1], and_63_out[1], and_86_out[1], and_109_out[1]);
  or or_39 (or_39_out, and_32_out[0], and_63_out[0], and_86_out[0], and_109_out[0]);
  or or_40 (or_40_out, READ_RELAYING_STATE_UPDATE_3, WRITE_RELAYING_STATE_UPDATE_3);
  Decoder #(.select(3)) decoder_6 (
    .out0(decoder_6_out0), .out1(decoder_6_out1), .out2(decoder_6_out2), .out3(decoder_6_out3),
    .out4(decoder_6_out4), .out5(decoder_6_out5), .out6(decoder_6_out6), .out7(decoder_6_out7),
    .sel(current_consumer_3), .en(or_40_out));
  Multiplexer #(.width(3)) multiplexer_40 (
    .in0(multiplexer_39_out), .in1(3'b100), .out(multiplexer_40_out), .sel(READ_WAITING_STATE_UPDATE_2));
  Multiplexer #(.width(3)) multiplexer_41 (
    .in0(multiplexer_40_out), .in1(3'b011), .out(multiplexer_41_out), .sel(IDLE_TYPE_WRITE_2));
  or or_41 (or_41_out, READ_WAITING_STATE_UPDATE_2, READ_RELAYING_STATE_UPDATE_2, WRITE_RELAYING_STATE_UPDATE_2);
  or or_42 (or_42_out, decoder_6_out7, decoder_5_out7, decoder_4_out7, decoder_3_out7);
  or or_43 (or_43_out, decoder_6_out6, decoder_5_out6, decoder_4_out6, decoder_3_out6);
  or or_44 (or_44_out, decoder_6_out5, decoder_5_out5, decoder_4_out5, decoder_3_out5);
  or or_45 (or_45_out, decoder_6_out4, decoder_5_out4, decoder_4_out4, decoder_3_out4);
  or or_46 (or_46_out, decoder_6_out3, decoder_5_out3, decoder_4_out3, decoder_3_out3);
  or or_47 (or_47_out, decoder_6_out2, decoder_5_out2, decoder_4_out2, decoder_3_out2);
  or or_48 (or_48_out, decoder_6_out1, decoder_5_out1, decoder_4_out1, decoder_3_out1);
  or or_49 (or_49_out, decoder_6_out0, decoder_5_out0, decoder_4_out0, decoder_3_out0);
  not not_19 (not_19_out, consumer_read_valid[7]);
  not not_20 (not_20_out, consumer_read_valid[6]);
  WR_WAITING_MERGER_CC_ENABLE wr_waiting_merger_cc_enable_1 (
    .e0(WRITE_WAITING_STATE_UPDATE_0), .e1(WRITE_WAITING_STATE_UPDATE_1), .e2(WRITE_WAITING_STATE_UPDATE_2),
    .e3(WRITE_WAITING_STATE_UPDATE_3), .i0(current_consumer_0), .i1(current_consumer_1),
    .i2(current_consumer_2), .i3(current_consumer_3), .v0(channel_sc_reg_0), .v1(channel_sc_reg_1),
    .v2(channel_sc_reg_2), .v3(channel_sc_reg_3), .v4(channel_sc_reg_4), .v5(channel_sc_reg_5),
    .v6(channel_sc_reg_6), .v7(channel_sc_reg_7), .c0(WRITE_RELAYING_STATE_UPDATE_0),
    .c1(WRITE_RELAYING_STATE_UPDATE_1), .c2(WRITE_RELAYING_STATE_UPDATE_2),
    .c3(WRITE_RELAYING_STATE_UPDATE_3), .o7(wr_waiting_merger_cc_enable_1_o7),
    .o6(wr_waiting_merger_cc_enable_1_o6), .o5(wr_waiting_merger_cc_enable_1_o5),
    .o4(wr_waiting_merger_cc_enable_1_o4), .o3(wr_waiting_merger_cc_enable_1_o3),
    .o2(wr_waiting_merger_cc_enable_1_o2), .o1(wr_waiting_merger_cc_enable_1_o1),
    .o0(wr_waiting_merger_cc_enable_1_o0), .on7(wr_waiting_merger_cc_enable_1_on7),
    .on6(wr_waiting_merger_cc_enable_1_on6), .on5(wr_waiting_merger_cc_enable_1_on5),
    .on4(wr_waiting_merger_cc_enable_1_on4), .on3(wr_waiting_merger_cc_enable_1_on3),
    .on2(wr_waiting_merger_cc_enable_1_on2), .on1(wr_waiting_merger_cc_enable_1_on1),
    .on0(wr_waiting_merger_cc_enable_1_on0));
  Multiplexer #(.width(3)) multiplexer_42 (
    .in0(multiplexer_41_out), .in1(3'b010), .out(multiplexer_42_out), .sel(IDLE_TYPE_READ_2));
  or or_50 (or_50_out, RESET_t, or_41_out, WRITE_WAITING_STATE_UPDATE_2, IDLE_TYPE_WRITE_2, IDLE_TYPE_READ_2);
  and and_18 (and_32_out[7], IDLE_STATE_0, or_23_out, not_11_out);
  not not_21 (not_21_out, and_32_out[7]);
  and and_19 (and_19_out, IDLE_STATE_0, not_21_out);
  not not_22 (not_22_out, and_32_out[6]);
  and and_20 (and_32_out[6], and_19_out, or_24_out, not_12_out);
  not not_23 (not_23_out, and_32_out[6]);
  and and_21 (and_21_out, and_19_out, not_23_out);
  not not_24 (not_24_out, and_32_out[5]);
  and and_22 (and_32_out[5], and_21_out, or_25_out, not_13_out);
  not not_25 (not_25_out, and_32_out[5]);
  and and_23 (and_23_out, and_21_out, not_25_out);
  not not_26 (not_26_out, and_32_out[4]);
  and and_24 (and_32_out[4], and_23_out, or_26_out, not_14_out);
  not not_27 (not_27_out, and_32_out[4]);
  and and_25 (and_25_out, and_23_out, not_27_out);
  not not_28 (not_28_out, and_32_out[3]);
  and and_26 (and_32_out[3], and_25_out, or_27_out, not_15_out);
  not not_29 (not_29_out, and_32_out[3]);
  and and_27 (and_27_out, and_25_out, not_29_out);
  not not_30 (not_30_out, and_32_out[2]);
  and and_28 (and_32_out[2], and_27_out, or_28_out, not_16_out);
  not not_31 (not_31_out, and_63_out[2]);
  and and_29 (and_29_out, and_27_out, not_31_out);
  and and_30 (and_32_out[1], and_29_out, or_29_out, not_17_out);
  not not_32 (not_32_out, and_32_out[1]);
  and and_31 (and_31_out, and_29_out, not_32_out);
  and and_32 (and_32_out[0], and_31_out, or_30_out, not_18_out);
  BitFinder bitfinder_1 (.in(and_32_out), .index(Find_READ_IDLE_TYPE_BIT_0), .found(Find_READ_IDLE_TYPE_0));
  not not_33 (not_33_out, consumer_read_valid[5]);
  not not_34 (not_34_out, consumer_read_valid[4]);
  not not_35 (not_35_out, consumer_read_valid[3]);
  not not_36 (not_36_out, consumer_read_valid[2]);
  not not_37 (not_37_out, consumer_read_valid[1]);
  not not_38 (not_38_out, consumer_read_valid[0]);
  not not_39 (not_39_out, consumer_write_valid[7]);
  not not_40 (not_40_out, consumer_write_valid[6]);
  WR_WAITING_MERGER_CC_ENABLE wr_waiting_merger_cc_enable_2 (
    .e0(READ_WAITING_STATE_UPDATE_0), .e1(READ_WAITING_STATE_UPDATE_1), .e2(READ_WAITING_STATE_UPDATE_2),
    .e3(READ_WAITING_STATE_UPDATE_3), .i0(current_consumer_0), .i1(current_consumer_1),
    .i2(current_consumer_2), .i3(current_consumer_3), .v0(channel_sc_reg_0), .v1(channel_sc_reg_1),
    .v2(channel_sc_reg_2), .v3(channel_sc_reg_3), .v4(channel_sc_reg_4), .v5(channel_sc_reg_5),
    .v6(channel_sc_reg_6), .v7(channel_sc_reg_7), .c0(READ_RELAYING_STATE_UPDATE_0),
    .c1(READ_RELAYING_STATE_UPDATE_1), .c2(READ_RELAYING_STATE_UPDATE_2), .c3(READ_RELAYING_STATE_UPDATE_3),
    .o7(wr_waiting_merger_cc_enable_2_o7), .o6(wr_waiting_merger_cc_enable_2_o6),
    .o5(wr_waiting_merger_cc_enable_2_o5), .o4(wr_waiting_merger_cc_enable_2_o4),
    .o3(wr_waiting_merger_cc_enable_2_o3), .o2(wr_waiting_merger_cc_enable_2_o2),
    .o1(wr_waiting_merger_cc_enable_2_o1), .o0(wr_waiting_merger_cc_enable_2_o0),
    .on7(wr_waiting_merger_cc_enable_2_on7), .on6(wr_waiting_merger_cc_enable_2_on6),
    .on5(wr_waiting_merger_cc_enable_2_on5), .on4(wr_waiting_merger_cc_enable_2_on4),
    .on3(wr_waiting_merger_cc_enable_2_on3), .on2(wr_waiting_merger_cc_enable_2_on2),
    .on1(wr_waiting_merger_cc_enable_2_on1), .on0(wr_waiting_merger_cc_enable_2_on0));
  Register #(.width(3)) register_33 (
    .D(multiplexer_43_out), .en(or_50_out), .clk(clk), .Q(register_33_q), .clr(RESET_t));
  Multiplexer #(.width(3)) multiplexer_43 (
    .in0(multiplexer_42_out), .in1(3'b000), .out(multiplexer_43_out), .sel(RESET_t));
  and and_33 (and_33_out, or_23_out, not_41_out);
  not not_41 (not_41_out, and_32_out[7]);
  and and_34 (and_34_out, or_24_out, not_22_out);
  and and_35 (and_35_out, or_25_out, not_24_out);
  and and_36 (and_36_out, or_26_out, not_26_out);
  and and_37 (and_37_out, or_27_out, not_28_out);
  and and_38 (and_38_out, or_28_out, not_30_out);
  and and_39 (and_39_out, or_29_out, not_42_out);
  not not_42 (not_42_out, and_32_out[1]);
  and and_40 (and_40_out, or_30_out, not_43_out);
  not not_43 (not_43_out, and_32_out[0]);
  not not_44 (not_44_out, consumer_write_valid[5]);
  not not_45 (not_45_out, consumer_write_valid[4]);
  not not_46 (not_46_out, consumer_write_valid[3]);
  not not_47 (not_47_out, consumer_write_valid[2]);
  not not_48 (not_48_out, consumer_write_valid[1]);
  not not_49 (not_49_out, consumer_write_valid[0]);
  or or_51 (or_51_out, not_19_out, not_39_out);
  and and_41 (channel_sc_reg_7, or_51_out, or_42_out);
  or or_52 (or_52_out, not_20_out, not_40_out);
  and and_42 (channel_sc_reg_6, or_52_out, or_43_out);
  or or_53 (or_53_out, not_33_out, not_44_out);
  and and_43 (channel_sc_reg_5, or_53_out, or_44_out);
  or or_54 (or_54_out, not_34_out, not_45_out);
  and and_44 (channel_sc_reg_4, or_54_out, or_45_out);
  or or_55 (or_55_out, not_35_out, not_46_out);
  and and_45 (channel_sc_reg_3, or_55_out, or_46_out);
  or or_56 (or_56_out, not_36_out, not_47_out);
  and and_46 (channel_sc_reg_2, or_56_out, or_47_out);
  or or_57 (or_57_out, not_37_out, not_48_out);
  and and_47 (channel_sc_reg_1, or_57_out, or_48_out);
  or or_58 (or_58_out, not_38_out, not_49_out);
  and and_48 (channel_sc_reg_0, or_58_out, or_49_out);
  not not_50 (not_50_out, RESET_t);
  Decoder #(.select(3)) decoder_7 (
    .out0(IDLE_STATE_2), .out2(READ_WAITING_STATE_2), .out3(WRITE_WAITING_STATE_2),
    .out4(READ_RELAYING_STATE_2), .out5(WRITE_RELAYING_STATE_2), .sel(register_33_q), .en(not_50_out));  // open: out1, out6, out7
  and and_49 (and_63_out[7], IDLE_STATE_1, and_33_out, not_11_out);
  not not_51 (not_51_out, and_63_out[7]);
  and and_50 (and_50_out, IDLE_STATE_1, not_51_out);
  not not_52 (not_52_out, and_63_out[6]);
  and and_51 (and_63_out[6], and_50_out, and_34_out, not_12_out);
  not not_53 (not_53_out, and_63_out[6]);
  and and_52 (and_52_out, and_50_out, not_53_out);
  not not_54 (not_54_out, and_63_out[5]);
  and and_53 (and_63_out[5], and_52_out, and_35_out, not_13_out);
  not not_55 (not_55_out, and_63_out[5]);
  and and_54 (and_54_out, and_52_out, not_55_out);
  not not_56 (not_56_out, and_63_out[4]);
  and and_55 (and_63_out[4], and_54_out, and_36_out, not_14_out);
  not not_57 (not_57_out, and_63_out[4]);
  and and_56 (and_56_out, and_54_out, not_57_out);
  not not_58 (not_58_out, and_63_out[3]);
  and and_57 (and_63_out[3], and_56_out, and_37_out, not_15_out);
  not not_59 (not_59_out, and_63_out[3]);
  and and_58 (and_58_out, and_56_out, not_59_out);
  not not_60 (not_60_out, and_63_out[2]);
  and and_59 (and_63_out[2], and_58_out, and_38_out, not_16_out);
  not not_61 (not_61_out, and_63_out[2]);
  and and_60 (and_60_out, and_58_out, not_61_out);
  not not_62 (not_62_out, and_63_out[1]);
  and and_61 (and_63_out[1], and_60_out, and_39_out, not_17_out);
  not not_63 (not_63_out, and_63_out[1]);
  and and_62 (and_62_out, and_60_out, not_63_out);
  not not_64 (not_64_out, and_63_out[0]);
  and and_63 (and_63_out[0], and_62_out, and_40_out, not_18_out);
  BitFinder bitfinder_2 (.in(and_63_out), .index(Find_READ_IDLE_TYPE_BIT_1), .found(Find_READ_IDLE_TYPE_1));
  Register #(.width(1)) consumer_write_ready_reg_0 (
    .D(wr_waiting_merger_cc_enable_1_on7), .en(wr_waiting_merger_cc_enable_1_o7), .clk(clk),
    .Q(consumer_write_ready[7]), .clr(RESET_t));
  Register #(.width(1)) register_34 (
    .D(wr_waiting_merger_cc_enable_1_on6), .en(wr_waiting_merger_cc_enable_1_o6), .clk(clk),
    .Q(consumer_write_ready[6]), .clr(RESET_t));
  Register #(.width(1)) register_35 (
    .D(wr_waiting_merger_cc_enable_1_on5), .en(wr_waiting_merger_cc_enable_1_o5), .clk(clk),
    .Q(consumer_write_ready[5]), .clr(RESET_t));
  Register #(.width(1)) register_36 (
    .D(wr_waiting_merger_cc_enable_1_on4), .en(wr_waiting_merger_cc_enable_1_o4), .clk(clk),
    .Q(consumer_write_ready[4]), .clr(RESET_t));
  Register #(.width(1)) register_37 (
    .D(wr_waiting_merger_cc_enable_1_on3), .en(wr_waiting_merger_cc_enable_1_o3), .clk(clk),
    .Q(consumer_write_ready[3]), .clr(RESET_t));
  Register #(.width(1)) register_38 (
    .D(wr_waiting_merger_cc_enable_1_on2), .en(wr_waiting_merger_cc_enable_1_o2), .clk(clk),
    .Q(consumer_write_ready[2]), .clr(RESET_t));
  Register #(.width(1)) register_39 (
    .D(wr_waiting_merger_cc_enable_1_on1), .en(wr_waiting_merger_cc_enable_1_o1), .clk(clk),
    .Q(consumer_write_ready[1]), .clr(RESET_t));
  Register #(.width(1)) register_40 (
    .D(wr_waiting_merger_cc_enable_1_on0), .en(wr_waiting_merger_cc_enable_1_o0), .clk(clk),
    .Q(consumer_write_ready[0]), .clr(RESET_t));
  Register #(.width(1)) register_41 (
    .D(wr_waiting_merger_cc_enable_2_on7), .en(wr_waiting_merger_cc_enable_2_o7), .clk(clk),
    .Q(consumer_read_ready[7]), .clr(RESET_t));
  Register #(.width(1)) register_42 (
    .D(wr_waiting_merger_cc_enable_2_on6), .en(wr_waiting_merger_cc_enable_2_o6), .clk(clk),
    .Q(consumer_read_ready[6]), .clr(RESET_t));
  Register #(.width(1)) register_43 (
    .D(wr_waiting_merger_cc_enable_2_on5), .en(wr_waiting_merger_cc_enable_2_o5), .clk(clk),
    .Q(consumer_read_ready[5]), .clr(RESET_t));
  Register #(.width(1)) register_44 (
    .D(wr_waiting_merger_cc_enable_2_on4), .en(wr_waiting_merger_cc_enable_2_o4), .clk(clk),
    .Q(consumer_read_ready[4]), .clr(RESET_t));
  Register #(.width(1)) register_45 (
    .D(wr_waiting_merger_cc_enable_2_on3), .en(wr_waiting_merger_cc_enable_2_o3), .clk(clk),
    .Q(consumer_read_ready[3]), .clr(RESET_t));
  Register #(.width(1)) register_46 (
    .D(wr_waiting_merger_cc_enable_2_on2), .en(wr_waiting_merger_cc_enable_2_o2), .clk(clk),
    .Q(consumer_read_ready[2]), .clr(RESET_t));
  Register #(.width(1)) register_47 (
    .D(wr_waiting_merger_cc_enable_2_on1), .en(wr_waiting_merger_cc_enable_2_o1), .clk(clk),
    .Q(consumer_read_ready[1]), .clr(RESET_t));
  Register #(.width(1)) register_48 (
    .D(wr_waiting_merger_cc_enable_2_on0), .en(wr_waiting_merger_cc_enable_2_o0), .clk(clk),
    .Q(consumer_read_ready[0]), .clr(RESET_t));
  and and_64 (and_64_out, and_33_out, not_65_out);
  not not_65 (not_65_out, and_63_out[7]);
  and and_65 (and_86_out[7], IDLE_STATE_2, and_64_out, not_11_out);
  not not_66 (not_66_out, and_86_out[7]);
  and and_66 (and_66_out, IDLE_STATE_2, not_66_out);
  and and_67 (and_67_out, and_34_out, not_52_out);
  and and_68 (and_86_out[6], and_66_out, and_67_out, not_12_out);
  not not_67 (not_67_out, and_86_out[6]);
  and and_69 (and_69_out, and_66_out, not_67_out);
  and and_70 (and_70_out, and_35_out, not_54_out);
  and and_71 (and_86_out[5], and_69_out, and_70_out, not_13_out);
  not not_68 (not_68_out, and_86_out[5]);
  and and_72 (and_72_out, and_69_out, not_68_out);
  and and_73 (and_73_out, and_36_out, not_56_out);
  and and_74 (and_86_out[4], and_72_out, and_73_out, not_14_out);
  not not_69 (not_69_out, and_86_out[4]);
  and and_75 (and_75_out, and_72_out, not_69_out);
  and and_76 (and_76_out, and_37_out, not_58_out);
  and and_77 (and_86_out[3], and_75_out, and_76_out, not_15_out);
  not not_70 (not_70_out, and_86_out[3]);
  and and_78 (and_78_out, and_75_out, not_70_out);
  and and_79 (and_79_out, and_38_out, not_60_out);
  and and_80 (and_86_out[2], and_78_out, and_79_out, not_16_out);
  not not_71 (not_71_out, and_86_out[2]);
  and and_81 (and_81_out, and_78_out, not_71_out);
  and and_82 (and_82_out, and_39_out, not_62_out);
  and and_83 (and_86_out[1], and_81_out, and_82_out, not_17_out);
  not not_72 (not_72_out, and_86_out[1]);
  and and_84 (and_84_out, and_81_out, not_72_out);
  and and_85 (and_85_out, and_40_out, not_64_out);
  and and_86 (and_86_out[0], and_84_out, and_85_out, not_18_out);
  BitFinder bitfinder_3 (.in(and_86_out), .index(Find_READ_IDLE_TYPE_BIT_2), .found(Find_READ_IDLE_TYPE_2));
  not not_73 (not_73_out, and_86_out[6]);
  not not_74 (not_74_out, and_86_out[5]);
  not not_75 (not_75_out, and_86_out[4]);
  not not_76 (not_76_out, and_86_out[3]);
  not not_77 (not_77_out, and_86_out[2]);
  not not_78 (not_78_out, and_86_out[1]);
  not not_79 (not_79_out, and_86_out[0]);
  and and_87 (and_87_out, and_64_out, not_80_out);
  not not_80 (not_80_out, and_86_out[7]);
  and and_88 (and_88_out, and_67_out, not_73_out);
  and and_89 (and_89_out, and_70_out, not_74_out);
  and and_90 (and_90_out, and_73_out, not_75_out);
  and and_91 (and_91_out, and_76_out, not_76_out);
  and and_92 (and_92_out, and_79_out, not_77_out);
  and and_93 (and_93_out, and_82_out, not_78_out);
  and and_94 (and_94_out, and_85_out, not_79_out);
  Multiplexer #(.width(3)) multiplexer_44 (
    .in0(3'b000), .in1(3'b101), .out(multiplexer_44_out), .sel(WRITE_WAITING_STATE_UPDATE_3));
  Multiplexer #(.width(3)) multiplexer_45 (
    .in0(multiplexer_44_out), .in1(3'b100), .out(multiplexer_45_out), .sel(READ_WAITING_STATE_UPDATE_3));
  and and_95 (and_109_out[7], IDLE_STATE_3, and_87_out, not_11_out);
  not not_81 (not_81_out, and_109_out[7]);
  and and_96 (and_96_out, IDLE_STATE_3, not_81_out);
  and and_97 (and_109_out[6], and_96_out, and_88_out, not_12_out);
  not not_82 (not_82_out, and_109_out[6]);
  and and_98 (and_98_out, and_96_out, not_82_out);
  and and_99 (and_109_out[5], and_98_out, and_89_out, not_13_out);
  not not_83 (not_83_out, and_109_out[5]);
  and and_100 (and_100_out, and_98_out, not_83_out);
  and and_101 (and_109_out[4], and_100_out, and_90_out, not_14_out);
  not not_84 (not_84_out, and_109_out[4]);
  and and_102 (and_102_out, and_100_out, not_84_out);
  and and_103 (and_109_out[3], and_102_out, and_91_out, not_15_out);
  not not_85 (not_85_out, and_109_out[3]);
  and and_104 (and_104_out, and_102_out, not_85_out);
  and and_105 (and_109_out[2], and_104_out, and_92_out, not_16_out);
  not not_86 (not_86_out, and_109_out[2]);
  and and_106 (and_106_out, and_104_out, not_86_out);
  and and_107 (and_109_out[1], and_106_out, and_93_out, not_17_out);
  not not_87 (not_87_out, and_109_out[1]);
  and and_108 (and_108_out, and_106_out, not_87_out);
  and and_109 (and_109_out[0], and_108_out, and_94_out, not_18_out);
  BitFinder bitfinder_4 (.in(and_109_out), .index(Find_READ_IDLE_TYPE_BIT_3), .found(Find_READ_IDLE_TYPE_3));
  Multiplexer #(.width(3)) multiplexer_46 (
    .in0(multiplexer_45_out), .in1(3'b011), .out(multiplexer_46_out), .sel(IDLE_TYPE_WRITE_3));
  or or_59 (or_59_out, READ_WAITING_STATE_UPDATE_3, READ_RELAYING_STATE_UPDATE_3, WRITE_RELAYING_STATE_UPDATE_3);
  Multiplexer #(.width(3)) multiplexer_47 (
    .in0(multiplexer_46_out), .in1(3'b010), .out(multiplexer_47_out), .sel(IDLE_TYPE_READ_3));
  Multiplexer #(.width(3)) multiplexer_48 (
    .in0(multiplexer_47_out), .in1(3'b000), .out(multiplexer_48_out), .sel(RESET_t));
  or or_60 (or_60_out, RESET_t, or_59_out, WRITE_WAITING_STATE_UPDATE_3, IDLE_TYPE_WRITE_3, IDLE_TYPE_READ_3);
  Register #(.width(3)) register_49 (
    .D(multiplexer_48_out), .en(or_60_out), .clk(clk), .Q(register_49_q), .clr(RESET_t));
  not not_88 (not_88_out, RESET_t);
  Decoder #(.select(3)) decoder_8 (
    .out0(IDLE_STATE_3), .out2(READ_WAITING_STATE_3), .out3(WRITE_WAITING_STATE_3),
    .out4(READ_RELAYING_STATE_3), .out5(WRITE_RELAYING_STATE_3), .sel(register_49_q), .en(not_88_out));  // open: out1, out6, out7
  BitSelector bitselector_9 (.in(consumer_read_valid), .out(bitselector_9_out), .sel(Find_READ_IDLE_TYPE_BIT_0));
  BitSelector bitselector_10 (.in(consumer_read_valid), .out(bitselector_10_out), .sel(Find_READ_IDLE_TYPE_BIT_1));
  BitSelector bitselector_11 (.in(consumer_read_valid), .out(bitselector_11_out), .sel(Find_READ_IDLE_TYPE_BIT_2));
  BitSelector bitselector_12 (.in(consumer_read_valid), .out(bitselector_12_out), .sel(Find_READ_IDLE_TYPE_BIT_3));
  not not_89 (not_89_out, IDLE_TYPE_READ_0);
  and and_110 (IDLE_TYPE_READ_0, Find_READ_IDLE_TYPE_0, bitselector_9_out);
  not not_90 (not_90_out, IDLE_TYPE_READ_1);
  and and_111 (IDLE_TYPE_READ_1, Find_READ_IDLE_TYPE_1, bitselector_10_out);
  not not_91 (not_91_out, IDLE_TYPE_READ_2);
  and and_112 (IDLE_TYPE_READ_2, Find_READ_IDLE_TYPE_2, bitselector_11_out);
  not not_92 (not_92_out, IDLE_TYPE_READ_3);
  and and_113 (IDLE_TYPE_READ_3, Find_READ_IDLE_TYPE_3, bitselector_12_out);
  and and_114 (IDLE_TYPE_WRITE_0, Find_READ_IDLE_TYPE_0, not_89_out);
  and and_115 (IDLE_TYPE_WRITE_1, Find_READ_IDLE_TYPE_1, not_90_out);
  and and_116 (IDLE_TYPE_WRITE_2, Find_READ_IDLE_TYPE_2, not_91_out);
  and and_117 (IDLE_TYPE_WRITE_3, Find_READ_IDLE_TYPE_3, not_92_out);

  // Other names for the same wires on the sheet: mem_read_valid_0 = mem_read_valid[0];
  //   mem_read_valid_1 = mem_read_valid[1]; mem_read_valid_2 = mem_read_valid[2];
  //   mem_read_valid_3 = mem_read_valid[3]; mem_write_valid_0 = mem_write_valid[0];
  //   mem_write_valid_1 = mem_write_valid[1]; mem_write_valid_2 = mem_write_valid[2];
  //   mem_write_valid_3 = mem_write_valid[3]
endmodule

module CHECK_TARGET_WRITE_ENABLE (
  input  ENABLE,
  input  [2:0] CHECK,
  input  [7:0] W,
  output READ_ENABLE,
  output WRITE_ENABLE
);

  wire and_1_out, and_2_out, and_3_out, and_4_out, and_5_out, and_6_out, and_7_out, and_8_out,
       decoder_1_out0, decoder_1_out1, decoder_1_out2, decoder_1_out3, decoder_1_out4, decoder_1_out5,
       decoder_1_out6, decoder_1_out7, not_1_out;

  Decoder #(.select(3)) decoder_1 (
    .out0(decoder_1_out0), .out1(decoder_1_out1), .out2(decoder_1_out2), .out3(decoder_1_out3),
    .out4(decoder_1_out4), .out5(decoder_1_out5), .out6(decoder_1_out6), .out7(decoder_1_out7), .sel(CHECK),
    .en(ENABLE));
  and and_1 (and_1_out, W[0], decoder_1_out0);
  and and_2 (and_2_out, W[1], decoder_1_out1);
  and and_3 (and_3_out, W[2], decoder_1_out2);
  and and_4 (and_4_out, W[3], decoder_1_out3);
  and and_5 (and_5_out, W[4], decoder_1_out4);
  and and_6 (and_6_out, W[5], decoder_1_out5);
  and and_7 (and_7_out, W[6], decoder_1_out6);
  and and_8 (and_8_out, W[7], decoder_1_out7);
  or or_1 (WRITE_ENABLE, and_1_out, and_2_out, and_3_out, and_4_out, and_5_out, and_6_out, and_7_out, and_8_out);
  not not_1 (not_1_out, WRITE_ENABLE);
  and and_9 (READ_ENABLE, ENABLE, not_1_out);
endmodule

module WR_WAITING_MERGER_CC_ENABLE (
  input  e0,
  input  e1,
  input  e2,
  input  e3,
  input  [2:0] i0,
  input  [2:0] i1,
  input  [2:0] i2,
  input  [2:0] i3,
  input  v0,
  input  v1,
  input  v2,
  input  v3,
  input  v4,
  input  v5,
  input  v6,
  input  v7,
  input  c0,
  input  c1,
  input  c2,
  input  c3,
  output o7,
  output o6,
  output o5,
  output o4,
  output o3,
  output o2,
  output o1,
  output o0,
  output on7,
  output on6,
  output on5,
  output on4,
  output on3,
  output on2,
  output on1,
  output on0
);

  wire and_1_out, and_2_out, and_3_out, and_4_out, and_5_out, and_6_out, and_7_out, and_8_out,
       decoder_1_out0, decoder_1_out1, decoder_1_out2, decoder_1_out3, decoder_1_out4, decoder_1_out5,
       decoder_1_out6, decoder_1_out7, decoder_2_out0, decoder_2_out1, decoder_2_out2, decoder_2_out3,
       decoder_2_out4, decoder_2_out5, decoder_2_out6, decoder_2_out7, decoder_3_out0, decoder_3_out1,
       decoder_3_out2, decoder_3_out3, decoder_3_out4, decoder_3_out5, decoder_3_out6, decoder_3_out7,
       decoder_4_out0, decoder_4_out1, decoder_4_out2, decoder_4_out3, decoder_4_out4, decoder_4_out5,
       decoder_4_out6, decoder_4_out7, or_9_out;

  Decoder #(.select(3)) decoder_1 (
    .out0(decoder_1_out0), .out1(decoder_1_out1), .out2(decoder_1_out2), .out3(decoder_1_out3),
    .out4(decoder_1_out4), .out5(decoder_1_out5), .out6(decoder_1_out6), .out7(decoder_1_out7), .sel(i0),
    .en(e0));
  Decoder #(.select(3)) decoder_2 (
    .out0(decoder_2_out0), .out1(decoder_2_out1), .out2(decoder_2_out2), .out3(decoder_2_out3),
    .out4(decoder_2_out4), .out5(decoder_2_out5), .out6(decoder_2_out6), .out7(decoder_2_out7), .sel(i1),
    .en(e1));
  Decoder #(.select(3)) decoder_3 (
    .out0(decoder_3_out0), .out1(decoder_3_out1), .out2(decoder_3_out2), .out3(decoder_3_out3),
    .out4(decoder_3_out4), .out5(decoder_3_out5), .out6(decoder_3_out6), .out7(decoder_3_out7), .sel(i2),
    .en(e2));
  Decoder #(.select(3)) decoder_4 (
    .out0(decoder_4_out0), .out1(decoder_4_out1), .out2(decoder_4_out2), .out3(decoder_4_out3),
    .out4(decoder_4_out4), .out5(decoder_4_out5), .out6(decoder_4_out6), .out7(decoder_4_out7), .sel(i3),
    .en(e3));
  or or_1 (on7, decoder_4_out7, decoder_3_out7, decoder_2_out7, decoder_1_out7);
  or or_2 (on6, decoder_4_out6, decoder_3_out6, decoder_2_out6, decoder_1_out6);
  or or_3 (on5, decoder_4_out5, decoder_3_out5, decoder_2_out5, decoder_1_out5);
  or or_4 (on4, decoder_4_out4, decoder_3_out4, decoder_2_out4, decoder_1_out4);
  or or_5 (on3, decoder_4_out3, decoder_3_out3, decoder_2_out3, decoder_1_out3);
  or or_6 (on2, decoder_4_out2, decoder_3_out2, decoder_2_out2, decoder_1_out2);
  or or_7 (on1, decoder_4_out1, decoder_3_out1, decoder_2_out1, decoder_1_out1);
  or or_8 (on0, decoder_4_out0, decoder_3_out0, decoder_2_out0, decoder_1_out0);
  or or_9 (or_9_out, c0, c1, c2, c3);
  and and_1 (and_1_out, v7, or_9_out);
  and and_2 (and_2_out, v6, or_9_out);
  and and_3 (and_3_out, v5, or_9_out);
  and and_4 (and_4_out, v4, or_9_out);
  and and_5 (and_5_out, v3, or_9_out);
  and and_6 (and_6_out, v2, or_9_out);
  and and_7 (and_7_out, v1, or_9_out);
  and and_8 (and_8_out, v0, or_9_out);
  or or_10 (o7, and_1_out, on7);
  or or_11 (o6, and_2_out, on6);
  or or_12 (o5, and_3_out, on5);
  or or_13 (o4, and_4_out, on4);
  or or_14 (o3, and_5_out, on3);
  or or_15 (o2, and_6_out, on2);
  or or_16 (o1, and_7_out, on1);
  or or_17 (o0, and_8_out, on0);
endmodule
module controller_1c2u (
  input  [1:0] consumer_write_valid,
  input  [1:0] consumer_read_valid,
  input  reset,
  input  clk,
  input  mem_read_ready,
  input  mem_write_ready,
  input  [7:0] consumer_write_address_0,
  input  [7:0] consumer_write_address_1,
  input  [15:0] consumer_write_data_0,
  input  [15:0] consumer_write_data_1,
  input  [7:0] consumer_read_address_0,
  input  [7:0] consumer_read_address_1,
  input  [15:0] mem_read_data_0,
  input  [1:0] consumer_write_ready,
  output mem_write_valid,
  output mem_read_valid,
  output [7:0] mem_read_address_0,
  output [7:0] mem_write_address_0,
  output [15:0] mem_write_data_0,
  output [1:0] consumer_read_ready,
  output [15:0] consumer_read_data_0,
  output [15:0] consumer_read_data_1
);

  wire and_6_out, bitselector_1_out, bitselector_2_out, bitselector_3_out, channel_sc_reg_0,
       channel_sc_reg_1, channel_serving_consumer_reg_0_q, channel_serving_consumer_reg_1_q,
       current_consumer_0, decoder_1_out0, decoder_1_out1, decoder_3_out0, decoder_3_out1,
       Find_READ_IDLE_TYPE_0, Find_READ_IDLE_TYPE_BIT_0, IDLE_STATE_0, IDLE_TYPE_READ_0, multiplexer_4_out,
       multiplexer_5_out, multiplexer_7_out, multiplexer_11_out, not_1_out, not_2_out, not_3_out, not_4_out,
       not_5_out, not_6_out, not_7_out, not_8_out, not_9_out, not_10_out, or_1_out, or_2_out, or_3_out,
       or_4_out, or_5_out, or_6_out, or_7_out, or_8_out, or_9_out, or_10_out, or_11_out,
       READ_RELAYING_STATE_0, READ_RELAYING_STATE_UPDATE_0, READ_WAITING_STATE_0,
       READ_WAITING_STATE_UPDATE_0, RESET_t, wr_waiting_merger_cc_enable_1_o0,
       wr_waiting_merger_cc_enable_1_o1, wr_waiting_merger_cc_enable_1_on0,
       wr_waiting_merger_cc_enable_1_on1, wr_waiting_merger_cc_enable_2_o0, wr_waiting_merger_cc_enable_2_o1,
       wr_waiting_merger_cc_enable_2_on0, wr_waiting_merger_cc_enable_2_on1, WRITE_RELAYING_STATE_0,
       WRITE_RELAYING_STATE_UPDATE_0, WRITE_WAITING_STATE_0, WRITE_WAITING_STATE_UPDATE_0;
  wire [1:0] and_8_out;
  wire [2:0] controller_state_reg_0_q, multiplexer_1_out, multiplexer_2_out, multiplexer_3_out,
       multiplexer_6_out;
  wire [7:0] multiplexer_9_out, multiplexer_10_out;
  wire [15:0] multiplexer_8_out;

  and and_1 (RESET_t, reset, clk);
  and and_2 (WRITE_WAITING_STATE_UPDATE_0, WRITE_WAITING_STATE_0, mem_write_ready);
  and and_3 (READ_WAITING_STATE_UPDATE_0, READ_WAITING_STATE_0, mem_read_ready);
  Multiplexer #(.width(3)) multiplexer_1 (
    .in0(3'b000), .in1(3'b101), .out(multiplexer_1_out), .sel(WRITE_WAITING_STATE_UPDATE_0));
  or or_1 (or_1_out, READ_RELAYING_STATE_UPDATE_0, WRITE_RELAYING_STATE_UPDATE_0);
  not not_1 (not_1_out, bitselector_1_out);
  BitSelector #(.width(2)) bitselector_1 (.in(consumer_read_valid), .out(bitselector_1_out), .sel(current_consumer_0));
  Multiplexer #(.width(3)) multiplexer_2 (
    .in0(multiplexer_1_out), .in1(3'b100), .out(multiplexer_2_out), .sel(READ_WAITING_STATE_UPDATE_0));
  Multiplexer #(.width(3)) multiplexer_3 (
    .in0(multiplexer_2_out), .in1(3'b010), .out(multiplexer_3_out), .sel(Find_READ_IDLE_TYPE_0));
  or or_2 (or_2_out, RESET_t, or_1_out, WRITE_WAITING_STATE_UPDATE_0, READ_WAITING_STATE_UPDATE_0, Find_READ_IDLE_TYPE_0);
  and and_4 (READ_RELAYING_STATE_UPDATE_0, READ_RELAYING_STATE_0, not_1_out);
  Decoder decoder_1 (
    .out0(decoder_1_out0), .out1(decoder_1_out1), .sel(current_consumer_0), .en(READ_WAITING_STATE_UPDATE_0));
  Register #(.width(1)) current_consumer_reg_0 (
    .D(Find_READ_IDLE_TYPE_BIT_0), .en(Find_READ_IDLE_TYPE_0), .clk(clk), .Q(current_consumer_0),
    .clr(RESET_t));
  Multiplexer multiplexer_4 (.in0(1'b0), .in1(1'b1), .out(multiplexer_4_out), .sel(and_8_out[1]));
  or or_3 (or_3_out, channel_sc_reg_1, and_8_out[1]);
  Multiplexer multiplexer_5 (.in0(1'b0), .in1(1'b1), .out(multiplexer_5_out), .sel(and_8_out[0]));
  or or_4 (or_4_out, channel_sc_reg_0, and_8_out[0]);
  Register #(.width(3)) controller_state_reg_0 (
    .D(multiplexer_6_out), .en(or_2_out), .clk(clk), .Q(controller_state_reg_0_q), .clr(RESET_t));
  Multiplexer #(.width(3)) multiplexer_6 (
    .in0(multiplexer_3_out), .in1(3'b000), .out(multiplexer_6_out), .sel(RESET_t));
  Register #(.width(16)) consumer_read_data_reg_0 (
    .D(mem_read_data_0), .en(decoder_1_out0), .clk(clk), .Q(consumer_read_data_0), .clr(RESET_t));
  Register #(.width(1)) channel_serving_consumer_reg_1 (
    .D(multiplexer_4_out), .en(or_3_out), .clk(clk), .Q(channel_serving_consumer_reg_1_q), .clr(RESET_t));
  Register #(.width(1)) channel_serving_consumer_reg_0 (
    .D(multiplexer_5_out), .en(or_4_out), .clk(clk), .Q(channel_serving_consumer_reg_0_q), .clr(RESET_t));
  Register #(.width(16)) consumer_read_data_reg_1 (
    .D(mem_read_data_0), .en(decoder_1_out1), .clk(clk), .Q(consumer_read_data_1), .clr(RESET_t));
  not not_2 (not_2_out, channel_serving_consumer_reg_1_q);
  not not_3 (not_3_out, channel_serving_consumer_reg_0_q);
  not not_4 (not_4_out, RESET_t);
  Decoder #(.select(3)) decoder_2 (
    .out0(IDLE_STATE_0), .out2(READ_WAITING_STATE_0), .out3(WRITE_WAITING_STATE_0),
    .out4(READ_RELAYING_STATE_0), .out5(WRITE_RELAYING_STATE_0), .sel(controller_state_reg_0_q),
    .en(not_4_out));  // open: out1, out6, out7
  not not_5 (not_5_out, bitselector_2_out);
  BitSelector #(.width(2)) bitselector_2 (.in(consumer_write_valid), .out(bitselector_2_out), .sel(current_consumer_0));
  and and_5 (WRITE_RELAYING_STATE_UPDATE_0, WRITE_RELAYING_STATE_0, not_5_out);
  or or_5 (or_5_out, READ_RELAYING_STATE_UPDATE_0, WRITE_RELAYING_STATE_UPDATE_0);
  or or_6 (or_6_out, consumer_write_valid[1], consumer_read_valid[1]);
  or or_7 (or_7_out, consumer_write_valid[0], consumer_read_valid[0]);
  Decoder decoder_3 (.out0(decoder_3_out0), .out1(decoder_3_out1), .sel(current_consumer_0), .en(or_5_out));
  not not_6 (not_6_out, and_8_out[1]);
  and and_6 (and_6_out, IDLE_STATE_0, not_6_out);
  not not_7 (not_7_out, consumer_read_valid[1]);
  not not_8 (not_8_out, consumer_read_valid[0]);
  and and_7 (and_8_out[1], IDLE_STATE_0, or_6_out, not_2_out);
  and and_8 (and_8_out[0], and_6_out, or_7_out, not_3_out);
  BitFinder #(.width(2)) bitfinder_1 (.in(and_8_out), .index(Find_READ_IDLE_TYPE_BIT_0), .found(Find_READ_IDLE_TYPE_0));
  not not_9 (not_9_out, consumer_write_valid[1]);
  not not_10 (not_10_out, consumer_write_valid[0]);
  or or_8 (or_8_out, not_7_out, not_9_out);
  and and_9 (channel_sc_reg_1, or_8_out, decoder_3_out1);
  or or_9 (or_9_out, not_8_out, not_10_out);
  and and_10 (channel_sc_reg_0, or_9_out, decoder_3_out0);
  BitSelector #(.width(2)) bitselector_3 (
    .in(consumer_read_valid), .out(bitselector_3_out), .sel(Find_READ_IDLE_TYPE_BIT_0));
  and and_11 (IDLE_TYPE_READ_0, Find_READ_IDLE_TYPE_0, bitselector_3_out);
  or or_10 (or_10_out, READ_WAITING_STATE_UPDATE_0, IDLE_TYPE_READ_0);
  Multiplexer multiplexer_7 (.in0(1'b1), .in1(1'b0), .out(multiplexer_7_out), .sel(READ_WAITING_STATE_UPDATE_0));
  Multiplexer #(.width(16)) multiplexer_8 (
    .in0(consumer_write_data_0), .in1(consumer_write_data_1), .out(multiplexer_8_out),
    .sel(Find_READ_IDLE_TYPE_BIT_0));
  Multiplexer #(.width(8)) multiplexer_9 (
    .in0(consumer_write_address_0), .in1(consumer_write_address_1), .out(multiplexer_9_out),
    .sel(Find_READ_IDLE_TYPE_BIT_0));
  Register #(.width(1)) mem_read_valid_reg_0 (
    .D(multiplexer_7_out), .en(or_10_out), .clk(clk), .Q(mem_read_valid), .clr(RESET_t));
  Multiplexer #(.enable("true"), .width(8)) multiplexer_10 (
    .in0(consumer_read_address_0), .in1(consumer_read_address_1), .out(multiplexer_10_out),
    .sel(Find_READ_IDLE_TYPE_BIT_0), .en(IDLE_TYPE_READ_0));
  or or_11 (or_11_out, Find_READ_IDLE_TYPE_0, WRITE_RELAYING_STATE_0);
  Register #(.width(16)) mem_write_data_reg_0 (
    .D(multiplexer_8_out), .en(Find_READ_IDLE_TYPE_0), .clk(clk), .Q(mem_write_data_0), .clr(RESET_t));
  Register mem_write_address_reg_0 (
    .D(multiplexer_9_out), .en(Find_READ_IDLE_TYPE_0), .clk(clk), .Q(mem_write_address_0), .clr(RESET_t));
  Register #(.width(1)) mem_write_valid_reg_0 (
    .D(multiplexer_11_out), .en(or_11_out), .clk(clk), .Q(mem_write_valid), .clr(RESET_t));
  Multiplexer multiplexer_11 (.in0(1'b1), .in1(1'b0), .out(multiplexer_11_out), .sel(WRITE_RELAYING_STATE_0));
  Register mem_read_address_reg_0 (
    .D(multiplexer_10_out), .en(IDLE_TYPE_READ_0), .clk(clk), .Q(mem_read_address_0), .clr(RESET_t));
  WR_WAITING_MERGER_CC_ENABLE wr_waiting_merger_cc_enable_1 (
    .e0(WRITE_WAITING_STATE_UPDATE_0), .i0({2'b00, current_consumer_0}), .v0(channel_sc_reg_0),
    .v1(channel_sc_reg_1), .c0(WRITE_RELAYING_STATE_UPDATE_0), .o1(wr_waiting_merger_cc_enable_1_o1),
    .o0(wr_waiting_merger_cc_enable_1_o0), .on1(wr_waiting_merger_cc_enable_1_on1),
    .on0(wr_waiting_merger_cc_enable_1_on0));  // open: e1, e2, e3, i1, i2, i3, v2, v3, v4, v5, v6, v7, c1, c2, c3, o7, o6, o5, o4, o3, o2, on7, on6, on5, on4, on3, on2
  WR_WAITING_MERGER_CC_ENABLE wr_waiting_merger_cc_enable_2 (
    .e0(READ_WAITING_STATE_UPDATE_0), .i0({2'b00, current_consumer_0}), .v0(channel_sc_reg_0),
    .v1(channel_sc_reg_1), .c0(READ_RELAYING_STATE_UPDATE_0), .o1(wr_waiting_merger_cc_enable_2_o1),
    .o0(wr_waiting_merger_cc_enable_2_o0), .on1(wr_waiting_merger_cc_enable_2_on1),
    .on0(wr_waiting_merger_cc_enable_2_on0));  // open: e1, e2, e3, i1, i2, i3, v2, v3, v4, v5, v6, v7, c1, c2, c3, o7, o6, o5, o4, o3, o2, on7, on6, on5, on4, on3, on2
  Register #(.width(1)) consumer_read_write_reg_1 (
    .D(wr_waiting_merger_cc_enable_1_on1), .en(wr_waiting_merger_cc_enable_1_o1), .clk(clk),
    .Q(consumer_write_ready[1]), .clr(RESET_t));
  Register #(.width(1)) consumer_read_write_reg_0 (
    .D(wr_waiting_merger_cc_enable_1_on0), .en(wr_waiting_merger_cc_enable_1_o0), .clk(clk),
    .Q(consumer_write_ready[0]), .clr(RESET_t));
  Register #(.width(1)) consumer_read_ready_reg_1 (
    .D(wr_waiting_merger_cc_enable_2_on1), .en(wr_waiting_merger_cc_enable_2_o1), .clk(clk),
    .Q(consumer_read_ready[1]), .clr(RESET_t));
  Register #(.width(1)) consumer_read_ready_reg_0 (
    .D(wr_waiting_merger_cc_enable_2_on0), .en(wr_waiting_merger_cc_enable_2_o0), .clk(clk),
    .Q(consumer_read_ready[0]), .clr(RESET_t));

  // Other names for the same wires on the sheet: IDLE_TYPE_WRITE_0 = Find_READ_IDLE_TYPE_0;
  //   mem_read_valid_0 = mem_read_valid; mem_write_valid_0 = mem_write_valid
endmodule

module READ_DATA_ROUTER (
  input  en_0,
  input  en_1,
  input  en_2,
  input  en_3,
  input  [2:0] cn_0,
  input  [2:0] cn_1,
  input  [2:0] cn_2,
  input  [2:0] cn_3,
  input  [7:0] c0,
  input  [7:0] c1,
  input  [7:0] c2,
  input  [7:0] c3,
  output e_0,
  output e_1,
  output e_2,
  output e_3,
  output e_4,
  output e_5,
  output e_6,
  output e_7,
  output [7:0] o_0,
  output [7:0] o_1,
  output [7:0] o_2,
  output [7:0] o_3,
  output [7:0] o_4,
  output [7:0] o_5,
  output [7:0] o_6,
  output [7:0] o_7
);

  wire decoder_1_out0, decoder_1_out1, decoder_1_out2, decoder_1_out3, decoder_1_out4, decoder_1_out5,
       decoder_1_out6, decoder_1_out7, decoder_2_out0, decoder_2_out1, decoder_2_out2, decoder_2_out3,
       decoder_2_out4, decoder_2_out5, decoder_2_out6, decoder_2_out7, decoder_3_out0, decoder_3_out1,
       decoder_3_out2, decoder_3_out3, decoder_3_out4, decoder_3_out5, decoder_3_out6, decoder_3_out7,
       decoder_4_out0, decoder_4_out1, decoder_4_out2, decoder_4_out3, decoder_4_out4, decoder_4_out5,
       decoder_4_out6, decoder_4_out7;
  wire [7:0] multiplexer_1_out, multiplexer_2_out, multiplexer_3_out, multiplexer_4_out, multiplexer_5_out,
       multiplexer_6_out, multiplexer_7_out, multiplexer_8_out, multiplexer_9_out, multiplexer_10_out,
       multiplexer_11_out, multiplexer_12_out, multiplexer_13_out, multiplexer_14_out, multiplexer_15_out,
       multiplexer_16_out;

  Decoder #(.select(3)) decoder_1 (
    .out0(decoder_1_out0), .out1(decoder_1_out1), .out2(decoder_1_out2), .out3(decoder_1_out3),
    .out4(decoder_1_out4), .out5(decoder_1_out5), .out6(decoder_1_out6), .out7(decoder_1_out7), .sel(cn_0),
    .en(en_0));
  Multiplexer #(.width(8)) multiplexer_1 (.in0(c0), .in1(c1), .out(multiplexer_1_out), .sel(decoder_2_out0));
  Multiplexer #(.width(8)) multiplexer_2 (.in0(c0), .in1(c1), .out(multiplexer_2_out), .sel(decoder_2_out1));
  Multiplexer #(.width(8)) multiplexer_3 (.in0(c0), .in1(c1), .out(multiplexer_3_out), .sel(decoder_2_out2));
  Multiplexer #(.width(8)) multiplexer_4 (.in0(c0), .in1(c1), .out(multiplexer_4_out), .sel(decoder_2_out3));
  Multiplexer #(.width(8)) multiplexer_5 (.in0(c0), .in1(c1), .out(multiplexer_5_out), .sel(decoder_2_out4));
  Multiplexer #(.width(8)) multiplexer_6 (.in0(c0), .in1(c1), .out(multiplexer_6_out), .sel(decoder_2_out5));
  Multiplexer #(.width(8)) multiplexer_7 (.in0(c0), .in1(c1), .out(multiplexer_7_out), .sel(decoder_2_out6));
  Multiplexer #(.width(8)) multiplexer_8 (.in0(c0), .in1(c1), .out(multiplexer_8_out), .sel(decoder_2_out7));
  Decoder #(.select(3)) decoder_2 (
    .out0(decoder_2_out0), .out1(decoder_2_out1), .out2(decoder_2_out2), .out3(decoder_2_out3),
    .out4(decoder_2_out4), .out5(decoder_2_out5), .out6(decoder_2_out6), .out7(decoder_2_out7), .sel(cn_1),
    .en(en_1));
  Multiplexer #(.width(8)) multiplexer_9 (
    .in0(multiplexer_1_out), .in1(c2), .out(multiplexer_9_out), .sel(decoder_3_out0));
  Multiplexer #(.width(8)) multiplexer_10 (
    .in0(multiplexer_2_out), .in1(c2), .out(multiplexer_10_out), .sel(decoder_3_out1));
  Multiplexer #(.width(8)) multiplexer_11 (
    .in0(multiplexer_3_out), .in1(c2), .out(multiplexer_11_out), .sel(decoder_3_out2));
  Multiplexer #(.width(8)) multiplexer_12 (
    .in0(multiplexer_4_out), .in1(c2), .out(multiplexer_12_out), .sel(decoder_3_out3));
  Multiplexer #(.width(8)) multiplexer_13 (
    .in0(multiplexer_5_out), .in1(c2), .out(multiplexer_13_out), .sel(decoder_3_out4));
  Multiplexer #(.width(8)) multiplexer_14 (
    .in0(multiplexer_6_out), .in1(c2), .out(multiplexer_14_out), .sel(decoder_3_out5));
  Multiplexer #(.width(8)) multiplexer_15 (
    .in0(multiplexer_7_out), .in1(c2), .out(multiplexer_15_out), .sel(decoder_3_out6));
  Multiplexer #(.width(8)) multiplexer_16 (
    .in0(multiplexer_8_out), .in1(c2), .out(multiplexer_16_out), .sel(decoder_3_out7));
  Decoder #(.select(3)) decoder_3 (
    .out0(decoder_3_out0), .out1(decoder_3_out1), .out2(decoder_3_out2), .out3(decoder_3_out3),
    .out4(decoder_3_out4), .out5(decoder_3_out5), .out6(decoder_3_out6), .out7(decoder_3_out7), .sel(cn_2),
    .en(en_2));
  Multiplexer #(.width(8)) multiplexer_17 (.in0(multiplexer_9_out), .in1(c3), .out(o_0), .sel(decoder_4_out0));
  Multiplexer #(.width(8)) multiplexer_18 (.in0(multiplexer_10_out), .in1(c3), .out(o_1), .sel(decoder_4_out1));
  Multiplexer #(.width(8)) multiplexer_19 (.in0(multiplexer_11_out), .in1(c3), .out(o_2), .sel(decoder_4_out2));
  Multiplexer #(.width(8)) multiplexer_20 (.in0(multiplexer_12_out), .in1(c3), .out(o_3), .sel(decoder_4_out3));
  Multiplexer #(.width(8)) multiplexer_21 (.in0(multiplexer_13_out), .in1(c3), .out(o_4), .sel(decoder_4_out4));
  Multiplexer #(.width(8)) multiplexer_22 (.in0(multiplexer_14_out), .in1(c3), .out(o_5), .sel(decoder_4_out5));
  Multiplexer #(.width(8)) multiplexer_23 (.in0(multiplexer_15_out), .in1(c3), .out(o_6), .sel(decoder_4_out6));
  Multiplexer #(.width(8)) multiplexer_24 (.in0(multiplexer_16_out), .in1(c3), .out(o_7), .sel(decoder_4_out7));
  Decoder #(.select(3)) decoder_4 (
    .out0(decoder_4_out0), .out1(decoder_4_out1), .out2(decoder_4_out2), .out3(decoder_4_out3),
    .out4(decoder_4_out4), .out5(decoder_4_out5), .out6(decoder_4_out6), .out7(decoder_4_out7), .sel(cn_3),
    .en(en_3));
  or or_1 (e_0, decoder_4_out0, decoder_3_out0, decoder_2_out0, decoder_1_out0);
  or or_2 (e_1, decoder_4_out1, decoder_3_out1, decoder_2_out1, decoder_1_out1);
  or or_3 (e_2, decoder_4_out2, decoder_3_out2, decoder_2_out2, decoder_1_out2);
  or or_4 (e_3, decoder_4_out3, decoder_3_out3, decoder_2_out3, decoder_1_out3);
  or or_5 (e_4, decoder_4_out4, decoder_3_out4, decoder_2_out4, decoder_1_out4);
  or or_6 (e_5, decoder_4_out5, decoder_3_out5, decoder_2_out5, decoder_1_out5);
  or or_7 (e_6, decoder_4_out6, decoder_3_out6, decoder_2_out6, decoder_1_out6);
  or or_8 (e_7, decoder_4_out7, decoder_3_out7, decoder_2_out7, decoder_1_out7);
endmodule

module register_w (
  input  [7:0] THREAD_ID,
  input  [3:0] decoded_rs_address,
  input  [7:0] block_id,
  input  enable,
  input  reset,
  input  clk,
  input  [3:0] decoded_rt_address,
  input  [3:0] decoded_rd_address,
  input  decoded_reg_write_enable,
  input  [1:0] decoded_reg_input_mux,
  input  [7:0] alu_out,
  input  [7:0] lsu_out,
  input  [7:0] decoded_immediate,
  input  [2:0] core_state,
  output [7:0] rs,
  output [7:0] rt
);

  wire and_1_out, decoder_1_out3, decoder_1_out6, decoder_2_out0, decoder_2_out1, decoder_2_out2,
       decoder_2_out3, decoder_2_out4, decoder_2_out5, decoder_2_out6, decoder_2_out7, decoder_2_out8,
       decoder_2_out9, decoder_2_out10, decoder_2_out11, decoder_2_out12, or_1_out, or_2_out, or_3_out;
  wire [7:0] multiplexer_1_out, multiplexer_2_out, multiplexer_3_out, reg_0_q, reg_1_q, reg_2_q, reg_3_q,
       reg_4_q, reg_5_q, reg_6_q, reg_7_q, reg_8_q, reg_9_q, reg_10_q, reg_11_q, reg_12_q, reg_13_q,
       reg_14_q, reg_15_q;

  // Probe on decoded_rd_address
  Multiplexer #(.select(2), .width(8)) multiplexer_1 (
    .in0(alu_out), .in1(lsu_out), .in2(decoded_immediate), .out(multiplexer_1_out),
    .sel(decoded_reg_input_mux));  // open: in3
  // Probe on core_state
  or or_1 (or_1_out, enable, reset);
  or or_2 (or_2_out, enable, reset);
  or or_3 (or_3_out, enable, enable);
  Decoder #(.select(3)) decoder_1 (
    .out3(decoder_1_out3), .out6(decoder_1_out6), .sel(core_state), .en(enable));  // open: out0, out1, out2, out4, out5, out7
  Register reg_14 (.D(8'h4), .en(or_1_out), .clk(clk), .Q(reg_14_q));  // open: clr
  Register reg_15 (.D(THREAD_ID), .en(or_2_out), .clk(clk), .Q(reg_15_q));  // open: clr
  Register reg_13 (.D(block_id), .en(or_3_out), .clk(clk), .Q(reg_13_q), .clr(reset));
  // Probe on multiplexer_1_out
  Decoder #(.select(4)) decoder_2 (
    .out0(decoder_2_out0), .out1(decoder_2_out1), .out2(decoder_2_out2), .out3(decoder_2_out3),
    .out4(decoder_2_out4), .out5(decoder_2_out5), .out6(decoder_2_out6), .out7(decoder_2_out7),
    .out8(decoder_2_out8), .out9(decoder_2_out9), .out10(decoder_2_out10), .out11(decoder_2_out11),
    .out12(decoder_2_out12), .sel(decoded_rd_address), .en(and_1_out));  // open: out13, out14, out15
  and and_1 (and_1_out, decoded_reg_write_enable, decoder_1_out6);
  Register reg_0 (.D(multiplexer_1_out), .en(decoder_2_out0), .clk(clk), .Q(reg_0_q), .clr(reset));
  Register reg_1 (.D(multiplexer_1_out), .en(decoder_2_out1), .clk(clk), .Q(reg_1_q), .clr(reset));
  Register reg_2 (.D(multiplexer_1_out), .en(decoder_2_out2), .clk(clk), .Q(reg_2_q), .clr(reset));
  Register reg_3 (.D(multiplexer_1_out), .en(decoder_2_out3), .clk(clk), .Q(reg_3_q), .clr(reset));
  Register reg_4 (.D(multiplexer_1_out), .en(decoder_2_out4), .clk(clk), .Q(reg_4_q), .clr(reset));
  Register reg_5 (.D(multiplexer_1_out), .en(decoder_2_out5), .clk(clk), .Q(reg_5_q), .clr(reset));
  Register reg_6 (.D(multiplexer_1_out), .en(decoder_2_out6), .clk(clk), .Q(reg_6_q), .clr(reset));
  Register reg_7 (.D(multiplexer_1_out), .en(decoder_2_out7), .clk(clk), .Q(reg_7_q), .clr(reset));
  Register reg_8 (.D(multiplexer_1_out), .en(decoder_2_out8), .clk(clk), .Q(reg_8_q), .clr(reset));
  Register reg_9 (.D(multiplexer_1_out), .en(decoder_2_out9), .clk(clk), .Q(reg_9_q), .clr(reset));
  Register reg_10 (.D(multiplexer_1_out), .en(decoder_2_out10), .clk(clk), .Q(reg_10_q), .clr(reset));
  Register reg_11 (.D(multiplexer_1_out), .en(decoder_2_out11), .clk(clk), .Q(reg_11_q), .clr(reset));
  Register reg_12 (.D(multiplexer_1_out), .en(decoder_2_out12), .clk(clk), .Q(reg_12_q), .clr(reset));
  Multiplexer #(.select(4), .width(8)) multiplexer_2 (
    .in0(reg_0_q), .in1(reg_1_q), .in2(reg_2_q), .in3(reg_3_q), .in4(reg_4_q), .in5(reg_5_q), .in6(reg_6_q),
    .in7(reg_7_q), .in8(reg_8_q), .in9(reg_9_q), .in10(reg_10_q), .in11(reg_11_q), .in12(reg_12_q),
    .in13(reg_13_q), .in14(reg_14_q), .in15(reg_15_q), .out(multiplexer_2_out), .sel(decoded_rs_address));
  Multiplexer #(.select(4), .width(8)) multiplexer_3 (
    .in0(reg_0_q), .in1(reg_1_q), .in2(reg_2_q), .in3(reg_3_q), .in4(reg_4_q), .in5(reg_5_q), .in6(reg_6_q),
    .in7(reg_7_q), .in8(reg_8_q), .in9(reg_9_q), .in10(reg_10_q), .in11(reg_11_q), .in12(reg_12_q),
    .in13(reg_13_q), .in14(reg_14_q), .in15(reg_15_q), .out(multiplexer_3_out), .sel(decoded_rt_address));
  Register reg_rs (.D(multiplexer_2_out), .en(decoder_1_out3), .clk(clk), .Q(rs));  // open: clr
  Register reg_rt (.D(multiplexer_3_out), .en(decoder_1_out3), .clk(clk), .Q(rt));  // open: clr
endmodule

module decoder_w (
  input  [15:0] instruction,
  input  [2:0] core_state,
  input  clk,
  input  reset,
  output [7:0] decoded_immediate,
  output [3:0] decoded_rd_address,
  output [2:0] decoded_nzp,
  output [3:0] decoded_rs_address,
  output [3:0] decoded_rt_address,
  output decoded_pc_mux,
  output decoded_alu_output_mux,
  output decoded_nzp_write_enable,
  output decoded_mem_write_enable,
  output decoded_reg_write_enable,
  output [1:0] decoded_reg_input_mux,
  output decoded_mem_read_enable,
  output [1:0] decoded_alu_arithmetic_mux,
  output decoded_ret
);

  wire decoder_1_out2, decoder_2_out1, decoder_2_out2, decoder_2_out3, decoder_2_out4, decoder_2_out5,
       decoder_2_out6, decoder_2_out8, decoder_2_out15, or_1_out, or_2_out, or_3_out, or_4_out;
  wire [1:0] decoder_2_out7, multiplexer_1_out, multiplexer_2_out, multiplexer_3_out, multiplexer_4_out,
       multiplexer_5_out;

  Multiplexer #(.width(2)) multiplexer_1 (.in0(2'b00), .in1(2'b11), .out(multiplexer_1_out), .sel(decoder_2_out6));
  Decoder #(.select(3)) decoder_1 (
    .out2(decoder_1_out2), .sel(core_state));  // open: out0, out1, out3, out4, out5, out6, out7, en
  Multiplexer #(.width(2)) multiplexer_2 (
    .in0(multiplexer_1_out), .in1(2'b10), .out(multiplexer_2_out), .sel(decoder_2_out5));
  Multiplexer #(.width(2)) multiplexer_3 (
    .in0(multiplexer_2_out), .in1(2'b01), .out(multiplexer_3_out), .sel(decoder_2_out4));
  Decoder #(.select(4)) decoder_2 (
    .out1(decoder_2_out1), .out2(decoder_2_out2), .out3(decoder_2_out3), .out4(decoder_2_out4),
    .out5(decoder_2_out5), .out6(decoder_2_out6), .out7(decoder_2_out7[0]), .out8(decoder_2_out8),
    .out9(decoder_2_out7[1]), .out15(decoder_2_out15), .sel(instruction[15:12]), .en(decoder_1_out2));  // open: out0, out10, out11, out12, out13, out14
  or or_1 (or_1_out, decoder_2_out3, decoder_2_out4, decoder_2_out5, decoder_2_out6);
  Multiplexer #(.width(2)) multiplexer_4 (
    .in0(multiplexer_3_out), .in1(2'b00), .out(multiplexer_4_out), .sel(decoder_2_out3));
  or or_2 (or_2_out, decoder_2_out7[0], decoder_2_out7[1], or_1_out);
  or or_3 (or_3_out, decoder_2_out7[0], decoder_2_out7[1]);
  or or_4 (or_4_out, decoder_1_out2, decoder_2_out7[0]);
  Register #(.width(1)) decoded_pc_mux_reg (
    .D(decoder_2_out1), .en(decoder_1_out2), .clk(clk), .Q(decoded_pc_mux), .clr(reset));
  Register #(.width(1)) decoded_alu_output_mux_reg (
    .D(decoder_2_out2), .en(decoder_1_out2), .clk(clk), .Q(decoded_alu_output_mux), .clr(reset));
  Register #(.width(1)) decoded_nzp_write_enable_reg (
    .D(decoder_2_out2), .en(decoder_1_out2), .clk(clk), .Q(decoded_nzp_write_enable), .clr(reset));
  Register #(.width(1)) decoded_mem_write_enable_reg (
    .D(decoder_2_out8), .en(decoder_1_out2), .clk(clk), .Q(decoded_mem_write_enable), .clr(reset));
  Register #(.width(1)) decoded_reg_write_enable_reg (
    .D(or_2_out), .en(decoder_1_out2), .clk(clk), .Q(decoded_reg_write_enable), .clr(reset));
  Register #(.width(2)) decoded_reg_input_mux_reg (
    .D(multiplexer_5_out), .en(decoder_1_out2), .clk(clk), .Q(decoded_reg_input_mux), .clr(reset));
  Multiplexer #(.width(2)) multiplexer_5 (.in0(2'b00), .in1(decoder_2_out7), .out(multiplexer_5_out), .sel(or_3_out));
  Register #(.width(1)) decoded_mem_read_enable_reg (
    .D(decoder_2_out7[0]), .en(or_4_out), .clk(clk), .Q(decoded_mem_read_enable), .clr(reset));
  Register #(.width(2)) decoded_alu_arithmetic_mux_reg (
    .D(multiplexer_4_out), .en(decoder_1_out2), .clk(clk), .Q(decoded_alu_arithmetic_mux), .clr(reset));
  Register #(.width(1)) decoded_ret_reg (
    .D(decoder_2_out15), .en(decoder_1_out2), .clk(clk), .Q(decoded_ret), .clr(reset));

  assign decoded_immediate = instruction[7:0];
  assign decoded_nzp = instruction[11:9];
  assign decoded_rd_address = instruction[11:8];
  assign decoded_rs_address = instruction[7:4];
  assign decoded_rt_address = instruction[3:0];
endmodule

module mem_4c_cache (
  input  [3:0] c_write_valid,
  input  [3:0] c_read_valid,
  input  [7:0] mem_read_data,
  input  reset,
  input  clk,
  input  [7:0] write_data_0,
  input  [7:0] write_data_1,
  input  [7:0] write_data_2,
  input  [7:0] write_data_3,
  input  [7:0] read_addr_0,
  input  [7:0] read_addr_1,
  input  [7:0] read_addr_2,
  input  [7:0] read_addr_3,
  input  [7:0] write_addr_0,
  input  [7:0] write_addr_1,
  input  [7:0] write_addr_2,
  input  [7:0] write_addr_3,
  output [3:0] read_ready,
  output [3:0] write_ready,
  output [7:0] mem_addr,
  output mem_we,
  output mem_re,
  output [7:0] mem_w_data,
  output [7:0] read_data_0,
  output [7:0] read_data_1,
  output [7:0] read_data_2,
  output [7:0] read_data_3
);

  wire and_1_out, and_2_out, and_3_out, and_5_out, bitselector_1_out, busy, can_init, can_select, can_update,
       comparator_1_eq, comparator_1_lt, find_bit, not_2_out, not_3_out, or_1_out, or_2_out;
  wire [1:0] adder_1_out, register_3_q;
  wire [2:0] current_index, finder_select_value, multiplexer_9_out;
  wire [7:0] multiplexer_1_out, multiplexer_2_out, multiplexer_3_out, multiplexer_4_out, multiplexer_5_out,
       multiplexer_6_out, multiplexer_7_out, multiplexer_8_out, multiplexer_10_out;

  Multiplexer #(.enable("true"), .width(8)) multiplexer_1 (
    .in1(write_addr_3), .out(multiplexer_1_out), .sel(c_write_valid[3]), .en(can_select));  // open: in0
  and and_1 (and_1_out, can_select, find_bit);
  Multiplexer #(.enable("true"), .width(8)) multiplexer_2 (
    .in0(multiplexer_1_out), .in1(write_addr_2), .out(multiplexer_2_out), .sel(c_write_valid[2]),
    .en(can_select));
  BitFinder bitfinder_1 (.in({c_write_valid, c_read_valid}), .index(finder_select_value), .found(find_bit));
  and and_2 (and_2_out, and_1_out, can_update);
  or or_1 (or_1_out, and_2_out, can_update);
  Multiplexer #(.enable("true"), .width(8)) multiplexer_3 (
    .in0(multiplexer_2_out), .in1(write_addr_1), .out(multiplexer_3_out), .sel(c_write_valid[1]),
    .en(can_select));
  Register #(.width(1)) u_busy (.D(and_2_out), .en(or_1_out), .clk(clk), .Q(busy), .clr(reset));
  Multiplexer #(.enable("true"), .width(8)) multiplexer_4 (
    .in0(multiplexer_3_out), .in1(write_addr_0), .out(multiplexer_4_out), .sel(c_write_valid[0]),
    .en(can_select));
  not not_1 (can_select, busy);
  Multiplexer #(.enable("true"), .width(8)) multiplexer_5 (
    .in0(multiplexer_4_out), .in1(read_addr_3), .out(multiplexer_5_out), .sel(c_read_valid[3]),
    .en(can_select));
  Multiplexer #(.enable("true"), .width(8)) multiplexer_6 (
    .in0(multiplexer_5_out), .in1(read_addr_2), .out(multiplexer_6_out), .sel(c_read_valid[2]),
    .en(can_select));
  not not_2 (not_2_out, can_init);
  Multiplexer #(.enable("true"), .width(8)) multiplexer_7 (
    .in0(multiplexer_6_out), .in1(read_addr_1), .out(multiplexer_7_out), .sel(c_read_valid[1]),
    .en(can_select));
  and and_3 (and_3_out, not_2_out, can_update);
  Multiplexer #(.enable("true"), .width(8)) multiplexer_8 (
    .in0(multiplexer_7_out), .in1(read_addr_0), .out(multiplexer_8_out), .sel(c_read_valid[0]),
    .en(can_select));
  Multiplexer #(.enable("true"), .width(3)) multiplexer_9 (
    .in0(finder_select_value), .in1(3'b000), .out(multiplexer_9_out), .sel(and_3_out));  // open: en
  BitSelector bitselector_1 (.in({c_write_valid, c_read_valid}), .out(bitselector_1_out), .sel(current_index));
  Register #(.width(3)) index (.D(multiplexer_9_out), .en(can_update), .clk(clk), .Q(current_index), .clr(reset));
  Register register_1 (.D(multiplexer_8_out), .en(can_update), .clk(clk), .Q(mem_addr), .clr(reset));
  Comparator #(.mode("unsigned"), .width(3)) comparator_1 (
    .a(finder_select_value), .b(3'b011), .gt(mem_we), .eq(comparator_1_eq), .lt(comparator_1_lt));
  not not_3 (not_3_out, bitselector_1_out);
  // Probe on mem_addr
  or or_2 (or_2_out, comparator_1_eq, comparator_1_lt);
  and and_4 (can_init, can_select, not_3_out);
  or or_3 (can_update, not_3_out, and_5_out);
  and and_5 (and_5_out, find_bit, can_select);
  and and_6 (mem_re, or_2_out, find_bit);
  Multiplexer #(.enable("true"), .select(3), .width(8)) multiplexer_10 (
    .in4(write_data_0), .in5(write_data_1), .in6(write_data_2), .in7(write_data_3), .out(multiplexer_10_out),
    .sel(current_index), .en(mem_we));  // open: in0, in1, in2, in3
  Register register_2 (.D(multiplexer_10_out), .en(mem_we), .clk(clk), .Q(mem_w_data), .clr(reset));
  Adder #(.width(2)) adder_1 (.a(register_3_q), .b(2'b00), .out(adder_1_out), .cin(busy));  // open: cout
  Register #(.width(2)) register_3 (.D(adder_1_out), .en(busy), .clk(clk), .Q(register_3_q));  // open: clr
  Demultiplexer #(.enable("true"), .select(3), .width(8)) demultiplexer_1 (
    .out0(read_data_0), .out1(read_data_1), .out2(read_data_2), .out3(read_data_3), .in(mem_read_data),
    .sel(current_index), .en(mem_re));  // open: out4, out5, out6, out7
  Decoder #(.select(3)) decoder_1 (
    .out0(read_ready[0]), .out1(read_ready[1]), .out2(read_ready[2]), .out3(read_ready[3]),
    .out4(write_ready[0]), .out5(write_ready[1]), .out6(write_ready[2]), .out7(write_ready[3]),
    .sel(current_index), .en(register_3_q[1]));

  // Other names for the same wires on the sheet: find_addredd[7:0] = mem_addr; read_data[7:0] = mem_read_data;
  //   read_type = mem_re; consumer_read_valid[3:0] = c_read_valid; select_value[7:0] = {c_write_valid, c_read_valid};
  //   consumer_write_valid[3:0] = c_write_valid; write_data[7:0] = mem_w_data; write_type = mem_we
endmodule

module gpu_mult_ram (
  input  in_1,
  input  [7:0] in_2,
  input  in_3,
  output done,
  output out_5
);

  wire clk, core_done_0, core_done_1, core_reset_0, core_reset_1, core_start_0, core_start_1, mem_re, mem_we,
       pmr_ready_0, pmr_ready_1, pmr_v0, pmr_v1, register_1_q;
  wire [2:0] core_thread_count_0, core_thread_count_1;
  wire [3:0] lsu_cr_v0, lsu_cr_v1, lsu_cw_v0, lsu_cw_v1, lsu_read_ready_0, lsu_read_ready_1,
       lsu_write_ready_0, lsu_write_ready_1, mem_read_channels, mem_write_channels, read_ready, write_ready;
  wire [7:0] core_block_id_0, core_block_id_1, lsu_read_address_0, lsu_read_address_1, lsu_read_address_2,
       lsu_read_address_3, lsu_read_address_4, lsu_read_address_5, lsu_read_address_6, lsu_read_address_7,
       lsu_read_data_0, lsu_read_data_1, lsu_read_data_2, lsu_read_data_3, lsu_read_data_4, lsu_read_data_5,
       lsu_read_data_6, lsu_read_data_7, lsu_write_address_0, lsu_write_address_1, lsu_write_address_2,
       lsu_write_address_3, lsu_write_address_4, lsu_write_address_5, lsu_write_address_6,
       lsu_write_address_7, lsu_write_data_0, lsu_write_data_1, lsu_write_data_2, lsu_write_data_3,
       lsu_write_data_4, lsu_write_data_5, lsu_write_data_6, lsu_write_data_7, mem_addr, mem_rdata,
       mem_wdata, pmr_addr_0, pmr_addr_1, ram_ra_0, ram_ra_1, ram_ra_2, ram_ra_3, ram_rd_0, ram_rd_1,
       ram_rd_2, ram_rd_3, ram_wa_0, ram_wa_1, ram_wa_2, ram_wa_3, ram_wd_0, ram_wd_1, ram_wd_2, ram_wd_3,
       rom_addr;
  wire [15:0] pmr_data_0, pmr_data_1, rom_data;

  RAM #(.asyncread("true"), .dataWidth(16), .\type ("nonvolatile")) ram_1 (
    .addr(rom_addr), .dout(rom_data));  // open: we, oe, clk, din
  mem_4c_cache mem_4c_cache_1 (
    .c_write_valid(mem_write_channels), .c_read_valid(mem_read_channels), .mem_read_data(mem_rdata),
    .reset(in_1), .clk(clk), .write_data_0(ram_wd_0), .write_data_1(ram_wd_1), .write_data_2(ram_wd_2),
    .write_data_3(ram_wd_3), .read_addr_0(ram_ra_0), .read_addr_1(ram_ra_1), .read_addr_2(ram_ra_2),
    .read_addr_3(ram_ra_3), .write_addr_0(ram_wa_0), .write_addr_1(ram_wa_1), .write_addr_2(ram_wa_2),
    .write_addr_3(ram_wa_3), .read_ready(read_ready), .write_ready(write_ready), .mem_addr(mem_addr),
    .mem_we(mem_we), .mem_re(mem_re), .mem_w_data(mem_wdata), .read_data_0(ram_rd_0), .read_data_1(ram_rd_1),
    .read_data_2(ram_rd_2), .read_data_3(ram_rd_3));
  Clock clock_1 (.out(clk));
  RAM #(.clearpin("true"), .readbehav("war"), .\type ("nonvolatile")) ram_2 (
    .addr(mem_addr), .we(mem_we), .oe(mem_re), .clk(clk), .din(mem_wdata), .dout(mem_rdata));  // open: clr
  Register #(.width(1)) register_1 (.D(out_5), .en(1'b1), .clk(clk), .Q(register_1_q));  // open: clr
  // Probe on {lsu_cw_v1, lsu_cw_v0}
  // Probe on {lsu_cr_v1, lsu_cr_v0}
  controller_1c2u ProgramMemoryController (
    .clk(clk), .reset(in_1), .consumer_read_address_0(pmr_addr_0), .consumer_read_address_1(pmr_addr_1),
    .consumer_read_valid({pmr_v1, pmr_v0}), .mem_read_data_0(rom_data), .mem_read_ready(register_1_q),
    .mem_read_address_0(rom_addr), .consumer_read_ready({pmr_ready_1, pmr_ready_0}),
    .consumer_read_data_0(pmr_data_0), .consumer_read_data_1(pmr_data_1), .mem_read_valid(out_5));  // open: consumer_write_address_0, consumer_write_address_1, mem_write_ready, consumer_write_data_0, consumer_write_data_1, consumer_write_valid, consumer_write_ready, mem_write_data_0, mem_write_address_0, mem_write_valid
  controller_4c8u controller_4c8u_1 (
    .clk(clk), .reset(in_1), .mem_read_data_0(ram_rd_0), .mem_read_data_1(ram_rd_1),
    .mem_read_data_2(ram_rd_2), .mem_read_data_3(ram_rd_3), .mem_read_ready(read_ready),
    .consumer_write_address_0(lsu_write_address_0), .consumer_write_address_1(lsu_write_address_1),
    .consumer_write_address_2(lsu_write_address_2), .consumer_write_address_3(lsu_write_address_3),
    .consumer_write_address_4(lsu_write_address_4), .consumer_write_address_5(lsu_write_address_5),
    .consumer_write_address_6(lsu_write_address_6), .consumer_write_address_7(lsu_write_address_7),
    .mem_write_ready(write_ready), .consumer_write_data_0(lsu_write_data_0),
    .consumer_write_data_1(lsu_write_data_1), .consumer_write_data_2(lsu_write_data_2),
    .consumer_write_data_3(lsu_write_data_3), .consumer_write_data_4(lsu_write_data_4),
    .consumer_write_data_5(lsu_write_data_5), .consumer_write_data_6(lsu_write_data_6),
    .consumer_write_data_7(lsu_write_data_7), .consumer_read_address_0(lsu_read_address_0),
    .consumer_read_address_1(lsu_read_address_1), .consumer_read_address_2(lsu_read_address_2),
    .consumer_read_address_3(lsu_read_address_3), .consumer_read_address_4(lsu_read_address_4),
    .consumer_read_address_5(lsu_read_address_5), .consumer_read_address_6(lsu_read_address_6),
    .consumer_read_address_7(lsu_read_address_7), .consumer_read_valid({lsu_cr_v1, lsu_cr_v0}),
    .consumer_write_valid({lsu_cw_v1, lsu_cw_v0}), .consumer_read_data_0(lsu_read_data_0),
    .consumer_read_data_1(lsu_read_data_1), .consumer_read_data_2(lsu_read_data_2),
    .consumer_read_data_3(lsu_read_data_3), .consumer_read_data_4(lsu_read_data_4),
    .consumer_read_data_5(lsu_read_data_5), .consumer_read_data_6(lsu_read_data_6),
    .consumer_read_data_7(lsu_read_data_7), .mem_write_data_0(ram_wd_0), .mem_write_data_1(ram_wd_1),
    .mem_write_data_2(ram_wd_2), .mem_write_data_3(ram_wd_3), .mem_read_address_2(ram_ra_2),
    .mem_read_address_3(ram_ra_3), .mem_write_address_0(ram_wa_0), .mem_write_address_1(ram_wa_1),
    .mem_write_address_2(ram_wa_2), .mem_write_address_3(ram_wa_3), .mem_read_address_0(ram_ra_0),
    .mem_read_address_1(ram_ra_1), .consumer_write_ready({lsu_write_ready_1, lsu_write_ready_0}),
    .consumer_read_ready({lsu_read_ready_1, lsu_read_ready_0}), .mem_read_valid(mem_read_channels),
    .mem_write_valid(mem_write_channels));
  // dispatch dispatch_1: pin names not known; wires that end beside it: in_3, clk, in_1, in_2, {core_done_1, core_done_0}, {core_reset_1, core_reset_0}, done, {core_start_1, core_start_0}, core_block_id_0, core_thread_count_0, core_block_id_1, core_thread_count_1
  core core0 (
    .thread_count(core_thread_count_0), .clk(clk), .reset(core_reset_0), .block_id(core_block_id_0),
    .program_mem_read_ready(pmr_ready_0), .data_mem_read_ready(lsu_read_ready_0),
    .data_mem_write_ready_0(lsu_write_ready_0), .data_mem_read_data_0(lsu_read_data_0),
    .data_mem_read_data_1(lsu_read_data_1), .data_mem_read_data_2(lsu_read_data_2),
    .data_mem_read_data_3(lsu_read_data_3), .program_mem_read_data(pmr_data_0), .start(core_start_0),
    .done(core_done_0), .program_mem_read_address(pmr_addr_0), .program_mem_read_valid(pmr_v0),
    .data_mem_write_data_0(lsu_write_data_0), .data_mem_write_data_1(lsu_write_data_1),
    .data_mem_write_data_2(lsu_write_data_2), .data_mem_write_data_3(lsu_write_data_3),
    .data_mem_write_address_0(lsu_write_address_0), .data_mem_write_address_1(lsu_write_address_1),
    .data_mem_write_address_2(lsu_write_address_2), .data_mem_write_address_3(lsu_write_address_3),
    .data_mem_read_address_0(lsu_read_address_0), .data_mem_read_address_1(lsu_read_address_1),
    .data_mem_read_address_2(lsu_read_address_2), .data_mem_read_address_3(lsu_read_address_3),
    .data_mem_write_valid(lsu_cw_v0), .data_mem_read_valid(lsu_cr_v0));
  core core1 (
    .thread_count(core_thread_count_1), .clk(clk), .reset(core_reset_1), .block_id(core_block_id_1),
    .program_mem_read_ready(pmr_ready_1), .data_mem_read_ready(lsu_read_ready_1),
    .data_mem_write_ready_0(lsu_write_ready_1), .data_mem_read_data_0(lsu_read_data_4),
    .data_mem_read_data_1(lsu_read_data_5), .data_mem_read_data_2(lsu_read_data_6),
    .data_mem_read_data_3(lsu_read_data_7), .program_mem_read_data(pmr_data_1), .start(core_start_1),
    .done(core_done_1), .program_mem_read_address(pmr_addr_1), .program_mem_read_valid(pmr_v1),
    .data_mem_write_data_0(lsu_write_data_4), .data_mem_write_data_1(lsu_write_data_5),
    .data_mem_write_data_2(lsu_write_data_6), .data_mem_write_data_3(lsu_write_data_7),
    .data_mem_write_address_0(lsu_write_address_4), .data_mem_write_address_1(lsu_write_address_5),
    .data_mem_write_address_2(lsu_write_address_6), .data_mem_write_address_3(lsu_write_address_7),
    .data_mem_read_address_0(lsu_read_address_4), .data_mem_read_address_1(lsu_read_address_5),
    .data_mem_read_address_2(lsu_read_address_6), .data_mem_read_address_3(lsu_read_address_7),
    .data_mem_write_valid(lsu_cw_v1), .data_mem_read_valid(lsu_cr_v1));

  // Other names for the same wires on the sheet: reset = in_1; start = in_3; thread_count[7:0] = in_2

  // Notes on the sheet:
  //   done: pull=down
endmodule

module gpu (
  input  reset,
  input  [7:0] thread_count,
  input  start,
  input  program_read_ready,
  input  [3:0] data_mem_read_ready,
  input  [3:0] data_mem_write_ready,
  output done,
  output program_read_valid,
  output [3:0] data_mem_write_valid,
  output [3:0] data_mem_read_valid
);

  wire clk, core_done_0, core_done_1, core_reset_0, core_reset_1, core_start_0, core_start_1, pmr_ready_0,
       pmr_ready_1, pmr_v0, pmr_v1;
  wire [2:0] core_thread_count_0, core_thread_count_1;
  wire [3:0] lsu_cr_v0, lsu_cr_v1, lsu_cw_v0, lsu_cw_v1, lsu_read_ready_0, lsu_read_ready_1,
       lsu_write_ready_0, lsu_write_ready_1;
  wire [7:0] core_block_id_0, core_block_id_1, lsu_read_address_0, lsu_read_address_1, lsu_read_address_2,
       lsu_read_address_3, lsu_read_address_4, lsu_read_address_5, lsu_read_address_6, lsu_read_address_7,
       lsu_read_data_0, lsu_read_data_1, lsu_read_data_2, lsu_read_data_3, lsu_read_data_4, lsu_read_data_5,
       lsu_read_data_6, lsu_read_data_7, lsu_write_address_0, lsu_write_address_1, lsu_write_address_2,
       lsu_write_address_3, lsu_write_address_4, lsu_write_address_5, lsu_write_address_6,
       lsu_write_address_7, lsu_write_data_0, lsu_write_data_1, lsu_write_data_2, lsu_write_data_3,
       lsu_write_data_4, lsu_write_data_5, lsu_write_data_6, lsu_write_data_7, pmr_addr_0, pmr_addr_1,
       program_addr, ram_ra_0, ram_ra_1, ram_ra_2, ram_ra_3, ram_rd_0, ram_rd_1, ram_rd_2, ram_rd_3,
       ram_wa_0, ram_wa_1, ram_wa_2, ram_wa_3, ram_wd_0, ram_wd_1, ram_wd_2, ram_wd_3;
  wire [15:0] pmr_data_0, pmr_data_1, program_data;

  Clock u_clk (.out(clk));
  // Probe on {lsu_cw_v1, lsu_cw_v0}
  // Probe on {lsu_cr_v1, lsu_cr_v0}
  controller_1c2u ProgramMemoryController (
    .clk(clk), .reset(reset), .consumer_read_address_0(pmr_addr_0), .consumer_read_address_1(pmr_addr_1),
    .consumer_read_valid({pmr_v1, pmr_v0}), .mem_read_data_0(program_data),
    .mem_read_ready(program_read_ready), .mem_read_address_0(program_addr),
    .consumer_read_ready({pmr_ready_1, pmr_ready_0}), .consumer_read_data_0(pmr_data_0),
    .consumer_read_data_1(pmr_data_1), .mem_read_valid(program_read_valid));  // open: consumer_write_address_0, consumer_write_address_1, mem_write_ready, consumer_write_data_0, consumer_write_data_1, consumer_write_valid, consumer_write_ready, mem_write_data_0, mem_write_address_0, mem_write_valid
  controller_4c8u controller_4c8u_1 (
    .clk(clk), .reset(reset), .mem_read_data_0(ram_rd_0), .mem_read_data_1(ram_rd_1),
    .mem_read_data_2(ram_rd_2), .mem_read_data_3(ram_rd_3), .mem_read_ready(data_mem_read_ready),
    .consumer_write_address_0(lsu_write_address_0), .consumer_write_address_1(lsu_write_address_1),
    .consumer_write_address_2(lsu_write_address_2), .consumer_write_address_3(lsu_write_address_3),
    .consumer_write_address_4(lsu_write_address_4), .consumer_write_address_5(lsu_write_address_5),
    .consumer_write_address_6(lsu_write_address_6), .consumer_write_address_7(lsu_write_address_7),
    .mem_write_ready(data_mem_write_ready), .consumer_write_data_0(lsu_write_data_0),
    .consumer_write_data_1(lsu_write_data_1), .consumer_write_data_2(lsu_write_data_2),
    .consumer_write_data_3(lsu_write_data_3), .consumer_write_data_4(lsu_write_data_4),
    .consumer_write_data_5(lsu_write_data_5), .consumer_write_data_6(lsu_write_data_6),
    .consumer_write_data_7(lsu_write_data_7), .consumer_read_address_0(lsu_read_address_0),
    .consumer_read_address_1(lsu_read_address_1), .consumer_read_address_2(lsu_read_address_2),
    .consumer_read_address_3(lsu_read_address_3), .consumer_read_address_4(lsu_read_address_4),
    .consumer_read_address_5(lsu_read_address_5), .consumer_read_address_6(lsu_read_address_6),
    .consumer_read_address_7(lsu_read_address_7), .consumer_read_valid({lsu_cr_v1, lsu_cr_v0}),
    .consumer_write_valid({lsu_cw_v1, lsu_cw_v0}), .consumer_read_data_0(lsu_read_data_0),
    .consumer_read_data_1(lsu_read_data_1), .consumer_read_data_2(lsu_read_data_2),
    .consumer_read_data_3(lsu_read_data_3), .consumer_read_data_4(lsu_read_data_4),
    .consumer_read_data_5(lsu_read_data_5), .consumer_read_data_6(lsu_read_data_6),
    .consumer_read_data_7(lsu_read_data_7), .mem_write_data_0(ram_wd_0), .mem_write_data_1(ram_wd_1),
    .mem_write_data_2(ram_wd_2), .mem_write_data_3(ram_wd_3), .mem_read_address_2(ram_ra_2),
    .mem_read_address_3(ram_ra_3), .mem_write_address_0(ram_wa_0), .mem_write_address_1(ram_wa_1),
    .mem_write_address_2(ram_wa_2), .mem_write_address_3(ram_wa_3), .mem_read_address_0(ram_ra_0),
    .mem_read_address_1(ram_ra_1), .consumer_write_ready({lsu_write_ready_1, lsu_write_ready_0}),
    .consumer_read_ready({lsu_read_ready_1, lsu_read_ready_0}), .mem_read_valid(data_mem_read_valid),
    .mem_write_valid(data_mem_write_valid));
  // dispatch dispatch_1: pin names not known; wires that end beside it: start, clk, reset, thread_count, {core_done_1, core_done_0}, {core_reset_1, core_reset_0}, done, {core_start_1, core_start_0}, core_block_id_0, core_thread_count_0, core_block_id_1, core_thread_count_1
  core core0 (
    .thread_count(core_thread_count_0), .clk(clk), .reset(core_reset_0), .block_id(core_block_id_0),
    .program_mem_read_ready(pmr_ready_0), .data_mem_read_ready(lsu_read_ready_0),
    .data_mem_write_ready_0(lsu_write_ready_0), .data_mem_read_data_0(lsu_read_data_0),
    .data_mem_read_data_1(lsu_read_data_1), .data_mem_read_data_2(lsu_read_data_2),
    .data_mem_read_data_3(lsu_read_data_3), .program_mem_read_data(pmr_data_0), .start(core_start_0),
    .done(core_done_0), .program_mem_read_address(pmr_addr_0), .program_mem_read_valid(pmr_v0),
    .data_mem_write_data_0(lsu_write_data_0), .data_mem_write_data_1(lsu_write_data_1),
    .data_mem_write_data_2(lsu_write_data_2), .data_mem_write_data_3(lsu_write_data_3),
    .data_mem_write_address_0(lsu_write_address_0), .data_mem_write_address_1(lsu_write_address_1),
    .data_mem_write_address_2(lsu_write_address_2), .data_mem_write_address_3(lsu_write_address_3),
    .data_mem_read_address_0(lsu_read_address_0), .data_mem_read_address_1(lsu_read_address_1),
    .data_mem_read_address_2(lsu_read_address_2), .data_mem_read_address_3(lsu_read_address_3),
    .data_mem_write_valid(lsu_cw_v0), .data_mem_read_valid(lsu_cr_v0));
  core core1 (
    .thread_count(core_thread_count_1), .clk(clk), .reset(core_reset_1), .block_id(core_block_id_1),
    .program_mem_read_ready(pmr_ready_1), .data_mem_read_ready(lsu_read_ready_1),
    .data_mem_write_ready_0(lsu_write_ready_1), .data_mem_read_data_0(lsu_read_data_4),
    .data_mem_read_data_1(lsu_read_data_5), .data_mem_read_data_2(lsu_read_data_6),
    .data_mem_read_data_3(lsu_read_data_7), .program_mem_read_data(pmr_data_1), .start(core_start_1),
    .done(core_done_1), .program_mem_read_address(pmr_addr_1), .program_mem_read_valid(pmr_v1),
    .data_mem_write_data_0(lsu_write_data_4), .data_mem_write_data_1(lsu_write_data_5),
    .data_mem_write_data_2(lsu_write_data_6), .data_mem_write_data_3(lsu_write_data_7),
    .data_mem_write_address_0(lsu_write_address_4), .data_mem_write_address_1(lsu_write_address_5),
    .data_mem_write_address_2(lsu_write_address_6), .data_mem_write_address_3(lsu_write_address_7),
    .data_mem_read_address_0(lsu_read_address_4), .data_mem_read_address_1(lsu_read_address_5),
    .data_mem_read_address_2(lsu_read_address_6), .data_mem_read_address_3(lsu_read_address_7),
    .data_mem_write_valid(lsu_cw_v1), .data_mem_read_valid(lsu_cr_v1));

  // Other names for the same wires on the sheet: mem_read_ready[3:0] = data_mem_read_ready;
  //   mem_read_valid[3:0] = data_mem_read_valid; mem_write_ready[3:0] = data_mem_write_ready;
  //   mem_write_valid[3:0] = data_mem_write_valid
endmodule
