// Logisim project lsu_module.circ as structural Verilog: 1 circuit, main circuit lsu
module lsu (
  input  [7:0] rt,
  input  [7:0] rs,
  input  [7:0] mem_read_data,
  input  enable,
  input  decoded_mem_read_enable,
  input  decoded_mem_write_enable,
  input  [2:0] core_state,
  input  mem_write_ready,
  input  mem_read_ready,
  input  reset,
  input  clk,
  output [7:0] mem_write_data,
  output [7:0] mem_write_address,
  output mem_write_valid,
  output [7:0] mem_read_address,
  output mem_read_valid,
  output [7:0] lsu_out,
  output [1:0] lus_state
);

  wire and_1_out, and_2_out, and_3_out, and_4_out, and_5_out, decoder_1_out1, decoder_1_out2, decoder_2_out3,
       decoder_2_out6, or_1_out, or_2_out, or_3_out, or_4_out;
  wire [1:0] bit_extender_1_out, multiplexer_1_out, multiplexer_2_out, multiplexer_3_out;

  or or_1 (or_1_out, mem_write_ready, mem_read_ready);
  Decoder #(.select(2)) decoder_1 (
    .out1(decoder_1_out1), .out2(decoder_1_out2), .sel(lus_state));  // open: out0, out3, en
  Decoder #(.select(3)) decoder_2 (
    .out3(decoder_2_out3), .out6(decoder_2_out6), .sel(core_state));  // open: out0, out1, out2, out4, out5, out7, en
  and and_1 (and_1_out, decoded_mem_write_enable, decoder_1_out1);
  and and_2 (and_2_out, decoder_1_out1, decoded_mem_read_enable);
  and and_3 (and_3_out, decoder_1_out2, decoded_mem_read_enable, mem_read_ready);
  or or_2 (or_2_out, decoded_mem_read_enable, decoded_mem_write_enable);
  assign bit_extender_1_out = {{1{1'b0}}, decoder_2_out3};  // Bit_Extender bit_extender_1
  Multiplexer #(.width(2)) multiplexer_1 (.in0(2'b11), .in1(2'b00), .out(multiplexer_1_out), .sel(decoder_2_out6));
  and and_4 (and_4_out, mem_write_ready, decoder_1_out2);
  or or_3 (or_3_out, and_2_out, and_3_out);
  and and_5 (and_5_out, enable, or_2_out);
  Multiplexer #(.width(2)) multiplexer_2 (.in0(2'b10), .in1(2'b11), .out(multiplexer_2_out), .sel(or_1_out));
  Register #(.width(1)) mem_write_valid_reg (.D(and_1_out), .en(or_4_out), .clk(clk), .Q(mem_write_valid), .clr(reset));
  or or_4 (or_4_out, and_1_out, and_4_out);
  Register #(.width(1)) mem_read_valid_reg (.D(and_2_out), .en(or_3_out), .clk(clk), .Q(mem_read_valid), .clr(reset));
  Multiplexer #(.enable("true"), .select(2), .width(2)) multiplexer_3 (
    .in0(bit_extender_1_out), .in1(2'b10), .in2(multiplexer_2_out), .in3(multiplexer_1_out),
    .out(multiplexer_3_out), .sel(lus_state), .en(and_5_out));
  Register #(.width(2)) lsu_state_reg (.D(multiplexer_3_out), .en(and_5_out), .clk(clk), .Q(lus_state), .clr(reset));
  Register mem_write_data_reg (.D(rt), .en(and_1_out), .clk(clk), .Q(mem_write_data), .clr(reset));
  Register mem_write_address_reg (.D(rs), .en(and_1_out), .clk(clk), .Q(mem_write_address), .clr(reset));
  Register mem_read_address_reg (.D(rs), .en(and_2_out), .clk(clk), .Q(mem_read_address), .clr(reset));
  Register lsu_out_reg (.D(mem_read_data), .en(and_3_out), .clk(clk), .Q(lsu_out), .clr(reset));

  // Other names for the same wires on the sheet: lsu_state[1:0] = lus_state
endmodule
