// Logisim project my_dcr_test.circ as structural Verilog
module dcr_test (
  input  [7:0] device_control_data,
  input  device_control_write_enable,
  input  clk,
  input  reset,
  output [7:0] thread_count
);

  wire [7:0] device_conrol_register_reg_q;

  Register device_conrol_register_reg (
    .D(device_control_data), .en(device_control_write_enable), .clk(clk), .Q(device_conrol_register_reg_q),
    .clr(reset));
  Register thread_count_reg (
    .D(device_conrol_register_reg_q), .en(device_control_write_enable), .clk(clk), .Q(thread_count),
    .clr(reset));
endmodule
