// Logisim project my_pc_test.circ as structural Verilog
module pc_test (
  input  [7:0] alu_out,
  input  decoded_nzp_write_enable,
  input  [2:0] core_state,
  input  [2:0] decoded_nzp,
  input  enable,
  input  decoded_pc_mux,
  input  [7:0] current_pc,
  input  [7:0] decoded_immediate,
  input  reset,
  input  clk,
  output [7:0] next_pc
);

  wire and_1_out, and_2_out, and_3_out, and_4_out, and_5_out, decoder_1_out5, decoder_1_out6, or_1_out,
       or_2_out;
  wire [2:0] bit_extender_1_out, nzp_reg_q;
  wire [7:0] adder_1_out, multiplexer_1_out;

  Decoder #(.select(3)) decoder_1 (
    .out5(decoder_1_out5), .out6(decoder_1_out6), .sel(core_state), .en(enable));  // open: out0, out1, out2, out3, out4, out7
  Adder adder_1 (.a(8'h1), .b(current_pc), .out(adder_1_out));  // open: cin, cout
  Bit_Extender #(.out_width(3), .\type ("zero")) bit_extender_1 (.in(alu_out), .out(bit_extender_1_out));
  Multiplexer #(.enable("true"), .width(8)) multiplexer_1 (
    .in0(adder_1_out), .in1(decoded_immediate), .out(multiplexer_1_out), .sel(and_5_out), .en(decoder_1_out5));
  Register #(.width(3)) nzp_reg (.D(bit_extender_1_out), .en(and_1_out), .clk(clk), .Q(nzp_reg_q), .clr(reset));
  and and_1 (and_1_out, decoded_nzp_write_enable, decoder_1_out6);
  Register next_pc_reg (.D(multiplexer_1_out), .en(decoder_1_out5), .clk(clk), .Q(next_pc), .clr(reset));
  and and_2 (and_2_out, nzp_reg_q[0], decoded_nzp[0]);
  and and_3 (and_3_out, nzp_reg_q[1], decoded_nzp[1]);
  and and_4 (and_4_out, nzp_reg_q[2], decoded_nzp[2]);
  or or_1 (or_1_out, and_2_out, and_3_out);
  or or_2 (or_2_out, or_1_out, and_4_out);
  and and_5 (and_5_out, or_2_out, decoded_pc_mux);
endmodule
