// Logisim project controller_data.circ as structural Verilog: 6 circuits, main circuit controller
module controller (
  input  reset,
  input  clk,
  input  [3:0] consumer_read_valid,
  input  mem_read_ready,
  input  [7:0] consumer_read_address_0,
  input  [7:0] consumer_read_address_1,
  input  [7:0] consumer_read_address_2,
  input  [7:0] consumer_read_address_3,
  input  mem_write_ready,
  input  [3:0] consumer_write_valid,
  input  [15:0] consumer_write_data_0,
  input  [15:0] consumer_write_data_1,
  input  [15:0] consumer_write_data_2,
  input  [15:0] consumer_write_data_3,
  input  [7:0] consumer_write_address_0,
  input  [7:0] consumer_write_address_1,
  input  [7:0] consumer_write_address_2,
  input  [7:0] consumer_write_address_3,
  output mem_read_valid,
  output [7:0] mem_read_address,
  output mem_write_valid,
  output [15:0] mem_write_data,
  output [7:0] mem_write_address,
  output [3:0] consumer_read_ready,
  output [3:0] consumer_write_ready
);

  wire and_1_out, and_2_out, and_3_out, and_4_out, and_5_out, and_6_out, and_7_out, and_8_out, and_18_out,
       bitfinder_1_found, bitfinder_2_found, channel_serving_consumer_reg_0_q,
       channel_serving_consumer_reg_1_q, channel_serving_consumer_reg_2_q, channel_serving_consumer_reg_3_q,
       consumer_rw_and_channel_serving_consumer_success, decoder_2_out0, decoder_2_out1, decoder_2_out2,
       decoder_2_out3, decoder_3_out0, decoder_3_out1, decoder_3_out2, decoder_3_out3, decoder_4_out0,
       decoder_4_out1, decoder_4_out2, decoder_4_out3, decoder_5_out0, decoder_5_out1, decoder_5_out2,
       decoder_5_out3, decoder_6_out0, decoder_6_out1, decoder_6_out2, decoder_6_out3, IDLE_STATE,
       multiplexer_5_out, multiplexer_6_out, multiplexer_7_out, multiplexer_11_out, multiplexer_13_out,
       not_1_out, not_2_out, not_3_out, not_4_out, not_5_out, not_6_out, not_7_out, not_8_out, not_9_out,
       not_10_out, not_11_out, not_12_out, not_13_out, not_14_out, or_1_out, or_2_out, or_3_out, or_6_out,
       or_7_out, or_9_out, or_10_out, READ_RELAYING_STATE, READ_RELAYING_STATE_UPDATE, READ_WAITING_STATE,
       READ_WAITING_STATE_UPDATE, WRITE_RELAYING_STATE, WRITE_RELAYING_STATE_UPDATE, WRITE_WAITING_STATE,
       WRITE_WAITING_STATE_UPDATE;
  wire [1:0] bitfinder_1_index, bitfinder_2_index, consumer_rw_and_channel_serving_consumer_bit,
       current_consumer;
  wire [2:0] controller_state_reg_q, multiplexer_1_out, multiplexer_2_out, multiplexer_3_out,
       multiplexer_4_out;
  wire [3:0] and_9_out, and_13_out;
  wire [7:0] multiplexer_10_out, multiplexer_12_out;
  wire [15:0] multiplexer_9_out;

  Multiplexer #(.width(3)) multiplexer_1 (
    .in0(3'b000), .in1(3'b101), .out(multiplexer_1_out), .sel(WRITE_WAITING_STATE_UPDATE));
  not not_1 (not_1_out, reset);
  Decoder #(.select(3)) decoder_1 (
    .out0(IDLE_STATE), .out2(READ_WAITING_STATE), .out3(WRITE_WAITING_STATE), .out4(READ_RELAYING_STATE),
    .out5(WRITE_RELAYING_STATE), .sel(controller_state_reg_q), .en(not_1_out));  // open: out1, out6, out7
  Decoder #(.select(2)) decoder_2 (
    .out0(decoder_2_out0), .out1(decoder_2_out1), .out2(decoder_2_out2), .out3(decoder_2_out3),
    .sel(current_consumer), .en(READ_RELAYING_STATE));
  Decoder #(.select(2)) decoder_3 (
    .out0(decoder_3_out0), .out1(decoder_3_out1), .out2(decoder_3_out2), .out3(decoder_3_out3),
    .sel(current_consumer), .en(WRITE_RELAYING_STATE));
  Multiplexer #(.width(3)) multiplexer_2 (
    .in0(multiplexer_1_out), .in1(3'b100), .out(multiplexer_2_out), .sel(READ_WAITING_STATE_UPDATE));
  or or_1 (or_1_out, reset, consumer_rw_and_channel_serving_consumer_success, READ_WAITING_STATE_UPDATE, WRITE_WAITING_STATE_UPDATE, or_3_out);
  or or_2 (or_2_out, WRITE_WAITING_STATE_UPDATE, WRITE_RELAYING_STATE_UPDATE);
  Multiplexer #(.width(3)) multiplexer_3 (
    .in0(multiplexer_2_out), .in1(3'b010), .out(multiplexer_3_out),
    .sel(consumer_rw_and_channel_serving_consumer_success));
  Multiplexer #(.width(3)) multiplexer_4 (.in0(multiplexer_3_out), .in1(3'b000), .out(multiplexer_4_out), .sel(reset));
  not not_2 (not_2_out, consumer_read_valid[0]);
  not not_3 (not_3_out, consumer_read_valid[1]);
  not not_4 (not_4_out, consumer_read_valid[2]);
  not not_5 (not_5_out, consumer_read_valid[3]);
  not not_6 (not_6_out, consumer_write_valid[0]);
  not not_7 (not_7_out, consumer_write_valid[1]);
  not not_8 (not_8_out, consumer_write_valid[2]);
  not not_9 (not_9_out, consumer_write_valid[3]);
  Decoder #(.select(2)) decoder_4 (
    .out0(decoder_4_out0), .out1(decoder_4_out1), .out2(decoder_4_out2), .out3(decoder_4_out3),
    .sel(current_consumer), .en(or_2_out));
  or or_3 (or_3_out, WRITE_RELAYING_STATE_UPDATE, READ_RELAYING_STATE_UPDATE);
  Register #(.width(3)) controller_state_reg (
    .D(multiplexer_4_out), .en(or_1_out), .clk(clk), .Q(controller_state_reg_q));  // open: clr
  and and_1 (and_1_out, decoder_2_out0, not_2_out);
  and and_2 (and_2_out, decoder_2_out1, not_3_out);
  and and_3 (and_3_out, decoder_2_out2, not_4_out);
  and and_4 (and_4_out, decoder_2_out3, not_5_out);
  and and_5 (and_5_out, decoder_3_out0, not_6_out);
  and and_6 (and_6_out, decoder_3_out1, not_7_out);
  and and_7 (and_7_out, decoder_3_out2, not_8_out);
  and and_8 (and_8_out, decoder_3_out3, not_9_out);
  Multiplexer multiplexer_5 (.in0(1'b0), .in1(1'b1), .out(multiplexer_5_out), .sel(WRITE_WAITING_STATE_UPDATE));
  or or_4 (READ_RELAYING_STATE_UPDATE, and_1_out, and_2_out, and_3_out, and_4_out);
  or or_5 (WRITE_RELAYING_STATE_UPDATE, and_5_out, and_6_out, and_7_out, and_8_out);
  Register #(.width(1)) consumer_write_ready_reg_0 (
    .D(multiplexer_5_out), .en(decoder_4_out0), .clk(clk), .Q(consumer_write_ready[0]), .clr(reset));
  Register #(.width(1)) consumer_write_ready_reg_1 (
    .D(multiplexer_5_out), .en(decoder_4_out1), .clk(clk), .Q(consumer_write_ready[1]), .clr(reset));
  Register #(.width(1)) consumer_write_ready_reg_2 (
    .D(multiplexer_5_out), .en(decoder_4_out2), .clk(clk), .Q(consumer_write_ready[2]), .clr(reset));
  Register #(.width(1)) consumer_write_ready_reg_3 (
    .D(multiplexer_5_out), .en(decoder_4_out3), .clk(clk), .Q(consumer_write_ready[3]), .clr(reset));
  or or_6 (or_6_out, consumer_rw_and_channel_serving_consumer_success, WRITE_RELAYING_STATE_UPDATE, READ_RELAYING_STATE_UPDATE);
  Decoder #(.select(2)) decoder_5 (
    .out0(decoder_5_out0), .out1(decoder_5_out1), .out2(decoder_5_out2), .out3(decoder_5_out3),
    .sel(consumer_rw_and_channel_serving_consumer_bit), .en(or_6_out));
  or or_7 (or_7_out, READ_WAITING_STATE_UPDATE, READ_RELAYING_STATE_UPDATE);
  Decoder #(.select(2)) decoder_6 (
    .out0(decoder_6_out0), .out1(decoder_6_out1), .out2(decoder_6_out2), .out3(decoder_6_out3),
    .sel(current_consumer), .en(or_7_out));
  Multiplexer multiplexer_6 (
    .in0(1'b0), .in1(1'b1), .out(multiplexer_6_out), .sel(consumer_rw_and_channel_serving_consumer_success));
  Register #(.width(1)) channel_serving_consumer_reg_0 (
    .D(multiplexer_6_out), .en(decoder_5_out0), .clk(clk), .Q(channel_serving_consumer_reg_0_q), .clr(reset));
  Register #(.width(1)) channel_serving_consumer_reg_1 (
    .D(multiplexer_6_out), .en(decoder_5_out1), .clk(clk), .Q(channel_serving_consumer_reg_1_q), .clr(reset));
  Register #(.width(1)) channel_serving_consumer_reg_2 (
    .D(multiplexer_6_out), .en(decoder_5_out2), .clk(clk), .Q(channel_serving_consumer_reg_2_q), .clr(reset));
  Register #(.width(1)) channel_serving_consumer_reg_3 (
    .D(multiplexer_6_out), .en(decoder_5_out3), .clk(clk), .Q(channel_serving_consumer_reg_3_q), .clr(reset));
  Multiplexer multiplexer_7 (.in0(1'b0), .in1(1'b1), .out(multiplexer_7_out), .sel(READ_WAITING_STATE_UPDATE));
  not not_10 (not_10_out, channel_serving_consumer_reg_0_q);
  not not_11 (not_11_out, channel_serving_consumer_reg_1_q);
  not not_12 (not_12_out, channel_serving_consumer_reg_2_q);
  not not_13 (not_13_out, channel_serving_consumer_reg_3_q);
  Register #(.width(1)) consumer_read_ready_reg_0 (
    .D(multiplexer_7_out), .en(decoder_6_out0), .clk(clk), .Q(consumer_read_ready[0]), .clr(reset));
  Register #(.width(1)) consumer_read_ready_reg_1 (
    .D(multiplexer_7_out), .en(decoder_6_out1), .clk(clk), .Q(consumer_read_ready[1]), .clr(reset));
  Register #(.width(1)) consumer_read_ready_reg_2 (
    .D(multiplexer_7_out), .en(decoder_6_out2), .clk(clk), .Q(consumer_read_ready[2]), .clr(reset));
  Register #(.width(1)) consumer_read_ready_reg_3 (
    .D(multiplexer_7_out), .en(decoder_6_out3), .clk(clk), .Q(consumer_read_ready[3]), .clr(reset));
  and and_9 (and_9_out[0], consumer_read_valid[0], not_10_out, IDLE_STATE);
  and and_10 (and_9_out[1], consumer_read_valid[1], not_11_out, IDLE_STATE);
  and and_11 (and_9_out[2], consumer_read_valid[2], not_12_out, IDLE_STATE);
  and and_12 (and_9_out[3], consumer_read_valid[3], not_13_out, IDLE_STATE);
  and and_13 (and_13_out[0], not_10_out, IDLE_STATE, consumer_write_valid[0]);
  and and_14 (and_13_out[1], not_11_out, IDLE_STATE, consumer_write_valid[1]);
  and and_15 (and_13_out[2], not_12_out, IDLE_STATE, consumer_write_valid[2]);
  and and_16 (and_13_out[3], not_13_out, IDLE_STATE, consumer_write_valid[3]);
  BitFinder #(.width(4)) bitfinder_1 (.in(and_9_out), .index(bitfinder_1_index), .found(bitfinder_1_found));
  or or_8 (consumer_rw_and_channel_serving_consumer_success, bitfinder_1_found, bitfinder_2_found);
  BitFinder #(.width(4)) bitfinder_2 (.in(and_13_out), .index(bitfinder_2_index), .found(bitfinder_2_found));
  Multiplexer #(.width(2)) multiplexer_8 (
    .in0(bitfinder_1_index), .in1(bitfinder_2_index), .out(consumer_rw_and_channel_serving_consumer_bit),
    .sel(bitfinder_2_found));
  and and_17 (READ_WAITING_STATE_UPDATE, mem_read_ready, READ_WAITING_STATE);
  not not_14 (not_14_out, bitfinder_1_found);
  and and_18 (and_18_out, not_14_out, bitfinder_2_found);
  Multiplexer #(.select(2), .width(16)) multiplexer_9 (
    .in0(consumer_write_data_0), .in1(consumer_write_data_1), .in2(consumer_write_data_2),
    .in3(consumer_write_data_3), .out(multiplexer_9_out), .sel(bitfinder_2_index));
  Multiplexer #(.select(2), .width(8)) multiplexer_10 (
    .in0(consumer_write_address_0), .in1(consumer_write_address_1), .in2(consumer_write_address_2),
    .in3(consumer_write_address_3), .out(multiplexer_10_out), .sel(bitfinder_2_index));
  Register #(.width(2)) current_consumer_reg (
    .D(consumer_rw_and_channel_serving_consumer_bit), .en(consumer_rw_and_channel_serving_consumer_success),
    .clk(clk), .Q(current_consumer), .clr(reset));
  Multiplexer multiplexer_11 (.in0(1'b0), .in1(or_9_out), .out(multiplexer_11_out), .sel(bitfinder_1_found));
  or or_9 (or_9_out, READ_WAITING_STATE_UPDATE, bitfinder_1_found);
  Multiplexer #(.select(2), .width(8)) multiplexer_12 (
    .in0(consumer_read_address_0), .in1(consumer_read_address_1), .in2(consumer_read_address_2),
    .in3(consumer_read_address_3), .out(multiplexer_12_out), .sel(bitfinder_1_index));
  Register #(.width(16)) mem_write_data_reg (
    .D(multiplexer_9_out), .en(and_18_out), .clk(clk), .Q(mem_write_data), .clr(reset));
  Register mem_write_address_reg (
    .D(multiplexer_10_out), .en(and_18_out), .clk(clk), .Q(mem_write_address), .clr(reset));
  Register #(.width(1)) mem_read_valid_reg (
    .D(multiplexer_11_out), .en(or_9_out), .clk(clk), .Q(mem_read_valid), .clr(reset));
  Multiplexer multiplexer_13 (.in0(1'b0), .in1(or_10_out), .out(multiplexer_13_out), .sel(and_18_out));
  or or_10 (or_10_out, WRITE_WAITING_STATE_UPDATE, and_18_out);
  Register mem_read_address_reg (
    .D(multiplexer_12_out), .en(consumer_rw_and_channel_serving_consumer_success), .clk(clk),
    .Q(mem_read_address), .clr(reset));
  Register #(.width(1)) mem_write_valid_reg (
    .D(multiplexer_13_out), .en(or_10_out), .clk(clk), .Q(mem_write_valid), .clr(reset));
  and and_19 (WRITE_WAITING_STATE_UPDATE, WRITE_WAITING_STATE, mem_write_ready);
endmodule

module data_controller (
  input  reset,
  input  clk,
  input  [3:0] mem_read_ready,
  input  [7:0] consumer_read_address_0,
  input  [7:0] consumer_read_address_1,
  input  [7:0] consumer_read_address_2,
  input  [7:0] consumer_read_address_3,
  input  [7:0] consumer_read_address_4,
  input  [7:0] consumer_read_address_5,
  input  [7:0] consumer_read_address_6,
  input  [7:0] consumer_read_address_7,
  input  [3:0] mem_write_ready,
  input  [7:0] consumer_read_valid,
  input  [7:0] consumer_write_valid,
  input  [7:0] consumer_write_data_0,
  input  [7:0] consumer_write_data_1,
  input  [7:0] consumer_write_data_2,
  input  [7:0] consumer_write_data_3,
  input  [7:0] in_19,
  input  [7:0] in_20,
  input  [7:0] in_21,
  input  [7:0] in_22,
  input  [7:0] consumer_write_address_0,
  input  [7:0] consumer_write_address_1,
  input  [7:0] consumer_write_address_2,
  input  [7:0] consumer_write_address_3,
  input  [7:0] in_27,
  input  [7:0] in_28,
  input  [7:0] in_29,
  input  [7:0] in_30,
  output out_31,
  output [7:0] mem_read_address,
  output mem_read_valid,
  output [7:0] out_34,
  output out_35,
  output [7:0] out_36,
  output [7:0] out_37,
  output out_38,
  output [7:0] mem_write_data,
  output [3:0] consumer_write_ready,
  output [7:0] mem_write_address
);

  wire and_1_out, and_2_out, and_3_out, and_4_out, and_5_out, and_6_out, and_7_out, and_8_out, and_25_out,
       and_26_out, and_27_out, and_28_out, channel_serving_consumer_reg_0_q,
       channel_serving_consumer_reg_1_q, channel_serving_consumer_reg_2_q, channel_serving_consumer_reg_3_q,
       consumer_rw_and_channel_serving_consumer_success, decoder_2_out0, decoder_2_out1, decoder_2_out2,
       decoder_2_out3, decoder_3_out0, decoder_3_out1, decoder_3_out2, decoder_3_out3, decoder_4_out0,
       decoder_4_out1, decoder_4_out2, decoder_4_out3, decoder_6_out0, decoder_6_out1, decoder_6_out2,
       decoder_6_out3, decoder_6_out4, decoder_6_out5, decoder_6_out6, decoder_6_out7,
       Find_READ_IDLE_TYPE_SUCCESS, Find_WRITE_IDLE_TYPE_SUCCESS, IDLE_STATE, IDLE_STATE_0, IDLE_STATE_1,
       IDLE_STATE_2, mem_write_valid_reg_0_q, multiplexer_8_out, multiplexer_10_out, multiplexer_14_out,
       multiplexer_15_out, multiplexer_16_out, multiplexer_17_out, multiplexer_18_out, not_1_out, not_2_out,
       not_3_out, not_4_out, not_5_out, not_6_out, not_7_out, not_8_out, not_9_out, not_10_out, or_1_out,
       or_2_out, or_3_out, or_4_out, or_7_out, or_8_out, or_9_out, or_10_out, or_11_out, or_12_out,
       or_13_out, or_14_out, READ_RELAYING_STATE, READ_RELAYING_STATE_0, READ_RELAYING_STATE_UPDATE,
       READ_RELAYING_STATE_UPDATE_0, READ_WAITING_STATE, READ_WAITING_STATE_0, READ_WAITING_STATE_1,
       READ_WAITING_STATE_2, READ_WAITING_STATE_3, READ_WAITING_STATE_UPDATE, READ_WAITING_STATE_UPDATE_0,
       READ_WAITING_STATE_UPDATE_1, READ_WAITING_STATE_UPDATE_2, READ_WAITING_STATE_UPDATE_3, register_1_q,
       register_2_q, register_3_q, register_4_q, undriven_3, undriven_4, undriven_5, undriven_6, undriven_7,
       undriven_8, undriven_9, undriven_10, undriven_11, undriven_12, WRITE_RELAYING_STATE,
       WRITE_RELAYING_STATE_0, WRITE_RELAYING_STATE_UPDATE, WRITE_WAITING_STATE, WRITE_WAITING_STATE_0,
       WRITE_WAITING_STATE_UPDATE, WRITE_WAITING_STATE_UPDATE_0;
  wire [1:0] current_consumer;
  wire [2:0] consumer_rw_and_channel_serving_consumer_bit, controller_state_reg_0_q,
       controller_state_reg_2_q, current_consumer_0, Find_READ_IDLE_TYPE_BIT_SUCCESS,
       Find_WRITE_IDLE_TYPE_BIT_SUCCESS, multiplexer_1_out, multiplexer_2_out, multiplexer_3_out,
       multiplexer_4_out, multiplexer_5_out, multiplexer_6_out, multiplexer_7_out, undriven, undriven_2;
  wire [7:0] and_9_out, and_17_out, bitaorbandnc_1_o, bitaorbcd_1_o, channel_serving_consumer_no,
       consumer_read_ready_reg_q, multiplexer_9_out, multiplexer_11_out, multiplexer_12_out,
       multiplexer_13_out;

  Multiplexer #(.width(3)) multiplexer_1 (
    .in0(3'b000), .in1(3'b101), .out(multiplexer_1_out), .sel(WRITE_WAITING_STATE_UPDATE));
  not not_1 (not_1_out, reset);
  Decoder #(.select(3)) decoder_1 (
    .out0(IDLE_STATE), .out2(READ_WAITING_STATE), .out3(WRITE_WAITING_STATE), .out4(READ_RELAYING_STATE),
    .out5(WRITE_RELAYING_STATE), .sel(controller_state_reg_2_q), .en(not_1_out));  // open: out1, out6, out7
  Multiplexer #(.width(3)) multiplexer_2 (
    .in0(multiplexer_1_out), .in1(3'b100), .out(multiplexer_2_out), .sel(READ_WAITING_STATE_UPDATE));
  or or_1 (or_1_out, reset, consumer_rw_and_channel_serving_consumer_success, READ_WAITING_STATE_UPDATE, WRITE_WAITING_STATE_UPDATE, or_2_out);
  Decoder #(.select(2)) decoder_2 (
    .out0(decoder_2_out0), .out1(decoder_2_out1), .out2(decoder_2_out2), .out3(decoder_2_out3),
    .sel(current_consumer), .en(READ_RELAYING_STATE));
  Decoder #(.select(2)) decoder_3 (
    .out0(decoder_3_out0), .out1(decoder_3_out1), .out2(decoder_3_out2), .out3(decoder_3_out3),
    .sel(current_consumer), .en(WRITE_RELAYING_STATE));
  Multiplexer #(.width(3)) multiplexer_3 (
    .in0(multiplexer_2_out), .in1(3'b010), .out(multiplexer_3_out),
    .sel(consumer_rw_and_channel_serving_consumer_success));
  Multiplexer #(.width(3)) multiplexer_4 (.in0(multiplexer_3_out), .in1(3'b000), .out(multiplexer_4_out), .sel(reset));
  or or_2 (or_2_out, WRITE_RELAYING_STATE_UPDATE, READ_RELAYING_STATE_UPDATE);
  Register #(.width(3)) controller_state_reg_2 (
    .D(multiplexer_4_out), .en(or_1_out), .clk(clk), .Q(controller_state_reg_2_q));  // open: clr
  not not_2 (not_2_out, consumer_read_valid[4]);
  not not_3 (not_3_out, consumer_read_valid[5]);
  not not_4 (not_4_out, consumer_read_valid[6]);
  not not_5 (not_5_out, consumer_read_valid[7]);
  not not_6 (not_6_out, consumer_write_valid[0]);
  not not_7 (not_7_out, consumer_write_valid[1]);
  not not_8 (not_8_out, consumer_write_valid[2]);
  not not_9 (not_9_out, consumer_write_valid[3]);
  or or_3 (or_3_out, WRITE_WAITING_STATE_UPDATE, WRITE_RELAYING_STATE_UPDATE);
  Decoder #(.select(2)) decoder_4 (
    .out0(decoder_4_out0), .out1(decoder_4_out1), .out2(decoder_4_out2), .out3(decoder_4_out3),
    .sel(current_consumer), .en(or_3_out));
  Multiplexer #(.width(3)) multiplexer_5 (
    .in0(undriven), .in1(3'b100), .out(multiplexer_5_out), .sel(READ_WAITING_STATE_UPDATE_0));
  Multiplexer #(.width(3)) multiplexer_6 (
    .in0(multiplexer_5_out), .in1(3'b010), .out(multiplexer_6_out), .sel(or_4_out));
  or or_4 (or_4_out, Find_READ_IDLE_TYPE_SUCCESS, Find_WRITE_IDLE_TYPE_SUCCESS);
  and and_1 (and_1_out, decoder_2_out0, not_2_out);
  and and_2 (and_2_out, decoder_2_out1, not_3_out);
  and and_3 (and_3_out, decoder_2_out2, not_4_out);
  and and_4 (and_4_out, decoder_2_out3, not_5_out);
  and and_5 (and_5_out, decoder_3_out0, not_6_out);
  and and_6 (and_6_out, decoder_3_out1, not_7_out);
  and and_7 (and_7_out, decoder_3_out2, not_8_out);
  and and_8 (and_8_out, decoder_3_out3, not_9_out);
  Register #(.width(3)) controller_state_reg_0 (
    .D(multiplexer_7_out), .Q(controller_state_reg_0_q));  // open: en, clk, clr
  Multiplexer #(.width(3)) multiplexer_7 (.in0(multiplexer_6_out), .in1(3'b000), .out(multiplexer_7_out), .sel(reset));
  or or_5 (READ_RELAYING_STATE_UPDATE, and_1_out, and_2_out, and_3_out, and_4_out);
  or or_6 (WRITE_RELAYING_STATE_UPDATE, and_5_out, and_6_out, and_7_out, and_8_out);
  Register #(.width(1)) consumer_write_ready_reg_0 (
    .D(multiplexer_8_out), .en(decoder_4_out0), .clk(clk), .Q(consumer_write_ready[0]), .clr(reset));
  Multiplexer multiplexer_8 (.in0(1'b0), .in1(1'b1), .out(multiplexer_8_out), .sel(WRITE_WAITING_STATE_UPDATE));
  Register #(.width(1)) consumer_write_ready_reg_1 (
    .D(multiplexer_8_out), .en(decoder_4_out1), .clk(clk), .Q(consumer_write_ready[1]), .clr(reset));
  Register #(.width(1)) consumer_write_ready_reg_2 (
    .D(multiplexer_8_out), .en(decoder_4_out2), .clk(clk), .Q(consumer_write_ready[2]), .clr(reset));
  Register #(.width(1)) consumer_write_ready_reg_3 (
    .D(multiplexer_8_out), .en(decoder_4_out3), .clk(clk), .Q(consumer_write_ready[3]), .clr(reset));
  not not_10 (not_10_out, reset);
  Decoder #(.select(3)) decoder_5 (
    .out0(IDLE_STATE_0), .out2(READ_WAITING_STATE_0), .out3(WRITE_WAITING_STATE_0),
    .out4(READ_RELAYING_STATE_0), .out5(WRITE_RELAYING_STATE_0), .sel(controller_state_reg_0_q),
    .en(not_10_out));  // open: out1, out6, out7
  or or_7 (or_7_out, READ_WAITING_STATE_UPDATE_0, READ_RELAYING_STATE_UPDATE_0);
  BitAorBCD bitaorbcd_1 (
    .enable(or_7_out), .D(current_consumer_0), .C(current_consumer_0), .B(current_consumer_0),
    .A(current_consumer_0), .O(bitaorbcd_1_o));
  Register consumer_read_ready_reg (
    .D(bitaorbandnc_1_o), .en(or_7_out), .Q(consumer_read_ready_reg_q));  // open: clk, clr
  Multiplexer #(.width(8)) multiplexer_9 (
    .in0({8{1'b0}}), .in1(bitaorbcd_1_o), .out(multiplexer_9_out), .sel(READ_RELAYING_STATE_UPDATE_0));
  or or_8 (or_8_out, consumer_rw_and_channel_serving_consumer_success, WRITE_RELAYING_STATE_UPDATE, READ_RELAYING_STATE_UPDATE);
  Decoder #(.select(3)) decoder_6 (
    .out0(decoder_6_out0), .out1(decoder_6_out1), .out2(decoder_6_out2), .out3(decoder_6_out3),
    .out4(decoder_6_out4), .out5(decoder_6_out5), .out6(decoder_6_out6), .out7(decoder_6_out7),
    .sel(consumer_rw_and_channel_serving_consumer_bit), .en(or_8_out));
  Multiplexer multiplexer_10 (
    .in0(1'b0), .in1(1'b1), .out(multiplexer_10_out), .sel(consumer_rw_and_channel_serving_consumer_success));
  BitAorBandNC bitaorbandnc_1 (
    .A(bitaorbcd_1_o), .B(consumer_read_ready_reg_q), .C(multiplexer_9_out), .O(bitaorbandnc_1_o));
  Register #(.width(1)) channel_serving_consumer_reg_0 (
    .D(multiplexer_10_out), .en(decoder_6_out0), .clk(clk), .Q(channel_serving_consumer_reg_0_q), .clr(reset));
  Register #(.width(1)) channel_serving_consumer_reg_1 (
    .D(multiplexer_10_out), .en(decoder_6_out1), .clk(clk), .Q(channel_serving_consumer_reg_1_q), .clr(reset));
  Register #(.width(1)) channel_serving_consumer_reg_2 (
    .D(multiplexer_10_out), .en(decoder_6_out2), .clk(clk), .Q(channel_serving_consumer_reg_2_q), .clr(reset));
  Register #(.width(1)) channel_serving_consumer_reg_3 (
    .D(multiplexer_10_out), .en(decoder_6_out3), .clk(clk), .Q(channel_serving_consumer_reg_3_q), .clr(reset));
  Register #(.width(1)) register_1 (
    .D(multiplexer_10_out), .en(decoder_6_out4), .clk(clk), .Q(register_1_q), .clr(reset));
  Register #(.width(1)) register_2 (
    .D(multiplexer_10_out), .en(decoder_6_out5), .clk(clk), .Q(register_2_q), .clr(reset));
  Register #(.width(1)) register_3 (
    .D(multiplexer_10_out), .en(decoder_6_out6), .clk(clk), .Q(register_3_q), .clr(reset));
  Register #(.width(1)) register_4 (
    .D(multiplexer_10_out), .en(decoder_6_out7), .clk(clk), .Q(register_4_q), .clr(reset));
  not not_11 (channel_serving_consumer_no[0], channel_serving_consumer_reg_0_q);
  not not_12 (channel_serving_consumer_no[1], channel_serving_consumer_reg_1_q);
  not not_13 (channel_serving_consumer_no[2], channel_serving_consumer_reg_2_q);
  not not_14 (channel_serving_consumer_no[3], channel_serving_consumer_reg_3_q);
  not not_15 (channel_serving_consumer_no[4], register_1_q);
  not not_16 (channel_serving_consumer_no[5], register_2_q);
  not not_17 (channel_serving_consumer_no[6], register_3_q);
  not not_18 (channel_serving_consumer_no[7], register_4_q);
  and and_9 (and_9_out[0], consumer_read_valid[0], channel_serving_consumer_no[0]);
  and and_10 (and_9_out[1], consumer_read_valid[1], channel_serving_consumer_no[1]);
  and and_11 (and_9_out[2], consumer_read_valid[2], channel_serving_consumer_no[2]);
  and and_12 (and_9_out[3], consumer_read_valid[3], channel_serving_consumer_no[3]);
  and and_13 (and_9_out[4], consumer_read_valid[4], channel_serving_consumer_no[4]);
  and and_14 (and_9_out[5], consumer_read_valid[5], channel_serving_consumer_no[5]);
  and and_15 (and_9_out[6], consumer_read_valid[6], channel_serving_consumer_no[6]);
  and and_16 (and_9_out[7], consumer_read_valid[7], channel_serving_consumer_no[7]);
  and and_17 (and_17_out[0], consumer_write_valid[0], channel_serving_consumer_no[0]);
  and and_18 (and_17_out[1], consumer_write_valid[1], channel_serving_consumer_no[1]);
  and and_19 (and_17_out[2], consumer_write_valid[2], channel_serving_consumer_no[2]);
  and and_20 (and_17_out[3], consumer_write_valid[3], channel_serving_consumer_no[3]);
  and and_21 (and_17_out[4], consumer_write_valid[4], channel_serving_consumer_no[4]);
  and and_22 (and_17_out[5], consumer_write_valid[5], channel_serving_consumer_no[5]);
  and and_23 (and_17_out[6], consumer_write_valid[6], channel_serving_consumer_no[6]);
  and and_24 (and_17_out[7], consumer_write_valid[7], channel_serving_consumer_no[7]);
  BitFinder bitfinder_1 (.in(and_9_out), .index(Find_READ_IDLE_TYPE_BIT_SUCCESS), .found(Find_READ_IDLE_TYPE_SUCCESS));
  BitFinder bitfinder_2 (
    .in(and_17_out), .index(Find_WRITE_IDLE_TYPE_BIT_SUCCESS), .found(Find_WRITE_IDLE_TYPE_SUCCESS));
  or or_9 (or_9_out, Find_READ_IDLE_TYPE_SUCCESS, Find_WRITE_IDLE_TYPE_SUCCESS);
  Multiplexer #(.enable("true"), .select(3), .width(8)) multiplexer_11 (
    .in0(consumer_read_address_0), .in1(consumer_read_address_1), .in2(consumer_read_address_2),
    .in3(consumer_read_address_3), .in4(consumer_read_address_4), .in5(consumer_read_address_5),
    .in6(consumer_read_address_6), .in7(consumer_read_address_7), .out(multiplexer_11_out),
    .sel(Find_READ_IDLE_TYPE_BIT_SUCCESS), .en(and_25_out));
  and and_25 (and_25_out, IDLE_STATE_0, or_9_out);
  and and_26 (and_26_out, or_9_out, IDLE_STATE_1);
  and and_27 (and_27_out, or_9_out, IDLE_STATE_2);
  and and_28 (and_28_out, or_9_out, IDLE_STATE_2);
  Register mem_read_address_reg (.D(multiplexer_11_out), .en(and_25_out), .clk(clk), .Q(mem_read_address), .clr(reset));
  Register register_5 (.D(multiplexer_11_out), .en(and_26_out), .Q(out_34));  // open: clk, clr
  Register register_6 (.D(multiplexer_11_out), .en(and_27_out), .Q(out_36));  // open: clk, clr
  Register register_7 (.D(multiplexer_11_out), .en(and_28_out), .Q(out_37));  // open: clk, clr
  Multiplexer #(.select(3), .width(8)) multiplexer_12 (
    .in0(consumer_write_data_0), .in1(consumer_write_data_1), .in2(consumer_write_data_2),
    .in3(consumer_write_data_3), .in4(in_19), .in5(in_20), .in6(in_21), .in7(in_22),
    .out(multiplexer_12_out), .sel(undriven_2));
  Multiplexer #(.select(3), .width(8)) multiplexer_13 (
    .in0(consumer_write_address_0), .in1(consumer_write_address_1), .in2(consumer_write_address_2),
    .in3(consumer_write_address_3), .in4(in_27), .in5(in_28), .in6(in_29), .in7(in_30),
    .out(multiplexer_13_out), .sel(undriven_2));
  Register mem_write_data_reg (.D(multiplexer_12_out), .en(undriven_3), .clk(clk), .Q(mem_write_data), .clr(reset));
  Register mem_write_address_reg (
    .D(multiplexer_13_out), .en(undriven_3), .clk(clk), .Q(mem_write_address), .clr(reset));
  Register #(.width(3)) current_consumer_reg_0 (
    .D(consumer_rw_and_channel_serving_consumer_bit), .en(consumer_rw_and_channel_serving_consumer_success),
    .clk(clk), .Q(current_consumer_0), .clr(reset));
  and and_29 (READ_WAITING_STATE_UPDATE_0, mem_read_ready[0], READ_WAITING_STATE_0);
  and and_30 (READ_WAITING_STATE_UPDATE_1, mem_read_ready[1], READ_WAITING_STATE_1);
  and and_31 (READ_WAITING_STATE_UPDATE_2, mem_read_ready[2], READ_WAITING_STATE_2);
  and and_32 (READ_WAITING_STATE_UPDATE_3, mem_read_ready[3], READ_WAITING_STATE_3);
  Multiplexer multiplexer_14 (.in0(1'b0), .in1(or_10_out), .out(multiplexer_14_out), .sel(and_25_out));
  or or_10 (or_10_out, READ_WAITING_STATE_UPDATE_0, and_25_out);
  Multiplexer multiplexer_15 (.in0(1'b0), .in1(or_11_out), .out(multiplexer_15_out), .sel(and_26_out));
  or or_11 (or_11_out, READ_WAITING_STATE_UPDATE_1, and_26_out);
  Multiplexer multiplexer_16 (.in0(1'b0), .in1(or_12_out), .out(multiplexer_16_out), .sel(and_27_out));
  or or_12 (or_12_out, READ_WAITING_STATE_UPDATE_2, and_27_out);
  Multiplexer multiplexer_17 (.in0(1'b0), .in1(or_13_out), .out(multiplexer_17_out), .sel(and_28_out));
  or or_13 (or_13_out, READ_WAITING_STATE_UPDATE_3, and_28_out);
  and and_33 (WRITE_WAITING_STATE_UPDATE_0, mem_write_ready[0], WRITE_WAITING_STATE_0);
  Register #(.width(1)) mem_read_valid_reg_0 (
    .D(multiplexer_14_out), .en(or_10_out), .clk(undriven_4), .Q(out_31), .clr(undriven_8));
  Register #(.width(1)) mem_read_valid_reg_1 (
    .D(multiplexer_15_out), .en(or_11_out), .clk(undriven_5), .Q(mem_read_valid), .clr(undriven_9));
  Register #(.width(1)) mem_read_valid_reg_2 (
    .D(multiplexer_16_out), .en(or_12_out), .clk(undriven_6), .Q(out_35), .clr(undriven_10));
  Register #(.width(1)) mem_read_valid_reg_3 (
    .D(multiplexer_17_out), .en(or_13_out), .clk(undriven_7), .Q(out_38), .clr(undriven_11));
  or or_14 (or_14_out, undriven_12, WRITE_WAITING_STATE_UPDATE_0);
  Multiplexer multiplexer_18 (.in0(1'b0), .in1(or_14_out), .out(multiplexer_18_out), .sel(undriven_12));
  Register #(.width(1)) mem_write_valid_reg_0 (
    .D(multiplexer_18_out), .en(or_14_out), .clk(clk), .Q(mem_write_valid_reg_0_q), .clr(reset));
endmodule

module mem_controller (
  input  reset,
  input  clk,
  input  mem_read_ready,
  input  [7:0] consumer_read_address_0,
  input  [7:0] consumer_read_address_1,
  input  [1:0] consumer_read_valid,
  input  mem_write_ready,
  input  [1:0] consumer_write_valid,
  input  [15:0] consumer_write_data_0,
  input  [15:0] consumer_write_data_1,
  input  [7:0] consumer_write_address_0,
  input  [7:0] consumer_write_address_1,
  output mem_read_valid,
  output [7:0] mem_read_address,
  output mem_write_valid,
  output [15:0] mem_write_data,
  output [7:0] mem_write_address,
  output [1:0] consumer_write_ready,
  output [1:0] consumer_read_ready
);

  wire and_1_out, and_2_out, and_3_out, and_4_out, and_10_out, bitfinder_1_found, bitfinder_1_index,
       bitfinder_2_found, bitfinder_2_index, channel_serving_consumer_reg_0_q,
       channel_serving_consumer_reg_1_q, consumer_rw_and_channel_serving_consumer_bit,
       consumer_rw_and_channel_serving_consumer_success, current_consumer, decoder_2_out0, decoder_2_out1,
       decoder_3_out0, decoder_3_out1, decoder_4_out0, decoder_4_out1, decoder_5_out0, decoder_5_out1,
       decoder_6_out0, decoder_6_out1, IDLE_STATE, multiplexer_5_out, multiplexer_6_out, multiplexer_7_out,
       multiplexer_11_out, multiplexer_13_out, not_1_out, not_2_out, not_3_out, not_4_out, not_5_out,
       not_6_out, not_7_out, not_8_out, or_1_out, or_2_out, or_3_out, or_6_out, or_7_out, or_9_out,
       or_10_out, READ_RELAYING_STATE, READ_RELAYING_STATE_UPDATE, READ_WAITING_STATE,
       READ_WAITING_STATE_UPDATE, WRITE_RELAYING_STATE, WRITE_RELAYING_STATE_UPDATE, WRITE_WAITING_STATE,
       WRITE_WAITING_STATE_UPDATE;
  wire [1:0] and_5_out, and_7_out;
  wire [2:0] controller_state_reg_q, multiplexer_1_out, multiplexer_2_out, multiplexer_3_out,
       multiplexer_4_out;
  wire [7:0] multiplexer_10_out, multiplexer_12_out;
  wire [15:0] multiplexer_9_out;

  Multiplexer #(.width(3)) multiplexer_1 (
    .in0(3'b000), .in1(3'b101), .out(multiplexer_1_out), .sel(WRITE_WAITING_STATE_UPDATE));
  not not_1 (not_1_out, reset);
  Decoder #(.select(3)) decoder_1 (
    .out0(IDLE_STATE), .out2(READ_WAITING_STATE), .out3(WRITE_WAITING_STATE), .out4(READ_RELAYING_STATE),
    .out5(WRITE_RELAYING_STATE), .sel(controller_state_reg_q), .en(not_1_out));  // open: out1, out6, out7
  Decoder decoder_2 (.out0(decoder_2_out0), .out1(decoder_2_out1), .sel(current_consumer), .en(READ_RELAYING_STATE));
  Decoder decoder_3 (.out0(decoder_3_out0), .out1(decoder_3_out1), .sel(current_consumer), .en(WRITE_RELAYING_STATE));
  Multiplexer #(.width(3)) multiplexer_2 (
    .in0(multiplexer_1_out), .in1(3'b100), .out(multiplexer_2_out), .sel(READ_WAITING_STATE_UPDATE));
  or or_1 (or_1_out, reset, consumer_rw_and_channel_serving_consumer_success, READ_WAITING_STATE_UPDATE, WRITE_WAITING_STATE_UPDATE, or_3_out);
  or or_2 (or_2_out, WRITE_WAITING_STATE_UPDATE, WRITE_RELAYING_STATE_UPDATE);
  Multiplexer #(.width(3)) multiplexer_3 (
    .in0(multiplexer_2_out), .in1(3'b010), .out(multiplexer_3_out),
    .sel(consumer_rw_and_channel_serving_consumer_success));
  Multiplexer #(.width(3)) multiplexer_4 (.in0(multiplexer_3_out), .in1(3'b000), .out(multiplexer_4_out), .sel(reset));
  not not_2 (not_2_out, consumer_read_valid[0]);
  not not_3 (not_3_out, consumer_read_valid[1]);
  not not_4 (not_4_out, consumer_write_valid[0]);
  not not_5 (not_5_out, consumer_write_valid[1]);
  Decoder decoder_4 (.out0(decoder_4_out0), .out1(decoder_4_out1), .sel(current_consumer), .en(or_2_out));
  or or_3 (or_3_out, WRITE_RELAYING_STATE_UPDATE, READ_RELAYING_STATE_UPDATE);
  Register #(.width(3)) controller_state_reg (
    .D(multiplexer_4_out), .en(or_1_out), .clk(clk), .Q(controller_state_reg_q));  // open: clr
  and and_1 (and_1_out, decoder_2_out0, not_2_out);
  and and_2 (and_2_out, decoder_2_out1, not_3_out);
  and and_3 (and_3_out, decoder_3_out0, not_4_out);
  and and_4 (and_4_out, decoder_3_out1, not_5_out);
  Multiplexer multiplexer_5 (.in0(1'b0), .in1(1'b1), .out(multiplexer_5_out), .sel(WRITE_WAITING_STATE_UPDATE));
  or or_4 (READ_RELAYING_STATE_UPDATE, and_1_out, and_2_out);
  or or_5 (WRITE_RELAYING_STATE_UPDATE, and_3_out, and_4_out);
  Register #(.width(1)) consumer_write_ready_reg_0 (
    .D(multiplexer_5_out), .en(decoder_4_out0), .clk(clk), .Q(consumer_write_ready[0]), .clr(reset));
  Register #(.width(1)) consumer_write_ready_reg_1 (
    .D(multiplexer_5_out), .en(decoder_4_out1), .clk(clk), .Q(consumer_write_ready[1]), .clr(reset));
  or or_6 (or_6_out, READ_WAITING_STATE_UPDATE, READ_RELAYING_STATE_UPDATE);
  Decoder decoder_5 (.out0(decoder_5_out0), .out1(decoder_5_out1), .sel(current_consumer), .en(or_6_out));
  or or_7 (or_7_out, consumer_rw_and_channel_serving_consumer_success, WRITE_RELAYING_STATE_UPDATE, READ_RELAYING_STATE_UPDATE);
  Decoder decoder_6 (
    .out0(decoder_6_out0), .out1(decoder_6_out1), .sel(consumer_rw_and_channel_serving_consumer_bit),
    .en(or_7_out));
  Multiplexer multiplexer_6 (
    .in0(1'b0), .in1(1'b1), .out(multiplexer_6_out), .sel(consumer_rw_and_channel_serving_consumer_success));
  Multiplexer multiplexer_7 (.in0(1'b0), .in1(1'b1), .out(multiplexer_7_out), .sel(READ_WAITING_STATE_UPDATE));
  Register #(.width(1)) channel_serving_consumer_reg_0 (
    .D(multiplexer_6_out), .en(decoder_6_out0), .clk(clk), .Q(channel_serving_consumer_reg_0_q), .clr(reset));
  Register #(.width(1)) channel_serving_consumer_reg_1 (
    .D(multiplexer_6_out), .en(decoder_6_out1), .clk(clk), .Q(channel_serving_consumer_reg_1_q), .clr(reset));
  Register #(.width(1)) consumer_read_ready_reg_0 (
    .D(multiplexer_7_out), .en(decoder_5_out0), .clk(clk), .Q(consumer_read_ready[0]), .clr(reset));
  Register #(.width(1)) consumer_read_ready_reg_1 (
    .D(multiplexer_7_out), .en(decoder_5_out1), .clk(clk), .Q(consumer_read_ready[1]), .clr(reset));
  not not_6 (not_6_out, channel_serving_consumer_reg_0_q);
  not not_7 (not_7_out, channel_serving_consumer_reg_1_q);
  and and_5 (and_5_out[0], consumer_read_valid[0], not_6_out, IDLE_STATE);
  and and_6 (and_5_out[1], consumer_read_valid[1], not_7_out, IDLE_STATE);
  and and_7 (and_7_out[0], not_6_out, IDLE_STATE, consumer_write_valid[0]);
  and and_8 (and_7_out[1], not_7_out, IDLE_STATE, consumer_write_valid[1]);
  BitFinder #(.width(2)) bitfinder_1 (.in(and_5_out), .index(bitfinder_1_index), .found(bitfinder_1_found));
  or or_8 (consumer_rw_and_channel_serving_consumer_success, bitfinder_1_found, bitfinder_2_found);
  BitFinder #(.width(2)) bitfinder_2 (.in(and_7_out), .index(bitfinder_2_index), .found(bitfinder_2_found));
  Multiplexer multiplexer_8 (
    .in0(bitfinder_1_index), .in1(bitfinder_2_index), .out(consumer_rw_and_channel_serving_consumer_bit),
    .sel(bitfinder_2_found));
  and and_9 (READ_WAITING_STATE_UPDATE, mem_read_ready, READ_WAITING_STATE);
  not not_8 (not_8_out, bitfinder_1_found);
  and and_10 (and_10_out, not_8_out, bitfinder_2_found);
  Multiplexer #(.width(16)) multiplexer_9 (
    .in0(consumer_write_data_0), .in1(consumer_write_data_1), .out(multiplexer_9_out), .sel(bitfinder_2_index));
  Multiplexer #(.width(8)) multiplexer_10 (
    .in0(consumer_write_address_0), .in1(consumer_write_address_1), .out(multiplexer_10_out),
    .sel(bitfinder_2_index));
  Register #(.width(1)) current_consumer_reg (
    .D(consumer_rw_and_channel_serving_consumer_bit), .en(consumer_rw_and_channel_serving_consumer_success),
    .clk(clk), .Q(current_consumer), .clr(reset));
  Multiplexer multiplexer_11 (.in0(1'b0), .in1(or_9_out), .out(multiplexer_11_out), .sel(bitfinder_1_found));
  or or_9 (or_9_out, READ_WAITING_STATE_UPDATE, bitfinder_1_found);
  Multiplexer #(.width(8)) multiplexer_12 (
    .in0(consumer_read_address_0), .in1(consumer_read_address_1), .out(multiplexer_12_out),
    .sel(bitfinder_1_index));
  Register #(.width(16)) mem_write_data_reg (
    .D(multiplexer_9_out), .en(and_10_out), .clk(clk), .Q(mem_write_data), .clr(reset));
  Register mem_write_address_reg (
    .D(multiplexer_10_out), .en(and_10_out), .clk(clk), .Q(mem_write_address), .clr(reset));
  Register #(.width(1)) mem_read_valid_reg (
    .D(multiplexer_11_out), .en(or_9_out), .clk(clk), .Q(mem_read_valid), .clr(reset));
  Multiplexer multiplexer_13 (.in0(1'b0), .in1(or_10_out), .out(multiplexer_13_out), .sel(and_10_out));
  or or_10 (or_10_out, WRITE_WAITING_STATE_UPDATE, and_10_out);
  Register mem_read_address_reg (
    .D(multiplexer_12_out), .en(consumer_rw_and_channel_serving_consumer_success), .clk(clk),
    .Q(mem_read_address), .clr(reset));
  Register #(.width(1)) mem_write_valid_reg (
    .D(multiplexer_13_out), .en(or_10_out), .clk(clk), .Q(mem_write_valid), .clr(reset));
  and and_11 (WRITE_WAITING_STATE_UPDATE, WRITE_WAITING_STATE, mem_write_ready);
endmodule

module bak_mem (
  input  [7:0] consumer_read_address_0,
  input  [7:0] consumer_read_address_1,
  input  [7:0] consumer_read_address_2,
  input  [7:0] consumer_read_address_3,
  input  [7:0] consumer_read_address_4,
  input  [7:0] consumer_read_address_5,
  input  [7:0] consumer_read_address_6,
  input  [7:0] consumer_read_address_7,
  output [7:0] mem_read_address,
  output [7:0] out_10,
  output [7:0] out_11,
  output [7:0] out_12,
  output [7:0] consumer_read_ready
);

  wire and_1_out, and_2_out, and_3_out, and_4_out, CLK, Find_READ_IDLE_TYPE_SUCCESS,
       Find_WRITE_IDLE_TYPE_SUCCESS, multiplexer_1_out, or_1_out, RESET, undriven_2;
  wire [2:0] Find_READ_IDLE_TYPE_BIT_SUCCESS;
  wire [7:0] multiplexer_2_out, multiplexer_3_out, multiplexer_4_out, multiplexer_5_out, undriven;

  Multiplexer multiplexer_1 (.in0(1'b0), .in1(1'b1), .out(multiplexer_1_out), .sel(undriven_2));
  Register #(.width(1)) consumer_read_ready_reg_0 (
    .D(multiplexer_1_out), .en(undriven[0]), .clk(CLK), .Q(consumer_read_ready[0]), .clr(RESET));
  Register #(.width(1)) consumer_read_ready_reg_1 (
    .D(multiplexer_1_out), .en(undriven[1]), .clk(CLK), .Q(consumer_read_ready[1]), .clr(RESET));
  Register #(.width(1)) consumer_read_ready_reg_2 (
    .D(multiplexer_1_out), .en(undriven[2]), .clk(CLK), .Q(consumer_read_ready[2]), .clr(RESET));
  Register #(.width(1)) consumer_read_ready_reg_3 (
    .D(multiplexer_1_out), .en(undriven[3]), .clk(CLK), .Q(consumer_read_ready[3]), .clr(RESET));
  Register #(.width(1)) consumer_read_ready_reg_4 (
    .D(multiplexer_1_out), .en(undriven[4]), .clk(CLK), .Q(consumer_read_ready[4]), .clr(RESET));
  Register #(.width(1)) consumer_read_ready_reg_5 (
    .D(multiplexer_1_out), .en(undriven[5]), .clk(CLK), .Q(consumer_read_ready[5]), .clr(RESET));
  Register #(.width(1)) consumer_read_ready_reg_6 (
    .D(multiplexer_1_out), .en(undriven[6]), .clk(CLK), .Q(consumer_read_ready[6]), .clr(RESET));
  Register #(.width(1)) consumer_read_ready_reg_7 (
    .D(multiplexer_1_out), .en(undriven[7]), .clk(CLK), .Q(consumer_read_ready[7]), .clr(RESET));
  or or_1 (or_1_out, Find_READ_IDLE_TYPE_SUCCESS, Find_WRITE_IDLE_TYPE_SUCCESS);
  // AND_Gate and_1 has open pins: out=and_1_out
  // AND_Gate and_2 has open pins: out=and_2_out
  // AND_Gate and_3 has open pins: out=and_3_out
  // AND_Gate and_4 has open pins: out=and_4_out
  Multiplexer #(.enable("true"), .select(3), .width(8)) multiplexer_2 (
    .in0(consumer_read_address_0), .in1(consumer_read_address_1), .in2(consumer_read_address_2),
    .in3(consumer_read_address_3), .in4(consumer_read_address_4), .in5(consumer_read_address_5),
    .in6(consumer_read_address_6), .in7(consumer_read_address_7), .out(multiplexer_2_out),
    .sel(Find_READ_IDLE_TYPE_BIT_SUCCESS), .en(and_1_out));
  Multiplexer #(.enable("true"), .select(3), .width(8)) multiplexer_3 (
    .in0(consumer_read_address_0), .in1(consumer_read_address_1), .in2(consumer_read_address_2),
    .in3(consumer_read_address_3), .in4(consumer_read_address_4), .in5(consumer_read_address_5),
    .in6(consumer_read_address_6), .in7(consumer_read_address_7), .out(multiplexer_3_out),
    .sel(Find_READ_IDLE_TYPE_BIT_SUCCESS), .en(and_2_out));
  Multiplexer #(.enable("true"), .select(3), .width(8)) multiplexer_4 (
    .in0(consumer_read_address_0), .in1(consumer_read_address_1), .in2(consumer_read_address_2),
    .in3(consumer_read_address_3), .in4(consumer_read_address_4), .in5(consumer_read_address_5),
    .in6(consumer_read_address_6), .in7(consumer_read_address_7), .out(multiplexer_4_out),
    .sel(Find_READ_IDLE_TYPE_BIT_SUCCESS), .en(and_3_out));
  Multiplexer #(.enable("true"), .select(3), .width(8)) multiplexer_5 (
    .in0(consumer_read_address_0), .in1(consumer_read_address_1), .in2(consumer_read_address_2),
    .in3(consumer_read_address_3), .in4(consumer_read_address_4), .in5(consumer_read_address_5),
    .in6(consumer_read_address_6), .in7(consumer_read_address_7), .out(multiplexer_5_out),
    .sel(Find_READ_IDLE_TYPE_BIT_SUCCESS), .en(and_4_out));
  Register mem_read_address_reg (.D(multiplexer_2_out), .en(and_1_out), .clk(CLK), .Q(mem_read_address), .clr(RESET));
  Register register_1 (.D(multiplexer_3_out), .en(and_2_out), .Q(out_10));  // open: clk, clr
  Register register_2 (.D(multiplexer_4_out), .en(and_3_out), .Q(out_11));  // open: clk, clr
  Register register_3 (.D(multiplexer_5_out), .en(and_4_out), .Q(out_12));  // open: clk, clr
endmodule

module BitAorBandNC (
  input  [7:0] A,
  input  [7:0] B,
  input  [7:0] C,
  output [7:0] O
);

  wire or_1_out, or_2_out, or_3_out, or_4_out, or_5_out, or_6_out, or_7_out, or_8_out;

  or or_1 (or_1_out, A[0], B[0]);
  or or_2 (or_2_out, A[1], B[1]);
  or or_3 (or_3_out, A[2], B[2]);
  or or_4 (or_4_out, A[3], B[3]);
  or or_5 (or_5_out, A[4], B[4]);
  or or_6 (or_6_out, A[5], B[5]);
  or or_7 (or_7_out, A[6], B[6]);
  or or_8 (or_8_out, A[7], B[7]);
  and and_1 (O[0], or_1_out, C[0]);
  and and_2 (O[1], or_2_out, C[1]);
  and and_3 (O[2], or_3_out, C[2]);
  and and_4 (O[3], or_4_out, C[3]);
  and and_5 (O[4], or_5_out, C[4]);
  and and_6 (O[5], or_6_out, C[5]);
  and and_7 (O[6], or_7_out, C[6]);
  and and_8 (O[7], or_8_out, C[7]);
endmodule

module BitAorBCD (
  input  enable,
  input  [2:0] D,
  input  [2:0] C,
  input  [2:0] B,
  input  [2:0] A,
  output [7:0] O
);

  wire decoder_1_out0, decoder_1_out1, decoder_1_out2, decoder_1_out3, decoder_1_out4, decoder_1_out5,
       decoder_1_out6, decoder_1_out7, decoder_2_out0, decoder_2_out1, decoder_2_out2, decoder_2_out3,
       decoder_2_out4, decoder_2_out5, decoder_2_out6, decoder_2_out7, decoder_3_out0, decoder_3_out1,
       decoder_3_out2, decoder_3_out3, decoder_3_out4, decoder_3_out5, decoder_3_out6, decoder_3_out7,
       decoder_4_out0, decoder_4_out1, decoder_4_out2, decoder_4_out3, decoder_4_out4, decoder_4_out5,
       decoder_4_out6, decoder_4_out7;

  Decoder #(.select(3)) decoder_1 (
    .out0(decoder_1_out0), .out1(decoder_1_out1), .out2(decoder_1_out2), .out3(decoder_1_out3),
    .out4(decoder_1_out4), .out5(decoder_1_out5), .out6(decoder_1_out6), .out7(decoder_1_out7), .sel(A),
    .en(enable));
  Decoder #(.select(3)) decoder_2 (
    .out0(decoder_2_out0), .out1(decoder_2_out1), .out2(decoder_2_out2), .out3(decoder_2_out3),
    .out4(decoder_2_out4), .out5(decoder_2_out5), .out6(decoder_2_out6), .out7(decoder_2_out7), .sel(B),
    .en(enable));
  Decoder #(.select(3)) decoder_3 (
    .out0(decoder_3_out0), .out1(decoder_3_out1), .out2(decoder_3_out2), .out3(decoder_3_out3),
    .out4(decoder_3_out4), .out5(decoder_3_out5), .out6(decoder_3_out6), .out7(decoder_3_out7), .sel(C),
    .en(enable));
  Decoder #(.select(3)) decoder_4 (
    .out0(decoder_4_out0), .out1(decoder_4_out1), .out2(decoder_4_out2), .out3(decoder_4_out3),
    .out4(decoder_4_out4), .out5(decoder_4_out5), .out6(decoder_4_out6), .out7(decoder_4_out7), .sel(D),
    .en(enable));
  or or_1 (O[7], decoder_1_out7, decoder_2_out7, decoder_3_out7, decoder_4_out7);
  or or_2 (O[6], decoder_1_out6, decoder_2_out6, decoder_3_out6, decoder_4_out6);
  or or_3 (O[5], decoder_1_out5, decoder_2_out5, decoder_3_out5, decoder_4_out5);
  or or_4 (O[4], decoder_1_out4, decoder_2_out4, decoder_3_out4, decoder_4_out4);
  or or_5 (O[3], decoder_1_out3, decoder_2_out3, decoder_3_out3, decoder_4_out3);
  or or_6 (O[2], decoder_1_out2, decoder_2_out2, decoder_3_out2, decoder_4_out2);
  or or_7 (O[1], decoder_1_out1, decoder_2_out1, decoder_3_out1, decoder_4_out1);
  or or_8 (O[0], decoder_1_out0, decoder_2_out0, decoder_3_out0, decoder_4_out0);
endmodule
