// Logisim project dispatch_test.circ as structural Verilog: 1 circuit, main circuit dispath_bit
module dispath_bit (
  input  start,
  input  clk,
  input  reset,
  input  [7:0] thread_count,
  input  [1:0] core_done,
  output [1:0] core_reset,
  output done,
  output [1:0] core_start,
  output [7:0] core_block_id_0,
  output [2:0] core_thread_count_0,
  output [7:0] core_block_id_1,
  output [2:0] core_thread_count_1
);

  wire and_1_out, and_4_out, and_9_out, and_10_out, and_11_out, and_12_out, and_13_out, comparator_1_gt,
       comparator_2_eq, comparator_3_eq, comparator_4_lt, CORE_RESET_BIT0, CORE_RESET_BIT1, not_1_out,
       not_2_out, not_3_out, or_1_out, or_2_out, or_3_out, or_4_out, or_5_out, or_6_out, or_7_out, or_8_out,
       or_9_out, or_10_out, or_11_out, start_execution_reg_q;
  wire [1:0] and_2_out, and_5_out, bitadder_1_out, multiplexer_1_out, multiplexer_2_out, multiplexer_3_out,
       multiplexer_4_out, multiplexer_6_out;
  wire [2:0] bit_extender_2_out, bit_extender_3_out;
  wire [7:0] adder_1_out, adder_2_out, adder_3_out, adder_4_out, bit_extender_1_out, blocks_dispatched_reg_q,
       blocks_done_reg_q, multiplexer_5_out, multiplexer_7_out, multiplexer_8_out, multiplier_1_out,
       multiplier_2_out, subtractor_1_out, subtractor_2_out, subtractor_3_out, subtractor_4_out, total_blocks;

  and and_1 (and_1_out, not_1_out, start);
  Multiplexer #(.width(2)) multiplexer_1 (
    .in0(2'b00), .in1({CORE_RESET_BIT1, CORE_RESET_BIT0}), .out(multiplexer_1_out), .sel(or_9_out));
  not not_1 (not_1_out, start_execution_reg_q);
  Register #(.width(1)) start_execution_reg (
    .D(not_1_out), .en(and_1_out), .clk(clk), .Q(start_execution_reg_q), .clr(reset));
  not not_2 (not_2_out, and_5_out[0]);
  or or_1 (or_1_out, not_2_out, multiplexer_1_out[0]);
  not not_3 (not_3_out, and_5_out[1]);
  or or_2 (or_2_out, and_1_out, reset);
  Multiplexer #(.width(2)) multiplexer_2 (.in0(2'b00), .in1(2'b11), .out(multiplexer_2_out), .sel(or_2_out));
  or or_3 (or_3_out, not_3_out, multiplexer_1_out[1]);
  and and_2 (and_2_out[0], CORE_RESET_BIT0, 1'b0);
  and and_3 (and_2_out[1], 1'b0, CORE_RESET_BIT1);
  Multiplexer #(.width(2)) multiplexer_3 (
    .in0(multiplexer_2_out), .in1(and_5_out), .out(multiplexer_3_out), .sel(or_8_out));
  or or_4 (or_4_out, and_5_out[0], or_9_out);
  or or_5 (or_5_out, and_5_out[1], or_9_out);
  Multiplexer #(.width(2)) multiplexer_4 (
    .in0(multiplexer_3_out), .in1(and_2_out), .out(multiplexer_4_out), .sel(or_6_out));
  assign bit_extender_1_out = {{6{1'b0}}, bitadder_1_out};  // Bit_Extender bit_extender_1
  BitAdder #(.width(2)) bitadder_1 (.in0(and_5_out), .out(bitadder_1_out));
  Register #(.width(1)) core_start_reg_bit0 (.D(or_1_out), .en(or_4_out), .clk(clk), .Q(core_start[0]), .clr(reset));
  Register #(.width(1)) core_start_reg_bit1 (.D(or_3_out), .en(or_5_out), .clk(clk), .Q(core_start[1]), .clr(reset));
  or or_6 (or_6_out, CORE_RESET_BIT0, CORE_RESET_BIT1);
  and and_4 (and_4_out, start, or_8_out);
  Multiplexer #(.width(8)) multiplexer_5 (
    .in0({8{1'b0}}), .in1(bit_extender_1_out), .out(multiplexer_5_out), .sel(or_8_out));
  Register #(.width(2)) core_reset_reg (.D(multiplexer_6_out), .en(or_7_out), .clk(clk), .Q(core_reset));  // open: clr
  Multiplexer #(.width(2)) multiplexer_6 (.in0(multiplexer_4_out), .in1(2'b11), .out(multiplexer_6_out), .sel(reset));
  or or_7 (or_7_out, or_6_out, or_2_out, and_4_out);
  and and_5 (and_5_out[0], core_start[0], core_done[0]);
  and and_6 (and_5_out[1], core_start[1], core_done[1]);
  or or_8 (or_8_out, and_5_out[0], and_5_out[1]);
  Adder adder_1 (.a(blocks_dispatched_reg_q), .b({8{1'b0}}), .out(adder_1_out), .cin(and_10_out));  // open: cout
  and and_7 (CORE_RESET_BIT0, start, core_reset[0]);
  and and_8 (CORE_RESET_BIT1, core_reset[1], start);
  and and_9 (and_9_out, start, or_8_out);
  or or_9 (or_9_out, and_12_out, and_13_out);
  Adder adder_2 (.a(adder_1_out), .b({8{1'b0}}), .out(adder_2_out), .cin(and_11_out));  // open: cout
  and and_10 (and_10_out, CORE_RESET_BIT0, comparator_4_lt);
  and and_11 (and_11_out, comparator_4_lt, CORE_RESET_BIT1);
  Adder adder_3 (.a(blocks_done_reg_q), .b(multiplexer_5_out), .out(adder_3_out));  // open: cin, cout
  and and_12 (and_12_out, CORE_RESET_BIT1, comparator_1_gt);
  and and_13 (and_13_out, comparator_1_gt, CORE_RESET_BIT0);
  Adder adder_4 (.a(thread_count), .b(8'h3), .out(adder_4_out));  // open: cin, cout
  Register blocks_done_reg (.D(adder_3_out), .en(and_9_out), .clk(clk), .Q(blocks_done_reg_q), .clr(reset));
  Shifter #(.shift("lr")) shifter_1 (.in(adder_4_out), .\dist (3'b010), .out(total_blocks));
  Register blocks_dispatched_reg (
    .D(adder_2_out), .en(comparator_4_lt), .clk(clk), .Q(blocks_dispatched_reg_q), .clr(reset));
  Register core_block_id_reg_1 (.D(adder_2_out), .en(and_11_out), .clk(clk), .Q(core_block_id_1), .clr(reset));
  Register core_block_id_reg_0 (.D(adder_1_out), .en(and_10_out), .clk(clk), .Q(core_block_id_0), .clr(reset));
  Multiplier multiplier_1 (.a(8'h4), .b(adder_2_out), .out(multiplier_1_out));  // open: cin, cout
  Multiplier multiplier_2 (.a(adder_1_out), .b(8'h4), .out(multiplier_2_out));  // open: cin, cout
  Subtractor subtractor_1 (.a(total_blocks), .b(multiplier_1_out), .out(subtractor_1_out));  // open: bin, bout
  Comparator comparator_1 (.a(total_blocks), .b(blocks_done_reg_q), .gt(comparator_1_gt), .eq(done));  // open: lt
  Comparator comparator_2 (.a(adder_1_out), .b(subtractor_2_out), .eq(comparator_2_eq));  // open: gt, lt
  Subtractor subtractor_2 (.a(total_blocks), .b(8'h1), .out(subtractor_2_out));  // open: bin, bout
  Subtractor subtractor_3 (.a(total_blocks), .b(multiplier_2_out), .out(subtractor_3_out));  // open: bin, bout
  or or_10 (or_10_out, and_10_out, reset);
  Comparator comparator_3 (.a(adder_2_out), .b(subtractor_4_out), .eq(comparator_3_eq));  // open: gt, lt
  Subtractor subtractor_4 (.a(total_blocks), .b(8'h1), .out(subtractor_4_out));  // open: bin, bout
  or or_11 (or_11_out, and_11_out, reset);
  Comparator comparator_4 (.a(blocks_dispatched_reg_q), .b(total_blocks), .lt(comparator_4_lt));  // open: gt, eq
  Multiplexer #(.width(8)) multiplexer_7 (
    .in0(8'h4), .in1(subtractor_3_out), .out(multiplexer_7_out), .sel(comparator_2_eq));
  Multiplexer #(.width(8)) multiplexer_8 (
    .in0(8'h4), .in1(subtractor_1_out), .out(multiplexer_8_out), .sel(comparator_3_eq));
  Register #(.width(3)) core_thread_count_reg_0 (
    .D(bit_extender_2_out), .en(or_10_out), .clk(clk), .Q(core_thread_count_0));  // open: clr
  Bit_Extender #(.out_width(3)) bit_extender_2 (.in(multiplexer_7_out), .out(bit_extender_2_out));
  Register #(.width(3)) core_thread_count_reg_1 (
    .D(bit_extender_3_out), .en(or_11_out), .clk(clk), .Q(core_thread_count_1));  // open: clr
  Bit_Extender #(.out_width(3)) bit_extender_3 (.in(multiplexer_8_out), .out(bit_extender_3_out));
endmodule
