// Logisim project dispatch_test_old.circ as structural Verilog: 4 circuits, main circuit main
module main (
  input  [7:0] in_1,
  input  in_2,
  input  in_3,
  input  [7:0] thread_count,
  input  [7:0] in_5,
  output [7:0] out_6,
  output [7:0] out_7,
  output [3:0] out_8
);

  wire and_1_out;
  wire [7:0] adder_1_out, adder_2_out, adder_3_out;

  Adder adder_1 (.a(in_1), .b(8'h1), .out(adder_1_out));  // open: cin, cout
  Adder adder_2 (.a(adder_1_out), .b(8'h1), .out(adder_2_out));  // open: cin, cout
  Multiplexer #(.width(8)) multiplexer_1 (.in0(adder_1_out), .in1(adder_2_out), .out(out_6), .sel(and_1_out));
  and and_1 (and_1_out, in_2, in_3);
  BitAdder bitadder_1 (.in0(in_5), .out(out_8));
  Adder adder_3 (.a(thread_count), .b(8'h3), .out(adder_3_out));  // open: cin, cout
  Shifter #(.shift("lr")) shifter_1 (.in(adder_3_out), .\dist (3'b010), .out(out_7));
endmodule

module dispatch (
  input  start,
  input  clk,
  input  reset,
  input  [7:0] thread_count
);

  wire and_1_out, comparator_1_eq, comparator_2_lt, not_1_out, or_1_out, or_2_out, or_3_out, or_4_out,
       or_5_out, or_6_out, start_execution_reg_q;
  wire [1:0] and_2_out, core_done_reg_q, core_reset_reg_q, core_start_reg_q, multiplexer_1_out,
       multiplexer_3_out, multiplexer_4_out, multiplexer_6_out, not_2_out;
  wire [2:0] multiplexer_5_out;
  wire [7:0] adder_1_out, adder_2_out, blocks_dispatched_reg_q, blocks_done_reg_q, multiplexer_2_out,
       shifter_1_out;

  Multiplexer #(.width(2)) multiplexer_1 (.in1(and_2_out), .out(multiplexer_1_out), .sel(or_1_out));  // open: in0
  Register #(.width(2)) core_start_reg (
    .D(multiplexer_1_out), .en(or_1_out), .clk(clk), .Q(core_start_reg_q), .clr(reset));
  Register #(.width(2)) core_done_reg (.clk(clk), .Q(core_done_reg_q), .clr(reset));  // open: D, en
  not not_1 (not_1_out, start_execution_reg_q);
  and and_1 (and_1_out, not_1_out, start);
  Register #(.width(1)) start_execution_reg (
    .D(and_1_out), .en(and_1_out), .clk(clk), .Q(start_execution_reg_q), .clr(reset));
  and and_2 (and_2_out[0], core_start_reg_q[0], core_done_reg_q[0]);
  and and_3 (and_2_out[1], core_start_reg_q[1], core_done_reg_q[1]);
  or or_1 (or_1_out, and_2_out[0], and_2_out[1]);
  or or_2 (or_2_out, and_1_out, reset);
  Multiplexer #(.width(8)) multiplexer_2 (.in0({8{1'b0}}), .in1(8'h1), .out(multiplexer_2_out), .sel(or_1_out));
  Multiplexer #(.width(2)) multiplexer_3 (.in0(2'b00), .in1(2'b11), .out(multiplexer_3_out), .sel(or_2_out));
  Register core_block_id_0 (.clr(reset));  // open: D, en, clk, Q
  Register core_block_id_1 (.clr(reset));  // open: D, en, clk, Q
  Adder adder_1 (.a(thread_count), .b(8'h3), .out(adder_1_out));  // open: cin, cout
  Adder adder_2 (.a(blocks_done_reg_q), .b(multiplexer_2_out), .out(adder_2_out));  // open: cin, cout
  Shifter #(.shift("lr")) shifter_1 (.in(adder_1_out), .\dist (3'b010), .out(shifter_1_out));
  Register blocks_done_reg (.D(adder_2_out), .Q(blocks_done_reg_q), .clr(reset));  // open: en, clk
  Multiplexer #(.width(2)) multiplexer_4 (
    .in0(multiplexer_3_out), .in1(and_2_out), .out(multiplexer_4_out), .sel(or_1_out));
  not not_2 (not_2_out[0], core_reset_reg_q[0]);
  not not_3 (not_2_out[1], core_reset_reg_q[1]);
  or or_3 (or_3_out, or_2_out, or_1_out);
  Multiplexer #(.width(3)) multiplexer_5 (.in0(3'b000), .in1(3'b100), .out(multiplexer_5_out), .sel(reset));
  buf or_4 (or_4_out, reset);  // OR_Gate
  Comparator comparator_1 (.a(shifter_1_out), .b(blocks_done_reg_q), .eq(comparator_1_eq));  // open: gt, lt
  Multiplexer #(.width(2)) multiplexer_6 (
    .in0(multiplexer_4_out), .in1(not_2_out), .out(multiplexer_6_out), .sel(or_6_out));
  Register #(.width(3)) core_thread_count_reg_0 (.D(multiplexer_5_out), .en(or_4_out), .clk(clk));  // open: Q, clr
  Register #(.width(3)) core_thread_count_reg_1 (.D(multiplexer_5_out), .en(or_4_out), .clk(clk));  // open: Q, clr
  or or_5 (or_5_out, or_6_out, or_3_out);
  Register #(.width(1)) done_reg (.D(comparator_1_eq), .en(comparator_1_eq), .clr(reset));  // open: clk, Q
  Register #(.width(2)) core_reset_reg (
    .D(multiplexer_6_out), .en(or_5_out), .clk(clk), .Q(core_reset_reg_q));  // open: clr
  Register blocks_dispatched_reg (.Q(blocks_dispatched_reg_q));  // open: D, en, clk, clr
  or or_6 (or_6_out, core_reset_reg_q[0], core_reset_reg_q[1]);
  Comparator comparator_2 (.a(blocks_dispatched_reg_q), .b(shifter_1_out), .lt(comparator_2_lt));  // open: gt, eq
endmodule

module dispatch_new (
  input  start,
  input  clk,
  input  reset,
  input  [7:0] thread_count,
  input  [1:0] core_done
);

  wire and_1_out, comparator_1_eq, comparator_2_gt, not_1_out, or_1_out, or_2_out, or_3_out, or_4_out,
       or_5_out, or_6_out, start_execution_reg_q;
  wire [1:0] and_3_out, core_reset_reg_q, core_start_reg_q, multiplexer_1_out, multiplexer_2_out,
       multiplexer_3_out, multiplexer_4_out, multiplexer_5_out, not_2_out, not_4_out;
  wire [2:0] multiplexer_7_out;
  wire [7:0] adder_1_out, adder_2_out, adder_3_out, blocks_dispatched_reg_q, blocks_done_reg_q,
       core_block_id_0_q, core_block_id_1_q, multiplexer_6_out, shifter_1_out;

  and and_1 (and_1_out, not_1_out, start);
  not not_1 (not_1_out, start_execution_reg_q);
  Register #(.width(1)) start_execution_reg (
    .D(and_1_out), .en(and_1_out), .clk(reset), .Q(start_execution_reg_q));  // open: clr
  or or_1 (or_1_out, and_1_out, reset);
  Multiplexer #(.width(2)) multiplexer_1 (.in0(2'b00), .in1(2'b11), .out(multiplexer_1_out), .sel(or_1_out));
  not not_2 (not_2_out[0], core_reset_reg_q[0]);
  not not_3 (not_2_out[1], core_reset_reg_q[1]);
  Multiplexer #(.width(2)) multiplexer_2 (
    .in0(multiplexer_1_out), .in1(and_3_out), .out(multiplexer_2_out), .sel(or_5_out));
  not not_4 (not_4_out[0], and_3_out[1]);
  not not_5 (not_4_out[1], and_3_out[0]);
  Multiplexer #(.width(2)) multiplexer_3 (.in0(2'b00), .in1(2'b11), .out(multiplexer_3_out), .sel(comparator_2_gt));
  Multiplexer #(.width(2)) multiplexer_4 (
    .in0(multiplexer_2_out), .in1(not_2_out), .out(multiplexer_4_out), .sel(or_4_out));
  Multiplexer #(.width(2)) multiplexer_5 (
    .in0(multiplexer_3_out), .in1(not_4_out), .out(multiplexer_5_out), .sel(or_5_out));
  Register #(.width(2)) core_reset_reg (
    .D(multiplexer_4_out), .en(or_2_out), .clk(clk), .Q(core_reset_reg_q), .clr(reset));
  or or_2 (or_2_out, or_4_out, or_1_out, or_5_out);
  Register #(.width(2)) core_start_reg (
    .D(multiplexer_5_out), .en(or_3_out), .clk(clk), .Q(core_start_reg_q), .clr(reset));
  or or_3 (or_3_out, or_5_out, comparator_2_gt);
  Adder adder_1 (.a(thread_count), .b(8'h3), .out(adder_1_out));  // open: cin, cout
  or or_4 (or_4_out, core_reset_reg_q[0], core_reset_reg_q[1]);
  and and_2 (and_3_out[1], core_start_reg_q[0], core_done[0]);
  and and_3 (and_3_out[0], core_start_reg_q[1], core_done[1]);
  or or_5 (or_5_out, and_3_out[1], and_3_out[0]);
  Shifter #(.shift("lr")) shifter_1 (.in(adder_1_out), .\dist (3'b010), .out(shifter_1_out));
  Multiplexer #(.width(8)) multiplexer_6 (.in0({8{1'b0}}), .in1(8'h1), .out(multiplexer_6_out), .sel(and_3_out[1]));
  Register blocks_done_reg (.D(adder_2_out), .clk(clk), .Q(blocks_done_reg_q), .clr(reset));  // open: en
  Adder adder_2 (.a(blocks_done_reg_q), .b(multiplexer_6_out), .out(adder_2_out), .cin(and_3_out[0]));  // open: cout
  Register blocks_dispatched_reg (
    .D(adder_3_out), .en(comparator_2_gt), .clk(clk), .Q(blocks_dispatched_reg_q), .clr(reset));
  Adder adder_3 (.a(blocks_dispatched_reg_q), .b(8'h1), .out(adder_3_out));  // open: cin, cout
  Comparator comparator_1 (.a(shifter_1_out), .b(blocks_done_reg_q), .eq(comparator_1_eq));  // open: gt, lt
  Comparator comparator_2 (.a(shifter_1_out), .b(blocks_dispatched_reg_q), .gt(comparator_2_gt));  // open: eq, lt
  Register #(.width(1)) done_reg (.D(comparator_1_eq), .en(comparator_1_eq), .clk(clk), .clr(reset));  // open: Q
  Register core_block_id_0 (.clk(clk), .Q(core_block_id_0_q), .clr(reset));  // open: D, en
  Register core_block_id_1 (.clk(clk), .Q(core_block_id_1_q), .clr(reset));  // open: D, en
  Comparator comparator_3 (.a(core_block_id_0_q), .b(core_block_id_1_q));  // open: gt, eq, lt
  Multiplexer #(.width(3)) multiplexer_7 (.in0(3'b000), .in1(3'b100), .out(multiplexer_7_out), .sel(reset));
  buf or_6 (or_6_out, reset);  // OR_Gate
  Register #(.width(3)) core_thread_count_reg_0 (.D(multiplexer_7_out), .en(or_6_out), .clk(clk));  // open: Q, clr
  Register #(.width(3)) core_thread_count_reg_1 (.D(multiplexer_7_out), .en(or_6_out), .clk(clk));  // open: Q, clr
endmodule

module dispath_bit (
  input  [7:0] thread_count,
  input  start,
  input  clk,
  input  reset,
  input  [1:0] core_done,
  output done,
  output [1:0] core_reset,
  output [2:0] core_thread_count_0,
  output [1:0] core_start,
  output [2:0] core_thread_count_1,
  output [7:0] core_block_id_0,
  output [7:0] core_block_id_1
);

  wire and_1_out, and_2_out, and_9_out, and_10_out, and_11_out, and_12_out, and_13_out, comparator_1_gt,
       comparator_2_gt, comparator_3_eq, comparator_4_eq, not_1_out, or_1_out, or_2_out, or_3_out, or_4_out,
       or_5_out, or_6_out, or_7_out, or_8_out, or_9_out, start_execution_reg_q;
  wire [1:0] and_3_out, and_5_out, and_7_out, bitadder_1_out, multiplexer_1_out, multiplexer_2_out,
       multiplexer_3_out, multiplexer_4_out, multiplexer_5_out, multiplexer_7_out;
  wire [2:0] bit_extender_2_out, bit_extender_3_out;
  wire [7:0] adder_1_out, adder_2_out, adder_3_out, adder_4_out, bit_extender_1_out, blocks_dispatched_reg_q,
       blocks_done_reg_q, multiplexer_6_out, multiplexer_8_out, multiplexer_9_out, multiplier_1_out,
       multiplier_2_out, shifter_1_out, subtractor_1_out, subtractor_2_out, subtractor_3_out,
       subtractor_4_out;

  and and_1 (and_1_out, not_1_out, start);
  not not_1 (not_1_out, start_execution_reg_q);
  Register #(.width(1)) start_execution_reg (
    .D(not_1_out), .en(and_1_out), .clk(clk), .Q(start_execution_reg_q), .clr(reset));
  or or_1 (or_1_out, and_1_out, reset);
  and and_2 (and_2_out, start, or_6_out);
  Multiplexer #(.width(2)) multiplexer_1 (.in0(2'b00), .in1(2'b11), .out(multiplexer_1_out), .sel(or_1_out));
  and and_3 (and_3_out[0], core_reset[0], 1'b0);
  and and_4 (and_3_out[1], 1'b0, core_reset[1]);
  Multiplexer #(.width(2)) multiplexer_2 (
    .in0(multiplexer_3_out), .in1(and_3_out), .out(multiplexer_2_out), .sel(or_5_out));
  Multiplexer #(.width(2)) multiplexer_3 (
    .in0(multiplexer_1_out), .in1(and_7_out), .out(multiplexer_3_out), .sel(or_6_out));
  and and_5 (and_5_out[0], and_7_out[0], 1'b0);
  and and_6 (and_5_out[1], 1'b0, and_7_out[1]);
  or or_2 (or_2_out, reset, and_1_out);
  Register #(.width(2)) core_reset_reg (.D(multiplexer_4_out), .en(or_3_out), .clk(clk), .Q(core_reset));  // open: clr
  Multiplexer #(.width(2)) multiplexer_4 (
    .in0(multiplexer_2_out), .in1(2'b11), .out(multiplexer_4_out), .sel(or_2_out));
  or or_3 (or_3_out, or_5_out, or_1_out, and_2_out);
  Multiplexer #(.width(2)) multiplexer_5 (
    .in0(multiplexer_7_out), .in1(and_5_out), .out(multiplexer_5_out), .sel(or_6_out));
  Register #(.width(2)) core_start_reg (.D(multiplexer_5_out), .en(or_4_out), .clk(clk), .Q(core_start), .clr(reset));
  or or_4 (or_4_out, or_6_out, or_7_out);
  and and_7 (and_7_out[0], core_start[0], core_done[0]);
  and and_8 (and_7_out[1], core_start[1], core_done[1]);
  or or_5 (or_5_out, core_reset[0], core_reset[1]);
  BitAdder #(.width(2)) bitadder_1 (.in0(and_7_out), .out(bitadder_1_out));
  or or_6 (or_6_out, and_7_out[0], and_7_out[1]);
  assign bit_extender_1_out = {{6{1'b0}}, bitadder_1_out};  // Bit_Extender bit_extender_1
  Adder adder_1 (.a(blocks_done_reg_q), .b(multiplexer_6_out), .out(adder_1_out));  // open: cin, cout
  Multiplexer #(.width(8)) multiplexer_6 (
    .in0({8{1'b0}}), .in1(bit_extender_1_out), .out(multiplexer_6_out), .sel(or_6_out));
  and and_9 (and_9_out, or_6_out, start);
  Multiplexer #(.width(2)) multiplexer_7 (.in0(2'b00), .in1(core_reset), .out(multiplexer_7_out), .sel(or_7_out));
  Adder adder_2 (.a(thread_count), .b(8'h3), .out(adder_2_out));  // open: cin, cout
  Register blocks_done_reg (.D(adder_1_out), .en(and_9_out), .clk(clk), .Q(blocks_done_reg_q), .clr(reset));
  and and_10 (and_10_out, comparator_1_gt, core_reset[1]);
  and and_11 (and_11_out, core_reset[0], comparator_1_gt);
  and and_12 (and_12_out, core_reset[0], comparator_2_gt);
  and and_13 (and_13_out, core_reset[1], comparator_2_gt);
  Shifter #(.shift("lr")) shifter_1 (.in(adder_2_out), .\dist (3'b010), .out(shifter_1_out));
  or or_7 (or_7_out, and_10_out, and_11_out);
  Comparator comparator_1 (.a(shifter_1_out), .b(blocks_done_reg_q), .gt(comparator_1_gt), .eq(done));  // open: lt
  Adder adder_3 (.a(blocks_dispatched_reg_q), .b({8{1'b0}}), .out(adder_3_out), .cin(and_12_out));  // open: cout
  Adder adder_4 (.a(adder_3_out), .b({8{1'b0}}), .out(adder_4_out), .cin(and_13_out));  // open: cout
  Register core_block_id_reg_2 (.D(adder_3_out), .en(and_12_out), .clk(clk), .Q(core_block_id_0), .clr(reset));
  Register core_block_id_reg_3 (.D(adder_4_out), .en(and_13_out), .clk(clk), .Q(core_block_id_1), .clr(reset));
  Register blocks_dispatched_reg (
    .D(adder_4_out), .en(comparator_2_gt), .clk(clk), .Q(blocks_dispatched_reg_q), .clr(reset));
  Comparator comparator_2 (.a(shifter_1_out), .b(blocks_dispatched_reg_q), .gt(comparator_2_gt));  // open: eq, lt
  Subtractor subtractor_1 (.a(shifter_1_out), .b(8'h1), .out(subtractor_1_out));  // open: bin, bout
  Subtractor subtractor_2 (.a(shifter_1_out), .b(8'h1), .out(subtractor_2_out));  // open: bin, bout
  Comparator comparator_3 (.a(adder_3_out), .b(subtractor_1_out), .eq(comparator_3_eq));  // open: gt, lt
  Multiplexer #(.width(8)) multiplexer_8 (
    .in0(8'h4), .in1(subtractor_3_out), .out(multiplexer_8_out), .sel(comparator_3_eq));
  Comparator comparator_4 (.a(adder_4_out), .b(subtractor_2_out), .eq(comparator_4_eq));  // open: gt, lt
  Multiplexer #(.width(8)) multiplexer_9 (
    .in0(8'h4), .in1(subtractor_4_out), .out(multiplexer_9_out), .sel(comparator_4_eq));
  Multiplier multiplier_1 (.a(adder_3_out), .b(8'h4), .out(multiplier_1_out));  // open: cin, cout
  Bit_Extender #(.out_width(3)) bit_extender_2 (.in(multiplexer_8_out), .out(bit_extender_2_out));
  Multiplier multiplier_2 (.a(adder_4_out), .b(8'h4), .out(multiplier_2_out));  // open: cin, cout
  Bit_Extender #(.out_width(3)) bit_extender_3 (.in(multiplexer_9_out), .out(bit_extender_3_out));
  Subtractor subtractor_3 (.a(shifter_1_out), .b(multiplier_1_out), .out(subtractor_3_out));  // open: bin, bout
  Subtractor subtractor_4 (.a(shifter_1_out), .b(multiplier_2_out), .out(subtractor_4_out));  // open: bin, bout
  Register #(.width(3)) core_thread_count_reg_0 (
    .D(bit_extender_2_out), .en(or_8_out), .clk(reset), .Q(core_thread_count_0));  // open: clr
  or or_8 (or_8_out, and_12_out, reset);
  Register #(.width(3)) core_thread_count_reg_1 (
    .D(bit_extender_3_out), .en(or_9_out), .clk(reset), .Q(core_thread_count_1));  // open: clr
  or or_9 (or_9_out, and_13_out, reset);
endmodule
