// Logisim project lsu_test.circ as structural Verilog: 2 circuits, main circuit main
module main (
  input  enable,
  input  decoded_mem_read_enable,
  input  [2:0] core_state,
  input  reset,
  input  mem_write_ready,
  input  [1:0] lus_state
);

  wire and_1_out, and_2_out, decoder_1_out3, decoder_1_out6, decoder_2_out1;
  wire [1:0] bit_extender_1_out, multiplexer_1_out, multiplexer_2_out, multiplexer_3_out;

  Decoder #(.select(3)) decoder_1 (
    .out3(decoder_1_out3), .out6(decoder_1_out6), .sel(core_state));  // open: out0, out1, out2, out4, out5, out7, en
  assign bit_extender_1_out = {{1{1'b0}}, decoder_1_out3};  // Bit_Extender bit_extender_1
  Multiplexer #(.width(2)) multiplexer_1 (.in0(2'b10), .in1(2'b11), .out(multiplexer_1_out), .sel(mem_write_ready));
  Multiplexer #(.width(2)) multiplexer_2 (.in0(2'b11), .in1(2'b00), .out(multiplexer_2_out), .sel(decoder_1_out6));
  and and_1 (and_1_out, enable, decoded_mem_read_enable);
  Multiplexer #(.enable("true"), .select(2), .width(2)) multiplexer_3 (
    .in0(bit_extender_1_out), .in1(2'b10), .in2(multiplexer_1_out), .in3(multiplexer_2_out),
    .out(multiplexer_3_out), .sel(lus_state), .en(and_1_out));
  Register #(.width(2)) lsu_state_reg (.D(multiplexer_3_out), .Q(lus_state), .clr(reset));  // open: en, clk
  Register register_1 (.clr(reset));  // open: D, en, clk, Q
  Register register_2 (.clr(reset));  // open: D, en, clk, Q
  Register lsu_out_reg ();  // open: D, en, clk, Q, clr
  Decoder #(.select(2)) decoder_2 (.out1(decoder_2_out1), .sel(lus_state));  // open: out0, out2, out3, en
  and and_2 (and_2_out, and_1_out, decoder_2_out1);
  Register #(.width(1)) mem_read_valid_reg (.D(and_2_out), .en(and_1_out), .clr(reset));  // open: clk, Q
  Register mem_read_address_reg (.clr(reset));  // open: D, en, clk, Q
endmodule

module lsu_mod (
  input  [7:0] rt,
  input  [7:0] rs,
  input  [7:0] mem_read_data,
  input  enable,
  input  decoded_mem_read_enable,
  input  decoded_mem_write_enable,
  input  [2:0] core_state,
  input  mem_write_ready,
  input  mem_read_ready,
  input  reset,
  input  clk,
  output [7:0] mem_write_data,
  output [7:0] mem_write_address,
  output mem_write_valid,
  output [7:0] mem_read_address,
  output mem_read_valid,
  output [7:0] lsu_out,
  output [1:0] lus_state
);

  wire and_1_out, and_2_out, and_3_out, and_4_out, and_5_out, and_6_out, decoder_1_out1, decoder_1_out2,
       decoder_2_out3, decoder_2_out6, or_1_out, or_2_out, or_3_out, or_4_out;
  wire [1:0] bit_extender_1_out, multiplexer_1_out, multiplexer_2_out, multiplexer_3_out;

  or or_1 (or_1_out, mem_write_ready, mem_read_ready);
  Decoder #(.select(2)) decoder_1 (
    .out1(decoder_1_out1), .out2(decoder_1_out2), .sel(lus_state));  // open: out0, out3, en
  Decoder #(.select(3)) decoder_2 (
    .out3(decoder_2_out3), .out6(decoder_2_out6), .sel(core_state));  // open: out0, out1, out2, out4, out5, out7, en
  and and_1 (and_1_out, decoded_mem_write_enable, decoder_1_out1);
  and and_2 (and_2_out, decoder_1_out1, decoded_mem_read_enable);
  and and_3 (and_3_out, decoder_1_out2, decoded_mem_read_enable);
  or or_2 (or_2_out, decoded_mem_read_enable, decoded_mem_write_enable);
  assign bit_extender_1_out = {{1{1'b0}}, decoder_2_out3};  // Bit_Extender bit_extender_1
  Multiplexer #(.width(2)) multiplexer_1 (.in0(2'b11), .in1(2'b00), .out(multiplexer_1_out), .sel(decoder_2_out6));
  and and_4 (and_4_out, mem_write_ready, decoder_1_out2);
  and and_5 (and_5_out, and_3_out, mem_read_ready);
  and and_6 (and_6_out, enable, or_2_out);
  Multiplexer #(.width(2)) multiplexer_2 (.in0(2'b10), .in1(2'b11), .out(multiplexer_2_out), .sel(or_1_out));
  Register #(.width(1)) mem_write_valid_reg (
    .D(and_1_out), .en(and_1_out), .clk(clk), .Q(mem_write_valid), .clr(or_3_out));
  or or_3 (or_3_out, and_4_out, reset);
  Register #(.width(1)) mem_read_valid_reg (
    .D(and_2_out), .en(and_2_out), .clk(clk), .Q(mem_read_valid), .clr(or_4_out));
  or or_4 (or_4_out, and_5_out, reset);
  Multiplexer #(.enable("true"), .select(2), .width(2)) multiplexer_3 (
    .in0(bit_extender_1_out), .in1(2'b10), .in2(multiplexer_2_out), .in3(multiplexer_1_out),
    .out(multiplexer_3_out), .sel(lus_state), .en(and_6_out));
  Register #(.width(2)) lsu_state_reg (.D(multiplexer_3_out), .en(and_6_out), .clk(clk), .Q(lus_state), .clr(reset));
  Register mem_write_data_reg (.D(rt), .en(and_1_out), .clk(clk), .Q(mem_write_data), .clr(reset));
  Register mem_write_address_reg (.D(rs), .en(and_1_out), .clk(clk), .Q(mem_write_address), .clr(reset));
  Register mem_read_address_reg (.D(rs), .en(and_2_out), .clk(clk), .Q(mem_read_address), .clr(reset));
  Register lsu_out_reg (.D(mem_read_data), .en(and_5_out), .clk(clk), .Q(lsu_out), .clr(reset));
endmodule
