// Logisim project my_alu_2.circ as structural Verilog
module main (
  input  in_1
);

  scheduler scheduler_1 (.clk(in_1));  // open: next_pc_1, next_pc_2, next_pc_3, next_pc_4, reset, decoded_ret, start, fetcher_state, lsu_state, current_pc_1, current_pc_2, current_pc_3, current_pc_4, core_state, done
  lsu_mod lsu_mod_1 (.clk(in_1));  // open: rt, rs, mem_read_data, enable, decoded_mem_read_enable, decoded_mem_write_enable, core_state, mem_write_ready, mem_read_ready, reset, mem_write_data, mem_write_address, mem_write_valid, mem_read_address, mem_read_valid, lsu_out, lus_state
  pc_test pc_test_1 (.clk(in_1));  // open: alu_out, decoded_nzp_write_enable, core_state, decoded_nzp, enable, decoded_pc_mux, current_pc, decoded_immediate, reset, next_pc
endmodule

module scheduler (
  input  [7:0] next_pc_1,
  input  [7:0] next_pc_2,
  input  [7:0] next_pc_3,
  input  [7:0] next_pc_4,
  input  reset,
  input  clk,
  input  decoded_ret,
  input  start,
  input  [2:0] fetcher_state,
  input  [7:0] lsu_state,
  output [7:0] current_pc_1,
  output [7:0] current_pc_2,
  output [7:0] current_pc_3,
  output [7:0] current_pc_4,
  output [2:0] core_state,
  output done
);

  wire and_1_out, and_2_out, comparator_1_eq, comparator_2_eq, multiplexer_1_out, not_1_out, not_2_out,
       not_3_out, or_1_out, or_2_out, or_3_out, or_4_out, or_5_out, or_6_out, or_7_out;
  wire [2:0] adder_1_out, bit_extender_1_out, multiplexer_2_out;

  or or_1 (or_1_out, lsu_state[0], lsu_state[1]);
  or or_2 (or_2_out, lsu_state[2], lsu_state[3]);
  or or_3 (or_3_out, lsu_state[4], lsu_state[5]);
  or or_4 (or_4_out, lsu_state[6], lsu_state[7]);
  or or_5 (or_5_out, or_1_out, or_2_out);
  or or_6 (or_6_out, or_3_out, or_4_out);
  or or_7 (or_7_out, or_5_out, or_6_out);
  not not_1 (not_1_out, or_7_out);
  Comparator #(.width(3)) comparator_1 (.a(fetcher_state), .b(3'b010), .eq(comparator_1_eq));  // open: gt, lt
  assign bit_extender_1_out = {{2{1'b0}}, multiplexer_1_out};  // Bit_Extender bit_extender_1
  Multiplexer #(.select(3)) multiplexer_1 (
    .in0(start), .in1(comparator_1_eq), .in2(1'b1), .in3(1'b1), .in4(not_1_out), .in5(1'b1), .in6(and_2_out),
    .in7(1'b0), .out(multiplexer_1_out), .sel(core_state));
  Adder #(.width(3)) adder_1 (.a(core_state), .b(bit_extender_1_out), .out(adder_1_out));  // open: cin, cout
  and and_1 (and_1_out, comparator_2_eq, not_2_out);
  Comparator #(.width(3)) comparator_2 (.a(core_state), .b(3'b110), .eq(comparator_2_eq));  // open: gt, lt
  Multiplexer #(.width(3)) multiplexer_2 (.in0(adder_1_out), .in1(3'b001), .out(multiplexer_2_out), .sel(and_1_out));
  not not_2 (not_2_out, and_2_out);
  and and_2 (and_2_out, comparator_2_eq, decoded_ret);
  Register current_pc_reg_1 (.D(next_pc_1), .en(and_1_out), .clk(clk), .Q(current_pc_1));  // open: clr
  Register current_pc_reg_2 (.D(next_pc_2), .en(and_1_out), .clk(clk), .Q(current_pc_2));  // open: clr
  Register current_pc_reg_3 (.D(next_pc_3), .en(and_1_out), .clk(clk), .Q(current_pc_3));  // open: clr
  Register current_pc_reg_4 (.D(next_pc_4), .en(and_1_out), .clk(clk), .Q(current_pc_4), .clr(reset));
  Register #(.width(3)) core_state_reg (.D(multiplexer_2_out), .en(not_3_out), .clk(clk), .Q(core_state), .clr(reset));
  not not_3 (not_3_out, reset);
  or or_8 (done, reset, and_2_out);
endmodule

module dlv (
  input  [7:0] divisor,
  input  [7:0] dividend,
  output [7:0] cout,
  output err
);

  wire [31:0] fpdivider_1_out, inttofp_1_p2, inttofp_2_p2;

  // IntToFP inttofp_1: pin names not known; wires that end beside it: divisor, inttofp_1_p2
  FPDivider fpdivider_1 (.a(inttofp_1_p2), .b(inttofp_2_p2), .out(fpdivider_1_out));
  // IntToFP inttofp_2: pin names not known; wires that end beside it: dividend, inttofp_2_p2, err
  // FPToInt fptoint_1: pin names not known; wires that end beside it: fpdivider_1_out, err, cout

  // Notes on the sheet:
  //   err: pull=down
endmodule

module alu (
  input  decoded_alu_output_mux,
  input  [7:0] rs,
  input  [7:0] rt,
  input  [1:0] decoded_alu_arithmetic_mux,
  input  reset,
  input  [2:0] core_state,
  input  enable,
  input  clk,
  output [7:0] alu_out
);

  wire decoder_1_out5, not_1_out;
  wire [2:0] comparator_1_lt;
  wire [7:0] adder_1_out, dlv_1_cout, multiplexer_1_out, multiplexer_2_out, multiplier_1_out,
       subtractor_1_out;

  Decoder #(.select(3)) decoder_1 (
    .out5(decoder_1_out5), .sel(core_state));  // open: out0, out1, out2, out3, out4, out6, out7, en
  Adder adder_1 (.a(rs), .b(rt), .out(adder_1_out));  // open: cin, cout
  Subtractor subtractor_1 (.a(rs), .b(rt), .out(subtractor_1_out));  // open: bin, bout
  Multiplier multiplier_1 (.a(rs), .b(rt), .out(multiplier_1_out));  // open: cin, cout
  dlv dlv_1 (.divisor(rs), .dividend(rt), .cout(dlv_1_cout));  // open: err
  Comparator comparator_1 (
    .a(subtractor_1_out), .b({8{1'b0}}), .gt(comparator_1_lt[2]), .eq(comparator_1_lt[1]),
    .lt(comparator_1_lt[0]));
  not not_1 (not_1_out, decoded_alu_output_mux);
  Multiplexer #(.enable("true"), .select(2), .width(8)) multiplexer_1 (
    .in0(adder_1_out), .in1(subtractor_1_out), .in2(multiplier_1_out), .in3(dlv_1_cout),
    .out(multiplexer_1_out), .sel(decoded_alu_arithmetic_mux), .en(decoder_1_out5));
  Multiplexer #(.width(8)) multiplexer_2 (
    .in0({{5{1'b0}}, comparator_1_lt}), .in1(multiplexer_1_out), .out(multiplexer_2_out), .sel(not_1_out));
  Register alu_out_reg (.D(multiplexer_2_out), .en(enable), .clk(clk), .Q(alu_out), .clr(reset));

  // Notes on the sheet:
  //   alu_out: pull=down
endmodule

module test_alu (
  output [7:0] out_1
);

  wire clock_1_out;

  Clock clock_1 (.out(clock_1_out));
  alu alu_1 (
    .enable(1'b1), .core_state(3'b101), .decoded_alu_output_mux(1'b0), .rs(8'h10), .rt(8'h4),
    .decoded_alu_arithmetic_mux(2'b00), .clk(clock_1_out), .reset(1'b0), .alu_out(out_1));
endmodule

module pc (
  input  enable,
  input  [2:0] core_state,
  input  [7:0] in_3,
  input  in_4
);

  wire [7:0] register_1_q;

  Register register_1 (.Q(register_1_q), .clr(in_4));  // open: D, en, clk
  Multiplexer #(.width(8)) multiplexer_1 (.in0(register_1_q), .in1({8{1'b0}}), .out(in_3), .sel(in_4));
endmodule

module register_16_new (
  input  [3:0] decoded_rs_address,
  input  [7:0] block_id,
  input  enable,
  input  reset,
  input  clk,
  input  [3:0] decoded_rt_address,
  input  [3:0] decoded_rd_address,
  input  decoded_reg_write_enable,
  input  [1:0] decoded_reg_input_mux,
  input  [7:0] alu_out,
  input  [7:0] lsu_out,
  input  [7:0] decoded_immediate,
  input  [2:0] core_state,
  output [7:0] rs,
  output [7:0] rt
);

  wire and_1_out, decoder_1_out3, decoder_1_out6, decoder_2_out0, decoder_2_out1, decoder_2_out2,
       decoder_2_out3, decoder_2_out4, decoder_2_out5, decoder_2_out6, decoder_2_out7, decoder_2_out8,
       decoder_2_out9, decoder_2_out10, decoder_2_out11, decoder_2_out12, or_1_out, or_2_out;
  wire [7:0] multiplexer_1_out, multiplexer_2_out, multiplexer_3_out, reg_0_q, reg_1_q, reg_2_q, reg_3_q,
       reg_4_q, reg_5_q, reg_6_q, reg_7_q, reg_8_q, reg_9_q, reg_10_q, reg_11_q, reg_12_q, reg_13_q,
       reg_14_q, reg_15_q;

  Multiplexer #(.select(2), .width(8)) multiplexer_1 (
    .in0(alu_out), .in1(lsu_out), .in2(decoded_immediate), .out(multiplexer_1_out),
    .sel(decoded_reg_input_mux));  // open: in3
  or or_1 (or_1_out, enable, reset);
  or or_2 (or_2_out, enable, reset);
  Decoder #(.select(3)) decoder_1 (
    .out3(decoder_1_out3), .out6(decoder_1_out6), .sel(core_state), .en(enable));  // open: out0, out1, out2, out4, out5, out7
  Register reg_14 (.D({8{1'b0}}), .en(or_1_out), .clk(clk), .Q(reg_14_q));  // open: clr
  Register reg_15 (.D(8'h4), .en(or_2_out), .clk(clk), .Q(reg_15_q));  // open: clr
  Register reg_13 (.D(block_id), .en(enable), .clk(clk), .Q(reg_13_q), .clr(reset));
  Decoder #(.select(4)) decoder_2 (
    .out0(decoder_2_out0), .out1(decoder_2_out1), .out2(decoder_2_out2), .out3(decoder_2_out3),
    .out4(decoder_2_out4), .out5(decoder_2_out5), .out6(decoder_2_out6), .out7(decoder_2_out7),
    .out8(decoder_2_out8), .out9(decoder_2_out9), .out10(decoder_2_out10), .out11(decoder_2_out11),
    .out12(decoder_2_out12), .sel(decoded_rd_address), .en(and_1_out));  // open: out13, out14, out15
  and and_1 (and_1_out, decoded_reg_write_enable, decoder_1_out6);
  Register reg_0 (.D(multiplexer_1_out), .en(decoder_2_out0), .clk(clk), .Q(reg_0_q), .clr(reset));
  Register reg_1 (.D(multiplexer_1_out), .en(decoder_2_out1), .clk(clk), .Q(reg_1_q), .clr(reset));
  Register reg_2 (.D(multiplexer_1_out), .en(decoder_2_out2), .clk(clk), .Q(reg_2_q), .clr(reset));
  Register reg_3 (.D(multiplexer_1_out), .en(decoder_2_out3), .clk(clk), .Q(reg_3_q), .clr(reset));
  Register reg_4 (.D(multiplexer_1_out), .en(decoder_2_out4), .clk(clk), .Q(reg_4_q), .clr(reset));
  Register reg_5 (.D(multiplexer_1_out), .en(decoder_2_out5), .clk(clk), .Q(reg_5_q), .clr(reset));
  Register reg_6 (.D(multiplexer_1_out), .en(decoder_2_out6), .clk(clk), .Q(reg_6_q), .clr(reset));
  Register reg_7 (.D(multiplexer_1_out), .en(decoder_2_out7), .clk(clk), .Q(reg_7_q), .clr(reset));
  Register reg_8 (.D(multiplexer_1_out), .en(decoder_2_out8), .clk(clk), .Q(reg_8_q), .clr(reset));
  Register reg_9 (.D(multiplexer_1_out), .en(decoder_2_out9), .clk(clk), .Q(reg_9_q), .clr(reset));
  Register reg_10 (.D(multiplexer_1_out), .en(decoder_2_out10), .clk(clk), .Q(reg_10_q), .clr(reset));
  Register reg_11 (.D(multiplexer_1_out), .en(decoder_2_out11), .clk(clk), .Q(reg_11_q), .clr(reset));
  Register reg_12 (.D(multiplexer_1_out), .en(decoder_2_out12), .clk(clk), .Q(reg_12_q), .clr(reset));
  Multiplexer #(.select(4), .width(8)) multiplexer_2 (
    .in0(reg_0_q), .in1(reg_1_q), .in2(reg_2_q), .in3(reg_3_q), .in4(reg_4_q), .in5(reg_5_q), .in6(reg_6_q),
    .in7(reg_7_q), .in8(reg_8_q), .in9(reg_9_q), .in10(reg_10_q), .in11(reg_11_q), .in12(reg_12_q),
    .in13(reg_13_q), .in14(reg_14_q), .in15(reg_15_q), .out(multiplexer_2_out), .sel(decoded_rs_address));
  Multiplexer #(.select(4), .width(8)) multiplexer_3 (
    .in0(reg_0_q), .in1(reg_1_q), .in2(reg_2_q), .in3(reg_3_q), .in4(reg_4_q), .in5(reg_5_q), .in6(reg_6_q),
    .in7(reg_7_q), .in8(reg_8_q), .in9(reg_9_q), .in10(reg_10_q), .in11(reg_11_q), .in12(reg_12_q),
    .in13(reg_13_q), .in14(reg_14_q), .in15(reg_15_q), .out(multiplexer_3_out), .sel(decoded_rt_address));
  Register reg_rs (.D(multiplexer_2_out), .en(decoder_1_out3), .clk(clk), .Q(rs));  // open: clr
  Register reg_rt (.D(multiplexer_3_out), .en(decoder_1_out3), .clk(clk), .Q(rt));  // open: clr
endmodule

module fetcher (
  input  [7:0] current_pc,
  input  mem_read_ready,
  input  [2:0] core_state,
  input  clk,
  input  reset,
  input  [15:0] mem_read_data,
  output [7:0] mem_read_address,
  output mem_read_valid,
  output [2:0] fetcher_state,
  output [15:0] instruction
);

  wire and_1_out, and_2_out, and_3_out, decoder_1_out0, decoder_1_out1, decoder_1_out2, decoder_2_out1,
       decoder_2_out2, or_1_out, or_2_out;
  wire [2:0] adder_1_out, bit_extender_1_out, multiplexer_1_out;

  Decoder #(.select(3)) decoder_1 (
    .out0(decoder_1_out0), .out1(decoder_1_out1), .out2(decoder_1_out2), .sel(fetcher_state));  // open: out3, out4, out5, out6, out7, en
  and and_1 (and_1_out, decoder_1_out1, mem_read_ready);
  Decoder #(.select(3)) decoder_2 (
    .out1(decoder_2_out1), .out2(decoder_2_out2), .sel(core_state));  // open: out0, out3, out4, out5, out6, out7, en
  and and_2 (and_2_out, decoder_1_out0, decoder_2_out1);
  or or_1 (or_1_out, and_2_out, and_1_out);
  and and_3 (and_3_out, decoder_1_out2, decoder_2_out2);
  Adder #(.width(3)) adder_1 (.a(fetcher_state), .b(bit_extender_1_out), .out(adder_1_out));  // open: cin, cout
  assign bit_extender_1_out = {{2{1'b0}}, or_1_out};  // Bit_Extender bit_extender_1
  or or_2 (or_2_out, or_1_out, and_3_out);
  Multiplexer #(.width(3)) multiplexer_1 (.in0(adder_1_out), .in1(3'b000), .out(multiplexer_1_out), .sel(and_3_out));
  Register mem_read_address_reg (.D(current_pc), .en(or_1_out), .clk(clk), .Q(mem_read_address), .clr(reset));
  Register #(.width(1)) mem_read_valid_reg (.D(and_2_out), .en(or_1_out), .clk(clk), .Q(mem_read_valid), .clr(reset));
  Register #(.width(3)) fetcher_state_reg (
    .D(multiplexer_1_out), .en(or_2_out), .clk(clk), .Q(fetcher_state), .clr(reset));
  Register #(.width(16)) instruction_reg (.D(mem_read_data), .en(and_1_out), .clk(clk), .Q(instruction), .clr(reset));
endmodule

module lsu_mod (
  input  [7:0] rt,
  input  [7:0] rs,
  input  [7:0] mem_read_data,
  input  enable,
  input  decoded_mem_read_enable,
  input  decoded_mem_write_enable,
  input  [2:0] core_state,
  input  mem_write_ready,
  input  mem_read_ready,
  input  reset,
  input  clk,
  output [7:0] mem_write_data,
  output [7:0] mem_write_address,
  output mem_write_valid,
  output [7:0] mem_read_address,
  output mem_read_valid,
  output [7:0] lsu_out,
  output [1:0] lus_state
);

  wire and_1_out, and_2_out, and_3_out, and_4_out, and_5_out, and_6_out, decoder_1_out1, decoder_1_out2,
       decoder_2_out3, decoder_2_out6, or_1_out, or_2_out, or_3_out, or_4_out;
  wire [1:0] bit_extender_1_out, multiplexer_1_out, multiplexer_2_out, multiplexer_3_out;

  or or_1 (or_1_out, mem_write_ready, mem_read_ready);
  Decoder #(.select(2)) decoder_1 (
    .out1(decoder_1_out1), .out2(decoder_1_out2), .sel(lus_state));  // open: out0, out3, en
  Decoder #(.select(3)) decoder_2 (
    .out3(decoder_2_out3), .out6(decoder_2_out6), .sel(core_state));  // open: out0, out1, out2, out4, out5, out7, en
  and and_1 (and_1_out, decoded_mem_write_enable, decoder_1_out1);
  and and_2 (and_2_out, decoder_1_out1, decoded_mem_read_enable);
  and and_3 (and_3_out, decoder_1_out2, decoded_mem_read_enable);
  or or_2 (or_2_out, decoded_mem_read_enable, decoded_mem_write_enable);
  assign bit_extender_1_out = {{1{1'b0}}, decoder_2_out3};  // Bit_Extender bit_extender_1
  Multiplexer #(.width(2)) multiplexer_1 (.in0(2'b11), .in1(2'b00), .out(multiplexer_1_out), .sel(decoder_2_out6));
  and and_4 (and_4_out, mem_write_ready, decoder_1_out2);
  and and_5 (and_5_out, and_3_out, mem_read_ready);
  and and_6 (and_6_out, enable, or_2_out);
  Multiplexer #(.width(2)) multiplexer_2 (.in0(2'b10), .in1(2'b11), .out(multiplexer_2_out), .sel(or_1_out));
  Register #(.width(1)) mem_write_valid_reg (
    .D(and_1_out), .en(and_1_out), .clk(clk), .Q(mem_write_valid), .clr(or_3_out));
  or or_3 (or_3_out, and_4_out, reset);
  Register #(.width(1)) mem_read_valid_reg (
    .D(and_2_out), .en(and_2_out), .clk(clk), .Q(mem_read_valid), .clr(or_4_out));
  or or_4 (or_4_out, and_5_out, reset);
  Multiplexer #(.enable("true"), .select(2), .width(2)) multiplexer_3 (
    .in0(bit_extender_1_out), .in1(2'b10), .in2(multiplexer_2_out), .in3(multiplexer_1_out),
    .out(multiplexer_3_out), .sel(lus_state), .en(and_6_out));
  Register #(.width(2)) lsu_state_reg (.D(multiplexer_3_out), .en(and_6_out), .clk(clk), .Q(lus_state), .clr(reset));
  Register mem_write_data_reg (.D(rt), .en(and_1_out), .clk(clk), .Q(mem_write_data), .clr(reset));
  Register mem_write_address_reg (.D(rs), .en(and_1_out), .clk(clk), .Q(mem_write_address), .clr(reset));
  Register mem_read_address_reg (.D(rs), .en(and_2_out), .clk(clk), .Q(mem_read_address), .clr(reset));
  Register lsu_out_reg (.D(mem_read_data), .en(and_5_out), .clk(clk), .Q(lsu_out), .clr(reset));
endmodule

module pc_test (
  input  [7:0] alu_out,
  input  decoded_nzp_write_enable,
  input  [2:0] core_state,
  input  [2:0] decoded_nzp,
  input  enable,
  input  decoded_pc_mux,
  input  [7:0] current_pc,
  input  [7:0] decoded_immediate,
  input  reset,
  input  clk,
  output [7:0] next_pc
);

  wire and_1_out, and_2_out, and_3_out, and_4_out, and_5_out, decoder_1_out5, decoder_1_out6, or_1_out,
       or_2_out;
  wire [2:0] bit_extender_1_out, nzp_reg_q;
  wire [7:0] adder_1_out, multiplexer_1_out;

  Decoder #(.select(3)) decoder_1 (
    .out5(decoder_1_out5), .out6(decoder_1_out6), .sel(core_state), .en(enable));  // open: out0, out1, out2, out3, out4, out7
  Adder adder_1 (.a(8'h1), .b(current_pc), .out(adder_1_out));  // open: cin, cout
  Bit_Extender #(.out_width(3), .\type ("zero")) bit_extender_1 (.in(alu_out), .out(bit_extender_1_out));
  Multiplexer #(.enable("true"), .width(8)) multiplexer_1 (
    .in0(adder_1_out), .in1(decoded_immediate), .out(multiplexer_1_out), .sel(and_5_out), .en(decoder_1_out5));
  Register #(.width(3)) nzp_reg (.D(bit_extender_1_out), .en(and_1_out), .clk(clk), .Q(nzp_reg_q), .clr(reset));
  and and_1 (and_1_out, decoded_nzp_write_enable, decoder_1_out6);
  Register next_pc_reg (.D(multiplexer_1_out), .en(decoder_1_out5), .clk(clk), .Q(next_pc), .clr(reset));
  and and_2 (and_2_out, nzp_reg_q[0], decoded_nzp[0]);
  and and_3 (and_3_out, nzp_reg_q[1], decoded_nzp[1]);
  and and_4 (and_4_out, nzp_reg_q[2], decoded_nzp[2]);
  or or_1 (or_1_out, and_2_out, and_3_out);
  or or_2 (or_2_out, or_1_out, and_4_out);
  and and_5 (and_5_out, or_2_out, decoded_pc_mux);
endmodule
