// Logisim project my_core.circ as structural Verilog: 13 circuits, main circuit decoder_w
module decoder_w (
  input  [15:0] instruction,
  input  [2:0] core_state,
  input  clk,
  input  reset,
  output [7:0] decoded_immediate,
  output [3:0] decoded_rd_address,
  output [2:0] decoded_nzp,
  output [3:0] decoded_rs_address,
  output [3:0] decoded_rt_address,
  output decoded_pc_mux,
  output decoded_alu_output_mux,
  output decoded_nzp_write_enable,
  output decoded_mem_write_enable,
  output decoded_reg_write_enable,
  output [1:0] decoded_reg_input_mux,
  output decoded_mem_read_enable,
  output [1:0] decoded_alu_arithmetic_mux,
  output decoded_ret
);

  wire and_1_out, decoder_1_out2, decoder_2_out1, decoder_2_out2, decoder_2_out3, decoder_2_out4,
       decoder_2_out5, decoder_2_out6, decoder_2_out8, decoder_2_out15, or_1_out, or_2_out, or_3_out;
  wire [1:0] decoder_2_out7, multiplexer_1_out, multiplexer_2_out, multiplexer_3_out, multiplexer_4_out,
       multiplexer_5_out;

  Multiplexer #(.width(2)) multiplexer_1 (.in0(2'b00), .in1(2'b11), .out(multiplexer_1_out), .sel(decoder_2_out6));
  Decoder #(.select(3)) decoder_1 (
    .out2(decoder_1_out2), .sel(core_state));  // open: out0, out1, out3, out4, out5, out6, out7, en
  Multiplexer #(.width(2)) multiplexer_2 (
    .in0(multiplexer_1_out), .in1(2'b10), .out(multiplexer_2_out), .sel(decoder_2_out5));
  Multiplexer #(.width(2)) multiplexer_3 (
    .in0(multiplexer_2_out), .in1(2'b01), .out(multiplexer_3_out), .sel(decoder_2_out4));
  Decoder #(.select(4)) decoder_2 (
    .out1(decoder_2_out1), .out2(decoder_2_out2), .out3(decoder_2_out3), .out4(decoder_2_out4),
    .out5(decoder_2_out5), .out6(decoder_2_out6), .out7(decoder_2_out7[0]), .out8(decoder_2_out8),
    .out9(decoder_2_out7[1]), .out15(decoder_2_out15), .sel(instruction[15:12]), .en(decoder_1_out2));  // open: out0, out10, out11, out12, out13, out14
  or or_1 (or_1_out, decoder_2_out3, decoder_2_out4, decoder_2_out5, decoder_2_out6);
  Multiplexer #(.width(2)) multiplexer_4 (
    .in0(multiplexer_3_out), .in1(2'b00), .out(multiplexer_4_out), .sel(decoder_2_out3));
  or or_2 (or_2_out, decoder_2_out7[0], or_1_out);
  or or_3 (or_3_out, decoder_2_out7[0], decoder_2_out7[1]);
  and and_1 (and_1_out, decoder_1_out2, decoder_2_out7[0]);
  Register #(.width(1)) decoded_pc_mux_reg (
    .D(decoder_2_out1), .en(decoder_1_out2), .clk(clk), .Q(decoded_pc_mux), .clr(reset));
  Register #(.width(1)) decoded_alu_output_mux_reg (
    .D(decoder_2_out2), .en(decoder_1_out2), .clk(clk), .Q(decoded_alu_output_mux), .clr(reset));
  Register #(.width(1)) decoded_nzp_write_enable_reg (
    .D(decoder_2_out2), .en(decoder_1_out2), .clk(clk), .Q(decoded_nzp_write_enable), .clr(reset));
  Register #(.width(1)) decoded_mem_write_enable_reg (
    .D(decoder_2_out8), .en(decoder_1_out2), .clk(clk), .Q(decoded_mem_write_enable), .clr(reset));
  Register #(.width(1)) decoded_reg_write_enable_reg (
    .D(or_2_out), .en(decoder_1_out2), .clk(clk), .Q(decoded_reg_write_enable), .clr(reset));
  Register #(.width(2)) decoded_reg_input_mux_reg (
    .D(multiplexer_5_out), .en(decoder_1_out2), .clk(clk), .Q(decoded_reg_input_mux), .clr(reset));
  Multiplexer #(.width(2)) multiplexer_5 (.in0(2'b00), .in1(decoder_2_out7), .out(multiplexer_5_out), .sel(or_3_out));
  Register #(.width(1)) decoded_mem_read_enable_reg (
    .D(decoder_2_out7[0]), .en(and_1_out), .clk(clk), .Q(decoded_mem_read_enable), .clr(reset));
  Register #(.width(2)) decoded_alu_arithmetic_mux_reg (
    .D(multiplexer_4_out), .en(decoder_1_out2), .clk(clk), .Q(decoded_alu_arithmetic_mux), .clr(reset));
  Register #(.width(1)) decoded_ret_reg (
    .D(decoder_2_out15), .en(decoder_1_out2), .clk(clk), .Q(decoded_ret), .clr(reset));

  assign decoded_immediate = instruction[7:0];
  assign decoded_nzp = instruction[11:9];
  assign decoded_rd_address = instruction[11:8];
  assign decoded_rs_address = instruction[7:4];
  assign decoded_rt_address = instruction[3:0];
endmodule

module dlv (
  input  [7:0] divisor,
  input  [7:0] dividend,
  output [7:0] cout,
  output err
);

  wire [31:0] fpdivider_1_out, inttofp_1_p2, inttofp_2_p2;

  // IntToFP inttofp_1: pin names not known; wires that end beside it: divisor, inttofp_1_p2
  FPDivider fpdivider_1 (.a(inttofp_1_p2), .b(inttofp_2_p2), .out(fpdivider_1_out));
  // IntToFP inttofp_2: pin names not known; wires that end beside it: dividend, inttofp_2_p2, err
  // FPToInt fptoint_1: pin names not known; wires that end beside it: fpdivider_1_out, err, cout

  // Notes on the sheet:
  //   err: pull=down
endmodule

module alu (
  input  decoded_alu_output_mux,
  input  [7:0] rs,
  input  [7:0] rt,
  input  [1:0] decoded_alu_arithmetic_mux,
  input  reset,
  input  [2:0] core_state,
  input  enable,
  input  clk,
  output [7:0] alu_out
);

  wire decoder_1_out5, not_1_out;
  wire [2:0] comparator_1_lt;
  wire [7:0] adder_1_out, dlv_1_cout, multiplexer_1_out, multiplexer_2_out, multiplier_1_out,
       subtractor_1_out;

  Decoder #(.select(3)) decoder_1 (
    .out5(decoder_1_out5), .sel(core_state));  // open: out0, out1, out2, out3, out4, out6, out7, en
  Adder adder_1 (.a(rs), .b(rt), .out(adder_1_out));  // open: cin, cout
  Subtractor subtractor_1 (.a(rs), .b(rt), .out(subtractor_1_out));  // open: bin, bout
  Multiplier multiplier_1 (.a(rs), .b(rt), .out(multiplier_1_out));  // open: cin, cout
  dlv dlv_1 (.divisor(rs), .dividend(rt), .cout(dlv_1_cout));  // open: err
  Comparator comparator_1 (
    .a(subtractor_1_out), .b({8{1'b0}}), .gt(comparator_1_lt[2]), .eq(comparator_1_lt[1]),
    .lt(comparator_1_lt[0]));
  not not_1 (not_1_out, decoded_alu_output_mux);
  Multiplexer #(.enable("true"), .select(2), .width(8)) multiplexer_1 (
    .in0(adder_1_out), .in1(subtractor_1_out), .in2(multiplier_1_out), .in3(dlv_1_cout),
    .out(multiplexer_1_out), .sel(decoded_alu_arithmetic_mux), .en(decoder_1_out5));
  Multiplexer #(.width(8)) multiplexer_2 (
    .in0({{5{1'b0}}, comparator_1_lt}), .in1(multiplexer_1_out), .out(multiplexer_2_out), .sel(not_1_out));
  Register alu_out_reg (.D(multiplexer_2_out), .en(enable), .clk(clk), .Q(alu_out), .clr(reset));

  // Notes on the sheet:
  //   alu_out: pull=down
endmodule

module lsu (
  input  [7:0] rt,
  input  [7:0] rs,
  input  [7:0] mem_read_data,
  input  enable,
  input  decoded_mem_read_enable,
  input  decoded_mem_write_enable,
  input  [2:0] core_state,
  input  mem_write_ready,
  input  mem_read_ready,
  input  reset,
  input  clk,
  output [7:0] mem_write_data,
  output [7:0] mem_write_address,
  output mem_write_valid,
  output [7:0] mem_read_address,
  output mem_read_valid,
  output [7:0] lsu_out,
  output [1:0] lus_state
);

  wire and_1_out, and_2_out, and_3_out, and_4_out, and_5_out, and_6_out, decoder_1_out1, decoder_1_out2,
       decoder_2_out3, decoder_2_out6, or_1_out, or_2_out, or_3_out, or_4_out;
  wire [1:0] bit_extender_1_out, multiplexer_1_out, multiplexer_2_out, multiplexer_3_out;

  or or_1 (or_1_out, mem_write_ready, mem_read_ready);
  Decoder #(.select(2)) decoder_1 (
    .out1(decoder_1_out1), .out2(decoder_1_out2), .sel(lus_state));  // open: out0, out3, en
  Decoder #(.select(3)) decoder_2 (
    .out3(decoder_2_out3), .out6(decoder_2_out6), .sel(core_state));  // open: out0, out1, out2, out4, out5, out7, en
  and and_1 (and_1_out, decoded_mem_write_enable, decoder_1_out1);
  and and_2 (and_2_out, decoder_1_out1, decoded_mem_read_enable);
  and and_3 (and_3_out, decoder_1_out2, decoded_mem_read_enable);
  or or_2 (or_2_out, decoded_mem_read_enable, decoded_mem_write_enable);
  assign bit_extender_1_out = {{1{1'b0}}, decoder_2_out3};  // Bit_Extender bit_extender_1
  Multiplexer #(.width(2)) multiplexer_1 (.in0(2'b11), .in1(2'b00), .out(multiplexer_1_out), .sel(decoder_2_out6));
  and and_4 (and_4_out, mem_write_ready, decoder_1_out2);
  and and_5 (and_5_out, and_3_out, mem_read_ready);
  and and_6 (and_6_out, enable, or_2_out);
  Multiplexer #(.width(2)) multiplexer_2 (.in0(2'b10), .in1(2'b11), .out(multiplexer_2_out), .sel(or_1_out));
  Register #(.width(1)) mem_write_valid_reg (
    .D(and_1_out), .en(and_1_out), .clk(clk), .Q(mem_write_valid), .clr(or_3_out));
  or or_3 (or_3_out, and_4_out, reset);
  Register #(.width(1)) mem_read_valid_reg (
    .D(and_2_out), .en(and_2_out), .clk(clk), .Q(mem_read_valid), .clr(or_4_out));
  or or_4 (or_4_out, and_5_out, reset);
  Multiplexer #(.enable("true"), .select(2), .width(2)) multiplexer_3 (
    .in0(bit_extender_1_out), .in1(2'b10), .in2(multiplexer_2_out), .in3(multiplexer_1_out),
    .out(multiplexer_3_out), .sel(lus_state), .en(and_6_out));
  Register #(.width(2)) lsu_state_reg (.D(multiplexer_3_out), .en(and_6_out), .clk(clk), .Q(lus_state), .clr(reset));
  Register mem_write_data_reg (.D(rt), .en(and_1_out), .clk(clk), .Q(mem_write_data), .clr(reset));
  Register mem_write_address_reg (.D(rs), .en(and_1_out), .clk(clk), .Q(mem_write_address), .clr(reset));
  Register mem_read_address_reg (.D(rs), .en(and_2_out), .clk(clk), .Q(mem_read_address), .clr(reset));
  Register lsu_out_reg (.D(mem_read_data), .en(and_5_out), .clk(clk), .Q(lsu_out), .clr(reset));
endmodule

module register_w (
  input  [3:0] decoded_rs_address,
  input  [7:0] block_id,
  input  enable,
  input  reset,
  input  clk,
  input  [3:0] decoded_rt_address,
  input  [3:0] decoded_rd_address,
  input  decoded_reg_write_enable,
  input  [1:0] decoded_reg_input_mux,
  input  [7:0] alu_out,
  input  [7:0] lsu_out,
  input  [7:0] decoded_immediate,
  input  [2:0] core_state,
  output [7:0] rs,
  output [7:0] rt
);

  wire and_1_out, decoder_1_out3, decoder_1_out6, decoder_2_out0, decoder_2_out1, decoder_2_out2,
       decoder_2_out3, decoder_2_out4, decoder_2_out5, decoder_2_out6, decoder_2_out7, decoder_2_out8,
       decoder_2_out9, decoder_2_out10, decoder_2_out11, decoder_2_out12, or_1_out, or_2_out;
  wire [7:0] multiplexer_1_out, multiplexer_2_out, multiplexer_3_out, reg_0_q, reg_1_q, reg_2_q, reg_3_q,
       reg_4_q, reg_5_q, reg_6_q, reg_7_q, reg_8_q, reg_9_q, reg_10_q, reg_11_q, reg_12_q, reg_13_q,
       reg_14_q, reg_15_q;

  Multiplexer #(.select(2), .width(8)) multiplexer_1 (
    .in0(alu_out), .in1(lsu_out), .in2(decoded_immediate), .out(multiplexer_1_out),
    .sel(decoded_reg_input_mux));  // open: in3
  or or_1 (or_1_out, enable, reset);
  or or_2 (or_2_out, enable, reset);
  Decoder #(.select(3)) decoder_1 (
    .out3(decoder_1_out3), .out6(decoder_1_out6), .sel(core_state), .en(enable));  // open: out0, out1, out2, out4, out5, out7
  Register reg_14 (.D({8{1'b0}}), .en(or_1_out), .clk(clk), .Q(reg_14_q));  // open: clr
  Register reg_15 (.D(8'h4), .en(or_2_out), .clk(clk), .Q(reg_15_q));  // open: clr
  Register reg_13 (.D(block_id), .en(enable), .clk(clk), .Q(reg_13_q), .clr(reset));
  Decoder #(.select(4)) decoder_2 (
    .out0(decoder_2_out0), .out1(decoder_2_out1), .out2(decoder_2_out2), .out3(decoder_2_out3),
    .out4(decoder_2_out4), .out5(decoder_2_out5), .out6(decoder_2_out6), .out7(decoder_2_out7),
    .out8(decoder_2_out8), .out9(decoder_2_out9), .out10(decoder_2_out10), .out11(decoder_2_out11),
    .out12(decoder_2_out12), .sel(decoded_rd_address), .en(and_1_out));  // open: out13, out14, out15
  and and_1 (and_1_out, decoded_reg_write_enable, decoder_1_out6);
  Register reg_0 (.D(multiplexer_1_out), .en(decoder_2_out0), .clk(clk), .Q(reg_0_q), .clr(reset));
  Register reg_1 (.D(multiplexer_1_out), .en(decoder_2_out1), .clk(clk), .Q(reg_1_q), .clr(reset));
  Register reg_2 (.D(multiplexer_1_out), .en(decoder_2_out2), .clk(clk), .Q(reg_2_q), .clr(reset));
  Register reg_3 (.D(multiplexer_1_out), .en(decoder_2_out3), .clk(clk), .Q(reg_3_q), .clr(reset));
  Register reg_4 (.D(multiplexer_1_out), .en(decoder_2_out4), .clk(clk), .Q(reg_4_q), .clr(reset));
  Register reg_5 (.D(multiplexer_1_out), .en(decoder_2_out5), .clk(clk), .Q(reg_5_q), .clr(reset));
  Register reg_6 (.D(multiplexer_1_out), .en(decoder_2_out6), .clk(clk), .Q(reg_6_q), .clr(reset));
  Register reg_7 (.D(multiplexer_1_out), .en(decoder_2_out7), .clk(clk), .Q(reg_7_q), .clr(reset));
  Register reg_8 (.D(multiplexer_1_out), .en(decoder_2_out8), .clk(clk), .Q(reg_8_q), .clr(reset));
  Register reg_9 (.D(multiplexer_1_out), .en(decoder_2_out9), .clk(clk), .Q(reg_9_q), .clr(reset));
  Register reg_10 (.D(multiplexer_1_out), .en(decoder_2_out10), .clk(clk), .Q(reg_10_q), .clr(reset));
  Register reg_11 (.D(multiplexer_1_out), .en(decoder_2_out11), .clk(clk), .Q(reg_11_q), .clr(reset));
  Register reg_12 (.D(multiplexer_1_out), .en(decoder_2_out12), .clk(clk), .Q(reg_12_q), .clr(reset));
  Multiplexer #(.select(4), .width(8)) multiplexer_2 (
    .in0(reg_0_q), .in1(reg_1_q), .in2(reg_2_q), .in3(reg_3_q), .in4(reg_4_q), .in5(reg_5_q), .in6(reg_6_q),
    .in7(reg_7_q), .in8(reg_8_q), .in9(reg_9_q), .in10(reg_10_q), .in11(reg_11_q), .in12(reg_12_q),
    .in13(reg_13_q), .in14(reg_14_q), .in15(reg_15_q), .out(multiplexer_2_out), .sel(decoded_rs_address));
  Multiplexer #(.select(4), .width(8)) multiplexer_3 (
    .in0(reg_0_q), .in1(reg_1_q), .in2(reg_2_q), .in3(reg_3_q), .in4(reg_4_q), .in5(reg_5_q), .in6(reg_6_q),
    .in7(reg_7_q), .in8(reg_8_q), .in9(reg_9_q), .in10(reg_10_q), .in11(reg_11_q), .in12(reg_12_q),
    .in13(reg_13_q), .in14(reg_14_q), .in15(reg_15_q), .out(multiplexer_3_out), .sel(decoded_rt_address));
  Register reg_rs (.D(multiplexer_2_out), .en(decoder_1_out3), .clk(clk), .Q(rs));  // open: clr
  Register reg_rt (.D(multiplexer_3_out), .en(decoder_1_out3), .clk(clk), .Q(rt));  // open: clr
endmodule

module pc (
  input  [7:0] alu_out,
  input  decoded_nzp_write_enable,
  input  [2:0] core_state,
  input  [2:0] decoded_nzp,
  input  enable,
  input  decoded_pc_mux,
  input  [7:0] current_pc,
  input  [7:0] decoded_immediate,
  input  reset,
  input  clk,
  output [7:0] next_pc
);

  wire and_1_out, and_2_out, and_3_out, and_4_out, and_5_out, decoder_1_out5, decoder_1_out6, or_1_out,
       or_2_out;
  wire [2:0] bit_extender_1_out, nzp_reg_q;
  wire [7:0] adder_1_out, multiplexer_1_out;

  Decoder #(.select(3)) decoder_1 (
    .out5(decoder_1_out5), .out6(decoder_1_out6), .sel(core_state), .en(enable));  // open: out0, out1, out2, out3, out4, out7
  Adder adder_1 (.a(8'h1), .b(current_pc), .out(adder_1_out));  // open: cin, cout
  Bit_Extender #(.out_width(3), .\type ("zero")) bit_extender_1 (.in(alu_out), .out(bit_extender_1_out));
  Multiplexer #(.enable("true"), .width(8)) multiplexer_1 (
    .in0(adder_1_out), .in1(decoded_immediate), .out(multiplexer_1_out), .sel(and_5_out), .en(decoder_1_out5));
  Register #(.width(3)) nzp_reg (.D(bit_extender_1_out), .en(and_1_out), .clk(clk), .Q(nzp_reg_q), .clr(reset));
  and and_1 (and_1_out, decoded_nzp_write_enable, decoder_1_out6);
  Register next_pc_reg (.D(multiplexer_1_out), .en(decoder_1_out5), .clk(clk), .Q(next_pc), .clr(reset));
  and and_2 (and_2_out, nzp_reg_q[0], decoded_nzp[0]);
  and and_3 (and_3_out, nzp_reg_q[1], decoded_nzp[1]);
  and and_4 (and_4_out, nzp_reg_q[2], decoded_nzp[2]);
  or or_1 (or_1_out, and_2_out, and_3_out);
  or or_2 (or_2_out, or_1_out, and_4_out);
  and and_5 (and_5_out, or_2_out, decoded_pc_mux);
endmodule

module scheduler (
  input  [7:0] next_pc_1,
  input  [7:0] next_pc_2,
  input  [7:0] next_pc_3,
  input  [7:0] next_pc_4,
  input  reset,
  input  clk,
  input  decoded_ret,
  input  start,
  input  [2:0] fetcher_state,
  input  [7:0] lsu_state,
  output [7:0] current_pc_1,
  output [7:0] current_pc_2,
  output [7:0] current_pc_3,
  output [7:0] current_pc_4,
  output [2:0] core_state,
  output done
);

  wire and_1_out, and_2_out, comparator_1_eq, comparator_2_eq, multiplexer_1_out, not_1_out, not_2_out,
       not_3_out, or_1_out, or_2_out, or_3_out, or_4_out, or_5_out, or_6_out, or_7_out;
  wire [2:0] adder_1_out, bit_extender_1_out, multiplexer_2_out;

  or or_1 (or_1_out, lsu_state[0], lsu_state[1]);
  or or_2 (or_2_out, lsu_state[2], lsu_state[3]);
  or or_3 (or_3_out, lsu_state[4], lsu_state[5]);
  or or_4 (or_4_out, lsu_state[6], lsu_state[7]);
  or or_5 (or_5_out, or_1_out, or_2_out);
  or or_6 (or_6_out, or_3_out, or_4_out);
  or or_7 (or_7_out, or_5_out, or_6_out);
  not not_1 (not_1_out, or_7_out);
  Comparator #(.width(3)) comparator_1 (.a(fetcher_state), .b(3'b010), .eq(comparator_1_eq));  // open: gt, lt
  assign bit_extender_1_out = {{2{1'b0}}, multiplexer_1_out};  // Bit_Extender bit_extender_1
  Multiplexer #(.select(3)) multiplexer_1 (
    .in0(start), .in1(comparator_1_eq), .in2(1'b1), .in3(1'b1), .in4(not_1_out), .in5(1'b1), .in6(and_2_out),
    .in7(1'b0), .out(multiplexer_1_out), .sel(core_state));
  Adder #(.width(3)) adder_1 (.a(core_state), .b(bit_extender_1_out), .out(adder_1_out));  // open: cin, cout
  and and_1 (and_1_out, comparator_2_eq, not_2_out);
  Comparator #(.width(3)) comparator_2 (.a(core_state), .b(3'b110), .eq(comparator_2_eq));  // open: gt, lt
  Multiplexer #(.width(3)) multiplexer_2 (.in0(adder_1_out), .in1(3'b001), .out(multiplexer_2_out), .sel(and_1_out));
  not not_2 (not_2_out, and_2_out);
  and and_2 (and_2_out, comparator_2_eq, decoded_ret);
  Register current_pc_reg_1 (.D(next_pc_1), .en(and_1_out), .clk(clk), .Q(current_pc_1));  // open: clr
  Register current_pc_reg_2 (.D(next_pc_2), .en(and_1_out), .clk(clk), .Q(current_pc_2));  // open: clr
  Register current_pc_reg_3 (.D(next_pc_3), .en(and_1_out), .clk(clk), .Q(current_pc_3));  // open: clr
  Register current_pc_reg_4 (.D(next_pc_4), .en(and_1_out), .clk(clk), .Q(current_pc_4), .clr(reset));
  Register #(.width(3)) core_state_reg (.D(multiplexer_2_out), .en(not_3_out), .clk(clk), .Q(core_state), .clr(reset));
  not not_3 (not_3_out, reset);
  or or_8 (done, reset, and_2_out);
endmodule

module fetcher (
  input  [7:0] current_pc,
  input  mem_read_ready,
  input  [2:0] core_state,
  input  clk,
  input  reset,
  input  [15:0] mem_read_data,
  output [7:0] mem_read_address,
  output mem_read_valid,
  output [2:0] fetcher_state,
  output [15:0] instruction
);

  wire and_1_out, and_2_out, and_3_out, decoder_1_out0, decoder_1_out1, decoder_1_out2, decoder_2_out1,
       decoder_2_out2, or_1_out, or_2_out;
  wire [2:0] adder_1_out, bit_extender_1_out, multiplexer_1_out;

  Decoder #(.select(3)) decoder_1 (
    .out0(decoder_1_out0), .out1(decoder_1_out1), .out2(decoder_1_out2), .sel(fetcher_state));  // open: out3, out4, out5, out6, out7, en
  and and_1 (and_1_out, decoder_1_out1, mem_read_ready);
  Decoder #(.select(3)) decoder_2 (
    .out1(decoder_2_out1), .out2(decoder_2_out2), .sel(core_state));  // open: out0, out3, out4, out5, out6, out7, en
  and and_2 (and_2_out, decoder_1_out0, decoder_2_out1);
  or or_1 (or_1_out, and_2_out, and_1_out);
  and and_3 (and_3_out, decoder_1_out2, decoder_2_out2);
  Adder #(.width(3)) adder_1 (.a(fetcher_state), .b(bit_extender_1_out), .out(adder_1_out));  // open: cin, cout
  assign bit_extender_1_out = {{2{1'b0}}, or_1_out};  // Bit_Extender bit_extender_1
  or or_2 (or_2_out, or_1_out, and_3_out);
  Multiplexer #(.width(3)) multiplexer_1 (.in0(adder_1_out), .in1(3'b000), .out(multiplexer_1_out), .sel(and_3_out));
  Register mem_read_address_reg (.D(current_pc), .en(or_1_out), .clk(clk), .Q(mem_read_address), .clr(reset));
  Register #(.width(1)) mem_read_valid_reg (.D(and_2_out), .en(or_1_out), .clk(clk), .Q(mem_read_valid), .clr(reset));
  Register #(.width(3)) fetcher_state_reg (
    .D(multiplexer_1_out), .en(or_2_out), .clk(clk), .Q(fetcher_state), .clr(reset));
  Register #(.width(16)) instruction_reg (.D(mem_read_data), .en(and_1_out), .clk(clk), .Q(instruction), .clr(reset));
endmodule

module core (
  input  [2:0] thread_count,
  input  start,
  input  [15:0] program_mem_read_data,
  input  program_mem_read_ready,
  input  clk,
  input  reset,
  input  [7:0] block_id,
  input  data_mem_read_ready_0,
  input  data_mem_read_ready_1,
  input  data_mem_read_ready_2,
  input  data_mem_read_ready_3,
  input  data_mem_write_ready_0,
  input  data_mem_write_ready_1,
  input  data_mem_write_ready_2,
  input  data_mem_write_ready_3,
  input  [7:0] data_mem_read_data_0,
  input  [7:0] data_mem_read_data_1,
  input  [7:0] data_mem_read_data_2,
  input  [7:0] data_mem_read_data_3,
  output done,
  output [7:0] program_mem_read_address,
  output program_mem_read_valid,
  output data_mem_read_valid_0,
  output data_mem_read_valid_1,
  output data_mem_read_valid_2,
  output data_mem_read_valid_3,
  output data_mem_write_valid_0,
  output data_mem_write_valid_1,
  output data_mem_write_valid_2,
  output data_mem_write_valid_3,
  output [7:0] data_mem_write_data_0,
  output [7:0] data_mem_write_data_1,
  output [7:0] data_mem_write_data_2,
  output [7:0] data_mem_write_data_3,
  output [7:0] data_mem_write_address_0,
  output [7:0] data_mem_write_address_1,
  output [7:0] data_mem_write_address_2,
  output [7:0] data_mem_write_address_3,
  output [7:0] data_mem_read_address_0,
  output [7:0] data_mem_read_address_1,
  output [7:0] data_mem_read_address_2,
  output [7:0] data_mem_read_address_3
);

  wire d_alu_o_m, d_mem_r_e, d_mem_w_e, d_nzp_w_e, d_pc_mux, d_reg_w_e, decoded_ret, decoder_1_out1,
       decoder_1_out2, decoder_1_out3, enable_0, enable_1, enable_2, enable_3;
  wire [1:0] d_alu_arit_mux, d_reg_i_mux, lsu_state_0, lsu_state_1, lsu_state_2, lsu_state_3;
  wire [2:0] CORE_STATE, d_nzp, fetcher_1_fetcher_state;
  wire [3:0] d_rd_addr, d_rs_addr, d_rt_addr;
  wire [7:0] alu_out_0, alu_out_1, alu_out_2, alu_out_3, current_pc, d_imme, lsu_out_0, lsu_out_1, lsu_out_2,
       lsu_out_3, next_pc_0, next_pc_1, next_pc_2, next_pc_3, register_w_1_rs, register_w_1_rt,
       register_w_2_rs, register_w_2_rt, register_w_3_rs, register_w_3_rt, register_w_4_rs, register_w_4_rt;
  wire [15:0] fetcher_1_instruction;

  fetcher fetcher_1 (
    .mem_read_ready(program_mem_read_ready), .core_state(CORE_STATE), .clk(clk), .reset(reset),
    .current_pc(current_pc), .mem_read_data(program_mem_read_data), .instruction(fetcher_1_instruction),
    .fetcher_state(fetcher_1_fetcher_state), .mem_read_address(program_mem_read_address),
    .mem_read_valid(program_mem_read_valid));
  decoder_w decoder_w_1 (
    .core_state(CORE_STATE), .instruction(fetcher_1_instruction), .clk(clk), .reset(reset),
    .decoded_nzp(d_nzp), .decoded_immediate(d_imme), .decoded_rd_address(d_rd_addr),
    .decoded_rs_address(d_rs_addr), .decoded_rt_address(d_rt_addr), .decoded_pc_mux(d_pc_mux),
    .decoded_alu_output_mux(d_alu_o_m), .decoded_nzp_write_enable(d_nzp_w_e),
    .decoded_mem_write_enable(d_mem_w_e), .decoded_reg_write_enable(d_reg_w_e),
    .decoded_mem_read_enable(d_mem_r_e), .decoded_alu_arithmetic_mux(d_alu_arit_mux),
    .decoded_ret(decoded_ret), .decoded_reg_input_mux(d_reg_i_mux));
  scheduler scheduler_1 (
    .next_pc_1(next_pc_0), .next_pc_2(next_pc_1), .next_pc_3(next_pc_2), .next_pc_4(next_pc_3),
    .reset(reset), .clk(clk), .decoded_ret(decoded_ret), .start(start),
    .fetcher_state(fetcher_1_fetcher_state),
    .lsu_state({lsu_state_3, lsu_state_2, lsu_state_1, lsu_state_0}), .current_pc_4(current_pc),
    .core_state(CORE_STATE), .done(done));  // open: current_pc_1, current_pc_2, current_pc_3
  register_w register_w_1 (
    .decoded_rs_address(d_rs_addr), .decoded_rt_address(d_rt_addr), .decoded_reg_input_mux(d_reg_i_mux),
    .alu_out(alu_out_0), .lsu_out(lsu_out_0), .decoded_immediate(d_imme), .enable(enable_0), .reset(reset),
    .clk(clk), .decoded_rd_address(d_rd_addr), .block_id(block_id), .decoded_reg_write_enable(d_reg_w_e),
    .core_state(CORE_STATE), .rs(register_w_1_rs), .rt(register_w_1_rt));
  register_w register_w_2 (
    .decoded_rs_address(d_rs_addr), .decoded_rt_address(d_rt_addr), .decoded_reg_input_mux(d_reg_i_mux),
    .alu_out(alu_out_1), .lsu_out(lsu_out_1), .decoded_immediate(d_imme), .enable(enable_1), .reset(reset),
    .clk(clk), .decoded_rd_address(d_rd_addr), .block_id(block_id), .decoded_reg_write_enable(d_reg_w_e),
    .core_state(CORE_STATE), .rs(register_w_2_rs), .rt(register_w_2_rt));
  register_w register_w_3 (
    .decoded_rs_address(d_rs_addr), .decoded_rt_address(d_rt_addr), .decoded_reg_input_mux(d_reg_i_mux),
    .alu_out(alu_out_2), .lsu_out(lsu_out_2), .decoded_immediate(d_imme), .enable(enable_2), .reset(reset),
    .clk(clk), .decoded_rd_address(d_rd_addr), .block_id(block_id), .decoded_reg_write_enable(d_reg_w_e),
    .core_state(CORE_STATE), .rs(register_w_3_rs), .rt(register_w_3_rt));
  register_w register_w_4 (
    .decoded_rs_address(d_rs_addr), .decoded_rt_address(d_rt_addr), .decoded_reg_input_mux(d_reg_i_mux),
    .alu_out(alu_out_3), .lsu_out(lsu_out_3), .decoded_immediate(d_imme), .enable(enable_3), .reset(reset),
    .clk(clk), .decoded_rd_address(d_rd_addr), .block_id(block_id), .decoded_reg_write_enable(d_reg_w_e),
    .core_state(CORE_STATE), .rs(register_w_4_rs), .rt(register_w_4_rt));
  Decoder #(.select(3)) decoder_1 (
    .out1(decoder_1_out1), .out2(decoder_1_out2), .out3(decoder_1_out3), .out4(enable_3), .sel(thread_count));  // open: out0, out5, out6, out7, en
  or or_1 (enable_0, decoder_1_out1, decoder_1_out2, decoder_1_out3, enable_3);
  or or_2 (enable_1, decoder_1_out2, decoder_1_out3, enable_3);
  or or_3 (enable_2, decoder_1_out3, enable_3);
  alu alu_1 (
    .enable(enable_0), .core_state(CORE_STATE), .decoded_alu_output_mux(d_alu_o_m), .rs(register_w_1_rs),
    .rt(register_w_1_rt), .decoded_alu_arithmetic_mux(d_alu_arit_mux), .clk(clk), .reset(reset),
    .alu_out(alu_out_0));
  alu alu_2 (
    .enable(enable_1), .core_state(CORE_STATE), .decoded_alu_output_mux(d_alu_o_m), .rs(register_w_2_rs),
    .rt(register_w_2_rt), .decoded_alu_arithmetic_mux(d_alu_arit_mux), .clk(clk), .reset(reset),
    .alu_out(alu_out_1));
  alu alu_3 (
    .enable(enable_2), .core_state(CORE_STATE), .decoded_alu_output_mux(d_alu_o_m), .rs(register_w_3_rs),
    .rt(register_w_3_rt), .decoded_alu_arithmetic_mux(d_alu_arit_mux), .clk(clk), .reset(reset),
    .alu_out(alu_out_2));
  alu alu_4 (
    .enable(enable_3), .core_state(CORE_STATE), .decoded_alu_output_mux(d_alu_o_m), .rs(register_w_4_rs),
    .rt(register_w_4_rt), .decoded_alu_arithmetic_mux(d_alu_arit_mux), .clk(clk), .reset(reset),
    .alu_out(alu_out_3));
  lsu lsu_1 (
    .mem_read_data(data_mem_read_data_0), .mem_write_ready(data_mem_write_ready_0),
    .mem_read_ready(data_mem_read_ready_0), .reset(reset), .clk(clk), .decoded_mem_read_enable(d_mem_r_e),
    .decoded_mem_write_enable(d_mem_w_e), .core_state(CORE_STATE), .enable(enable_0), .rs(register_w_1_rs),
    .rt(register_w_1_rt), .mem_read_address(data_mem_read_address_0), .lsu_out(lsu_out_0),
    .lus_state(lsu_state_0), .mem_write_data(data_mem_write_data_0),
    .mem_write_address(data_mem_write_address_0), .mem_write_valid(data_mem_write_valid_0),
    .mem_read_valid(data_mem_read_valid_0));
  lsu lsu_2 (
    .mem_read_data(data_mem_read_data_1), .mem_write_ready(data_mem_write_ready_1),
    .mem_read_ready(data_mem_read_ready_1), .reset(reset), .clk(clk), .decoded_mem_read_enable(d_mem_r_e),
    .decoded_mem_write_enable(d_mem_w_e), .core_state(CORE_STATE), .enable(enable_1), .rs(register_w_2_rs),
    .rt(register_w_2_rt), .mem_read_address(data_mem_read_address_1), .lsu_out(lsu_out_1),
    .lus_state(lsu_state_1), .mem_write_data(data_mem_write_data_1),
    .mem_write_address(data_mem_write_address_1), .mem_write_valid(data_mem_write_valid_1),
    .mem_read_valid(data_mem_read_valid_1));
  lsu lsu_3 (
    .mem_read_data(data_mem_read_data_2), .mem_write_ready(data_mem_write_ready_2),
    .mem_read_ready(data_mem_read_ready_2), .reset(reset), .clk(clk), .decoded_mem_read_enable(d_mem_r_e),
    .decoded_mem_write_enable(d_mem_w_e), .core_state(CORE_STATE), .enable(enable_2), .rs(register_w_3_rs),
    .rt(register_w_3_rt), .mem_read_address(data_mem_read_address_2), .lsu_out(lsu_out_2),
    .lus_state(lsu_state_2), .mem_write_data(data_mem_write_data_2),
    .mem_write_address(data_mem_write_address_2), .mem_write_valid(data_mem_write_valid_2),
    .mem_read_valid(data_mem_read_valid_2));
  lsu lsu_4 (
    .mem_read_data(data_mem_read_data_3), .mem_write_ready(data_mem_write_ready_3),
    .mem_read_ready(data_mem_read_ready_3), .reset(reset), .clk(clk), .decoded_mem_read_enable(d_mem_r_e),
    .decoded_mem_write_enable(d_mem_w_e), .core_state(CORE_STATE), .enable(enable_3), .rs(register_w_4_rs),
    .rt(register_w_4_rt), .mem_read_address(data_mem_read_address_3), .lsu_out(lsu_out_3),
    .lus_state(lsu_state_3), .mem_write_data(data_mem_write_data_3),
    .mem_write_address(data_mem_write_address_3), .mem_write_valid(data_mem_write_valid_3),
    .mem_read_valid(data_mem_read_valid_3));
  pc pc_1 (
    .enable(enable_0), .alu_out(alu_out_0), .decoded_nzp_write_enable(d_nzp_w_e), .core_state(CORE_STATE),
    .decoded_immediate(d_imme), .reset(reset), .clk(clk), .current_pc(current_pc), .decoded_nzp(d_nzp),
    .decoded_pc_mux(d_pc_mux), .next_pc(next_pc_0));
  pc pc_2 (
    .enable(enable_1), .alu_out(alu_out_1), .decoded_nzp_write_enable(d_nzp_w_e), .core_state(CORE_STATE),
    .decoded_immediate(d_imme), .reset(reset), .clk(clk), .current_pc(current_pc), .decoded_nzp(d_nzp),
    .decoded_pc_mux(d_pc_mux), .next_pc(next_pc_1));
  pc pc_3 (
    .enable(enable_2), .alu_out(alu_out_2), .decoded_nzp_write_enable(d_nzp_w_e), .core_state(CORE_STATE),
    .decoded_immediate(d_imme), .reset(reset), .clk(clk), .current_pc(current_pc), .decoded_nzp(d_nzp),
    .decoded_pc_mux(d_pc_mux), .next_pc(next_pc_2));
  pc pc_4 (
    .enable(enable_3), .alu_out(alu_out_3), .decoded_nzp_write_enable(d_nzp_w_e), .core_state(CORE_STATE),
    .decoded_immediate(d_imme), .reset(reset), .clk(clk), .current_pc(current_pc), .decoded_nzp(d_nzp),
    .decoded_pc_mux(d_pc_mux), .next_pc(next_pc_3));
endmodule

module dispath_bit (
  input  start,
  input  clk,
  input  reset,
  input  [7:0] thread_count,
  input  [1:0] core_done,
  output [1:0] core_reset,
  output done,
  output [1:0] core_start,
  output [7:0] core_block_id_0,
  output [2:0] core_thread_count_0,
  output [7:0] core_block_id_1,
  output [2:0] core_thread_count_1
);

  wire and_1_out, and_4_out, and_9_out, and_10_out, and_11_out, and_12_out, and_13_out, comparator_1_gt,
       comparator_2_eq, comparator_3_eq, comparator_4_lt, CORE_RESET_BIT0, CORE_RESET_BIT1, not_1_out,
       not_2_out, not_3_out, or_1_out, or_2_out, or_3_out, or_4_out, or_5_out, or_6_out, or_7_out, or_8_out,
       or_9_out, or_10_out, or_11_out, start_execution_reg_q;
  wire [1:0] and_2_out, and_5_out, bitadder_1_out, multiplexer_1_out, multiplexer_2_out, multiplexer_3_out,
       multiplexer_4_out, multiplexer_6_out;
  wire [2:0] bit_extender_2_out, bit_extender_3_out;
  wire [7:0] adder_1_out, adder_2_out, adder_3_out, adder_4_out, bit_extender_1_out, blocks_dispatched_reg_q,
       blocks_done_reg_q, multiplexer_5_out, multiplexer_7_out, multiplexer_8_out, multiplier_1_out,
       multiplier_2_out, subtractor_1_out, subtractor_2_out, subtractor_3_out, subtractor_4_out, total_blocks;

  and and_1 (and_1_out, not_1_out, start);
  Multiplexer #(.width(2)) multiplexer_1 (
    .in0(2'b00), .in1({CORE_RESET_BIT1, CORE_RESET_BIT0}), .out(multiplexer_1_out), .sel(or_9_out));
  not not_1 (not_1_out, start_execution_reg_q);
  Register #(.width(1)) start_execution_reg (
    .D(not_1_out), .en(and_1_out), .clk(clk), .Q(start_execution_reg_q), .clr(reset));
  not not_2 (not_2_out, and_5_out[0]);
  or or_1 (or_1_out, not_2_out, multiplexer_1_out[0]);
  not not_3 (not_3_out, and_5_out[1]);
  or or_2 (or_2_out, and_1_out, reset);
  Multiplexer #(.width(2)) multiplexer_2 (.in0(2'b00), .in1(2'b11), .out(multiplexer_2_out), .sel(or_2_out));
  or or_3 (or_3_out, not_3_out, multiplexer_1_out[1]);
  and and_2 (and_2_out[0], CORE_RESET_BIT0, 1'b0);
  and and_3 (and_2_out[1], 1'b0, CORE_RESET_BIT1);
  Multiplexer #(.width(2)) multiplexer_3 (
    .in0(multiplexer_2_out), .in1(and_5_out), .out(multiplexer_3_out), .sel(or_8_out));
  or or_4 (or_4_out, and_5_out[0], or_9_out);
  or or_5 (or_5_out, and_5_out[1], or_9_out);
  Multiplexer #(.width(2)) multiplexer_4 (
    .in0(multiplexer_3_out), .in1(and_2_out), .out(multiplexer_4_out), .sel(or_6_out));
  assign bit_extender_1_out = {{6{1'b0}}, bitadder_1_out};  // Bit_Extender bit_extender_1
  BitAdder #(.width(2)) bitadder_1 (.in0(and_5_out), .out(bitadder_1_out));
  Register #(.width(1)) core_start_reg_bit0 (.D(or_1_out), .en(or_4_out), .clk(clk), .Q(core_start[0]), .clr(reset));
  Register #(.width(1)) core_start_reg_bit1 (.D(or_3_out), .en(or_5_out), .clk(clk), .Q(core_start[1]), .clr(reset));
  or or_6 (or_6_out, CORE_RESET_BIT0, CORE_RESET_BIT1);
  and and_4 (and_4_out, start, or_8_out);
  Multiplexer #(.width(8)) multiplexer_5 (
    .in0({8{1'b0}}), .in1(bit_extender_1_out), .out(multiplexer_5_out), .sel(or_8_out));
  Register #(.width(2)) core_reset_reg (.D(multiplexer_6_out), .en(or_7_out), .clk(clk), .Q(core_reset));  // open: clr
  Multiplexer #(.width(2)) multiplexer_6 (.in0(multiplexer_4_out), .in1(2'b11), .out(multiplexer_6_out), .sel(reset));
  or or_7 (or_7_out, or_6_out, or_2_out, and_4_out);
  and and_5 (and_5_out[0], core_start[0], core_done[0]);
  and and_6 (and_5_out[1], core_start[1], core_done[1]);
  or or_8 (or_8_out, and_5_out[0], and_5_out[1]);
  Adder adder_1 (.a(blocks_dispatched_reg_q), .b({8{1'b0}}), .out(adder_1_out), .cin(and_10_out));  // open: cout
  and and_7 (CORE_RESET_BIT0, start, core_reset[0]);
  and and_8 (CORE_RESET_BIT1, core_reset[1], start);
  and and_9 (and_9_out, start, or_8_out);
  or or_9 (or_9_out, and_12_out, and_13_out);
  Adder adder_2 (.a(adder_1_out), .b({8{1'b0}}), .out(adder_2_out), .cin(and_11_out));  // open: cout
  and and_10 (and_10_out, CORE_RESET_BIT0, comparator_4_lt);
  and and_11 (and_11_out, comparator_4_lt, CORE_RESET_BIT1);
  Adder adder_3 (.a(blocks_done_reg_q), .b(multiplexer_5_out), .out(adder_3_out));  // open: cin, cout
  and and_12 (and_12_out, CORE_RESET_BIT1, comparator_1_gt);
  and and_13 (and_13_out, comparator_1_gt, CORE_RESET_BIT0);
  Adder adder_4 (.a(thread_count), .b(8'h3), .out(adder_4_out));  // open: cin, cout
  Register blocks_done_reg (.D(adder_3_out), .en(and_9_out), .clk(clk), .Q(blocks_done_reg_q), .clr(reset));
  Shifter #(.shift("lr")) shifter_1 (.in(adder_4_out), .\dist (3'b010), .out(total_blocks));
  Register blocks_dispatched_reg (
    .D(adder_2_out), .en(comparator_4_lt), .clk(clk), .Q(blocks_dispatched_reg_q), .clr(reset));
  Register core_block_id_reg_1 (.D(adder_2_out), .en(and_11_out), .clk(clk), .Q(core_block_id_1), .clr(reset));
  Register core_block_id_reg_0 (.D(adder_1_out), .en(and_10_out), .clk(clk), .Q(core_block_id_0), .clr(reset));
  Multiplier multiplier_1 (.a(8'h4), .b(adder_2_out), .out(multiplier_1_out));  // open: cin, cout
  Multiplier multiplier_2 (.a(adder_1_out), .b(8'h4), .out(multiplier_2_out));  // open: cin, cout
  Subtractor subtractor_1 (.a(total_blocks), .b(multiplier_1_out), .out(subtractor_1_out));  // open: bin, bout
  Comparator comparator_1 (.a(total_blocks), .b(blocks_done_reg_q), .gt(comparator_1_gt), .eq(done));  // open: lt
  Comparator comparator_2 (.a(adder_1_out), .b(subtractor_2_out), .eq(comparator_2_eq));  // open: gt, lt
  Subtractor subtractor_2 (.a(total_blocks), .b(8'h1), .out(subtractor_2_out));  // open: bin, bout
  Subtractor subtractor_3 (.a(total_blocks), .b(multiplier_2_out), .out(subtractor_3_out));  // open: bin, bout
  or or_10 (or_10_out, and_10_out, reset);
  Comparator comparator_3 (.a(adder_2_out), .b(subtractor_4_out), .eq(comparator_3_eq));  // open: gt, lt
  Subtractor subtractor_4 (.a(total_blocks), .b(8'h1), .out(subtractor_4_out));  // open: bin, bout
  or or_11 (or_11_out, and_11_out, reset);
  Comparator comparator_4 (.a(blocks_dispatched_reg_q), .b(total_blocks), .lt(comparator_4_lt));  // open: gt, eq
  Multiplexer #(.width(8)) multiplexer_7 (
    .in0(8'h4), .in1(subtractor_3_out), .out(multiplexer_7_out), .sel(comparator_2_eq));
  Multiplexer #(.width(8)) multiplexer_8 (
    .in0(8'h4), .in1(subtractor_1_out), .out(multiplexer_8_out), .sel(comparator_3_eq));
  Register #(.width(3)) core_thread_count_reg_0 (
    .D(bit_extender_2_out), .en(or_10_out), .clk(clk), .Q(core_thread_count_0));  // open: clr
  Bit_Extender #(.out_width(3)) bit_extender_2 (.in(multiplexer_7_out), .out(bit_extender_2_out));
  Register #(.width(3)) core_thread_count_reg_1 (
    .D(bit_extender_3_out), .en(or_11_out), .clk(clk), .Q(core_thread_count_1));  // open: clr
  Bit_Extender #(.out_width(3)) bit_extender_3 (.in(multiplexer_8_out), .out(bit_extender_3_out));
endmodule

module gpu (
  input  in_1,
  input  [7:0] in_2,
  input  in_3,
  output done
);

  wire core_done_0, core_done_1, core_reset_0, core_reset_1, core_start_0, core_start_1, reset;
  wire [2:0] core_thread_count_0, core_thread_count_1;
  wire [7:0] core_block_id_0, core_block_id_1;

  dispath_bit dispath_bit_1 (
    .start(in_1), .clk(in_3), .reset(reset), .core_done({core_done_1, core_done_0}), .thread_count(in_2),
    .core_block_id_1(core_block_id_1), .core_block_id_0(core_block_id_0), .done(done),
    .core_thread_count_1(core_thread_count_1), .core_thread_count_0(core_thread_count_0),
    .core_start({core_start_1, core_start_0}), .core_reset({core_reset_1, core_reset_0}));
  core core_1 (
    .thread_count(core_thread_count_0), .clk(in_3), .block_id(core_block_id_0), .start(core_start_0),
    .done(core_done_0));  // open: reset, data_mem_read_ready_0, data_mem_read_ready_1, data_mem_read_ready_2, data_mem_read_ready_3, data_mem_write_ready_0, data_mem_write_ready_1, data_mem_write_ready_2, data_mem_write_ready_3, program_mem_read_ready, data_mem_read_data_0, data_mem_read_data_1, data_mem_read_data_2, data_mem_read_data_3, program_mem_read_data, program_mem_read_address, program_mem_read_valid, data_mem_write_valid_0, data_mem_write_valid_1, data_mem_write_valid_2, data_mem_write_valid_3, data_mem_read_valid_0, data_mem_read_valid_1, data_mem_read_valid_2, data_mem_read_valid_3, data_mem_write_data_0, data_mem_write_data_1, data_mem_write_data_2, data_mem_write_data_3, data_mem_write_address_0, data_mem_write_address_1, data_mem_write_address_2, data_mem_write_address_3, data_mem_read_address_0, data_mem_read_address_1, data_mem_read_address_2, data_mem_read_address_3
  core core_2 (
    .thread_count(core_thread_count_1), .block_id(core_block_id_1), .start(core_start_1), .done(core_done_1));  // open: clk, reset, data_mem_read_ready_0, data_mem_read_ready_1, data_mem_read_ready_2, data_mem_read_ready_3, data_mem_write_ready_0, data_mem_write_ready_1, data_mem_write_ready_2, data_mem_write_ready_3, program_mem_read_ready, data_mem_read_data_0, data_mem_read_data_1, data_mem_read_data_2, data_mem_read_data_3, program_mem_read_data, program_mem_read_address, program_mem_read_valid, data_mem_write_valid_0, data_mem_write_valid_1, data_mem_write_valid_2, data_mem_write_valid_3, data_mem_read_valid_0, data_mem_read_valid_1, data_mem_read_valid_2, data_mem_read_valid_3, data_mem_write_data_0, data_mem_write_data_1, data_mem_write_data_2, data_mem_write_data_3, data_mem_write_address_0, data_mem_write_address_1, data_mem_write_address_2, data_mem_write_address_3, data_mem_read_address_0, data_mem_read_address_1, data_mem_read_address_2, data_mem_read_address_3

  // Other names for the same wires on the sheet: clk = in_3
endmodule

module controller (
  input  reset,
  input  clk,
  input  [3:0] consumer_read_valid,
  input  mem_read_ready,
  input  [7:0] consumer_read_address_0,
  input  [7:0] consumer_read_address_1,
  input  [7:0] consumer_read_address_2,
  input  [7:0] consumer_read_address_3,
  input  mem_write_ready,
  input  [3:0] consumer_write_valid,
  input  [15:0] consumer_write_data_0,
  input  [15:0] consumer_write_data_1,
  input  [15:0] consumer_write_data_2,
  input  [15:0] consumer_write_data_3,
  input  [7:0] consumer_write_address_0,
  input  [7:0] consumer_write_address_1,
  input  [7:0] consumer_write_address_2,
  input  [7:0] consumer_write_address_3,
  output mem_read_valid,
  output [7:0] mem_read_address,
  output mem_write_valid,
  output [15:0] mem_write_data,
  output [7:0] mem_write_address,
  output [3:0] consumer_read_ready,
  output [3:0] consumer_write_ready
);

  wire and_1_out, and_2_out, and_3_out, and_4_out, and_5_out, and_6_out, and_7_out, and_8_out, and_18_out,
       bitfinder_1_found, bitfinder_2_found, channel_serving_consumer_reg_0_q,
       channel_serving_consumer_reg_1_q, channel_serving_consumer_reg_2_q, channel_serving_consumer_reg_3_q,
       consumer_rw_and_channel_serving_consumer_success, decoder_2_out0, decoder_2_out1, decoder_2_out2,
       decoder_2_out3, decoder_3_out0, decoder_3_out1, decoder_3_out2, decoder_3_out3, decoder_4_out0,
       decoder_4_out1, decoder_4_out2, decoder_4_out3, decoder_5_out0, decoder_5_out1, decoder_5_out2,
       decoder_5_out3, decoder_6_out0, decoder_6_out1, decoder_6_out2, decoder_6_out3, IDLE_STATE,
       multiplexer_5_out, multiplexer_6_out, multiplexer_7_out, multiplexer_11_out, multiplexer_13_out,
       not_1_out, not_2_out, not_3_out, not_4_out, not_5_out, not_6_out, not_7_out, not_8_out, not_9_out,
       not_10_out, not_11_out, not_12_out, not_13_out, not_14_out, or_1_out, or_2_out, or_3_out, or_6_out,
       or_7_out, or_9_out, or_10_out, READ_RELAYING_STATE, READ_RELAYING_STATE_UPDATE, READ_WAITING_STATE,
       READ_WAITING_STATE_UPDATE, WRITE_RELAYING_STATE, WRITE_RELAYING_STATE_UPDATE, WRITE_WAITING_STATE,
       WRITE_WAITING_STATE_UPDATE;
  wire [1:0] bitfinder_1_index, bitfinder_2_index, consumer_rw_and_channel_serving_consumer_bit,
       current_consumer;
  wire [2:0] controller_state_reg_q, multiplexer_1_out, multiplexer_2_out, multiplexer_3_out,
       multiplexer_4_out;
  wire [3:0] and_9_out, and_13_out;
  wire [7:0] multiplexer_10_out, multiplexer_12_out;
  wire [15:0] multiplexer_9_out;

  Multiplexer #(.width(3)) multiplexer_1 (
    .in0(3'b000), .in1(3'b101), .out(multiplexer_1_out), .sel(WRITE_WAITING_STATE_UPDATE));
  not not_1 (not_1_out, reset);
  Decoder #(.select(3)) decoder_1 (
    .out0(IDLE_STATE), .out2(READ_WAITING_STATE), .out3(WRITE_WAITING_STATE), .out4(READ_RELAYING_STATE),
    .out5(WRITE_RELAYING_STATE), .sel(controller_state_reg_q), .en(not_1_out));  // open: out1, out6, out7
  Decoder #(.select(2)) decoder_2 (
    .out0(decoder_2_out0), .out1(decoder_2_out1), .out2(decoder_2_out2), .out3(decoder_2_out3),
    .sel(current_consumer), .en(READ_RELAYING_STATE));
  Decoder #(.select(2)) decoder_3 (
    .out0(decoder_3_out0), .out1(decoder_3_out1), .out2(decoder_3_out2), .out3(decoder_3_out3),
    .sel(current_consumer), .en(WRITE_RELAYING_STATE));
  Multiplexer #(.width(3)) multiplexer_2 (
    .in0(multiplexer_1_out), .in1(3'b100), .out(multiplexer_2_out), .sel(READ_WAITING_STATE_UPDATE));
  or or_1 (or_1_out, reset, consumer_rw_and_channel_serving_consumer_success, READ_WAITING_STATE_UPDATE, WRITE_WAITING_STATE_UPDATE, or_3_out);
  or or_2 (or_2_out, WRITE_WAITING_STATE_UPDATE, WRITE_RELAYING_STATE_UPDATE);
  Multiplexer #(.width(3)) multiplexer_3 (
    .in0(multiplexer_2_out), .in1(3'b010), .out(multiplexer_3_out),
    .sel(consumer_rw_and_channel_serving_consumer_success));
  Multiplexer #(.width(3)) multiplexer_4 (.in0(multiplexer_3_out), .in1(3'b000), .out(multiplexer_4_out), .sel(reset));
  not not_2 (not_2_out, consumer_read_valid[0]);
  not not_3 (not_3_out, consumer_read_valid[1]);
  not not_4 (not_4_out, consumer_read_valid[2]);
  not not_5 (not_5_out, consumer_read_valid[3]);
  not not_6 (not_6_out, consumer_write_valid[0]);
  not not_7 (not_7_out, consumer_write_valid[1]);
  not not_8 (not_8_out, consumer_write_valid[2]);
  not not_9 (not_9_out, consumer_write_valid[3]);
  Decoder #(.select(2)) decoder_4 (
    .out0(decoder_4_out0), .out1(decoder_4_out1), .out2(decoder_4_out2), .out3(decoder_4_out3),
    .sel(current_consumer), .en(or_2_out));
  or or_3 (or_3_out, WRITE_RELAYING_STATE_UPDATE, READ_RELAYING_STATE_UPDATE);
  Register #(.width(3)) controller_state_reg (
    .D(multiplexer_4_out), .en(or_1_out), .clk(clk), .Q(controller_state_reg_q));  // open: clr
  and and_1 (and_1_out, decoder_2_out0, not_2_out);
  and and_2 (and_2_out, decoder_2_out1, not_3_out);
  and and_3 (and_3_out, decoder_2_out2, not_4_out);
  and and_4 (and_4_out, decoder_2_out3, not_5_out);
  and and_5 (and_5_out, decoder_3_out0, not_6_out);
  and and_6 (and_6_out, decoder_3_out1, not_7_out);
  and and_7 (and_7_out, decoder_3_out2, not_8_out);
  and and_8 (and_8_out, decoder_3_out3, not_9_out);
  Multiplexer multiplexer_5 (.in0(1'b0), .in1(1'b1), .out(multiplexer_5_out), .sel(WRITE_WAITING_STATE_UPDATE));
  or or_4 (READ_RELAYING_STATE_UPDATE, and_1_out, and_2_out, and_3_out, and_4_out);
  or or_5 (WRITE_RELAYING_STATE_UPDATE, and_5_out, and_6_out, and_7_out, and_8_out);
  Register #(.width(1)) consumer_write_ready_reg_0 (
    .D(multiplexer_5_out), .en(decoder_4_out0), .clk(clk), .Q(consumer_write_ready[0]), .clr(reset));
  Register #(.width(1)) consumer_write_ready_reg_1 (
    .D(multiplexer_5_out), .en(decoder_4_out1), .clk(clk), .Q(consumer_write_ready[1]), .clr(reset));
  Register #(.width(1)) consumer_write_ready_reg_2 (
    .D(multiplexer_5_out), .en(decoder_4_out2), .clk(clk), .Q(consumer_write_ready[2]), .clr(reset));
  Register #(.width(1)) consumer_write_ready_reg_3 (
    .D(multiplexer_5_out), .en(decoder_4_out3), .clk(clk), .Q(consumer_write_ready[3]), .clr(reset));
  or or_6 (or_6_out, consumer_rw_and_channel_serving_consumer_success, WRITE_RELAYING_STATE_UPDATE, READ_RELAYING_STATE_UPDATE);
  Decoder #(.select(2)) decoder_5 (
    .out0(decoder_5_out0), .out1(decoder_5_out1), .out2(decoder_5_out2), .out3(decoder_5_out3),
    .sel(consumer_rw_and_channel_serving_consumer_bit), .en(or_6_out));
  or or_7 (or_7_out, READ_WAITING_STATE_UPDATE, READ_RELAYING_STATE_UPDATE);
  Decoder #(.select(2)) decoder_6 (
    .out0(decoder_6_out0), .out1(decoder_6_out1), .out2(decoder_6_out2), .out3(decoder_6_out3),
    .sel(current_consumer), .en(or_7_out));
  Multiplexer multiplexer_6 (
    .in0(1'b0), .in1(1'b1), .out(multiplexer_6_out), .sel(consumer_rw_and_channel_serving_consumer_success));
  Register #(.width(1)) channel_serving_consumer_reg_0 (
    .D(multiplexer_6_out), .en(decoder_5_out0), .clk(clk), .Q(channel_serving_consumer_reg_0_q), .clr(reset));
  Register #(.width(1)) channel_serving_consumer_reg_1 (
    .D(multiplexer_6_out), .en(decoder_5_out1), .clk(clk), .Q(channel_serving_consumer_reg_1_q), .clr(reset));
  Register #(.width(1)) channel_serving_consumer_reg_2 (
    .D(multiplexer_6_out), .en(decoder_5_out2), .clk(clk), .Q(channel_serving_consumer_reg_2_q), .clr(reset));
  Register #(.width(1)) channel_serving_consumer_reg_3 (
    .D(multiplexer_6_out), .en(decoder_5_out3), .clk(clk), .Q(channel_serving_consumer_reg_3_q), .clr(reset));
  Multiplexer multiplexer_7 (.in0(1'b0), .in1(1'b1), .out(multiplexer_7_out), .sel(READ_WAITING_STATE_UPDATE));
  not not_10 (not_10_out, channel_serving_consumer_reg_0_q);
  not not_11 (not_11_out, channel_serving_consumer_reg_1_q);
  not not_12 (not_12_out, channel_serving_consumer_reg_2_q);
  not not_13 (not_13_out, channel_serving_consumer_reg_3_q);
  Register #(.width(1)) consumer_read_ready_reg_0 (
    .D(multiplexer_7_out), .en(decoder_6_out0), .clk(clk), .Q(consumer_read_ready[0]), .clr(reset));
  Register #(.width(1)) consumer_read_ready_reg_1 (
    .D(multiplexer_7_out), .en(decoder_6_out1), .clk(clk), .Q(consumer_read_ready[1]), .clr(reset));
  Register #(.width(1)) consumer_read_ready_reg_2 (
    .D(multiplexer_7_out), .en(decoder_6_out2), .clk(clk), .Q(consumer_read_ready[2]), .clr(reset));
  Register #(.width(1)) consumer_read_ready_reg_3 (
    .D(multiplexer_7_out), .en(decoder_6_out3), .clk(clk), .Q(consumer_read_ready[3]), .clr(reset));
  and and_9 (and_9_out[0], consumer_read_valid[0], not_10_out, IDLE_STATE);
  and and_10 (and_9_out[1], consumer_read_valid[1], not_11_out, IDLE_STATE);
  and and_11 (and_9_out[2], consumer_read_valid[2], not_12_out, IDLE_STATE);
  and and_12 (and_9_out[3], consumer_read_valid[3], not_13_out, IDLE_STATE);
  and and_13 (and_13_out[0], not_10_out, IDLE_STATE, consumer_write_valid[0]);
  and and_14 (and_13_out[1], not_11_out, IDLE_STATE, consumer_write_valid[1]);
  and and_15 (and_13_out[2], not_12_out, IDLE_STATE, consumer_write_valid[2]);
  and and_16 (and_13_out[3], not_13_out, IDLE_STATE, consumer_write_valid[3]);
  BitFinder #(.width(4)) bitfinder_1 (.in(and_9_out), .index(bitfinder_1_index), .found(bitfinder_1_found));
  or or_8 (consumer_rw_and_channel_serving_consumer_success, bitfinder_1_found, bitfinder_2_found);
  BitFinder #(.width(4)) bitfinder_2 (.in(and_13_out), .index(bitfinder_2_index), .found(bitfinder_2_found));
  Multiplexer #(.width(2)) multiplexer_8 (
    .in0(bitfinder_1_index), .in1(bitfinder_2_index), .out(consumer_rw_and_channel_serving_consumer_bit),
    .sel(bitfinder_2_found));
  and and_17 (READ_WAITING_STATE_UPDATE, mem_read_ready, READ_WAITING_STATE);
  not not_14 (not_14_out, bitfinder_1_found);
  and and_18 (and_18_out, not_14_out, bitfinder_2_found);
  Multiplexer #(.select(2), .width(16)) multiplexer_9 (
    .in0(consumer_write_data_0), .in1(consumer_write_data_1), .in2(consumer_write_data_2),
    .in3(consumer_write_data_3), .out(multiplexer_9_out), .sel(bitfinder_2_index));
  Multiplexer #(.select(2), .width(8)) multiplexer_10 (
    .in0(consumer_write_address_0), .in1(consumer_write_address_1), .in2(consumer_write_address_2),
    .in3(consumer_write_address_3), .out(multiplexer_10_out), .sel(bitfinder_2_index));
  Register #(.width(2)) current_consumer_reg (
    .D(consumer_rw_and_channel_serving_consumer_bit), .en(consumer_rw_and_channel_serving_consumer_success),
    .clk(clk), .Q(current_consumer), .clr(reset));
  Multiplexer multiplexer_11 (.in0(1'b0), .in1(or_9_out), .out(multiplexer_11_out), .sel(bitfinder_1_found));
  or or_9 (or_9_out, READ_WAITING_STATE_UPDATE, bitfinder_1_found);
  Multiplexer #(.select(2), .width(8)) multiplexer_12 (
    .in0(consumer_read_address_0), .in1(consumer_read_address_1), .in2(consumer_read_address_2),
    .in3(consumer_read_address_3), .out(multiplexer_12_out), .sel(bitfinder_1_index));
  Register #(.width(16)) mem_write_data_reg (
    .D(multiplexer_9_out), .en(and_18_out), .clk(clk), .Q(mem_write_data), .clr(reset));
  Register mem_write_address_reg (
    .D(multiplexer_10_out), .en(and_18_out), .clk(clk), .Q(mem_write_address), .clr(reset));
  Register #(.width(1)) mem_read_valid_reg (
    .D(multiplexer_11_out), .en(or_9_out), .clk(clk), .Q(mem_read_valid), .clr(reset));
  Multiplexer multiplexer_13 (.in0(1'b0), .in1(or_10_out), .out(multiplexer_13_out), .sel(and_18_out));
  or or_10 (or_10_out, WRITE_WAITING_STATE_UPDATE, and_18_out);
  Register mem_read_address_reg (
    .D(multiplexer_12_out), .en(consumer_rw_and_channel_serving_consumer_success), .clk(clk),
    .Q(mem_read_address), .clr(reset));
  Register #(.width(1)) mem_write_valid_reg (
    .D(multiplexer_13_out), .en(or_10_out), .clk(clk), .Q(mem_write_valid), .clr(reset));
  and and_19 (WRITE_WAITING_STATE_UPDATE, WRITE_WAITING_STATE, mem_write_ready);
endmodule

module dcr (
  input  [7:0] device_control_data,
  input  device_control_write_enable,
  input  clk,
  input  reset,
  output [7:0] thread_count
);

  wire [7:0] device_conrol_register_reg_q;

  Register device_conrol_register_reg (
    .D(device_control_data), .en(device_control_write_enable), .clk(clk), .Q(device_conrol_register_reg_q),
    .clr(reset));
  Register thread_count_reg (
    .D(device_conrol_register_reg_q), .en(device_control_write_enable), .clk(clk), .Q(thread_count),
    .clr(reset));
endmodule
