// Logisim project register_module.circ as structural Verilog: 1 circuit, main circuit register_w
module register_w (
  input  [7:0] THREAD_ID,
  input  [3:0] decoded_rs_address,
  input  [7:0] block_id,
  input  enable,
  input  reset,
  input  clk,
  input  [3:0] decoded_rt_address,
  input  [3:0] decoded_rd_address,
  input  decoded_reg_write_enable,
  input  [1:0] decoded_reg_input_mux,
  input  [7:0] alu_out,
  input  [7:0] lsu_out,
  input  [7:0] decoded_immediate,
  input  [2:0] core_state,
  output [7:0] rs,
  output [7:0] rt
);

  wire and_1_out, decoder_1_out3, decoder_1_out6, decoder_2_out0, decoder_2_out1, decoder_2_out2,
       decoder_2_out3, decoder_2_out4, decoder_2_out5, decoder_2_out6, decoder_2_out7, decoder_2_out8,
       decoder_2_out9, decoder_2_out10, decoder_2_out11, decoder_2_out12, or_1_out, or_2_out, or_3_out;
  wire [7:0] multiplexer_1_out, multiplexer_2_out, multiplexer_3_out, reg_0_q, reg_1_q, reg_2_q, reg_3_q,
       reg_4_q, reg_5_q, reg_6_q, reg_7_q, reg_8_q, reg_9_q, reg_10_q, reg_11_q, reg_12_q, reg_13_q,
       reg_14_q, reg_15_q;

  // Probe on decoded_rd_address
  Multiplexer #(.select(2), .width(8)) multiplexer_1 (
    .in0(alu_out), .in1(lsu_out), .in2(decoded_immediate), .out(multiplexer_1_out),
    .sel(decoded_reg_input_mux));  // open: in3
  // Probe on core_state
  or or_1 (or_1_out, enable, reset);
  or or_2 (or_2_out, enable, reset);
  or or_3 (or_3_out, enable, enable);
  Decoder #(.select(3)) decoder_1 (
    .out3(decoder_1_out3), .out6(decoder_1_out6), .sel(core_state), .en(enable));  // open: out0, out1, out2, out4, out5, out7
  Register reg_14 (.D(8'h4), .en(or_1_out), .clk(clk), .Q(reg_14_q));  // open: clr
  Register reg_15 (.D(THREAD_ID), .en(or_2_out), .clk(clk), .Q(reg_15_q));  // open: clr
  Register reg_13 (.D(block_id), .en(or_3_out), .clk(clk), .Q(reg_13_q), .clr(reset));
  // Probe on multiplexer_1_out
  Decoder #(.select(4)) decoder_2 (
    .out0(decoder_2_out0), .out1(decoder_2_out1), .out2(decoder_2_out2), .out3(decoder_2_out3),
    .out4(decoder_2_out4), .out5(decoder_2_out5), .out6(decoder_2_out6), .out7(decoder_2_out7),
    .out8(decoder_2_out8), .out9(decoder_2_out9), .out10(decoder_2_out10), .out11(decoder_2_out11),
    .out12(decoder_2_out12), .sel(decoded_rd_address), .en(and_1_out));  // open: out13, out14, out15
  and and_1 (and_1_out, decoded_reg_write_enable, decoder_1_out6);
  Register reg_0 (.D(multiplexer_1_out), .en(decoder_2_out0), .clk(clk), .Q(reg_0_q), .clr(reset));
  Register reg_1 (.D(multiplexer_1_out), .en(decoder_2_out1), .clk(clk), .Q(reg_1_q), .clr(reset));
  Register reg_2 (.D(multiplexer_1_out), .en(decoder_2_out2), .clk(clk), .Q(reg_2_q), .clr(reset));
  Register reg_3 (.D(multiplexer_1_out), .en(decoder_2_out3), .clk(clk), .Q(reg_3_q), .clr(reset));
  Register reg_4 (.D(multiplexer_1_out), .en(decoder_2_out4), .clk(clk), .Q(reg_4_q), .clr(reset));
  Register reg_5 (.D(multiplexer_1_out), .en(decoder_2_out5), .clk(clk), .Q(reg_5_q), .clr(reset));
  Register reg_6 (.D(multiplexer_1_out), .en(decoder_2_out6), .clk(clk), .Q(reg_6_q), .clr(reset));
  Register reg_7 (.D(multiplexer_1_out), .en(decoder_2_out7), .clk(clk), .Q(reg_7_q), .clr(reset));
  Register reg_8 (.D(multiplexer_1_out), .en(decoder_2_out8), .clk(clk), .Q(reg_8_q), .clr(reset));
  Register reg_9 (.D(multiplexer_1_out), .en(decoder_2_out9), .clk(clk), .Q(reg_9_q), .clr(reset));
  Register reg_10 (.D(multiplexer_1_out), .en(decoder_2_out10), .clk(clk), .Q(reg_10_q), .clr(reset));
  Register reg_11 (.D(multiplexer_1_out), .en(decoder_2_out11), .clk(clk), .Q(reg_11_q), .clr(reset));
  Register reg_12 (.D(multiplexer_1_out), .en(decoder_2_out12), .clk(clk), .Q(reg_12_q), .clr(reset));
  Multiplexer #(.select(4), .width(8)) multiplexer_2 (
    .in0(reg_0_q), .in1(reg_1_q), .in2(reg_2_q), .in3(reg_3_q), .in4(reg_4_q), .in5(reg_5_q), .in6(reg_6_q),
    .in7(reg_7_q), .in8(reg_8_q), .in9(reg_9_q), .in10(reg_10_q), .in11(reg_11_q), .in12(reg_12_q),
    .in13(reg_13_q), .in14(reg_14_q), .in15(reg_15_q), .out(multiplexer_2_out), .sel(decoded_rs_address));
  Multiplexer #(.select(4), .width(8)) multiplexer_3 (
    .in0(reg_0_q), .in1(reg_1_q), .in2(reg_2_q), .in3(reg_3_q), .in4(reg_4_q), .in5(reg_5_q), .in6(reg_6_q),
    .in7(reg_7_q), .in8(reg_8_q), .in9(reg_9_q), .in10(reg_10_q), .in11(reg_11_q), .in12(reg_12_q),
    .in13(reg_13_q), .in14(reg_14_q), .in15(reg_15_q), .out(multiplexer_3_out), .sel(decoded_rt_address));
  Register reg_rs (.D(multiplexer_2_out), .en(decoder_1_out3), .clk(clk), .Q(rs));  // open: clr
  Register reg_rt (.D(multiplexer_3_out), .en(decoder_1_out3), .clk(clk), .Q(rt));  // open: clr
endmodule
