// Logisim project scheduler_module.circ as structural Verilog: 1 circuit, main circuit scheduler
module scheduler (
  input  [7:0] next_pc_1,
  input  [7:0] next_pc_2,
  input  [7:0] next_pc_3,
  input  [7:0] next_pc_4,
  input  reset,
  input  clk,
  input  decoded_ret,
  input  start,
  input  [1:0] fetcher_state,
  input  [7:0] lsu_state,
  output [7:0] current_pc_1,
  output [7:0] current_pc_2,
  output [7:0] current_pc_3,
  output [7:0] current_pc_4,
  output [2:0] core_state,
  output done
);

  wire and_1_out, and_2_out, comparator_1_eq, decoder_1_out2, multiplexer_1_out, nor_1_out, not_1_out,
       not_2_out, or_1_out, or_2_out, xor_1_out, xor_2_out, xor_3_out, xor_4_out;
  wire [2:0] adder_1_out, bit_extender_1_out, multiplexer_2_out;

  xor xor_1 (xor_1_out, lsu_state[0], lsu_state[1]);
  xor xor_2 (xor_2_out, lsu_state[2], lsu_state[3]);
  xor xor_3 (xor_3_out, lsu_state[4], lsu_state[5]);
  xor xor_4 (xor_4_out, lsu_state[6], lsu_state[7]);
  or or_1 (or_1_out, xor_1_out, xor_2_out);
  or or_2 (or_2_out, xor_3_out, xor_4_out);
  Decoder #(.select(2)) decoder_1 (.out2(decoder_1_out2), .sel(fetcher_state));  // open: out0, out1, out3, en
  nor nor_1 (nor_1_out, or_1_out, or_2_out);
  assign bit_extender_1_out = {{2{1'b0}}, multiplexer_1_out};  // Bit_Extender bit_extender_1
  Multiplexer #(.select(3)) multiplexer_1 (
    .in0(start), .in1(decoder_1_out2), .in2(1'b1), .in3(1'b1), .in4(nor_1_out), .in5(1'b1), .in6(and_2_out),
    .in7(1'b0), .out(multiplexer_1_out), .sel(core_state));
  Adder #(.width(3)) adder_1 (.a(core_state), .b(bit_extender_1_out), .out(adder_1_out));  // open: cin, cout
  and and_1 (and_1_out, comparator_1_eq, not_1_out);
  Comparator #(.width(3)) comparator_1 (.a(core_state), .b(3'b110), .eq(comparator_1_eq));  // open: gt, lt
  Multiplexer #(.width(3)) multiplexer_2 (.in0(adder_1_out), .in1(3'b001), .out(multiplexer_2_out), .sel(and_1_out));
  not not_1 (not_1_out, and_2_out);
  and and_2 (and_2_out, comparator_1_eq, decoded_ret);
  Register current_pc_reg_1 (.D(next_pc_1), .en(and_1_out), .clk(clk), .Q(current_pc_1), .clr(reset));
  Register current_pc_reg_2 (.D(next_pc_2), .en(and_1_out), .clk(clk), .Q(current_pc_2), .clr(reset));
  Register current_pc_reg_3 (.D(next_pc_3), .en(and_1_out), .clk(clk), .Q(current_pc_3), .clr(reset));
  Register current_pc_reg_4 (.D(next_pc_4), .en(and_1_out), .clk(clk), .Q(current_pc_4), .clr(reset));
  Register #(.width(3)) core_state_reg (.D(multiplexer_2_out), .en(not_2_out), .clk(clk), .Q(core_state), .clr(reset));
  not not_2 (not_2_out, reset);
  Register #(.width(1)) register_1 (.D(and_2_out), .en(and_2_out), .clk(clk), .Q(done), .clr(reset));
endmodule
