// Logisim project scheduler_test.circ as structural Verilog: 2 circuits, main circuit main
module main (
);

  Multiplexer #(.select(3), .width(8)) multiplexer_1 ();  // open: in0, in1, in2, in3, in4, in5, in6, in7, out, sel
endmodule

module scheduler (
  input  [7:0] next_pc_1,
  input  [7:0] next_pc_2,
  input  [7:0] next_pc_3,
  input  [7:0] next_pc_4,
  input  reset,
  input  clk,
  input  decoded_ret,
  input  start,
  input  [2:0] fetcher_state,
  input  [7:0] lsu_state,
  output [7:0] current_pc_1,
  output [7:0] current_pc_2,
  output [7:0] current_pc_3,
  output [7:0] current_pc_4,
  output [2:0] core_state,
  output done
);

  wire and_1_out, and_2_out, comparator_1_eq, comparator_2_eq, multiplexer_1_out, not_1_out, not_2_out,
       not_3_out, or_1_out, or_2_out, or_3_out, or_4_out, or_5_out, or_6_out, or_7_out;
  wire [2:0] adder_1_out, bit_extender_1_out, multiplexer_2_out;

  or or_1 (or_1_out, lsu_state[0], lsu_state[1]);
  or or_2 (or_2_out, lsu_state[2], lsu_state[3]);
  or or_3 (or_3_out, lsu_state[4], lsu_state[5]);
  or or_4 (or_4_out, lsu_state[6], lsu_state[7]);
  or or_5 (or_5_out, or_1_out, or_2_out);
  or or_6 (or_6_out, or_3_out, or_4_out);
  or or_7 (or_7_out, or_5_out, or_6_out);
  not not_1 (not_1_out, or_7_out);
  Comparator #(.width(3)) comparator_1 (.a(fetcher_state), .b(3'b010), .eq(comparator_1_eq));  // open: gt, lt
  assign bit_extender_1_out = {{2{1'b0}}, multiplexer_1_out};  // Bit_Extender bit_extender_1
  Multiplexer #(.select(3)) multiplexer_1 (
    .in0(start), .in1(comparator_1_eq), .in2(1'b1), .in3(1'b1), .in4(not_1_out), .in5(1'b1), .in6(and_2_out),
    .in7(1'b0), .out(multiplexer_1_out), .sel(core_state));
  Adder #(.width(3)) adder_1 (.a(core_state), .b(bit_extender_1_out), .out(adder_1_out));  // open: cin, cout
  and and_1 (and_1_out, comparator_2_eq, not_2_out);
  Comparator #(.width(3)) comparator_2 (.a(core_state), .b(3'b110), .eq(comparator_2_eq));  // open: gt, lt
  Multiplexer #(.width(3)) multiplexer_2 (.in0(adder_1_out), .in1(3'b001), .out(multiplexer_2_out), .sel(and_1_out));
  not not_2 (not_2_out, and_2_out);
  and and_2 (and_2_out, comparator_2_eq, decoded_ret);
  Register current_pc_reg_1 (.D(next_pc_1), .en(and_1_out), .clk(clk), .Q(current_pc_1));  // open: clr
  Register current_pc_reg_2 (.D(next_pc_2), .en(and_1_out), .clk(clk), .Q(current_pc_2));  // open: clr
  Register current_pc_reg_3 (.D(next_pc_3), .en(and_1_out), .clk(clk), .Q(current_pc_3));  // open: clr
  Register current_pc_reg_4 (.D(next_pc_4), .en(and_1_out), .clk(clk), .Q(current_pc_4), .clr(reset));
  Register #(.width(3)) core_state_reg (.D(multiplexer_2_out), .en(not_3_out), .clk(clk), .Q(core_state), .clr(reset));
  not not_3 (not_3_out, reset);
  or or_8 (done, reset, and_2_out);
endmodule
